// Logisim project Abel_Andrade_Santos.circ as structural Verilog: 5 circuits, main circuit main
module main (
  input  [7:0] Testes,
  input  in_2,
  input  s_R0,
  input  s_R1,
  input  s_R2,
  input  s_R3,
  input  e_R0,
  input  e_R1,
  input  e_R2,
  input  e_R3,
  input  in_11,
  output out_12
);

  wire [7:0] controlled_buffer_1_out;

  // Probe on controlled_buffer_1_out
  assign controlled_buffer_1_out = in_2 ? Testes : 8'bz;  // Controlled_Buffer controlled_buffer_1
  Registrador8bits R0 (
    .in_1(controlled_buffer_1_out), .Set(s_R0), .Enable(e_R0), .R_8bits_out(controlled_buffer_1_out));
  Registrador8bits R1 (
    .in_1(controlled_buffer_1_out), .Set(s_R1), .Enable(e_R1), .R_8bits_out(controlled_buffer_1_out));
  Registrador8bits R2 (
    .in_1(controlled_buffer_1_out), .Set(s_R2), .Enable(e_R2), .R_8bits_out(controlled_buffer_1_out));
  Registrador8bits R3 (
    .in_1(controlled_buffer_1_out), .Set(s_R3), .Enable(e_R3), .R_8bits_out(controlled_buffer_1_out));
  // Somador somador_1: pin names not known; wires that end beside it: controlled_buffer_1_out, controlled_buffer_1_out, in_11, out_12, controlled_buffer_1_out

  // Notes on the sheet:
  //   Abel Andrade Prazeres dos Santos
  //   Matricula:22450083
endmodule

module Somador (
  input  c_in8b,
  input  [7:0] a_8b,
  input  [7:0] b_8b,
  output [7:0] out_8b,
  output c_out8b
);

  wire somador1bit_1_c_out, somador1bit_2_c_out, somador1bit_3_c_out, somador1bit_4_c_out,
       somador1bit_5_c_out, somador1bit_6_c_out, somador1bit_7_c_out;

  somador1bit somador1bit_1 (.a(a_8b[0]), .b(b_8b[0]), .in_1(c_in8b), .C_out(somador1bit_1_c_out), .Sum_out(out_8b[0]));
  somador1bit somador1bit_2 (
    .a(a_8b[1]), .b(b_8b[1]), .in_1(somador1bit_1_c_out), .C_out(somador1bit_2_c_out), .Sum_out(out_8b[1]));
  somador1bit somador1bit_3 (
    .a(a_8b[2]), .b(b_8b[2]), .in_1(somador1bit_2_c_out), .C_out(somador1bit_3_c_out), .Sum_out(out_8b[2]));
  somador1bit somador1bit_4 (
    .a(a_8b[3]), .b(b_8b[3]), .in_1(somador1bit_3_c_out), .C_out(somador1bit_4_c_out), .Sum_out(out_8b[3]));
  somador1bit somador1bit_5 (
    .a(a_8b[4]), .b(b_8b[4]), .in_1(somador1bit_4_c_out), .C_out(somador1bit_5_c_out), .Sum_out(out_8b[4]));
  somador1bit somador1bit_6 (
    .a(a_8b[5]), .b(b_8b[5]), .in_1(somador1bit_5_c_out), .C_out(somador1bit_6_c_out), .Sum_out(out_8b[5]));
  somador1bit somador1bit_7 (
    .a(a_8b[6]), .b(b_8b[6]), .in_1(somador1bit_6_c_out), .C_out(somador1bit_7_c_out), .Sum_out(out_8b[6]));
  somador1bit somador1bit_8 (
    .a(a_8b[7]), .b(b_8b[7]), .in_1(somador1bit_7_c_out), .C_out(c_out8b), .Sum_out(out_8b[7]));
endmodule

module somador1bit (
  input  in_1,
  input  a,
  input  b,
  output Sum_out,
  output C_out
);

  wire and_1_out, and_2_out, and_3_out, xor_1_out;

  xor xor_1 (xor_1_out, a, b);
  and and_1 (and_1_out, in_1, a);
  and and_2 (and_2_out, in_1, b);
  and and_3 (and_3_out, a, b);
  xor xor_2 (Sum_out, xor_1_out, in_1);
  or or_1 (C_out, and_1_out, and_2_out, and_3_out);

  // Notes on the sheet:
  //   c_in
endmodule

module Registrador1bit (
  input  in_1,
  input  in_2,
  output out_3
);

  wire nand_1_out, nand_2_out, nand_4_out;

  nand nand_1 (nand_1_out, in_1, in_2);
  nand nand_2 (nand_2_out, nand_1_out, in_2);
  nand nand_3 (out_3, nand_1_out, nand_4_out);
  nand nand_4 (nand_4_out, out_3, nand_2_out);
endmodule

module Registrador8bits (
  input  [7:0] in_1,
  input  Set,
  input  Enable,
  output [7:0] R_8bits_out
);

  wire registrador1bit_1_out_3, registrador1bit_2_out_3, registrador1bit_3_out_3, registrador1bit_4_out_3,
       registrador1bit_5_out_3, registrador1bit_6_out_3, registrador1bit_7_out_3, registrador1bit_8_out_3;

  Registrador1bit registrador1bit_1 (.in_1(in_1[0]), .in_2(Set), .out_3(registrador1bit_1_out_3));
  Registrador1bit registrador1bit_2 (.in_1(in_1[1]), .in_2(Set), .out_3(registrador1bit_2_out_3));
  Registrador1bit registrador1bit_3 (.in_1(in_1[2]), .in_2(Set), .out_3(registrador1bit_3_out_3));
  Registrador1bit registrador1bit_4 (.in_1(in_1[3]), .in_2(Set), .out_3(registrador1bit_4_out_3));
  Registrador1bit registrador1bit_5 (.in_1(in_1[4]), .in_2(Set), .out_3(registrador1bit_5_out_3));
  Registrador1bit registrador1bit_6 (.in_1(in_1[5]), .in_2(Set), .out_3(registrador1bit_6_out_3));
  Registrador1bit registrador1bit_7 (.in_1(in_1[6]), .in_2(Set), .out_3(registrador1bit_7_out_3));
  Registrador1bit registrador1bit_8 (.in_1(in_1[7]), .in_2(Set), .out_3(registrador1bit_8_out_3));
  assign R_8bits_out[0] = Enable ? registrador1bit_1_out_3 : 1'bz;  // Controlled_Buffer controlled_buffer_1
  assign R_8bits_out[1] = Enable ? registrador1bit_2_out_3 : 1'bz;  // Controlled_Buffer controlled_buffer_2
  assign R_8bits_out[2] = Enable ? registrador1bit_3_out_3 : 1'bz;  // Controlled_Buffer controlled_buffer_3
  assign R_8bits_out[3] = Enable ? registrador1bit_4_out_3 : 1'bz;  // Controlled_Buffer controlled_buffer_4
  assign R_8bits_out[4] = Enable ? registrador1bit_5_out_3 : 1'bz;  // Controlled_Buffer controlled_buffer_5
  assign R_8bits_out[5] = Enable ? registrador1bit_6_out_3 : 1'bz;  // Controlled_Buffer controlled_buffer_6
  assign R_8bits_out[6] = Enable ? registrador1bit_7_out_3 : 1'bz;  // Controlled_Buffer controlled_buffer_7
  assign R_8bits_out[7] = Enable ? registrador1bit_8_out_3 : 1'bz;  // Controlled_Buffer controlled_buffer_8
endmodule
