// Logisim project Abel_Severo_Rocha.circ as structural Verilog: 7 circuits, main circuit main
module SOMADOR_BIN (
  input  C_in,
  input  A,
  input  B,
  output out_4,
  output C_out
);

  wire and_1_out, and_2_out, and_3_out, xor_1_out;

  xor xor_1 (xor_1_out, A, B);
  and and_1 (and_1_out, A, C_in);
  and and_2 (and_2_out, A, B);
  and and_3 (and_3_out, B, C_in);
  xor xor_2 (out_4, xor_1_out, C_in);
  or or_1 (C_out, and_1_out, and_2_out, and_3_out);

  // Notes on the sheet:
  //   Somador com cOUT
endmodule

module SOMADOR_8Bits (
  input  in_1,
  input  [7:0] in_2,
  input  [7:0] in_3,
  output [7:0] out_4,
  output C_out
);

  wire somador_bin_1_c_out, somador_bin_2_c_out, somador_bin_3_c_out, somador_bin_4_c_out,
       somador_bin_5_c_out, somador_bin_6_c_out, somador_bin_7_c_out;

  SOMADOR_BIN somador_bin_1 (.A(in_2[0]), .B(in_3[0]), .C_in(in_1), .C_out(somador_bin_1_c_out), .out_4(out_4[0]));
  SOMADOR_BIN somador_bin_2 (
    .A(in_2[1]), .B(in_3[1]), .C_in(somador_bin_1_c_out), .C_out(somador_bin_2_c_out), .out_4(out_4[1]));
  SOMADOR_BIN somador_bin_3 (
    .A(in_2[2]), .B(in_3[2]), .C_in(somador_bin_2_c_out), .C_out(somador_bin_3_c_out), .out_4(out_4[2]));
  SOMADOR_BIN somador_bin_4 (
    .A(in_2[3]), .B(in_3[3]), .C_in(somador_bin_3_c_out), .C_out(somador_bin_4_c_out), .out_4(out_4[3]));
  SOMADOR_BIN somador_bin_5 (
    .A(in_2[4]), .B(in_3[4]), .C_in(somador_bin_4_c_out), .C_out(somador_bin_5_c_out), .out_4(out_4[4]));
  SOMADOR_BIN somador_bin_6 (
    .A(in_2[5]), .B(in_3[5]), .C_in(somador_bin_5_c_out), .C_out(somador_bin_6_c_out), .out_4(out_4[5]));
  SOMADOR_BIN somador_bin_7 (
    .A(in_2[6]), .B(in_3[6]), .C_in(somador_bin_6_c_out), .C_out(somador_bin_7_c_out), .out_4(out_4[6]));
  SOMADOR_BIN somador_bin_8 (.A(in_2[7]), .B(in_3[7]), .C_in(somador_bin_7_c_out), .C_out(C_out), .out_4(out_4[7]));
endmodule

module MEMORY_1bit (
  input  in_1,
  input  in_2,
  output out_3
);

  wire nand_1_out, nand_2_out, nand_4_out;

  nand nand_1 (nand_1_out, in_1, in_2);
  nand nand_2 (nand_2_out, nand_1_out, in_2);
  nand nand_3 (out_3, nand_1_out, nand_4_out);
  nand nand_4 (nand_4_out, out_3, nand_2_out);
endmodule

module MEMORY_1byte (
  input  in_1,
  input  in_2,
  input  in_3,
  input  in_4,
  input  in_5,
  input  in_6,
  input  in_7,
  input  in_8,
  input  Set,
  output out_10,
  output out_11,
  output out_12,
  output out_13,
  output out_14,
  output out_15,
  output out_16,
  output out_17
);

  MEMORY_1bit memory_1bit_1 (.in_1(in_1), .in_2(Set), .out_3(out_10));
  MEMORY_1bit memory_1bit_2 (.in_1(in_2), .in_2(Set), .out_3(out_11));
  MEMORY_1bit memory_1bit_3 (.in_1(in_3), .in_2(Set), .out_3(out_12));
  MEMORY_1bit memory_1bit_4 (.in_1(in_4), .in_2(Set), .out_3(out_13));
  MEMORY_1bit memory_1bit_5 (.in_1(in_5), .in_2(Set), .out_3(out_14));
  MEMORY_1bit memory_1bit_6 (.in_1(in_6), .in_2(Set), .out_3(out_15));
  MEMORY_1bit memory_1bit_7 (.in_1(in_7), .in_2(Set), .out_3(out_16));
  MEMORY_1bit memory_1bit_8 (.in_1(in_8), .in_2(Set), .out_3(out_17));
endmodule

module main (
  input  in_1,
  input  [7:0] in_2,
  input  [7:0] in_3,
  input  in_4,
  input  Sety,
  input  in_6,
  input  in_7,
  input  in_8,
  input  [7:0] in_9,
  input  in_10,
  input  Enabley,
  input  [1:0] in_12,
  input  [7:0] in_13,
  input  [7:0] in_14,
  input  in_15,
  input  Set,
  input  in_17,
  input  in_18,
  input  in_19,
  input  setx,
  input  enablex,
  input  Enable,
  input  in_23,
  input  in_24,
  input  in_25,
  output [7:0] out_26,
  output [7:0] out_27,
  output [7:0] out_28,
  output [7:0] out_29
);

  wire demultiplexer_1_out0, demultiplexer_1_out1, demultiplexer_1_out2, demultiplexer_1_out3;

  SOMADOR_8Bits somador_8bits_1 (.in_2(in_3), .in_3(in_9), .in_1(in_1), .C_out(in_10), .out_4(out_27));
  REGISTRADOR registrador_1 (.in_1(in_14), .Set(setx), .enable(enablex), .out_4(out_29));
  assign out_26 = in_4 ? in_2 : 8'bz;  // Controlled_Buffer controlled_buffer_1
  Demultiplexer #(.select(2)) demultiplexer_1 (
    .out0(demultiplexer_1_out0), .out1(demultiplexer_1_out1), .out2(demultiplexer_1_out2),
    .out3(demultiplexer_1_out3), .in(Enabley), .sel(in_12));
  REGISTRADOR registrador_2 (.in_1(out_26), .Set(Sety), .enable(demultiplexer_1_out0), .out_4(out_26));
  assign out_28 = in_15 ? in_13 : 8'bz;  // Controlled_Buffer controlled_buffer_2
  REGISTRADOR registrador_3 (.in_1(out_26), .Set(in_6), .enable(demultiplexer_1_out1), .out_4(out_26));
  REGISTRADOR registrador_4 (.in_1(out_28), .Set(Set), .enable(Enable), .out_4(out_28));
  REGISTRADOR registrador_5 (.in_1(out_26), .Set(in_7), .enable(demultiplexer_1_out2), .out_4(out_26));
  REGISTRADOR registrador_6 (.in_1(out_28), .Set(in_17), .enable(in_23), .out_4(out_28));
  REGISTRADOR registrador_7 (.in_1(out_26), .Set(in_8), .enable(demultiplexer_1_out3), .out_4(out_26));
  REGISTRADOR registrador_8 (.in_1(out_28), .Set(in_18), .enable(in_24), .out_4(out_28));
  REGISTRADOR registrador_9 (.in_1(out_28), .Set(in_19), .enable(in_25), .out_4(out_28));

  // Notes on the sheet:
  //   Somador 
  //   ABEL SEVERO ROCHA 22401917
  //   registrador
  //   registradores com barramento com mux
  //   registradores com barramento sem mux
endmodule

module REGISTRADOR (
  input  [7:0] in_1,
  input  Set,
  input  enable,
  output [7:0] out_4
);

  wire memory_1byte_1_out_10, memory_1byte_1_out_11, memory_1byte_1_out_12, memory_1byte_1_out_13,
       memory_1byte_1_out_14, memory_1byte_1_out_15, memory_1byte_1_out_16, memory_1byte_1_out_17;
  wire [7:0] habilitador_1_out_10;

  MEMORY_1byte memory_1byte_1 (
    .in_1(in_1[0]), .in_2(in_1[1]), .in_3(in_1[2]), .in_4(in_1[3]), .in_5(in_1[4]), .in_6(in_1[5]),
    .in_7(in_1[6]), .in_8(in_1[7]), .Set(Set), .out_10(memory_1byte_1_out_10),
    .out_11(memory_1byte_1_out_11), .out_12(memory_1byte_1_out_12), .out_13(memory_1byte_1_out_13),
    .out_14(memory_1byte_1_out_14), .out_15(memory_1byte_1_out_15), .out_16(memory_1byte_1_out_16),
    .out_17(memory_1byte_1_out_17));
  HABILITADOR habilitador_1 (
    .in_1(memory_1byte_1_out_10), .in_2(memory_1byte_1_out_11), .in_3(memory_1byte_1_out_12),
    .in_4(memory_1byte_1_out_13), .in_5(memory_1byte_1_out_14), .in_6(memory_1byte_1_out_15),
    .in_7(memory_1byte_1_out_16), .in_8(memory_1byte_1_out_17), .Enable(enable),
    .out_10(habilitador_1_out_10[0]), .out_11(habilitador_1_out_10[1]), .out_12(habilitador_1_out_10[2]),
    .out_13(habilitador_1_out_10[3]), .out_14(habilitador_1_out_10[4]), .out_15(habilitador_1_out_10[5]),
    .out_16(habilitador_1_out_10[6]), .out_17(habilitador_1_out_10[7]));
  assign out_4 = enable ? habilitador_1_out_10 : 8'bz;  // Controlled_Buffer controlled_buffer_1
endmodule

module HABILITADOR (
  input  in_1,
  input  in_2,
  input  in_3,
  input  in_4,
  input  in_5,
  input  in_6,
  input  in_7,
  input  in_8,
  input  Enable,
  output out_10,
  output out_11,
  output out_12,
  output out_13,
  output out_14,
  output out_15,
  output out_16,
  output out_17
);

  and and_1 (out_10, in_1, Enable);
  and and_2 (out_11, in_2, Enable);
  and and_3 (out_12, in_3, Enable);
  and and_4 (out_13, in_4, Enable);
  and and_5 (out_14, in_5, Enable);
  and and_6 (out_15, in_6, Enable);
  and and_7 (out_16, in_7, Enable);
  and and_8 (out_17, in_8, Enable);
endmodule
