// Logisim project Adrian_Batista.circ as structural Verilog
module main (
  input  [7:0] input_main,
  input  enable_in,
  input  s1,
  input  s4,
  input  s2,
  input  s3,
  input  e4,
  input  e2,
  input  e3,
  input  e1,
  input  [7:0] A_s,
  input  c_in,
  input  [7:0] B_s,
  output [7:0] out_14,
  output [7:0] out_15,
  output out_16
);

  wire [7:0] registrador_8bits_1_dados, registrador_8bits_2_dados, registrador_8bits_3_dados,
       registrador_8bits_4_dados;

  assign out_14 = enable_in ? input_main : 8'bz;  // Controlled_Buffer controlled_buffer_1
  assign out_14 = e1 ? registrador_8bits_1_dados : 8'bz;  // Controlled_Buffer controlled_buffer_2
  registrador_8bits registrador_8bits_1 (.input_8(out_14), .s(s1), .enable_i(e1), .dados(registrador_8bits_1_dados));
  registrador_8bits registrador_8bits_2 (.input_8(out_14), .s(s2), .enable_i(e2), .dados(registrador_8bits_2_dados));
  assign out_14 = e2 ? registrador_8bits_2_dados : 8'bz;  // Controlled_Buffer controlled_buffer_3
  somador_8bits somador_8bits_1 (.A(A_s), .c_in(c_in), .B(B_s), .output_soma(out_15), .c_out(out_16));
  registrador_8bits registrador_8bits_3 (.input_8(out_14), .s(s3), .enable_i(e3), .dados(registrador_8bits_3_dados));
  assign out_14 = e3 ? registrador_8bits_3_dados : 8'bz;  // Controlled_Buffer controlled_buffer_4
  assign out_14 = e4 ? registrador_8bits_4_dados : 8'bz;  // Controlled_Buffer controlled_buffer_5
  registrador_8bits registrador_8bits_4 (.input_8(out_14), .s(s4), .enable_i(e4), .dados(registrador_8bits_4_dados));

  // Notes on the sheet:
  //   Adrian Batista Pereira
  //   22401915
endmodule

module somador1bti (
  input  cin,
  input  a,
  input  b,
  output c,
  output cout
);

  wire and_1_out, and_2_out, and_3_out, xor_1_out;

  xor xor_1 (xor_1_out, a, b);
  and and_1 (and_1_out, a, cin);
  and and_2 (and_2_out, a, b);
  and and_3 (and_3_out, b, cin);
  xor xor_2 (c, xor_1_out, cin);
  or or_1 (cout, and_1_out, and_2_out, and_3_out);
endmodule

module somador8bits (
  input  cin,
  input  [7:0] in_2,
  input  [7:0] in_3,
  output [7:0] out_4,
  output cout
);

  wire somador1bti_1_cout, somador1bti_2_cout, somador1bti_3_cout, somador1bti_4_cout, somador1bti_5_cout,
       somador1bti_6_cout, somador1bti_7_cout;

  somador1bti somador1bti_1 (.a(in_2[0]), .b(in_3[0]), .cin(cin), .c(out_4[0]), .cout(somador1bti_1_cout));
  somador1bti somador1bti_2 (
    .a(in_2[1]), .b(in_3[1]), .cin(somador1bti_1_cout), .c(out_4[1]), .cout(somador1bti_2_cout));
  somador1bti somador1bti_3 (
    .a(in_2[2]), .b(in_3[2]), .cin(somador1bti_2_cout), .c(out_4[2]), .cout(somador1bti_3_cout));
  somador1bti somador1bti_4 (
    .a(in_2[3]), .b(in_3[3]), .cin(somador1bti_3_cout), .c(out_4[3]), .cout(somador1bti_4_cout));
  somador1bti somador1bti_5 (
    .a(in_2[4]), .b(in_3[4]), .cin(somador1bti_4_cout), .c(out_4[4]), .cout(somador1bti_5_cout));
  somador1bti somador1bti_6 (
    .a(in_2[5]), .b(in_3[5]), .cin(somador1bti_5_cout), .c(out_4[5]), .cout(somador1bti_6_cout));
  somador1bti somador1bti_7 (
    .a(in_2[6]), .b(in_3[6]), .cin(somador1bti_6_cout), .c(out_4[6]), .cout(somador1bti_7_cout));
  somador1bti somador1bti_8 (.a(in_2[7]), .b(in_3[7]), .cin(somador1bti_7_cout), .c(out_4[7]), .cout(cout));
endmodule

module memory1bit (
  input  i,
  input  set,
  output out_3
);

  wire nand_1_out, nand_2_out, nand_4_out;

  nand nand_1 (nand_1_out, i, set);
  nand nand_2 (nand_2_out, nand_1_out, set);
  nand nand_3 (out_3, nand_1_out, nand_4_out);
  nand nand_4 (nand_4_out, out_3, nand_2_out);
endmodule

module memory8bits (
  input  i1,
  input  i2,
  input  i3,
  input  i4,
  input  i5,
  input  i6,
  input  i7,
  input  i8,
  input  set,
  output out_10,
  output out_11,
  output out_12,
  output out_13,
  output out_14,
  output out_15,
  output out_16,
  output out_17
);

  memory1bit memory1bit_1 (.i(i1), .set(set), .out_3(out_10));
  memory1bit memory1bit_2 (.i(i2), .set(set), .out_3(out_11));
  memory1bit memory1bit_3 (.i(i3), .set(set), .out_3(out_12));
  memory1bit memory1bit_4 (.i(i4), .set(set), .out_3(out_13));
  memory1bit memory1bit_5 (.i(i5), .set(set), .out_3(out_14));
  memory1bit memory1bit_6 (.i(i6), .set(set), .out_3(out_15));
  memory1bit memory1bit_7 (.i(i7), .set(set), .out_3(out_16));
  memory1bit memory1bit_8 (.i(i8), .set(set), .out_3(out_17));
endmodule

module memory1byte (
  input  in_1,
  input  in_2,
  input  in_3,
  input  in_4,
  input  in_5,
  input  in_6,
  input  in_7,
  input  in_8,
  input  set,
  output out_10,
  output out_11,
  output out_12,
  output out_13,
  output out_14,
  output out_15,
  output out_16,
  output out_17
);

  memory8bits memory8bits_1 (
    .i1(in_1), .i2(in_2), .i3(in_3), .i4(in_4), .i5(in_5), .i6(in_6), .i7(in_7), .i8(in_8), .set(set),
    .out_10(out_10), .out_11(out_11), .out_12(out_12), .out_13(out_13), .out_14(out_14), .out_15(out_15),
    .out_16(out_16), .out_17(out_17));
endmodule

// e
module enable (
  input  dado,
  input  input_enable,
  output output_dado
);

  and and_1 (output_dado, dado, input_enable);
endmodule

module mem1bytese (
  input  in_1,
  input  in_2,
  input  in_3,
  input  in_4,
  input  in_5,
  input  in_6,
  input  in_7,
  input  in_8,
  input  s,
  input  en,
  output out_11,
  output out_12,
  output out_13,
  output out_14,
  output out_15,
  output out_16,
  output out_17,
  output out_18
);

  wire B_out_10, B_out_11, B_out_12, B_out_13, B_out_14, B_out_15, B_out_16, B_out_17;

  memory1byte B (
    .in_1(in_1), .in_2(in_2), .in_3(in_3), .in_4(in_4), .in_5(in_5), .in_6(in_6), .in_7(in_7), .in_8(in_8),
    .set(s), .out_10(B_out_10), .out_11(B_out_11), .out_12(B_out_12), .out_13(B_out_13), .out_14(B_out_14),
    .out_15(B_out_15), .out_16(B_out_16), .out_17(B_out_17));
  enable E (.dado(B_out_10), .input_enable(B_out_11), .output_dado(out_11));
endmodule

module registrador (
  input  [7:0] in_1,
  input  s,
  input  e,
  output [7:0] out_4
);

  mem1bytese r (
    .in_1(in_1[0]), .in_2(in_1[1]), .in_3(in_1[2]), .in_4(in_1[3]), .in_5(in_1[4]), .in_6(in_1[5]),
    .in_7(in_1[6]), .in_8(in_1[7]), .s(s), .en(e), .out_11(out_4[0]), .out_12(out_4[1]), .out_13(out_4[2]),
    .out_14(out_4[3]), .out_15(out_4[4]), .out_16(out_4[5]), .out_17(out_4[6]), .out_18(out_4[7]));
endmodule

module somador_1bit (
  input  c_in,
  input  A,
  input  B,
  output output_soma,
  output c_out
);

  wire and_1_out, and_2_out, and_3_out, xor_1_out;

  xor xor_1 (xor_1_out, A, B);
  and and_1 (and_1_out, A, c_in);
  and and_2 (and_2_out, A, B);
  and and_3 (and_3_out, c_in, B);
  xor xor_2 (output_soma, xor_1_out, c_in);
  or or_1 (c_out, and_1_out, and_2_out, and_3_out);
endmodule

module somador_8bits (
  input  [7:0] A,
  input  c_in,
  input  [7:0] B,
  output [7:0] output_soma,
  output c_out
);

  wire input_A_a0, input_A_a1, input_A_a2, input_A_a3, input_A_a4, input_A_a5, input_A_a6, input_A_a7,
       input_B_a0, input_B_a1, input_B_a2, input_B_a3, input_B_a4, input_B_a5, input_B_a6, input_B_a7,
       soma_bit_mais_significativo_output_soma, soma_bit_menos_significativo_c_out,
       soma_bit_menos_significativo_output_soma, somador_1bit_1_c_out, somador_1bit_1_output_soma,
       somador_1bit_2_c_out, somador_1bit_2_output_soma, somador_1bit_3_c_out, somador_1bit_3_output_soma,
       somador_1bit_4_c_out, somador_1bit_4_output_soma, somador_1bit_5_c_out, somador_1bit_5_output_soma,
       somador_1bit_6_c_out, somador_1bit_6_output_soma;

  distribuidor_8bits input_A (
    .A_8bits(A), .A0(input_A_a0), .A1(input_A_a1), .A2(input_A_a2), .A3(input_A_a3), .A4(input_A_a4),
    .A5(input_A_a5), .A6(input_A_a6), .A7(input_A_a7));
  distribuidor_8bits input_B (
    .A_8bits(B), .A0(input_B_a0), .A1(input_B_a1), .A2(input_B_a2), .A3(input_B_a3), .A4(input_B_a4),
    .A5(input_B_a5), .A6(input_B_a6), .A7(input_B_a7));
  somador_1bit soma_bit_menos_significativo (
    .c_in(c_in), .A(input_A_a0), .B(input_B_a0), .output_soma(soma_bit_menos_significativo_output_soma),
    .c_out(soma_bit_menos_significativo_c_out));
  somador_1bit somador_1bit_1 (
    .c_in(soma_bit_menos_significativo_c_out), .A(input_A_a1), .B(input_B_a1),
    .output_soma(somador_1bit_1_output_soma), .c_out(somador_1bit_1_c_out));
  somador_1bit somador_1bit_2 (
    .c_in(somador_1bit_1_c_out), .A(input_A_a2), .B(input_B_a2), .output_soma(somador_1bit_2_output_soma),
    .c_out(somador_1bit_2_c_out));
  somador_1bit somador_1bit_3 (
    .c_in(somador_1bit_2_c_out), .A(input_A_a3), .B(input_B_a3), .output_soma(somador_1bit_3_output_soma),
    .c_out(somador_1bit_3_c_out));
  somador_1bit somador_1bit_4 (
    .c_in(somador_1bit_3_c_out), .A(input_A_a4), .B(input_B_a4), .output_soma(somador_1bit_4_output_soma),
    .c_out(somador_1bit_4_c_out));
  somador_1bit somador_1bit_5 (
    .c_in(somador_1bit_4_c_out), .A(input_A_a5), .B(input_B_a5), .output_soma(somador_1bit_5_output_soma),
    .c_out(somador_1bit_5_c_out));
  somador_1bit somador_1bit_6 (
    .c_in(somador_1bit_5_c_out), .A(input_A_a6), .B(input_B_a6), .output_soma(somador_1bit_6_output_soma),
    .c_out(somador_1bit_6_c_out));
  somador_1bit soma_bit_mais_significativo (
    .c_in(somador_1bit_6_c_out), .A(input_A_a7), .B(input_B_a7),
    .output_soma(soma_bit_mais_significativo_output_soma), .c_out(c_out));
  simplifica_bits output_C (
    .A0(soma_bit_menos_significativo_output_soma), .A1(somador_1bit_1_output_soma),
    .A2(somador_1bit_2_output_soma), .A3(somador_1bit_3_output_soma), .A4(somador_1bit_4_output_soma),
    .A5(somador_1bit_5_output_soma), .A6(somador_1bit_6_output_soma),
    .A7(soma_bit_mais_significativo_output_soma), .A_8bits(output_soma));

  // Notes on the sheet:
  //   C0
  //   C1
  //   C2
  //   C3
  //   C4
  //   C5
  //   C6
  //   C7
endmodule

module simplifica_bits (
  input  A0,
  input  A1,
  input  A2,
  input  A3,
  input  A4,
  input  A5,
  input  A6,
  input  A7,
  output [7:0] A_8bits
);


  assign A_8bits = {A7, A6, A5, A4, A3, A2, A1, A0};
endmodule

module distribuidor_8bits (
  input  [7:0] A_8bits,
  output A0,
  output A1,
  output A2,
  output A3,
  output A4,
  output A5,
  output A6,
  output A7
);


  assign A0 = A_8bits[0];
  assign A1 = A_8bits[1];
  assign A2 = A_8bits[2];
  assign A3 = A_8bits[3];
  assign A4 = A_8bits[4];
  assign A5 = A_8bits[5];
  assign A6 = A_8bits[6];
  assign A7 = A_8bits[7];
endmodule

// R
module registrador_1bit (
  input  input_1bit,
  input  set,
  output bit_armazenado
);

  wire nand_1_out, nand_2_out, nand_4_out;

  nand nand_1 (nand_1_out, input_1bit, set);
  nand nand_2 (nand_2_out, nand_1_out, set);
  nand nand_3 (bit_armazenado, nand_1_out, nand_4_out);
  nand nand_4 (nand_4_out, bit_armazenado, nand_2_out);
endmodule

module registrador_8bits (
  input  [7:0] input_8,
  input  s,
  input  enable_i,
  output [7:0] dados
);

  wire distribuidor_8bits_1_a0, distribuidor_8bits_1_a1, distribuidor_8bits_1_a2, distribuidor_8bits_1_a3,
       distribuidor_8bits_1_a4, distribuidor_8bits_1_a5, distribuidor_8bits_1_a6, distribuidor_8bits_1_a7,
       enable_1_output_dado, enable_2_output_dado, enable_3_output_dado, enable_4_output_dado,
       enable_5_output_dado, enable_6_output_dado, enable_7_output_dado, enable_8_output_dado,
       registrador_1bit_1_bit_armazenado, registrador_1bit_2_bit_armazenado,
       registrador_1bit_3_bit_armazenado, registrador_1bit_4_bit_armazenado,
       registrador_1bit_5_bit_armazenado, registrador_1bit_6_bit_armazenado,
       registrador_1bit_7_bit_armazenado, registrador_1bit_8_bit_armazenado;

  distribuidor_8bits distribuidor_8bits_1 (
    .A_8bits(input_8), .A0(distribuidor_8bits_1_a0), .A1(distribuidor_8bits_1_a1),
    .A2(distribuidor_8bits_1_a2), .A3(distribuidor_8bits_1_a3), .A4(distribuidor_8bits_1_a4),
    .A5(distribuidor_8bits_1_a5), .A6(distribuidor_8bits_1_a6), .A7(distribuidor_8bits_1_a7));
  registrador_1bit registrador_1bit_1 (
    .input_1bit(distribuidor_8bits_1_a0), .set(s), .bit_armazenado(registrador_1bit_1_bit_armazenado));
  registrador_1bit registrador_1bit_2 (
    .input_1bit(distribuidor_8bits_1_a1), .set(s), .bit_armazenado(registrador_1bit_2_bit_armazenado));
  registrador_1bit registrador_1bit_3 (
    .input_1bit(distribuidor_8bits_1_a2), .set(s), .bit_armazenado(registrador_1bit_3_bit_armazenado));
  registrador_1bit registrador_1bit_4 (
    .input_1bit(distribuidor_8bits_1_a3), .set(s), .bit_armazenado(registrador_1bit_4_bit_armazenado));
  registrador_1bit registrador_1bit_5 (
    .input_1bit(distribuidor_8bits_1_a4), .set(s), .bit_armazenado(registrador_1bit_5_bit_armazenado));
  registrador_1bit registrador_1bit_6 (
    .input_1bit(distribuidor_8bits_1_a5), .set(s), .bit_armazenado(registrador_1bit_6_bit_armazenado));
  registrador_1bit registrador_1bit_7 (
    .input_1bit(distribuidor_8bits_1_a6), .set(s), .bit_armazenado(registrador_1bit_7_bit_armazenado));
  registrador_1bit registrador_1bit_8 (
    .input_1bit(distribuidor_8bits_1_a7), .set(s), .bit_armazenado(registrador_1bit_8_bit_armazenado));
  enable enable_1 (
    .dado(registrador_1bit_1_bit_armazenado), .input_enable(enable_i), .output_dado(enable_1_output_dado));
  enable enable_2 (
    .dado(registrador_1bit_2_bit_armazenado), .input_enable(enable_i), .output_dado(enable_2_output_dado));
  enable enable_3 (
    .dado(registrador_1bit_3_bit_armazenado), .input_enable(enable_i), .output_dado(enable_3_output_dado));
  enable enable_4 (
    .dado(registrador_1bit_4_bit_armazenado), .input_enable(enable_i), .output_dado(enable_4_output_dado));
  enable enable_5 (
    .dado(registrador_1bit_5_bit_armazenado), .input_enable(enable_i), .output_dado(enable_5_output_dado));
  enable enable_6 (
    .dado(registrador_1bit_6_bit_armazenado), .input_enable(enable_i), .output_dado(enable_6_output_dado));
  enable enable_7 (
    .dado(registrador_1bit_7_bit_armazenado), .input_enable(enable_i), .output_dado(enable_7_output_dado));
  enable enable_8 (
    .dado(registrador_1bit_8_bit_armazenado), .input_enable(enable_i), .output_dado(enable_8_output_dado));
  simplifica_bits simplifica_bits_1 (
    .A0(enable_1_output_dado), .A1(enable_2_output_dado), .A2(enable_3_output_dado),
    .A3(enable_4_output_dado), .A4(enable_5_output_dado), .A5(enable_6_output_dado),
    .A6(enable_7_output_dado), .A7(enable_8_output_dado), .A_8bits(dados));
endmodule
