// Logisim project Aline_Cunha.circ as structural Verilog: 10 circuits, main circuit main
module main (
  input  s,
  input  in_2,
  input  in_3,
  input  in_4,
  input  e,
  input  in_6,
  input  in_7,
  input  in_8
);

  wire [7:0] registrador_1bit_set_enable_1_out_4;

  registrador_1bit_set_enable registrador_1bit_set_enable_1 (
    .in_1(registrador_1bit_set_enable_1_out_4), .set(s), .e(e), .out_4(registrador_1bit_set_enable_1_out_4));
  registrador_1bit_set_enable registrador_1bit_set_enable_2 (
    .in_1(registrador_1bit_set_enable_1_out_4), .set(in_2), .e(in_6),
    .out_4(registrador_1bit_set_enable_1_out_4));
  registrador_1bit_set_enable registrador_1bit_set_enable_3 (
    .in_1(registrador_1bit_set_enable_1_out_4), .set(in_3), .e(in_7),
    .out_4(registrador_1bit_set_enable_1_out_4));
  registrador_1bit_set_enable registrador_1bit_set_enable_4 (
    .in_1(registrador_1bit_set_enable_1_out_4), .set(in_4), .e(in_8),
    .out_4(registrador_1bit_set_enable_1_out_4));

  // Notes on the sheet:
  //   Nome: Aline Silva da Cunha
  //   Matrícula: 22250558
endmodule

module memoria_1bit (
  input  i,
  input  set,
  output out_3
);

  wire nand_1_out, nand_2_out, nand_4_out;

  nand nand_1 (nand_1_out, i, set);
  nand nand_2 (nand_2_out, nand_1_out, set);
  nand nand_3 (out_3, nand_1_out, nand_4_out);
  nand nand_4 (nand_4_out, out_3, nand_2_out);
endmodule

module memoria_2bits (
  input  in_1,
  input  in_2,
  input  s,
  output out_4,
  output out_5
);

  memoria_1bit memoria_1bit_1 (.i(in_1), .set(s), .out_3(out_4));
  memoria_1bit memoria_1bit_2 (.i(in_2), .set(s), .out_3(out_5));
endmodule

module memoria_8bits (
  input  [7:0] in_1,
  input  s,
  output [7:0] out_3
);

  memoria_1bit memoria_1bit_1 (.i(in_1[0]), .set(s), .out_3(out_3[0]));
  memoria_1bit memoria_1bit_2 (.i(in_1[1]), .set(s), .out_3(out_3[1]));
  memoria_1bit memoria_1bit_3 (.i(in_1[2]), .set(s), .out_3(out_3[2]));
  memoria_1bit memoria_1bit_4 (.i(in_1[3]), .set(s), .out_3(out_3[3]));
  memoria_1bit memoria_1bit_5 (.i(in_1[4]), .set(s), .out_3(out_3[4]));
  memoria_1bit memoria_1bit_6 (.i(in_1[5]), .set(s), .out_3(out_3[5]));
  memoria_1bit memoria_1bit_7 (.i(in_1[6]), .set(s), .out_3(out_3[6]));
  memoria_1bit memoria_1bit_8 (.i(in_1[7]), .set(s), .out_3(out_3[7]));
endmodule

module enable (
  input  [7:0] in_1,
  input  e,
  output [7:0] out_3
);

  and and_1 (out_3[0], in_1[0], e);
  and and_2 (out_3[1], in_1[1], e);
  and and_3 (out_3[2], in_1[2], e);
  and and_4 (out_3[3], in_1[3], e);
  and and_5 (out_3[4], in_1[4], e);
  and and_6 (out_3[5], in_1[5], e);
  and and_7 (out_3[6], in_1[6], e);
  and and_8 (out_3[7], in_1[7], e);
endmodule

module registrador_1bit_set_enable (
  input  [7:0] in_1,
  input  e,
  input  set,
  output [7:0] out_4
);

  wire [7:0] memoria_8bits_1_out_3;

  memoria_8bits memoria_8bits_1 (.in_1(in_1), .s(set), .out_3(memoria_8bits_1_out_3));
  enable enable_1 (.in_1(memoria_8bits_1_out_3), .e(e), .out_3(out_4));
endmodule

module somador_1bit (
  input  c_in,
  input  a,
  input  b,
  output c,
  output c_out
);

  wire and_1_out, and_2_out, and_3_out, xor_1_out;

  xor xor_1 (xor_1_out, a, b);
  and and_1 (and_1_out, a, c_in);
  and and_2 (and_2_out, a, b);
  and and_3 (and_3_out, b, c_in);
  xor xor_2 (c, xor_1_out, c_in);
  or or_1 (c_out, and_1_out, and_2_out, and_3_out);
endmodule

module meio_somador (
  input  a,
  input  b,
  output out_3,
  output out_4
);

  xor xor_1 (out_3, a, b);
  and and_1 (out_4, a, b);
endmodule

module somador_semcarry (
  input  in_1,
  input  in_2,
  input  in_3,
  output out_4
);

  wire xor_1_out;

  xor xor_1 (xor_1_out, in_2, in_3);
  xor xor_2 (out_4, xor_1_out, in_1);
endmodule

module somador_8bits (
  input  in_1,
  input  [7:0] in_2,
  input  [7:0] in_3,
  output [7:0] out_4,
  output out_5
);

  wire somador_1bit_1_c_out, somador_1bit_2_c_out, somador_1bit_3_c_out, somador_1bit_4_c_out,
       somador_1bit_5_c_out, somador_1bit_6_c_out, somador_1bit_7_c_out;

  somador_1bit somador_1bit_1 (.a(in_2[0]), .b(in_3[0]), .c_in(in_1), .c_out(somador_1bit_1_c_out), .c(out_4[0]));
  somador_1bit somador_1bit_2 (
    .a(in_2[1]), .b(in_3[1]), .c_in(somador_1bit_1_c_out), .c_out(somador_1bit_2_c_out), .c(out_4[1]));
  somador_1bit somador_1bit_3 (
    .a(in_2[2]), .b(in_3[2]), .c_in(somador_1bit_2_c_out), .c_out(somador_1bit_3_c_out), .c(out_4[2]));
  somador_1bit somador_1bit_4 (
    .a(in_2[3]), .b(in_3[3]), .c_in(somador_1bit_3_c_out), .c_out(somador_1bit_4_c_out), .c(out_4[3]));
  somador_1bit somador_1bit_5 (
    .a(in_2[4]), .b(in_3[4]), .c_in(somador_1bit_4_c_out), .c_out(somador_1bit_5_c_out), .c(out_4[4]));
  somador_1bit somador_1bit_6 (
    .a(in_2[5]), .b(in_3[5]), .c_in(somador_1bit_5_c_out), .c_out(somador_1bit_6_c_out), .c(out_4[5]));
  somador_1bit somador_1bit_7 (
    .a(in_2[6]), .b(in_3[6]), .c_in(somador_1bit_6_c_out), .c_out(somador_1bit_7_c_out), .c(out_4[6]));
  somador_1bit somador_1bit_8 (.a(in_2[7]), .b(in_3[7]), .c_in(somador_1bit_7_c_out), .c_out(out_5), .c(out_4[7]));
endmodule
