// Logisim project AnaCarla.circ as structural Verilog: 7 circuits, main circuit main
module main (
  input  in_1,
  input  in_2,
  input  in_3,
  input  in_4,
  input  Soma_binaria,
  input  in_6,
  input  in_7,
  input  in_8,
  input  in_9,
  input  in_10,
  input  in_11,
  input  in_12,
  input  in_13,
  input  [7:0] in_14,
  input  [7:0] in_15,
  input  [7:0] in_16,
  input  in_17,
  input  in_18,
  input  in_19,
  input  in_20,
  input  in_21,
  input  in_22,
  input  in_23,
  input  in_24,
  input  in_25,
  output out_26,
  output out_27,
  output out_28,
  output out_29,
  output out_30,
  output out_31,
  output out_32,
  output [7:0] out_33,
  output out_34
);

  wire and_1_out, xor_2_out;
  wire [7:0] controlled_buffer_1_out;

  and and_1 (and_1_out, in_1, in_2);
  and and_2 (out_27, in_3, in_4);
  xor xor_1 (out_28, Soma_binaria, in_6);
  somador_1bit somador_1bit_1 (.a(in_11), .b(in_12), .c_in(in_10), .c_out(out_32), .c(out_31));
  // Probe on controlled_buffer_1_out
  not not_1 (out_26, and_1_out);
  and and_3 (out_29, Soma_binaria, in_6);
  xor xor_2 (xor_2_out, in_8, in_9);
  somador_8bits somador_8bits_1 (.in_1(in_14), .in_2(in_15), .in_3(in_13), .out_4(out_33), .out_5(out_34));
  assign controlled_buffer_1_out = in_17 ? in_16 : 8'bz;  // Controlled_Buffer controlled_buffer_1
  registrador_1byte_set_enable registrador_1byte_set_enable_1 (
    .in_1(controlled_buffer_1_out), .set(in_18), .ene(in_22), .out_4(controlled_buffer_1_out));
  xor xor_3 (out_30, xor_2_out, in_7);
  registrador_1byte_set_enable registrador_1byte_set_enable_2 (
    .in_1(controlled_buffer_1_out), .set(in_19), .ene(in_23), .out_4(controlled_buffer_1_out));
  registrador_1byte_set_enable registrador_1byte_set_enable_3 (
    .in_1(controlled_buffer_1_out), .set(in_20), .ene(in_24), .out_4(controlled_buffer_1_out));
  registrador_1byte_set_enable registrador_1byte_set_enable_4 (
    .in_1(controlled_buffer_1_out), .set(in_21), .ene(in_25), .out_4(controlled_buffer_1_out));

  // Notes on the sheet:
  //   Ana Carla de Araujo Fernandes
  //   Somador Completo
  //   Somador Completo de 8 bits
  //   Registrador de 1 byte com set e enable
endmodule

module somador_1bit (
  input  c_in,
  input  a,
  input  b,
  output c,
  output c_out
);

  wire and_1_out, and_2_out, and_3_out, xor_1_out;

  xor xor_1 (xor_1_out, a, b);
  and and_1 (and_1_out, a, c_in);
  and and_2 (and_2_out, a, b);
  and and_3 (and_3_out, b, c_in);
  xor xor_2 (c, xor_1_out, c_in);
  or or_1 (c_out, and_1_out, and_2_out, and_3_out);
endmodule

module somador_8bits (
  input  [7:0] in_1,
  input  [7:0] in_2,
  input  in_3,
  output [7:0] out_4,
  output out_5
);

  wire somador_1bit_1_c_out, somador_1bit_2_c_out, somador_1bit_3_c_out, somador_1bit_4_c_out,
       somador_1bit_5_c_out, somador_1bit_6_c_out, somador_1bit_7_c_out;

  somador_1bit somador_1bit_1 (.a(in_2[0]), .b(in_1[0]), .c_in(in_3), .c_out(somador_1bit_1_c_out), .c(out_4[0]));
  somador_1bit somador_1bit_2 (
    .a(in_2[1]), .b(in_1[1]), .c_in(somador_1bit_1_c_out), .c_out(somador_1bit_2_c_out), .c(out_4[1]));
  somador_1bit somador_1bit_3 (
    .a(in_2[2]), .b(in_1[2]), .c_in(somador_1bit_2_c_out), .c_out(somador_1bit_3_c_out), .c(out_4[2]));
  somador_1bit somador_1bit_4 (
    .a(in_2[3]), .b(in_1[3]), .c_in(somador_1bit_3_c_out), .c_out(somador_1bit_4_c_out), .c(out_4[3]));
  somador_1bit somador_1bit_5 (
    .a(in_2[4]), .b(in_1[4]), .c_in(somador_1bit_4_c_out), .c_out(somador_1bit_5_c_out), .c(out_4[4]));
  somador_1bit somador_1bit_6 (
    .a(in_2[5]), .b(in_1[5]), .c_in(somador_1bit_5_c_out), .c_out(somador_1bit_6_c_out), .c(out_4[5]));
  somador_1bit somador_1bit_7 (
    .a(in_2[6]), .b(in_1[6]), .c_in(somador_1bit_6_c_out), .c_out(somador_1bit_7_c_out), .c(out_4[6]));
  somador_1bit somador_1bit_8 (.a(in_2[7]), .b(in_1[7]), .c_in(somador_1bit_7_c_out), .c_out(out_5), .c(out_4[7]));
endmodule

module registrador_1bits (
  input  i,
  input  set,
  output out_3
);

  wire nand_1_out, nand_2_out, nand_4_out;

  nand nand_1 (nand_1_out, i, set);
  nand nand_2 (nand_2_out, nand_1_out, set);
  nand nand_3 (out_3, nand_1_out, nand_4_out);
  nand nand_4 (nand_4_out, out_3, nand_2_out);
endmodule

module registrador_8bits (
  input  [7:0] i,
  input  set,
  output [7:0] o
);

  registrador_1bits registrador_1bits_1 (.i(i[0]), .set(set), .out_3(o[0]));
  registrador_1bits registrador_1bits_2 (.i(i[1]), .set(set), .out_3(o[1]));
  registrador_1bits registrador_1bits_3 (.i(i[2]), .set(set), .out_3(o[2]));
  registrador_1bits registrador_1bits_4 (.i(i[3]), .set(set), .out_3(o[3]));
  registrador_1bits registrador_1bits_5 (.i(i[4]), .set(set), .out_3(o[4]));
  registrador_1bits registrador_1bits_6 (.i(i[5]), .set(set), .out_3(o[5]));
  registrador_1bits registrador_1bits_7 (.i(i[6]), .set(set), .out_3(o[6]));
  registrador_1bits registrador_1bits_8 (.i(i[7]), .set(set), .out_3(o[7]));
endmodule

module enable (
  input  [7:0] i,
  input  set,
  output [7:0] o
);

  and and_1 (o[0], i[0], set);
  and and_2 (o[1], i[1], set);
  and and_3 (o[2], i[2], set);
  and and_4 (o[3], i[3], set);
  and and_5 (o[4], i[4], set);
  and and_6 (o[5], i[5], set);
  and and_7 (o[6], i[6], set);
  and and_8 (o[7], i[7], set);
endmodule

module registrador_1byte_set_enable (
  input  [7:0] in_1,
  input  set,
  input  ene,
  output [7:0] out_4
);

  wire [7:0] enable_1_o, registrador_8bits_1_o;

  registrador_8bits registrador_8bits_1 (.i(in_1), .set(set), .o(registrador_8bits_1_o));
  enable enable_1 (.i(registrador_8bits_1_o), .set(ene), .o(enable_1_o));
  assign out_4 = ene ? enable_1_o : 8'bz;  // Controlled_Buffer controlled_buffer_1
endmodule
