// Logisim project André_Kaled_Duarte_Coutinho_Andrade.circ as structural Verilog: 8 circuits, main circuit main
module main (
  input  [7:0] INPUTS,
  input  enable_input,
  input  s1,
  input  s2,
  input  s3,
  input  s4,
  input  e1,
  input  e2,
  input  e3,
  input  e4,
  input  [7:0] A_soma,
  input  c_in,
  input  [7:0] B_soma,
  output [7:0] dado,
  output [7:0] resultado,
  output c_out
);

  wire [7:0] registrador_8bits_1_dados, registrador_8bits_2_dados, registrador_8bits_3_dados,
       registrador_8bits_4_dados;

  assign dado = enable_input ? INPUTS : 8'bz;  // Controlled_Buffer controlled_buffer_1
  assign dado = e1 ? registrador_8bits_1_dados : 8'bz;  // Controlled_Buffer controlled_buffer_2
  registrador_8bits registrador_8bits_1 (
    .input_8bits(dado), .set(s1), .enable_in(e1), .dados(registrador_8bits_1_dados));
  registrador_8bits registrador_8bits_2 (
    .input_8bits(dado), .set(s2), .enable_in(e2), .dados(registrador_8bits_2_dados));
  assign dado = e2 ? registrador_8bits_2_dados : 8'bz;  // Controlled_Buffer controlled_buffer_3
  somador_8bits somador_8bits_1 (.A(A_soma), .c_in(c_in), .B(B_soma), .output_soma(resultado), .c_out(c_out));
  registrador_8bits registrador_8bits_3 (
    .input_8bits(dado), .set(s3), .enable_in(e3), .dados(registrador_8bits_3_dados));
  assign dado = e3 ? registrador_8bits_3_dados : 8'bz;  // Controlled_Buffer controlled_buffer_4
  assign dado = e4 ? registrador_8bits_4_dados : 8'bz;  // Controlled_Buffer controlled_buffer_5
  registrador_8bits registrador_8bits_4 (
    .input_8bits(dado), .set(s4), .enable_in(e4), .dados(registrador_8bits_4_dados));

  // Notes on the sheet:
  //   22450837
  //   André Kaled Duarte Coutinho Andrade
  //   Parte dos registradores
  //   Parte do somador
endmodule

module somador_1bit (
  input  c_in,
  input  A,
  input  B,
  output output_soma,
  output c_out
);

  wire and_1_out, and_2_out, and_3_out, xor_1_out;

  xor xor_1 (xor_1_out, A, B);
  and and_1 (and_1_out, A, c_in);
  and and_2 (and_2_out, A, B);
  and and_3 (and_3_out, c_in, B);
  xor xor_2 (output_soma, xor_1_out, c_in);
  or or_1 (c_out, and_1_out, and_2_out, and_3_out);
endmodule

module somador_8bits (
  input  [7:0] A,
  input  c_in,
  input  [7:0] B,
  output [7:0] output_soma,
  output c_out
);

  wire input_A_a0, input_A_a1, input_A_a2, input_A_a3, input_A_a4, input_A_a5, input_A_a6, input_A_a7,
       input_B_a0, input_B_a1, input_B_a2, input_B_a3, input_B_a4, input_B_a5, input_B_a6, input_B_a7,
       soma_bit_mais_significativo_output_soma, soma_bit_menos_significativo_c_out,
       soma_bit_menos_significativo_output_soma, somador_1bit_1_c_out, somador_1bit_1_output_soma,
       somador_1bit_2_c_out, somador_1bit_2_output_soma, somador_1bit_3_c_out, somador_1bit_3_output_soma,
       somador_1bit_4_c_out, somador_1bit_4_output_soma, somador_1bit_5_c_out, somador_1bit_5_output_soma,
       somador_1bit_6_c_out, somador_1bit_6_output_soma;

  distribuidor_8bits input_A (
    .A_8bits(A), .A0(input_A_a0), .A1(input_A_a1), .A2(input_A_a2), .A3(input_A_a3), .A4(input_A_a4),
    .A5(input_A_a5), .A6(input_A_a6), .A7(input_A_a7));
  distribuidor_8bits input_B (
    .A_8bits(B), .A0(input_B_a0), .A1(input_B_a1), .A2(input_B_a2), .A3(input_B_a3), .A4(input_B_a4),
    .A5(input_B_a5), .A6(input_B_a6), .A7(input_B_a7));
  somador_1bit soma_bit_menos_significativo (
    .c_in(c_in), .A(input_A_a0), .B(input_B_a0), .output_soma(soma_bit_menos_significativo_output_soma),
    .c_out(soma_bit_menos_significativo_c_out));
  somador_1bit somador_1bit_1 (
    .c_in(soma_bit_menos_significativo_c_out), .A(input_A_a1), .B(input_B_a1),
    .output_soma(somador_1bit_1_output_soma), .c_out(somador_1bit_1_c_out));
  somador_1bit somador_1bit_2 (
    .c_in(somador_1bit_1_c_out), .A(input_A_a2), .B(input_B_a2), .output_soma(somador_1bit_2_output_soma),
    .c_out(somador_1bit_2_c_out));
  somador_1bit somador_1bit_3 (
    .c_in(somador_1bit_2_c_out), .A(input_A_a3), .B(input_B_a3), .output_soma(somador_1bit_3_output_soma),
    .c_out(somador_1bit_3_c_out));
  somador_1bit somador_1bit_4 (
    .c_in(somador_1bit_3_c_out), .A(input_A_a4), .B(input_B_a4), .output_soma(somador_1bit_4_output_soma),
    .c_out(somador_1bit_4_c_out));
  somador_1bit somador_1bit_5 (
    .c_in(somador_1bit_4_c_out), .A(input_A_a5), .B(input_B_a5), .output_soma(somador_1bit_5_output_soma),
    .c_out(somador_1bit_5_c_out));
  somador_1bit somador_1bit_6 (
    .c_in(somador_1bit_5_c_out), .A(input_A_a6), .B(input_B_a6), .output_soma(somador_1bit_6_output_soma),
    .c_out(somador_1bit_6_c_out));
  somador_1bit soma_bit_mais_significativo (
    .c_in(somador_1bit_6_c_out), .A(input_A_a7), .B(input_B_a7),
    .output_soma(soma_bit_mais_significativo_output_soma), .c_out(c_out));
  simplifica_bits output_C (
    .A0(soma_bit_menos_significativo_output_soma), .A1(somador_1bit_1_output_soma),
    .A2(somador_1bit_2_output_soma), .A3(somador_1bit_3_output_soma), .A4(somador_1bit_4_output_soma),
    .A5(somador_1bit_5_output_soma), .A6(somador_1bit_6_output_soma),
    .A7(soma_bit_mais_significativo_output_soma), .A_8bits(output_soma));

  // Notes on the sheet:
  //   C0
  //   C1
  //   C2
  //   C3
  //   C4
  //   C5
  //   C6
  //   C7
endmodule

module simplifica_bits (
  input  A0,
  input  A1,
  input  A2,
  input  A3,
  input  A4,
  input  A5,
  input  A6,
  input  A7,
  output [7:0] A_8bits
);


  assign A_8bits = {A7, A6, A5, A4, A3, A2, A1, A0};
endmodule

module distribuidor_8bits (
  input  [7:0] A_8bits,
  output A0,
  output A1,
  output A2,
  output A3,
  output A4,
  output A5,
  output A6,
  output A7
);


  assign A0 = A_8bits[0];
  assign A1 = A_8bits[1];
  assign A2 = A_8bits[2];
  assign A3 = A_8bits[3];
  assign A4 = A_8bits[4];
  assign A5 = A_8bits[5];
  assign A6 = A_8bits[6];
  assign A7 = A_8bits[7];
endmodule

// R
module registrador_1bit (
  input  input_1bit,
  input  set,
  output bit_armazenado
);

  wire nand_1_out, nand_2_out, nand_4_out;

  nand nand_1 (nand_1_out, input_1bit, set);
  nand nand_2 (nand_2_out, nand_1_out, set);
  nand nand_3 (bit_armazenado, nand_1_out, nand_4_out);
  nand nand_4 (nand_4_out, bit_armazenado, nand_2_out);
endmodule

module registrador_8bits (
  input  [7:0] input_8bits,
  input  set,
  input  enable_in,
  output [7:0] dados
);

  wire distribuidor_8bits_1_a0, distribuidor_8bits_1_a1, distribuidor_8bits_1_a2, distribuidor_8bits_1_a3,
       distribuidor_8bits_1_a4, distribuidor_8bits_1_a5, distribuidor_8bits_1_a6, distribuidor_8bits_1_a7,
       enable_1_output_dado, enable_2_output_dado, enable_3_output_dado, enable_4_output_dado,
       enable_5_output_dado, enable_6_output_dado, enable_7_output_dado, enable_8_output_dado,
       registrador_1bit_1_bit_armazenado, registrador_1bit_2_bit_armazenado,
       registrador_1bit_3_bit_armazenado, registrador_1bit_4_bit_armazenado,
       registrador_1bit_5_bit_armazenado, registrador_1bit_6_bit_armazenado,
       registrador_1bit_7_bit_armazenado, registrador_1bit_8_bit_armazenado;

  distribuidor_8bits distribuidor_8bits_1 (
    .A_8bits(input_8bits), .A0(distribuidor_8bits_1_a0), .A1(distribuidor_8bits_1_a1),
    .A2(distribuidor_8bits_1_a2), .A3(distribuidor_8bits_1_a3), .A4(distribuidor_8bits_1_a4),
    .A5(distribuidor_8bits_1_a5), .A6(distribuidor_8bits_1_a6), .A7(distribuidor_8bits_1_a7));
  registrador_1bit registrador_1bit_1 (
    .input_1bit(distribuidor_8bits_1_a0), .set(set), .bit_armazenado(registrador_1bit_1_bit_armazenado));
  registrador_1bit registrador_1bit_2 (
    .input_1bit(distribuidor_8bits_1_a1), .set(set), .bit_armazenado(registrador_1bit_2_bit_armazenado));
  registrador_1bit registrador_1bit_3 (
    .input_1bit(distribuidor_8bits_1_a2), .set(set), .bit_armazenado(registrador_1bit_3_bit_armazenado));
  registrador_1bit registrador_1bit_4 (
    .input_1bit(distribuidor_8bits_1_a3), .set(set), .bit_armazenado(registrador_1bit_4_bit_armazenado));
  registrador_1bit registrador_1bit_5 (
    .input_1bit(distribuidor_8bits_1_a4), .set(set), .bit_armazenado(registrador_1bit_5_bit_armazenado));
  registrador_1bit registrador_1bit_6 (
    .input_1bit(distribuidor_8bits_1_a5), .set(set), .bit_armazenado(registrador_1bit_6_bit_armazenado));
  registrador_1bit registrador_1bit_7 (
    .input_1bit(distribuidor_8bits_1_a6), .set(set), .bit_armazenado(registrador_1bit_7_bit_armazenado));
  registrador_1bit registrador_1bit_8 (
    .input_1bit(distribuidor_8bits_1_a7), .set(set), .bit_armazenado(registrador_1bit_8_bit_armazenado));
  enable enable_1 (
    .dado(registrador_1bit_1_bit_armazenado), .input_enable(enable_in), .output_dado(enable_1_output_dado));
  enable enable_2 (
    .dado(registrador_1bit_2_bit_armazenado), .input_enable(enable_in), .output_dado(enable_2_output_dado));
  enable enable_3 (
    .dado(registrador_1bit_3_bit_armazenado), .input_enable(enable_in), .output_dado(enable_3_output_dado));
  enable enable_4 (
    .dado(registrador_1bit_4_bit_armazenado), .input_enable(enable_in), .output_dado(enable_4_output_dado));
  enable enable_5 (
    .dado(registrador_1bit_5_bit_armazenado), .input_enable(enable_in), .output_dado(enable_5_output_dado));
  enable enable_6 (
    .dado(registrador_1bit_6_bit_armazenado), .input_enable(enable_in), .output_dado(enable_6_output_dado));
  enable enable_7 (
    .dado(registrador_1bit_7_bit_armazenado), .input_enable(enable_in), .output_dado(enable_7_output_dado));
  enable enable_8 (
    .dado(registrador_1bit_8_bit_armazenado), .input_enable(enable_in), .output_dado(enable_8_output_dado));
  simplifica_bits simplifica_bits_1 (
    .A0(enable_1_output_dado), .A1(enable_2_output_dado), .A2(enable_3_output_dado),
    .A3(enable_4_output_dado), .A4(enable_5_output_dado), .A5(enable_6_output_dado),
    .A6(enable_7_output_dado), .A7(enable_8_output_dado), .A_8bits(dados));
endmodule

// e
module enable (
  input  dado,
  input  input_enable,
  output output_dado
);

  and and_1 (output_dado, dado, input_enable);
endmodule
