// Logisim project Bruna_Brasil.circ as structural Verilog: 5 circuits, main circuit main
module main (
  input  [7:0] in_1,
  input  in_2,
  input  in_3,
  input  in_4,
  input  in_5,
  input  in_6,
  input  in_7,
  input  in_8,
  input  in_9,
  input  in_10,
  input  in_11,
  output out_12
);

  wire [7:0] controlled_buffer_1_out, SOMA_08_out_4, undriven, undriven_2;

  // Probe on controlled_buffer_1_out
  assign controlled_buffer_1_out = in_2 ? in_1 : 8'bz;  // Controlled_Buffer controlled_buffer_1
  registrador_8 reg_0 (.in_1(controlled_buffer_1_out), .S(in_3), .E(in_7), .out_4(controlled_buffer_1_out));
  registrador_8 reg_1 (.in_1(controlled_buffer_1_out), .S(in_4), .E(in_8), .out_4(controlled_buffer_1_out));
  registrador_8 reg_2 (.in_1(controlled_buffer_1_out), .S(in_5), .E(in_9), .out_4(controlled_buffer_1_out));
  registrador_8 reg_3 (.in_1(controlled_buffer_1_out), .S(in_6), .E(in_10), .out_4(controlled_buffer_1_out));
  somador_8 SOMA_08 (.c_in(in_11), .A(undriven_2), .B(undriven), .out_4(SOMA_08_out_4), .c_out(out_12));

  // Notes on the sheet:
  //   Bruna de Souza Brasil
  //   Matricula 22450657
  //   está desconectado para evitar o curto!
endmodule

module somador_1 (
  input  C_IN,
  input  A,
  input  B,
  output out_4,
  output C_OUT
);

  wire and_1_out, and_2_out, and_3_out, xor_1_out;

  and and_1 (and_1_out, A, C_IN);
  and and_2 (and_2_out, A, B);
  and and_3 (and_3_out, B, C_IN);
  xor xor_1 (xor_1_out, A, B);
  xor xor_2 (out_4, xor_1_out, C_IN);
  or or_1 (C_OUT, and_1_out, and_2_out, and_3_out);
endmodule

module somador_8 (
  input  c_in,
  input  [7:0] A,
  input  [7:0] B,
  output [7:0] out_4,
  output c_out
);

  wire somador_1_1_c_out, somador_1_2_c_out, somador_1_3_c_out, somador_1_4_c_out, somador_1_5_c_out,
       somador_1_6_c_out, somador_1_7_c_out;

  somador_1 somador_1_1 (.A(A[0]), .B(B[0]), .C_IN(c_in), .C_OUT(somador_1_1_c_out), .out_4(out_4[0]));
  somador_1 somador_1_2 (.A(A[1]), .B(B[1]), .C_IN(somador_1_1_c_out), .C_OUT(somador_1_2_c_out), .out_4(out_4[1]));
  somador_1 somador_1_3 (.A(A[2]), .B(B[2]), .C_IN(somador_1_2_c_out), .C_OUT(somador_1_3_c_out), .out_4(out_4[2]));
  somador_1 somador_1_4 (.A(A[3]), .B(B[3]), .C_IN(somador_1_3_c_out), .C_OUT(somador_1_4_c_out), .out_4(out_4[3]));
  somador_1 somador_1_5 (.A(A[4]), .B(B[4]), .C_IN(somador_1_4_c_out), .C_OUT(somador_1_5_c_out), .out_4(out_4[4]));
  somador_1 somador_1_6 (.A(A[5]), .B(B[5]), .C_IN(somador_1_5_c_out), .C_OUT(somador_1_6_c_out), .out_4(out_4[5]));
  somador_1 somador_1_7 (.A(A[6]), .B(B[6]), .C_IN(somador_1_6_c_out), .C_OUT(somador_1_7_c_out), .out_4(out_4[6]));
  somador_1 somador_1_8 (.A(A[7]), .B(B[7]), .C_IN(somador_1_7_c_out), .C_OUT(c_out), .out_4(out_4[7]));
endmodule

module circuito_1 (
  input  i,
  input  s,
  output o
);

  wire nand_1_out, nand_2_out, nand_4_out;

  nand nand_1 (nand_1_out, i, s);
  nand nand_2 (nand_2_out, nand_1_out, s);
  nand nand_3 (o, nand_1_out, nand_4_out);
  nand nand_4 (nand_4_out, o, nand_2_out);
endmodule

module registrador_8 (
  input  [7:0] in_1,
  input  E,
  input  S,
  output [7:0] out_4
);

  wire circuito_1_1_o, circuito_1_2_o, circuito_1_3_o, circuito_1_4_o, circuito_1_5_o, circuito_1_6_o,
       circuito_1_7_o, M_o;

  circuito_1 M (.i(in_1[0]), .s(S), .o(M_o));
  circuito_1 circuito_1_1 (.i(in_1[1]), .s(S), .o(circuito_1_1_o));
  circuito_1 circuito_1_2 (.i(in_1[2]), .s(S), .o(circuito_1_2_o));
  circuito_1 circuito_1_3 (.i(in_1[3]), .s(S), .o(circuito_1_3_o));
  circuito_1 circuito_1_4 (.i(in_1[4]), .s(S), .o(circuito_1_4_o));
  circuito_1 circuito_1_5 (.i(in_1[5]), .s(S), .o(circuito_1_5_o));
  circuito_1 circuito_1_6 (.i(in_1[6]), .s(S), .o(circuito_1_6_o));
  circuito_1 circuito_1_7 (.i(in_1[7]), .s(S), .o(circuito_1_7_o));
  assign out_4[0] = E ? M_o : 1'bz;  // Controlled_Buffer controlled_buffer_1
  assign out_4[1] = E ? circuito_1_1_o : 1'bz;  // Controlled_Buffer controlled_buffer_2
  assign out_4[2] = E ? circuito_1_2_o : 1'bz;  // Controlled_Buffer controlled_buffer_3
  assign out_4[3] = E ? circuito_1_3_o : 1'bz;  // Controlled_Buffer controlled_buffer_4
  assign out_4[4] = E ? circuito_1_4_o : 1'bz;  // Controlled_Buffer controlled_buffer_5
  assign out_4[5] = E ? circuito_1_5_o : 1'bz;  // Controlled_Buffer controlled_buffer_6
  assign out_4[6] = E ? circuito_1_6_o : 1'bz;  // Controlled_Buffer controlled_buffer_7
  assign out_4[7] = E ? circuito_1_7_o : 1'bz;  // Controlled_Buffer controlled_buffer_8
endmodule
