// Logisim project Carlos_Henrick_Cavalcante_Gomes.circ as structural Verilog: 10 circuits, main circuit main
module main (
  input  [7:0] in_1,
  input  in_2,
  input  in_3,
  input  in_4,
  input  in_5,
  input  in_6,
  input  in_7,
  input  in_8,
  input  in_9,
  input  in_10,
  input  in_11,
  input  in_12,
  input  in_13,
  output [7:0] out_14
);

  wire [7:0] registrador_1byte_s_e_1_out_4, registrador_1byte_s_e_2_out_4, registrador_1byte_s_e_3_out_4,
       registrador_1byte_s_e_4_out_4;

  registrador_1byte_s_e registrador_1byte_s_e_1 (
    .in_1(in_1), .in_2(in_5), .in_3(in_8), .out_4(registrador_1byte_s_e_1_out_4));
  assign out_14 = in_10 ? registrador_1byte_s_e_1_out_4 : 8'bz;  // Controlled_Buffer controlled_buffer_1
  registrador_1byte_s_e registrador_1byte_s_e_2 (
    .in_1(in_1), .in_2(in_2), .in_3(in_6), .out_4(registrador_1byte_s_e_2_out_4));
  assign out_14 = in_11 ? registrador_1byte_s_e_2_out_4 : 8'bz;  // Controlled_Buffer controlled_buffer_2
  registrador_1byte_s_e registrador_1byte_s_e_3 (
    .in_1(in_1), .in_2(in_3), .in_3(in_7), .out_4(registrador_1byte_s_e_3_out_4));
  assign out_14 = in_13 ? registrador_1byte_s_e_3_out_4 : 8'bz;  // Controlled_Buffer controlled_buffer_3
  registrador_1byte_s_e registrador_1byte_s_e_4 (
    .in_1(in_1), .in_2(in_4), .in_3(in_9), .out_4(registrador_1byte_s_e_4_out_4));
  assign out_14 = in_12 ? registrador_1byte_s_e_4_out_4 : 8'bz;  // Controlled_Buffer controlled_buffer_4

  // Notes on the sheet:
  //   Matricula: 22400691
  //   Carlos Henrick Cavalcante Gomes
endmodule

module somador_completo (
  input  in_1,
  input  a,
  input  b,
  output c,
  output out_5
);

  wire and_1_out, and_2_out, and_3_out, xor_1_out;

  xor xor_1 (xor_1_out, a, b);
  and and_1 (and_1_out, a, in_1);
  and and_2 (and_2_out, a, b);
  and and_3 (and_3_out, b, in_1);
  xor xor_2 (c, xor_1_out, in_1);
  or or_1 (out_5, and_1_out, and_2_out, and_3_out);

  // Notes on the sheet:
  //   c_in
  //   c_out
endmodule

module somador_8bits (
  input  in_1,
  input  [7:0] in_2,
  input  [7:0] in_3,
  output [7:0] out_4,
  output out_5
);

  wire somador_completo_1_out_5, somador_completo_2_out_5, somador_completo_3_out_5,
       somador_completo_4_out_5, somador_completo_5_out_5, somador_completo_6_out_5, somador_completo_7_out_5;

  somador_completo somador_completo_1 (
    .a(in_2[0]), .b(in_3[0]), .in_1(in_1), .out_5(somador_completo_1_out_5), .c(out_4[0]));
  somador_completo somador_completo_2 (
    .a(in_2[1]), .b(in_3[1]), .in_1(somador_completo_1_out_5), .out_5(somador_completo_2_out_5), .c(out_4[1]));
  somador_completo somador_completo_3 (
    .a(in_2[2]), .b(in_3[2]), .in_1(somador_completo_2_out_5), .out_5(somador_completo_3_out_5), .c(out_4[2]));
  somador_completo somador_completo_4 (
    .a(in_2[3]), .b(in_3[3]), .in_1(somador_completo_3_out_5), .out_5(somador_completo_4_out_5), .c(out_4[3]));
  somador_completo somador_completo_5 (
    .a(in_2[4]), .b(in_3[4]), .in_1(somador_completo_4_out_5), .out_5(somador_completo_5_out_5), .c(out_4[4]));
  somador_completo somador_completo_6 (
    .a(in_2[5]), .b(in_3[5]), .in_1(somador_completo_5_out_5), .out_5(somador_completo_6_out_5), .c(out_4[5]));
  somador_completo somador_completo_7 (
    .a(in_2[6]), .b(in_3[6]), .in_1(somador_completo_6_out_5), .out_5(somador_completo_7_out_5), .c(out_4[6]));
  somador_completo somador_completo_8 (
    .a(in_2[7]), .b(in_3[7]), .in_1(somador_completo_7_out_5), .out_5(out_5), .c(out_4[7]));
endmodule

module meio_somador (
  input  in_1,
  input  in_2,
  output out_3,
  output out_4
);

  xor xor_1 (out_3, in_1, in_2);
  and and_1 (out_4, in_1, in_2);
endmodule

module circuito1bit (
  input  i,
  input  s,
  output out_3
);

  wire nand_1_out, nand_2_out, nand_4_out;

  nand nand_1 (nand_1_out, i, s);
  nand nand_2 (nand_2_out, s, nand_1_out);
  nand nand_3 (out_3, nand_1_out, nand_4_out);
  nand nand_4 (nand_4_out, out_3, nand_2_out);

  // Notes on the sheet:
  //   o
endmodule

module memoria_8bits (
  input  in_1,
  input  in_2,
  input  in_3,
  input  in_4,
  input  in_5,
  input  in_6,
  input  in_7,
  input  in_8,
  input  in_9,
  output out_10,
  output out_11,
  output out_12,
  output out_13,
  output out_14,
  output out_15,
  output out_16,
  output out_17
);

  circuito1bit circuito1bit_1 (.i(in_1), .s(in_9), .out_3(out_10));
  circuito1bit circuito1bit_2 (.i(in_2), .s(in_9), .out_3(out_11));
  circuito1bit circuito1bit_3 (.i(in_3), .s(in_9), .out_3(out_12));
  circuito1bit circuito1bit_4 (.i(in_4), .s(in_9), .out_3(out_13));
  circuito1bit circuito1bit_5 (.i(in_5), .s(in_9), .out_3(out_14));
  circuito1bit circuito1bit_6 (.i(in_6), .s(in_9), .out_3(out_15));
  circuito1bit circuito1bit_7 (.i(in_7), .s(in_9), .out_3(out_16));
  circuito1bit circuito1bit_8 (.i(in_8), .s(in_9), .out_3(out_17));
endmodule

module enable (
  input  in_1,
  input  in_2,
  input  in_3,
  input  in_4,
  input  in_5,
  input  in_6,
  input  in_7,
  input  in_8,
  input  in_9,
  output out_10,
  output out_11,
  output out_12,
  output out_13,
  output out_14,
  output out_15,
  output out_16,
  output out_17
);

  and and_1 (out_10, in_1, in_9);
  and and_2 (out_11, in_2, in_9);
  and and_3 (out_12, in_3, in_9);
  and and_4 (out_13, in_4, in_9);
  and and_5 (out_14, in_5, in_9);
  and and_6 (out_15, in_6, in_9);
  and and_7 (out_16, in_7, in_9);
  and and_8 (out_17, in_8, in_9);
endmodule

module set (
  input  in_1,
  input  in_2,
  input  in_3,
  input  in_4,
  input  in_5,
  input  in_6,
  input  in_7,
  input  in_8,
  input  s,
  output out_10,
  output out_11,
  output out_12,
  output out_13,
  output out_14,
  output out_15,
  output out_16,
  output out_17
);

  memoria_8bits B (
    .in_1(in_1), .in_2(in_2), .in_3(in_3), .in_4(in_4), .in_5(in_5), .in_6(in_6), .in_7(in_7), .in_8(in_8),
    .in_9(s), .out_10(out_10), .out_11(out_11), .out_12(out_12), .out_13(out_13), .out_14(out_14),
    .out_15(out_15), .out_16(out_16), .out_17(out_17));
endmodule

module memoria_1byte_s_e (
  input  in_1,
  input  in_2,
  input  in_3,
  input  in_4,
  input  in_5,
  input  in_6,
  input  in_7,
  input  in_8,
  input  s,
  input  e,
  output out_11,
  output out_12,
  output out_13,
  output out_14,
  output out_15,
  output out_16,
  output out_17,
  output out_18
);

  wire B_out_10, B_out_11, B_out_12, B_out_13, B_out_14, B_out_15, B_out_16, B_out_17;

  set B (
    .in_1(in_1), .in_2(in_2), .in_3(in_3), .in_4(in_4), .in_5(in_5), .in_6(in_6), .in_7(in_7), .in_8(in_8),
    .s(s), .out_10(B_out_10), .out_11(B_out_11), .out_12(B_out_12), .out_13(B_out_13), .out_14(B_out_14),
    .out_15(B_out_15), .out_16(B_out_16), .out_17(B_out_17));
  enable enable_1 (
    .in_1(B_out_10), .in_2(B_out_11), .in_3(B_out_12), .in_4(B_out_13), .in_5(B_out_14), .in_6(B_out_15),
    .in_7(B_out_16), .in_8(B_out_17), .in_9(e), .out_10(out_11), .out_11(out_12), .out_12(out_13),
    .out_13(out_14), .out_14(out_15), .out_15(out_16), .out_16(out_17), .out_17(out_18));
endmodule

module registrador_1byte_s_e (
  input  [7:0] in_1,
  input  in_2,
  input  in_3,
  output [7:0] out_4
);

  memoria_1byte_s_e memoria_1byte_s_e_1 (
    .in_1(in_1[0]), .in_2(in_1[1]), .in_3(in_1[2]), .in_4(in_1[3]), .in_5(in_1[4]), .in_6(in_1[5]),
    .in_7(in_1[6]), .in_8(in_1[7]), .s(in_2), .e(in_3), .out_11(out_4[0]), .out_12(out_4[1]),
    .out_13(out_4[2]), .out_14(out_4[3]), .out_15(out_4[4]), .out_16(out_4[5]), .out_17(out_4[6]),
    .out_18(out_4[7]));
endmodule
