// Logisim project David_Lucas_Lopes_Caetano.circ as structural Verilog: 6 circuits, main circuit main
module main (
  input  [7:0] in_1,
  input  en_in,
  input  r0_s,
  input  r0_en,
  input  r1_s,
  input  r1_en,
  input  r2_s,
  input  r2_en,
  input  r3_s,
  input  r3_en,
  input  c_in,
  input  [7:0] a,
  input  [7:0] b
);

  wire adder_8bit_1_c_out;
  wire [7:0] adder_8bit_1_res_8bit_out, controlled_buffer_1_out;

  // Probe on controlled_buffer_1_out
  assign controlled_buffer_1_out = en_in ? in_1 : 8'bz;  // Controlled_Buffer controlled_buffer_1
  register_8bit r0 (.in_8bit(controlled_buffer_1_out), .set(r0_s), .enable(r0_en), .out_8bit(controlled_buffer_1_out));
  // Probe on adder_8bit_1_res_8bit_out
  adder_8bit adder_8bit_1 (
    .a_8bit_in(a), .b_8bit_in(b), .c_in(c_in), .c_out(adder_8bit_1_c_out),
    .res_8bit_out(adder_8bit_1_res_8bit_out));
  // Probe on adder_8bit_1_c_out
  register_8bit r1 (.in_8bit(controlled_buffer_1_out), .set(r1_s), .enable(r1_en), .out_8bit(controlled_buffer_1_out));
  register_8bit r2 (.in_8bit(controlled_buffer_1_out), .set(r2_s), .enable(r2_en), .out_8bit(controlled_buffer_1_out));
  register_8bit r3 (.in_8bit(controlled_buffer_1_out), .set(r3_s), .enable(r3_en), .out_8bit(controlled_buffer_1_out));

  // Notes on the sheet:
  //   David Lucas Lopes Caetano
  //   Matricula: 2240748
  //   somador de 8 bits
endmodule

module half_adder (
  input  a,
  input  b,
  output c,
  output c_out
);

  xor xor_1 (c, a, b);
  and and_1 (c_out, a, b);
endmodule

module full_adder (
  input  c_in,
  input  a,
  input  b,
  output c,
  output c_out
);

  wire and_1_out, and_2_out, xor_1_out;

  xor xor_1 (xor_1_out, a, b);
  and and_1 (and_1_out, b, a);
  xor xor_2 (c, xor_1_out, c_in);
  and and_2 (and_2_out, xor_1_out, c_in);
  or or_1 (c_out, and_1_out, and_2_out);
endmodule

module adder_8bit (
  input  c_in,
  input  [7:0] a_8bit_in,
  input  [7:0] b_8bit_in,
  output [7:0] res_8bit_out,
  output c_out
);

  wire full_adder_1_c_out, full_adder_2_c_out, full_adder_3_c_out, full_adder_4_c_out, full_adder_5_c_out,
       full_adder_6_c_out, full_adder_7_c_out;

  full_adder full_adder_1 (
    .a(a_8bit_in[0]), .b(b_8bit_in[0]), .c_in(c_in), .c_out(full_adder_1_c_out), .c(res_8bit_out[0]));
  full_adder full_adder_2 (
    .a(a_8bit_in[1]), .b(b_8bit_in[1]), .c_in(full_adder_1_c_out), .c_out(full_adder_2_c_out),
    .c(res_8bit_out[1]));
  full_adder full_adder_3 (
    .a(a_8bit_in[2]), .b(b_8bit_in[2]), .c_in(full_adder_2_c_out), .c_out(full_adder_3_c_out),
    .c(res_8bit_out[2]));
  full_adder full_adder_4 (
    .a(a_8bit_in[3]), .b(b_8bit_in[3]), .c_in(full_adder_3_c_out), .c_out(full_adder_4_c_out),
    .c(res_8bit_out[3]));
  full_adder full_adder_5 (
    .a(a_8bit_in[4]), .b(b_8bit_in[4]), .c_in(full_adder_4_c_out), .c_out(full_adder_5_c_out),
    .c(res_8bit_out[4]));
  full_adder full_adder_6 (
    .a(a_8bit_in[5]), .b(b_8bit_in[5]), .c_in(full_adder_5_c_out), .c_out(full_adder_6_c_out),
    .c(res_8bit_out[5]));
  full_adder full_adder_7 (
    .a(a_8bit_in[6]), .b(b_8bit_in[6]), .c_in(full_adder_6_c_out), .c_out(full_adder_7_c_out),
    .c(res_8bit_out[6]));
  full_adder full_adder_8 (
    .a(a_8bit_in[7]), .b(b_8bit_in[7]), .c_in(full_adder_7_c_out), .c_out(c_out), .c(res_8bit_out[7]));
endmodule

module flip_flop_latch (
  input  i,
  input  set,
  output o
);

  wire nand_1_out, nand_2_out, nand_4_out;

  nand nand_1 (nand_1_out, i, set);
  nand nand_2 (nand_2_out, nand_1_out, set);
  nand nand_3 (o, nand_1_out, nand_4_out);
  nand nand_4 (nand_4_out, o, nand_2_out);
endmodule

module register_8bit (
  input  [7:0] in_8bit,
  input  set,
  input  enable,
  output [7:0] out_8bit
);

  wire flip_flop_latch_1_o, flip_flop_latch_2_o, flip_flop_latch_3_o, flip_flop_latch_4_o,
       flip_flop_latch_5_o, flip_flop_latch_6_o, flip_flop_latch_7_o, flip_flop_latch_8_o;

  assign out_8bit[0] = enable ? flip_flop_latch_1_o : 1'bz;  // Controlled_Buffer controlled_buffer_1
  flip_flop_latch flip_flop_latch_1 (.i(in_8bit[0]), .set(set), .o(flip_flop_latch_1_o));
  assign out_8bit[1] = enable ? flip_flop_latch_2_o : 1'bz;  // Controlled_Buffer controlled_buffer_2
  flip_flop_latch flip_flop_latch_2 (.i(in_8bit[1]), .set(set), .o(flip_flop_latch_2_o));
  assign out_8bit[2] = enable ? flip_flop_latch_3_o : 1'bz;  // Controlled_Buffer controlled_buffer_3
  flip_flop_latch flip_flop_latch_3 (.i(in_8bit[2]), .set(set), .o(flip_flop_latch_3_o));
  assign out_8bit[3] = enable ? flip_flop_latch_4_o : 1'bz;  // Controlled_Buffer controlled_buffer_4
  flip_flop_latch flip_flop_latch_4 (.i(in_8bit[3]), .set(set), .o(flip_flop_latch_4_o));
  assign out_8bit[4] = enable ? flip_flop_latch_5_o : 1'bz;  // Controlled_Buffer controlled_buffer_5
  flip_flop_latch flip_flop_latch_5 (.i(in_8bit[4]), .set(set), .o(flip_flop_latch_5_o));
  assign out_8bit[5] = enable ? flip_flop_latch_6_o : 1'bz;  // Controlled_Buffer controlled_buffer_6
  flip_flop_latch flip_flop_latch_6 (.i(in_8bit[5]), .set(set), .o(flip_flop_latch_6_o));
  assign out_8bit[6] = enable ? flip_flop_latch_7_o : 1'bz;  // Controlled_Buffer controlled_buffer_7
  flip_flop_latch flip_flop_latch_7 (.i(in_8bit[6]), .set(set), .o(flip_flop_latch_7_o));
  assign out_8bit[7] = enable ? flip_flop_latch_8_o : 1'bz;  // Controlled_Buffer controlled_buffer_8
  flip_flop_latch flip_flop_latch_8 (.i(in_8bit[7]), .set(set), .o(flip_flop_latch_8_o));
endmodule
