// Logisim project ERICK_GOMES_DA_SILVA.circ as structural Verilog: 6 circuits, main circuit main
module main (
  input  [7:0] in_1,
  input  S_MAR,
  input  E_MAR,
  input  S1,
  input  E1,
  input  S2,
  input  E2,
  input  S3,
  input  E3,
  input  S4,
  input  E4,
  input  Carry_IN,
  input  [7:0] input_A,
  input  [7:0] input_B,
  output [7:0] out_15,
  output [7:0] output_soma_A_B,
  output Carry_OUT
);

  wire [7:0] MAR_out_8bits, R1_out_8bits, R2_out_8bits, R3_out_8bits, R4_out_8bits;

  registrador MAR (.input_8bits(in_1), .set_8bits(S_MAR), .enable_8bits(E_MAR), .out_8bits(MAR_out_8bits));
  somador_8bits somador_8bits_1 (
    .A_8bits(input_A), .B_8bits(input_B), .Carry_In_8bits(Carry_IN), .Carry_Out_8bits(Carry_OUT),
    .S(output_soma_A_B));
  assign out_15 = E_MAR ? MAR_out_8bits : 8'bz;  // Controlled_Buffer controlled_buffer_1
  registrador R1 (.input_8bits(out_15), .set_8bits(S1), .enable_8bits(E1), .out_8bits(R1_out_8bits));
  assign out_15 = E1 ? R1_out_8bits : 8'bz;  // Controlled_Buffer controlled_buffer_2
  registrador R2 (.input_8bits(out_15), .set_8bits(S2), .enable_8bits(E2), .out_8bits(R2_out_8bits));
  assign out_15 = E2 ? R2_out_8bits : 8'bz;  // Controlled_Buffer controlled_buffer_3
  registrador R3 (.input_8bits(out_15), .set_8bits(S3), .enable_8bits(E3), .out_8bits(R3_out_8bits));
  assign out_15 = E3 ? R3_out_8bits : 8'bz;  // Controlled_Buffer controlled_buffer_4
  registrador R4 (.input_8bits(out_15), .set_8bits(S4), .enable_8bits(E4), .out_8bits(R4_out_8bits));
  assign out_15 = E4 ? R4_out_8bits : 8'bz;  // Controlled_Buffer controlled_buffer_5

  // Notes on the sheet:
  //   Erick Gomes da Silva - 22401913 - CB01
endmodule

module somador (
  input  C_in,
  input  A,
  input  B,
  output S,
  output C_out
);

  wire and_1_out, and_2_out, and_3_out, xor_1_out;

  xor xor_1 (xor_1_out, A, B);
  and and_1 (and_1_out, B, C_in);
  and and_2 (and_2_out, A, C_in);
  and and_3 (and_3_out, A, B);
  xor xor_2 (S, xor_1_out, C_in);
  or or_1 (C_out, and_1_out, and_2_out, and_3_out);

  // Notes on the sheet:
  //   Erick Gomes da Silva - 22401913 - CB01
endmodule

module somador_8bits (
  input  Carry_In_8bits,
  input  [7:0] A_8bits,
  input  [7:0] B_8bits,
  output [7:0] S,
  output Carry_Out_8bits
);

  wire somador_1_c_out, somador_2_c_out, somador_3_c_out, somador_4_c_out, somador_5_c_out, somador_6_c_out,
       somador_7_c_out;

  somador somador_1 (.A(A_8bits[0]), .B(B_8bits[0]), .C_in(Carry_In_8bits), .C_out(somador_1_c_out), .S(S[0]));
  somador somador_2 (.A(A_8bits[1]), .B(B_8bits[1]), .C_in(somador_1_c_out), .C_out(somador_2_c_out), .S(S[1]));
  somador somador_3 (.A(A_8bits[2]), .B(B_8bits[2]), .C_in(somador_2_c_out), .C_out(somador_3_c_out), .S(S[2]));
  somador somador_4 (.A(A_8bits[3]), .B(B_8bits[3]), .C_in(somador_3_c_out), .C_out(somador_4_c_out), .S(S[3]));
  somador somador_5 (.A(A_8bits[4]), .B(B_8bits[4]), .C_in(somador_4_c_out), .C_out(somador_5_c_out), .S(S[4]));
  somador somador_6 (.A(A_8bits[5]), .B(B_8bits[5]), .C_in(somador_5_c_out), .C_out(somador_6_c_out), .S(S[5]));
  somador somador_7 (.A(A_8bits[6]), .B(B_8bits[6]), .C_in(somador_6_c_out), .C_out(somador_7_c_out), .S(S[6]));
  somador somador_8 (.A(A_8bits[7]), .B(B_8bits[7]), .C_in(somador_7_c_out), .C_out(Carry_Out_8bits), .S(S[7]));

  // Notes on the sheet:
  //   Erick Gomes da Silva - 22401913 - CB01
endmodule

module meio_somador (
  input  A,
  input  B,
  output S,
  output C_out
);

  xor xor_1 (S, A, B);
  and and_1 (C_out, A, B);

  // Notes on the sheet:
  //   Erick Gomes da Silva - 22401913 - CB01
endmodule

module memoria_1bit (
  input  input_r,
  input  set_r,
  output output_r
);

  wire nand_1_out, nand_2_out, nand_4_out;

  nand nand_1 (nand_1_out, input_r, set_r);
  nand nand_2 (nand_2_out, nand_1_out, set_r);
  nand nand_3 (output_r, nand_1_out, nand_4_out);
  nand nand_4 (nand_4_out, output_r, nand_2_out);

  // Notes on the sheet:
  //   Erick Gomes da Silva - 22401913 - CB01
endmodule

module registrador (
  input  [7:0] input_8bits,
  input  set_8bits,
  input  enable_8bits,
  output [7:0] out_8bits
);

  wire memoria_1bit_1_output_r, memoria_1bit_2_output_r, memoria_1bit_3_output_r, memoria_1bit_4_output_r,
       memoria_1bit_5_output_r, memoria_1bit_6_output_r, memoria_1bit_7_output_r, memoria_1bit_8_output_r;

  memoria_1bit memoria_1bit_1 (.input_r(input_8bits[0]), .set_r(set_8bits), .output_r(memoria_1bit_1_output_r));
  memoria_1bit memoria_1bit_2 (.input_r(input_8bits[1]), .set_r(set_8bits), .output_r(memoria_1bit_2_output_r));
  memoria_1bit memoria_1bit_3 (.input_r(input_8bits[2]), .set_r(set_8bits), .output_r(memoria_1bit_3_output_r));
  memoria_1bit memoria_1bit_4 (.input_r(input_8bits[3]), .set_r(set_8bits), .output_r(memoria_1bit_4_output_r));
  memoria_1bit memoria_1bit_5 (.input_r(input_8bits[4]), .set_r(set_8bits), .output_r(memoria_1bit_5_output_r));
  memoria_1bit memoria_1bit_6 (.input_r(input_8bits[5]), .set_r(set_8bits), .output_r(memoria_1bit_6_output_r));
  memoria_1bit memoria_1bit_7 (.input_r(input_8bits[6]), .set_r(set_8bits), .output_r(memoria_1bit_7_output_r));
  memoria_1bit memoria_1bit_8 (.input_r(input_8bits[7]), .set_r(set_8bits), .output_r(memoria_1bit_8_output_r));
  assign out_8bits[0] = enable_8bits ? memoria_1bit_1_output_r : 1'bz;  // Controlled_Buffer controlled_buffer_1
  assign out_8bits[1] = enable_8bits ? memoria_1bit_2_output_r : 1'bz;  // Controlled_Buffer controlled_buffer_2
  assign out_8bits[2] = enable_8bits ? memoria_1bit_3_output_r : 1'bz;  // Controlled_Buffer controlled_buffer_3
  assign out_8bits[3] = enable_8bits ? memoria_1bit_4_output_r : 1'bz;  // Controlled_Buffer controlled_buffer_4
  assign out_8bits[4] = enable_8bits ? memoria_1bit_5_output_r : 1'bz;  // Controlled_Buffer controlled_buffer_5
  assign out_8bits[5] = enable_8bits ? memoria_1bit_6_output_r : 1'bz;  // Controlled_Buffer controlled_buffer_6
  assign out_8bits[6] = enable_8bits ? memoria_1bit_7_output_r : 1'bz;  // Controlled_Buffer controlled_buffer_7
  assign out_8bits[7] = enable_8bits ? memoria_1bit_8_output_r : 1'bz;  // Controlled_Buffer controlled_buffer_8

  // Notes on the sheet:
  //   Erick Gomes da Silva - 22401913 - CB01
endmodule
