// Logisim project Gabriel_Almeida_de_Paula_Fonseca.circ as structural Verilog: 7 circuits, main circuit main
module main (
  input  [7:0] in_1,
  input  in_2,
  input  s1,
  input  s2,
  input  s3,
  input  s4,
  input  e1,
  input  e2,
  input  e3,
  input  e4,
  input  Cin,
  input  [7:0] a,
  input  [7:0] b,
  output [7:0] c,
  output Cout
);

  wire [7:0] controlled_buffer_1_out, R1_out_4, R2_out_4, R3_out_4, R4_out_4;

  assign controlled_buffer_1_out = in_2 ? in_1 : 8'bz;  // Controlled_Buffer controlled_buffer_1
  registrador_8bits_com_enable R1 (.in_1(controlled_buffer_1_out), .s(s1), .e(e1), .out_4(R1_out_4));
  somador_8bits somador_8bits_1 (.a(a), .b(b), .Cin(Cin), .Cout(Cout), .c(c));
  assign controlled_buffer_1_out = e1 ? R1_out_4 : 8'bz;  // Controlled_Buffer controlled_buffer_2
  registrador_8bits_com_enable R2 (.in_1(controlled_buffer_1_out), .s(s2), .e(e2), .out_4(R2_out_4));
  assign controlled_buffer_1_out = e2 ? R2_out_4 : 8'bz;  // Controlled_Buffer controlled_buffer_3
  assign controlled_buffer_1_out = e3 ? R3_out_4 : 8'bz;  // Controlled_Buffer controlled_buffer_4
  registrador_8bits_com_enable R3 (.in_1(controlled_buffer_1_out), .s(s3), .e(e3), .out_4(R3_out_4));
  assign controlled_buffer_1_out = e4 ? R4_out_4 : 8'bz;  // Controlled_Buffer controlled_buffer_5
  registrador_8bits_com_enable R4 (.in_1(controlled_buffer_1_out), .s(s4), .e(e4), .out_4(R4_out_4));
  // Probe on controlled_buffer_1_out

  // Notes on the sheet:
  //   22450084
  //   Gabriel Almeida de Paula Fonseca
endmodule

module somador (
  input  a,
  input  b,
  input  Cin,
  output c,
  output Cout
);

  wire and_1_out, and_2_out, xor_1_out;

  xor xor_1 (xor_1_out, a, b);
  and and_1 (and_1_out, Cin, xor_1_out);
  and and_2 (and_2_out, a, b);
  xor xor_2 (c, xor_1_out, Cin);
  or or_1 (Cout, and_1_out, and_2_out);
endmodule

module somador_8bits (
  input  [7:0] a,
  input  Cin,
  input  [7:0] b,
  output [7:0] c,
  output Cout
);

  wire somador_1_cout, somador_2_cout, somador_3_cout, somador_4_cout, somador_5_cout, somador_6_cout,
       somador_7_cout;

  somador somador_1 (.a(a[0]), .b(b[0]), .Cin(Cin), .Cout(somador_1_cout), .c(c[0]));
  somador somador_2 (.a(a[1]), .b(b[1]), .Cin(somador_1_cout), .Cout(somador_2_cout), .c(c[1]));
  somador somador_3 (.a(a[2]), .b(b[2]), .Cin(somador_2_cout), .Cout(somador_3_cout), .c(c[2]));
  somador somador_4 (.a(a[3]), .b(b[3]), .Cin(somador_3_cout), .Cout(somador_4_cout), .c(c[3]));
  somador somador_5 (.a(a[4]), .b(b[4]), .Cin(somador_4_cout), .Cout(somador_5_cout), .c(c[4]));
  somador somador_6 (.a(a[5]), .b(b[5]), .Cin(somador_5_cout), .Cout(somador_6_cout), .c(c[5]));
  somador somador_7 (.a(a[6]), .b(b[6]), .Cin(somador_6_cout), .Cout(somador_7_cout), .c(c[6]));
  somador somador_8 (.a(a[7]), .b(b[7]), .Cin(somador_7_cout), .Cout(Cout), .c(c[7]));
endmodule

module registrador (
  input  i,
  input  set,
  output o
);

  wire nand_1_out, nand_2_out, nand_4_out;

  nand nand_1 (nand_1_out, i, set);
  nand nand_2 (nand_2_out, nand_1_out, set);
  nand nand_3 (o, nand_1_out, nand_4_out);
  nand nand_4 (nand_4_out, o, nand_2_out);
endmodule

module registrador_8bits (
  input  [7:0] in_1,
  input  in_2,
  output [7:0] out_3
);

  registrador registrador_1 (.i(in_1[0]), .set(in_2), .o(out_3[0]));
  registrador registrador_2 (.i(in_1[1]), .set(in_2), .o(out_3[1]));
  registrador registrador_3 (.i(in_1[2]), .set(in_2), .o(out_3[2]));
  registrador registrador_4 (.i(in_1[3]), .set(in_2), .o(out_3[3]));
  registrador registrador_5 (.i(in_1[4]), .set(in_2), .o(out_3[4]));
  registrador registrador_6 (.i(in_1[5]), .set(in_2), .o(out_3[5]));
  registrador registrador_7 (.i(in_1[6]), .set(in_2), .o(out_3[6]));
  registrador registrador_8 (.i(in_1[7]), .set(in_2), .o(out_3[7]));
endmodule

module enable_8bits (
  input  [7:0] in_1,
  input  e,
  output [7:0] out_3
);

  and and_1 (out_3[0], in_1[0], e);
  and and_2 (out_3[1], in_1[1], e);
  and and_3 (out_3[2], in_1[2], e);
  and and_4 (out_3[3], in_1[3], e);
  and and_5 (out_3[4], e, in_1[4]);
  and and_6 (out_3[5], e, in_1[5]);
  and and_7 (out_3[6], e, in_1[6]);
  and and_8 (out_3[7], e, in_1[7]);
endmodule

module registrador_8bits_com_enable (
  input  [7:0] in_1,
  input  e,
  input  s,
  output [7:0] out_4
);

  wire [7:0] registrador_8bits_1_out_3;

  registrador_8bits registrador_8bits_1 (.in_1(in_1), .in_2(s), .out_3(registrador_8bits_1_out_3));
  enable_8bits enable_8bits_1 (.in_1(registrador_8bits_1_out_3), .e(e), .out_3(out_4));
endmodule
