// Logisim project Gabriel_Gregorio_dos_Santos_Vitor.circ as structural Verilog: 7 circuits, main circuit main
module main (
  input  [7:0] i,
  input  s_MAR,
  input  e_MAR,
  input  s1,
  input  s2,
  input  s3,
  input  s4,
  input  e1,
  input  e2,
  input  e3,
  input  e4,
  output [7:0] out_12
);

  wire [7:0] registrador_1_out_4, registrador_2_out_4, registrador_3_out_4, registrador_4_out_4,
       registrador_5_out_4;

  Registrador registrador_1 (.i(i), .enable(s_MAR), .set(e_MAR), .out_4(registrador_1_out_4));
  assign out_12 = e_MAR ? registrador_1_out_4 : 8'bz;  // Controlled_Buffer controlled_buffer_1
  Registrador registrador_2 (.i(out_12), .enable(s1), .set(e1), .out_4(registrador_2_out_4));
  assign out_12 = e1 ? registrador_2_out_4 : 8'bz;  // Controlled_Buffer controlled_buffer_2
  assign out_12 = e2 ? registrador_3_out_4 : 8'bz;  // Controlled_Buffer controlled_buffer_3
  Registrador registrador_3 (.i(out_12), .enable(s2), .set(e2), .out_4(registrador_3_out_4));
  assign out_12 = e3 ? registrador_4_out_4 : 8'bz;  // Controlled_Buffer controlled_buffer_4
  Registrador registrador_4 (.i(out_12), .enable(s3), .set(e3), .out_4(registrador_4_out_4));
  Registrador registrador_5 (.i(out_12), .enable(s4), .set(e4), .out_4(registrador_5_out_4));
  assign out_12 = e4 ? registrador_5_out_4 : 8'bz;  // Controlled_Buffer controlled_buffer_5

  // Notes on the sheet:
  //   Gabriel Gregorio dos Santos Vitor
  //   Barramento
  //   -- 22401910
endmodule

module Somador_1bit (
  input  a,
  input  b,
  input  carry_in,
  output sum,
  output carry_out
);

  wire and_1_out, and_2_out, xor_1_out;

  xor xor_1 (xor_1_out, a, b);
  and and_1 (and_1_out, a, b);
  xor xor_2 (sum, xor_1_out, carry_in);
  and and_2 (and_2_out, xor_1_out, carry_in);
  or or_1 (carry_out, and_2_out, and_1_out);
endmodule

module Somador_8bits (
  input  [7:0] a,
  input  carry_in,
  input  [7:0] b,
  output [7:0] sum,
  output carry_out
);

  wire somador_1bit_1_carry_out, somador_1bit_2_carry_out, somador_1bit_3_carry_out,
       somador_1bit_4_carry_out, somador_1bit_5_carry_out, somador_1bit_6_carry_out, somador_1bit_7_carry_out;

  Somador_1bit somador_1bit_1 (
    .a(a[0]), .b(b[0]), .carry_in(carry_in), .sum(sum[0]), .carry_out(somador_1bit_1_carry_out));
  Somador_1bit somador_1bit_2 (
    .a(a[1]), .b(b[1]), .carry_in(somador_1bit_1_carry_out), .sum(sum[1]),
    .carry_out(somador_1bit_2_carry_out));
  Somador_1bit somador_1bit_3 (
    .a(a[2]), .b(b[2]), .carry_in(somador_1bit_2_carry_out), .sum(sum[2]),
    .carry_out(somador_1bit_3_carry_out));
  Somador_1bit somador_1bit_4 (
    .a(a[3]), .b(b[3]), .carry_in(somador_1bit_3_carry_out), .sum(sum[3]),
    .carry_out(somador_1bit_4_carry_out));
  Somador_1bit somador_1bit_5 (
    .a(a[4]), .b(b[4]), .carry_in(somador_1bit_4_carry_out), .sum(sum[4]),
    .carry_out(somador_1bit_5_carry_out));
  Somador_1bit somador_1bit_6 (
    .a(a[5]), .b(b[5]), .carry_in(somador_1bit_5_carry_out), .sum(sum[5]),
    .carry_out(somador_1bit_6_carry_out));
  Somador_1bit somador_1bit_7 (
    .a(a[6]), .b(b[6]), .carry_in(somador_1bit_6_carry_out), .sum(sum[6]),
    .carry_out(somador_1bit_7_carry_out));
  Somador_1bit somador_1bit_8 (
    .a(a[7]), .b(b[7]), .carry_in(somador_1bit_7_carry_out), .sum(sum[7]), .carry_out(carry_out));
endmodule

module memoria_1bit (
  input  i,
  input  s,
  output o
);

  wire nand_1_out, nand_2_out, nand_4_out;

  nand nand_1 (nand_1_out, i, s);
  nand nand_2 (nand_2_out, nand_1_out, s);
  nand nand_3 (o, nand_1_out, nand_4_out);
  nand nand_4 (nand_4_out, o, nand_2_out);
endmodule

module memoria_8bits (
  input  i1,
  input  i2,
  input  i3,
  input  i4,
  input  i5,
  input  i6,
  input  i7,
  input  i8,
  input  set,
  output o1,
  output o2,
  output o3,
  output o4,
  output o5,
  output o6,
  output o7,
  output o8
);

  memoria_1bit memoria_1bit_1 (.i(i1), .s(set), .o(o1));
  memoria_1bit memoria_1bit_2 (.i(i2), .s(set), .o(o2));
  memoria_1bit memoria_1bit_3 (.i(i3), .s(set), .o(o3));
  memoria_1bit memoria_1bit_4 (.i(i4), .s(set), .o(o4));
  memoria_1bit memoria_1bit_5 (.i(i5), .s(set), .o(o5));
  memoria_1bit memoria_1bit_6 (.i(i6), .s(set), .o(o6));
  memoria_1bit memoria_1bit_7 (.i(i7), .s(set), .o(o7));
  memoria_1bit memoria_1bit_8 (.i(i8), .s(set), .o(o8));
endmodule

module enable_8bits (
  input  i1,
  input  i2,
  input  i3,
  input  i4,
  input  i5,
  input  i6,
  input  i7,
  input  i8,
  input  enable,
  output o1,
  output o2,
  output o3,
  output o4,
  output o5,
  output o6,
  output o7,
  output o8
);

  and and_1 (o1, i1, enable);
  and and_2 (o2, i2, enable);
  and and_3 (o3, i3, enable);
  and and_4 (o4, i4, enable);
  and and_5 (o5, i5, enable);
  and and_6 (o6, i6, enable);
  and and_7 (o7, i7, enable);
  and and_8 (o8, i8, enable);
endmodule

module Registrador (
  input  [7:0] i,
  input  enable,
  input  set,
  output [7:0] out_4
);

  wire memoria_8bits_1_o1, memoria_8bits_1_o2, memoria_8bits_1_o3, memoria_8bits_1_o4, memoria_8bits_1_o5,
       memoria_8bits_1_o6, memoria_8bits_1_o7, memoria_8bits_1_o8;

  memoria_8bits memoria_8bits_1 (
    .i1(i[0]), .i2(i[1]), .i3(i[2]), .i4(i[3]), .i5(i[4]), .i6(i[5]), .i7(i[6]), .i8(i[7]), .set(set),
    .o1(memoria_8bits_1_o1), .o2(memoria_8bits_1_o2), .o3(memoria_8bits_1_o3), .o4(memoria_8bits_1_o4),
    .o5(memoria_8bits_1_o5), .o6(memoria_8bits_1_o6), .o7(memoria_8bits_1_o7), .o8(memoria_8bits_1_o8));
  enable_8bits enable_8bits_1 (
    .i1(memoria_8bits_1_o1), .i2(memoria_8bits_1_o2), .i3(memoria_8bits_1_o3), .i4(memoria_8bits_1_o4),
    .i5(memoria_8bits_1_o5), .i6(memoria_8bits_1_o6), .i7(memoria_8bits_1_o7), .i8(memoria_8bits_1_o8),
    .enable(enable), .o1(out_4[0]), .o2(out_4[1]), .o3(out_4[2]), .o4(out_4[3]), .o5(out_4[4]),
    .o6(out_4[5]), .o7(out_4[6]), .o8(out_4[7]));
endmodule
