// Logisim project Glorieux_Tresor_Kitsari.circ as structural Verilog: 15 circuits, main circuit main
module main (
  input  in_1,
  input  in_2,
  output out_3
);

  wire nand_1_out, nand_2_out, nand_4_out;

  nand nand_1 (nand_1_out, in_1, in_2);
  nand nand_2 (nand_2_out, nand_1_out, in_2);
  nand nand_3 (out_3, nand_1_out, nand_4_out);
  nand nand_4 (nand_4_out, out_3, nand_2_out);

  // Notes on the sheet:
  //   Glorieux Tresor Kitsari 22450221
endmodule

module memoria_1_bit (
  input  in_1,
  input  in_2,
  output out_3
);

  main main_1 (.in_1(in_1), .in_2(in_2), .out_3(out_3));
endmodule

module memoria_2_bits (
  input  in_1,
  input  in_2,
  input  in_3,
  output out_4,
  output out_5
);

  memoria_1_bit memoria_1_bit_1 (.in_1(in_1), .in_2(in_3), .out_3(out_4));
  memoria_1_bit memoria_1_bit_2 (.in_1(in_2), .in_2(in_3), .out_3(out_5));
endmodule

module memoria_8_bits (
  input  in_1,
  input  in_2,
  input  in_3,
  input  in_4,
  input  in_5,
  input  in_6,
  input  in_7,
  input  in_8,
  input  in_9,
  output out_10,
  output out_11,
  output out_12,
  output out_13,
  output out_14,
  output out_15,
  output out_16,
  output out_17
);

  memoria_1_bit memoria_1_bit_1 (.in_1(in_1), .in_2(in_9), .out_3(out_10));
  memoria_1_bit memoria_1_bit_2 (.in_1(in_2), .in_2(in_9), .out_3(out_11));
  memoria_1_bit memoria_1_bit_3 (.in_1(in_3), .in_2(in_9), .out_3(out_12));
  memoria_1_bit memoria_1_bit_4 (.in_1(in_4), .in_2(in_9), .out_3(out_13));
  memoria_1_bit memoria_1_bit_5 (.in_1(in_5), .in_2(in_9), .out_3(out_14));
  memoria_1_bit memoria_1_bit_6 (.in_1(in_6), .in_2(in_9), .out_3(out_15));
  memoria_1_bit memoria_1_bit_7 (.in_1(in_7), .in_2(in_9), .out_3(out_16));
  memoria_1_bit memoria_1_bit_8 (.in_1(in_8), .in_2(in_9), .out_3(out_17));
endmodule

module memoria_1_byte_com_set (
  input  in_1,
  input  in_2,
  input  in_3,
  input  in_4,
  input  in_5,
  input  in_6,
  input  in_7,
  input  in_8,
  input  in_9,
  output out_10,
  output out_11,
  output out_12,
  output out_13,
  output out_14,
  output out_15,
  output out_16,
  output out_17
);

  memoria_8_bits memoria_8_bits_1 (
    .in_1(in_1), .in_2(in_2), .in_3(in_3), .in_4(in_4), .in_5(in_5), .in_6(in_6), .in_7(in_7), .in_8(in_8),
    .in_9(in_9), .out_10(out_10), .out_11(out_11), .out_12(out_12), .out_13(out_13), .out_14(out_14),
    .out_15(out_15), .out_16(out_16), .out_17(out_17));
endmodule

module memoria_1_byte_com_set_enable (
  input  in_1,
  input  in_2,
  input  in_3,
  input  in_4,
  input  in_5,
  input  in_6,
  input  in_7,
  input  in_8,
  input  in_9,
  output out_10,
  output out_11,
  output out_12,
  output out_13,
  output out_14,
  output out_15,
  output out_16,
  output out_17
);

  and and_1 (out_10, in_1, in_9);
  and and_2 (out_11, in_2, in_9);
  and and_3 (out_12, in_3, in_9);
  and and_4 (out_13, in_4, in_9);
  and and_5 (out_14, in_5, in_9);
  and and_6 (out_15, in_6, in_9);
  and and_7 (out_16, in_7, in_9);
  and and_8 (out_17, in_8, in_9);
endmodule

module memoria_1_byte_com_set_enable_bits (
  input  in_1,
  input  in_2,
  input  in_3,
  input  in_4,
  input  in_5,
  input  in_6,
  input  in_7,
  input  in_8,
  input  in_9,
  input  in_10,
  output out_11,
  output out_12,
  output out_13,
  output out_14,
  output out_15,
  output out_16,
  output out_17,
  output out_18
);

  wire memoria_1_byte_com_set_1_out_10, memoria_1_byte_com_set_1_out_11, memoria_1_byte_com_set_1_out_12,
       memoria_1_byte_com_set_1_out_13, memoria_1_byte_com_set_1_out_14, memoria_1_byte_com_set_1_out_15,
       memoria_1_byte_com_set_1_out_16, memoria_1_byte_com_set_1_out_17;

  memoria_1_byte_com_set memoria_1_byte_com_set_1 (
    .in_1(in_1), .in_2(in_2), .in_3(in_3), .in_4(in_4), .in_5(in_5), .in_6(in_6), .in_7(in_8), .in_8(in_9),
    .in_9(in_10), .out_10(memoria_1_byte_com_set_1_out_10), .out_11(memoria_1_byte_com_set_1_out_11),
    .out_12(memoria_1_byte_com_set_1_out_12), .out_13(memoria_1_byte_com_set_1_out_13),
    .out_14(memoria_1_byte_com_set_1_out_14), .out_15(memoria_1_byte_com_set_1_out_15),
    .out_16(memoria_1_byte_com_set_1_out_16), .out_17(memoria_1_byte_com_set_1_out_17));
  memoria_1_byte_com_set_enable memoria_1_byte_com_set_enable_1 (
    .in_1(memoria_1_byte_com_set_1_out_10), .in_2(memoria_1_byte_com_set_1_out_11),
    .in_3(memoria_1_byte_com_set_1_out_12), .in_4(memoria_1_byte_com_set_1_out_13),
    .in_5(memoria_1_byte_com_set_1_out_14), .in_6(memoria_1_byte_com_set_1_out_15),
    .in_7(memoria_1_byte_com_set_1_out_16), .in_8(memoria_1_byte_com_set_1_out_17), .in_9(in_7),
    .out_10(out_11), .out_11(out_12), .out_12(out_13), .out_13(out_14), .out_14(out_15), .out_15(out_16),
    .out_16(out_17), .out_17(out_18));
endmodule

module registrador (
  input  [7:0] in_1,
  input  in_2,
  input  in_3,
  output [7:0] out_4
);

  memoria_1_byte_com_set_enable_bits memoria_1_byte_com_set_enable_bits_1 (
    .in_1(in_1[0]), .in_2(in_1[1]), .in_3(in_1[2]), .in_4(in_1[3]), .in_5(in_1[4]), .in_6(in_1[5]),
    .in_7(in_1[6]), .in_8(in_1[7]), .in_9(in_2), .in_10(in_3), .out_11(out_4[0]), .out_12(out_4[1]),
    .out_13(out_4[2]), .out_14(out_4[3]), .out_15(out_4[4]), .out_16(out_4[5]), .out_17(out_4[6]),
    .out_18(out_4[7]));
endmodule

module registradores (
  input  [7:0] in_1,
  input  in_2,
  input  in_3,
  input  in_4,
  input  in_5,
  input  in_6,
  input  in_7,
  input  in_8,
  input  in_9,
  output [7:0] out_10
);

  wire not_1_out, or_1_out;
  wire [7:0] or_2_out, registrador_1_out_4, registrador_2_out_4, registrador_3_out_4, registrador_4_out_4;

  registrador registrador_1 (.in_1(in_1), .in_2(in_2), .in_3(in_6), .out_4(registrador_1_out_4));
  registrador registrador_2 (.in_1(in_1), .in_2(in_3), .in_3(in_7), .out_4(registrador_2_out_4));
  registrador registrador_3 (.in_1(in_1), .in_2(in_4), .in_3(in_8), .out_4(registrador_3_out_4));
  registrador registrador_4 (.in_1(in_1), .in_2(in_5), .in_3(in_9), .out_4(registrador_4_out_4));
  not not_1 (not_1_out, or_1_out);
  or or_1 (or_1_out, in_9, in_8, in_7, in_6);
  assign or_2_out = registrador_4_out_4 | registrador_3_out_4 | registrador_2_out_4 | registrador_1_out_4;  // OR_Gate or_2, 8 bits wide
  assign out_10 = in_1;  // Buffer buffer_1, 8 bits wide
  assign out_10 = or_2_out;  // Buffer buffer_2, 8 bits wide
endmodule

module circuito_somador (
  input  in_1,
  input  in_2,
  output out_3
);

  wire and_1_out, and_2_out, not_1_out, not_2_out;

  not not_1 (not_1_out, in_2);
  not not_2 (not_2_out, in_1);
  and and_1 (and_1_out, in_1, not_1_out);
  and and_2 (and_2_out, not_2_out, in_2);
  or or_1 (out_3, and_1_out, and_2_out);
endmodule

module circuito (
  input  in_1,
  input  in_2,
  output out_3
);

  wire circuito_somador_1_out_3;

  circuito_somador circuito_somador_1 (.in_1(in_1), .in_2(in_2), .out_3(circuito_somador_1_out_3));
  not not_1 (out_3, circuito_somador_1_out_3);
endmodule

module meio_somador (
  input  in_1,
  input  in_2,
  output out_3,
  output out_4
);

  and and_1 (out_3, in_1, in_2);
  circuito circuito_1 (.in_1(in_1), .in_2(in_2), .out_3(out_4));
endmodule

module somador_completo (
  input  in_1,
  input  in_2,
  input  in_3,
  output out_4,
  output out_5
);

  wire and_1_out, and_2_out, and_3_out, circuito_somador_1_out_3;

  and and_1 (and_1_out, in_1, in_2);
  and and_2 (and_2_out, in_1, in_3);
  and and_3 (and_3_out, in_2, in_3);
  circuito_somador circuito_somador_1 (.in_1(in_1), .in_2(in_2), .out_3(circuito_somador_1_out_3));
  circuito_somador circuito_somador_2 (.in_1(circuito_somador_1_out_3), .in_2(in_3), .out_3(out_5));
  or or_1 (out_4, and_1_out, and_2_out, and_3_out);
endmodule

module somador_8_bits (
  input  [7:0] in_1,
  input  [7:0] in_2,
  output [7:0] out_3,
  output out_4
);

  wire somador_completo_1_out_4, somador_completo_2_out_4, somador_completo_3_out_4,
       somador_completo_4_out_4, somador_completo_5_out_4, somador_completo_6_out_4, somador_completo_7_out_4;

  somador_completo somador_completo_1 (
    .in_1(in_1[0]), .in_2(in_2[0]), .in_3(1'b0), .out_4(somador_completo_1_out_4), .out_5(out_3[0]));
  somador_completo somador_completo_2 (
    .in_1(in_1[1]), .in_2(in_2[1]), .in_3(somador_completo_1_out_4), .out_4(somador_completo_2_out_4),
    .out_5(out_3[1]));
  somador_completo somador_completo_3 (
    .in_1(in_1[2]), .in_2(in_2[2]), .in_3(somador_completo_2_out_4), .out_4(somador_completo_3_out_4),
    .out_5(out_3[2]));
  somador_completo somador_completo_4 (
    .in_1(in_1[3]), .in_2(in_2[3]), .in_3(somador_completo_3_out_4), .out_4(somador_completo_4_out_4),
    .out_5(out_3[3]));
  somador_completo somador_completo_5 (
    .in_1(in_1[4]), .in_2(in_2[4]), .in_3(somador_completo_4_out_4), .out_4(somador_completo_5_out_4),
    .out_5(out_3[4]));
  somador_completo somador_completo_6 (
    .in_1(in_1[5]), .in_2(in_2[5]), .in_3(somador_completo_5_out_4), .out_4(somador_completo_6_out_4),
    .out_5(out_3[5]));
  somador_completo somador_completo_7 (
    .in_1(in_1[6]), .in_2(in_2[6]), .in_3(somador_completo_6_out_4), .out_4(somador_completo_7_out_4),
    .out_5(out_3[6]));
  somador_completo somador_completo_8 (
    .in_1(in_1[7]), .in_2(in_2[7]), .in_3(somador_completo_7_out_4), .out_4(out_4), .out_5(out_3[7]));
endmodule

module somador_e_registrador (
  input  [7:0] in_1,
  input  in_2,
  input  in_3,
  input  in_4,
  input  in_5,
  input  in_6,
  input  in_7,
  input  in_8,
  input  in_9,
  input  [7:0] in_10,
  input  [7:0] in_11,
  input  in_12,
  output [7:0] out_13,
  output [7:0] out_14
);

  wire not_1_out, or_1_out;
  wire [7:0] or_2_out, registrador_1_out_4, registrador_2_out_4, registrador_3_out_4, registrador_4_out_4;

  registrador registrador_1 (.in_1(in_1), .in_2(in_2), .in_3(in_6), .out_4(registrador_1_out_4));
  somador_8_bits somador_8_bits_1 (.in_1(in_10), .in_2(in_11), .out_3(out_14), .out_4(in_12));
  registrador registrador_2 (.in_1(in_1), .in_2(in_3), .in_3(in_7), .out_4(registrador_2_out_4));
  registrador registrador_3 (.in_1(in_1), .in_2(in_4), .in_3(in_8), .out_4(registrador_3_out_4));
  registrador registrador_4 (.in_1(in_1), .in_2(in_5), .in_3(in_9), .out_4(registrador_4_out_4));
  or or_1 (or_1_out, in_9, in_8, in_7, in_6);
  assign or_2_out = registrador_4_out_4 | registrador_3_out_4 | registrador_2_out_4 | registrador_1_out_4;  // OR_Gate or_2, 8 bits wide
  assign out_13 = in_1;  // Buffer buffer_1, 8 bits wide
  not not_1 (not_1_out, or_1_out);
  assign out_13 = or_2_out;  // Buffer buffer_2, 8 bits wide

  // Notes on the sheet:
  //   Glorieux Tresor Kitsari 22450221
  //   somador de 8 bits
endmodule
