// Logisim project Jamily_Oliveira.circ as structural Verilog: 8 circuits, main circuit main
// 1
module main (
  input  carry_in,
  input  [7:0] in_2,
  input  [7:0] in_3,
  input  [7:0] in_4,
  input  s,
  input  e,
  input  [7:0] in_7,
  input  in_8,
  input  set,
  input  in_10,
  input  in_11,
  input  in_12,
  input  enable,
  input  in_14,
  input  in_15,
  input  in_16,
  output [7:0] out_17,
  output carry_out,
  output [7:0] out_19,
  output [7:0] out_20
);

  wire [7:0] registrador_set_enable_2_out_4, registrador_set_enable_3_out_4, registrador_set_enable_4_out_4,
       registrador_set_enable_5_out_4;

  somador_8bits somador_8bits_1 (.carry_in(carry_in), .e1(in_2), .e2(in_3), .out_1(out_17), .c_out(carry_out));
  registrador_set_enable registrador_set_enable_1 (.in_1(in_4), .s(s), .e(e), .out_4(out_19));
  // Probe on out_20
  assign out_20 = in_8 ? in_7 : 8'bz;  // Controlled_Buffer controlled_buffer_1
  assign out_20 = enable ? registrador_set_enable_2_out_4 : 8'bz;  // Controlled_Buffer controlled_buffer_2
  registrador_set_enable registrador_set_enable_2 (
    .in_1(out_20), .s(set), .e(enable), .out_4(registrador_set_enable_2_out_4));
  registrador_set_enable registrador_set_enable_3 (
    .in_1(out_20), .s(in_10), .e(in_14), .out_4(registrador_set_enable_3_out_4));
  assign out_20 = in_14 ? registrador_set_enable_3_out_4 : 8'bz;  // Controlled_Buffer controlled_buffer_3
  assign out_20 = in_15 ? registrador_set_enable_4_out_4 : 8'bz;  // Controlled_Buffer controlled_buffer_4
  registrador_set_enable registrador_set_enable_4 (
    .in_1(out_20), .s(in_11), .e(in_15), .out_4(registrador_set_enable_4_out_4));
  assign out_20 = in_16 ? registrador_set_enable_5_out_4 : 8'bz;  // Controlled_Buffer controlled_buffer_5
  registrador_set_enable registrador_set_enable_5 (
    .in_1(out_20), .s(in_12), .e(in_16), .out_4(registrador_set_enable_5_out_4));

  // Notes on the sheet:
  //   Jamily Oliveira Pereira - 22401911
  //   Somador de 8 bits
  //   Registrador com set e enable
  //   Barramento com 4 registradores
endmodule

module somador_1bit (
  input  c_in,
  input  e1,
  input  e2,
  output out_1,
  output c_out
);

  wire and_1_out, and_2_out, and_3_out, xor_1_out;

  and and_1 (and_1_out, e1, c_in);
  and and_2 (and_2_out, e1, e2);
  and and_3 (and_3_out, e2, c_in);
  xor xor_1 (xor_1_out, e1, e2);
  or or_1 (c_out, and_1_out, and_2_out, and_3_out);
  xor xor_2 (out_1, xor_1_out, c_in);
endmodule

module somador_8bits (
  input  carry_in,
  input  [7:0] e1,
  input  [7:0] e2,
  output [7:0] out_1,
  output c_out
);

  wire somador_1bit_1_c_out, somador_1bit_2_c_out, somador_1bit_3_c_out, somador_1bit_4_c_out,
       somador_1bit_5_c_out, somador_1bit_6_c_out, somador_1bit_7_c_out;

  somador_1bit somador_1bit_1 (.e1(e1[0]), .e2(e2[0]), .c_in(carry_in), .out_1(out_1[0]), .c_out(somador_1bit_1_c_out));
  somador_1bit somador_1bit_2 (
    .e1(e1[1]), .e2(e2[1]), .c_in(somador_1bit_1_c_out), .out_1(out_1[1]), .c_out(somador_1bit_2_c_out));
  somador_1bit somador_1bit_3 (
    .e1(e1[2]), .e2(e2[2]), .c_in(somador_1bit_2_c_out), .out_1(out_1[2]), .c_out(somador_1bit_3_c_out));
  somador_1bit somador_1bit_4 (
    .e1(e1[3]), .e2(e2[3]), .c_in(somador_1bit_3_c_out), .out_1(out_1[3]), .c_out(somador_1bit_4_c_out));
  somador_1bit somador_1bit_5 (
    .e1(e1[4]), .e2(e2[4]), .c_in(somador_1bit_4_c_out), .out_1(out_1[4]), .c_out(somador_1bit_5_c_out));
  somador_1bit somador_1bit_6 (
    .e1(e1[5]), .e2(e2[5]), .c_in(somador_1bit_5_c_out), .out_1(out_1[5]), .c_out(somador_1bit_6_c_out));
  somador_1bit somador_1bit_7 (
    .e1(e1[6]), .e2(e2[6]), .c_in(somador_1bit_6_c_out), .out_1(out_1[6]), .c_out(somador_1bit_7_c_out));
  somador_1bit somador_de_1_bit (.e1(e1[7]), .e2(e2[7]), .c_in(somador_1bit_7_c_out), .out_1(out_1[7]), .c_out(c_out));
endmodule

module memoria_1bit (
  input  i,
  input  s,
  output out_1
);

  wire nand_1_out, nand_2_out, nand_4_out;

  nand nand_1 (nand_1_out, i, s);
  nand nand_2 (nand_2_out, nand_1_out, s);
  nand nand_3 (out_1, nand_1_out, nand_4_out);
  nand nand_4 (nand_4_out, out_1, nand_2_out);
endmodule

module memoria_8bits (
  input  i0,
  input  i1,
  input  i2,
  input  i3,
  input  i4,
  input  i5,
  input  i6,
  input  i7,
  input  s,
  output o0,
  output o1,
  output o2,
  output o3,
  output o4,
  output o5,
  output o6,
  output o7
);

  memoria_1bit memoria_de_1_bit (.i(i0), .s(s), .out_1(o0));
  memoria_1bit memoria_1bit_1 (.i(i1), .s(s), .out_1(o1));
  memoria_1bit memoria_1bit_2 (.i(i2), .s(s), .out_1(o2));
  memoria_1bit memoria_1bit_3 (.i(i3), .s(s), .out_1(o3));
  memoria_1bit memoria_1bit_4 (.i(i4), .s(s), .out_1(o4));
  memoria_1bit memoria_1bit_5 (.i(i5), .s(s), .out_1(o5));
  memoria_1bit memoria_1bit_6 (.i(i6), .s(s), .out_1(o6));
  memoria_1bit memoria_1bit_7 (.i(i7), .s(s), .out_1(o7));
endmodule

module enable (
  input  in_1,
  input  in_2,
  input  in_3,
  input  in_4,
  input  in_5,
  input  in_6,
  input  in_7,
  input  in_8,
  input  e,
  output out_10,
  output out_11,
  output out_12,
  output out_13,
  output out_14,
  output out_15,
  output out_16,
  output out_17
);

  and and_1 (out_10, in_1, e);
  and and_2 (out_11, in_2, e);
  and and_3 (out_12, in_3, e);
  and and_4 (out_13, in_4, e);
  and and_5 (out_14, in_5, e);
  and and_6 (out_15, in_6, e);
  and and_7 (out_16, in_7, e);
  and and_8 (out_17, in_8, e);
endmodule

module memoria_set_enable (
  input  in_1,
  input  in_2,
  input  in_3,
  input  in_4,
  input  in_5,
  input  e,
  input  in_7,
  input  in_8,
  input  in_9,
  input  s,
  output out_11,
  output out_12,
  output out_13,
  output out_14,
  output out_15,
  output out_16,
  output out_17,
  output out_18
);

  wire memoria_8bits_1_o0, memoria_8bits_1_o1, memoria_8bits_1_o2, memoria_8bits_1_o3, memoria_8bits_1_o4,
       memoria_8bits_1_o5, memoria_8bits_1_o6, memoria_8bits_1_o7;

  memoria_8bits memoria_8bits_1 (
    .i0(in_1), .i1(in_2), .i2(in_3), .i3(in_4), .i4(in_5), .i5(in_7), .i6(in_8), .i7(in_9), .s(s),
    .o0(memoria_8bits_1_o0), .o1(memoria_8bits_1_o1), .o2(memoria_8bits_1_o2), .o3(memoria_8bits_1_o3),
    .o4(memoria_8bits_1_o4), .o5(memoria_8bits_1_o5), .o6(memoria_8bits_1_o6), .o7(memoria_8bits_1_o7));
  enable enable_1 (
    .in_1(memoria_8bits_1_o0), .in_2(memoria_8bits_1_o1), .in_3(memoria_8bits_1_o2),
    .in_4(memoria_8bits_1_o3), .in_5(memoria_8bits_1_o4), .in_6(memoria_8bits_1_o5),
    .in_7(memoria_8bits_1_o6), .in_8(memoria_8bits_1_o7), .e(e), .out_10(out_11), .out_11(out_12),
    .out_12(out_13), .out_13(out_14), .out_14(out_15), .out_15(out_16), .out_16(out_17), .out_17(out_18));
endmodule

module registrador_set_enable (
  input  [7:0] in_1,
  input  s,
  input  e,
  output [7:0] out_4
);

  memoria_set_enable memoria_set_enable_1 (
    .in_1(in_1[0]), .in_2(in_1[1]), .in_3(in_1[2]), .in_4(in_1[3]), .in_5(in_1[4]), .e(e), .in_7(in_1[5]),
    .in_8(in_1[6]), .in_9(in_1[7]), .s(s), .out_11(out_4[0]), .out_12(out_4[1]), .out_13(out_4[2]),
    .out_14(out_4[3]), .out_15(out_4[4]), .out_16(out_4[5]), .out_17(out_4[6]), .out_18(out_4[7]));
endmodule
