// Logisim project Jean_Seixas.circ as structural Verilog: 6 circuits, main circuit main
module main (
  input  [7:0] in_1,
  input  set,
  input  e,
  input  s1,
  input  s2,
  input  s3,
  input  s4,
  input  e1,
  input  e2,
  input  e3,
  input  e4,
  output [7:0] out_12
);

  wire [7:0] registrador_8bit_1_out_4, registrador_8bit_2_out_4, registrador_8bit_3_out_4,
       registrador_8bit_4_out_4, registrador_8bit_5_out_4;

  registrador_8bit registrador_8bit_1 (.in_1(in_1), .set(set), .enable(e), .out_4(registrador_8bit_1_out_4));
  assign out_12 = e ? registrador_8bit_1_out_4 : 8'bz;  // Controlled_Buffer controlled_buffer_1
  registrador_8bit registrador_8bit_2 (.in_1(out_12), .set(s1), .enable(e1), .out_4(registrador_8bit_2_out_4));
  assign out_12 = e1 ? registrador_8bit_2_out_4 : 8'bz;  // Controlled_Buffer controlled_buffer_2
  assign out_12 = e2 ? registrador_8bit_3_out_4 : 8'bz;  // Controlled_Buffer controlled_buffer_3
  registrador_8bit registrador_8bit_3 (.in_1(out_12), .set(s2), .enable(e2), .out_4(registrador_8bit_3_out_4));
  registrador_8bit registrador_8bit_4 (.in_1(out_12), .set(s3), .enable(e3), .out_4(registrador_8bit_4_out_4));
  assign out_12 = e3 ? registrador_8bit_4_out_4 : 8'bz;  // Controlled_Buffer controlled_buffer_4
  assign out_12 = e4 ? registrador_8bit_5_out_4 : 8'bz;  // Controlled_Buffer controlled_buffer_5
  registrador_8bit registrador_8bit_5 (.in_1(out_12), .set(s4), .enable(e4), .out_4(registrador_8bit_5_out_4));

  // Notes on the sheet:
  //   Jean Seixas de Souza-22154600
endmodule

module somador_1bit (
  input  c_in,
  input  a,
  input  b,
  output o,
  output c_out
);

  wire and_1_out, and_2_out, and_3_out, xor_1_out;

  xor xor_1 (xor_1_out, a, b);
  and and_1 (and_1_out, a, c_in);
  and and_2 (and_2_out, a, b);
  and and_3 (and_3_out, b, c_in);
  xor xor_2 (o, xor_1_out, c_in);
  or or_1 (c_out, and_1_out, and_2_out, and_3_out);
endmodule

module somador_8bit (
  input  c_int,
  input  [7:0] a,
  input  [7:0] b,
  output s0,
  output s1,
  output s2,
  output s3,
  output s4,
  output s5,
  output s6,
  output s7,
  output c_out
);

  wire somador_1bit_1_c_out, somador_1bit_2_c_out, somador_1bit_3_c_out, somador_1bit_4_c_out,
       somador_1bit_5_c_out, somador_1bit_6_c_out, somador_1bit_7_c_out;

  somador_1bit somador_1bit_1 (.a(a[0]), .b(b[0]), .c_in(c_int), .c_out(somador_1bit_1_c_out), .o(s0));
  somador_1bit somador_1bit_2 (.a(a[1]), .b(b[1]), .c_in(somador_1bit_1_c_out), .c_out(somador_1bit_2_c_out), .o(s1));
  somador_1bit somador_1bit_3 (.a(a[2]), .b(b[2]), .c_in(somador_1bit_2_c_out), .c_out(somador_1bit_3_c_out), .o(s2));
  somador_1bit somador_1bit_4 (.a(a[3]), .b(b[3]), .c_in(somador_1bit_3_c_out), .c_out(somador_1bit_4_c_out), .o(s3));
  somador_1bit somador_1bit_5 (.a(a[4]), .b(b[4]), .c_in(somador_1bit_4_c_out), .c_out(somador_1bit_5_c_out), .o(s4));
  somador_1bit somador_1bit_6 (.a(a[5]), .b(b[5]), .c_in(somador_1bit_5_c_out), .c_out(somador_1bit_6_c_out), .o(s5));
  somador_1bit somador_1bit_7 (.a(a[6]), .b(b[6]), .c_in(somador_1bit_6_c_out), .c_out(somador_1bit_7_c_out), .o(s6));
  somador_1bit somador_1bit_8 (.a(a[7]), .b(b[7]), .c_in(somador_1bit_7_c_out), .c_out(c_out), .o(s7));
endmodule

module registrador_1bit (
  input  i,
  input  s,
  output o
);

  wire nand_1_out, nand_2_out, nand_4_out;

  nand nand_1 (nand_1_out, i, s);
  nand nand_2 (nand_2_out, nand_1_out, s);
  nand nand_3 (o, nand_1_out, nand_4_out);
  nand nand_4 (nand_4_out, o, nand_2_out);
endmodule

module registrador_8bit (
  input  [7:0] in_1,
  input  set,
  input  enable,
  output [7:0] out_4
);

  wire registrador_1bit_1_o, registrador_1bit_2_o, registrador_1bit_3_o, registrador_1bit_4_o,
       registrador_1bit_5_o, registrador_1bit_6_o, registrador_1bit_7_o, registrador_1bit_8_o;

  registrador_1bit registrador_1bit_1 (.i(in_1[0]), .s(set), .o(registrador_1bit_1_o));
  registrador_1bit registrador_1bit_2 (.i(in_1[1]), .s(set), .o(registrador_1bit_2_o));
  registrador_1bit registrador_1bit_3 (.i(in_1[2]), .s(set), .o(registrador_1bit_3_o));
  registrador_1bit registrador_1bit_4 (.i(in_1[3]), .s(set), .o(registrador_1bit_4_o));
  registrador_1bit registrador_1bit_5 (.i(in_1[4]), .s(set), .o(registrador_1bit_5_o));
  registrador_1bit registrador_1bit_6 (.i(in_1[5]), .s(set), .o(registrador_1bit_6_o));
  registrador_1bit registrador_1bit_7 (.i(in_1[6]), .s(set), .o(registrador_1bit_7_o));
  registrador_1bit registrador_1bit_8 (.i(in_1[7]), .s(set), .o(registrador_1bit_8_o));
  enable_registrador enable_registrador_1 (
    .in_1(registrador_1bit_1_o), .in_2(registrador_1bit_2_o), .in_3(registrador_1bit_3_o),
    .in_4(registrador_1bit_4_o), .in_5(registrador_1bit_5_o), .in_6(registrador_1bit_6_o),
    .in_7(registrador_1bit_7_o), .in_8(registrador_1bit_8_o), .enable(enable), .out_10(out_4[0]),
    .out_11(out_4[1]), .out_12(out_4[2]), .out_13(out_4[3]), .out_14(out_4[4]), .out_15(out_4[5]),
    .out_16(out_4[6]), .out_17(out_4[7]));
endmodule

module enable_registrador (
  input  in_1,
  input  in_2,
  input  in_3,
  input  in_4,
  input  in_5,
  input  in_6,
  input  in_7,
  input  in_8,
  input  enable,
  output out_10,
  output out_11,
  output out_12,
  output out_13,
  output out_14,
  output out_15,
  output out_16,
  output out_17
);

  and and_1 (out_10, in_1, enable);
  and and_2 (out_11, in_2, enable);
  and and_3 (out_12, in_3, enable);
  and and_4 (out_13, in_4, enable);
  and and_5 (out_14, in_5, enable);
  and and_6 (out_15, in_6, enable);
  and and_7 (out_16, in_7, enable);
  and and_8 (out_17, in_8, enable);
endmodule
