// Logisim project Leticia_Souza_Souza.circ as structural Verilog: 7 circuits, main circuit main
module main (
  input  c_in,
  input  [7:0] a_8bit,
  input  [7:0] b_8bit,
  input  [7:0] in_4,
  input  in_5,
  input  in_6,
  input  in_7,
  input  in_8,
  input  in_9,
  input  in_10,
  input  in_11,
  input  in_12,
  input  in_13,
  input  in_14,
  output [7:0] o,
  output c_out,
  output [7:0] out_17
);

  wire [7:0] R1_out_4, R2_out_4, R3_out_4, R4_out_4, registrador_set_enable_1_out_4;

  registrador_set_enable registrador_set_enable_1 (
    .in_1(in_4), .s(in_5), .e(in_10), .out_4(registrador_set_enable_1_out_4));
  assign out_17 = in_10 ? registrador_set_enable_1_out_4 : 8'bz;  // Controlled_Buffer controlled_buffer_1
  somador_8bit somador (.a_8bit(a_8bit), .b_8bit(b_8bit), .c_in(c_in), .c_out(c_out), .s_8bit(o));
  registrador_set_enable R1 (.in_1(out_17), .s(in_6), .e(in_11), .out_4(R1_out_4));
  assign out_17 = in_11 ? R1_out_4 : 8'bz;  // Controlled_Buffer controlled_buffer_2
  assign out_17 = in_12 ? R2_out_4 : 8'bz;  // Controlled_Buffer controlled_buffer_3
  registrador_set_enable R2 (.in_1(out_17), .s(in_7), .e(in_12), .out_4(R2_out_4));
  assign out_17 = in_13 ? R3_out_4 : 8'bz;  // Controlled_Buffer controlled_buffer_4
  registrador_set_enable R3 (.in_1(out_17), .s(in_8), .e(in_13), .out_4(R3_out_4));
  assign out_17 = in_14 ? R4_out_4 : 8'bz;  // Controlled_Buffer controlled_buffer_5
  registrador_set_enable R4 (.in_1(out_17), .s(in_9), .e(in_14), .out_4(R4_out_4));

  // Notes on the sheet:
  //   22450212
  //   Leticia Souza de Souza
endmodule

module somador_1bit (
  input  c_in,
  input  a,
  input  b,
  output c,
  output c_out
);

  wire and_1_out, and_2_out, and_3_out, xor_1_out;

  xor xor_1 (xor_1_out, a, b);
  and and_1 (and_1_out, a, c_in);
  and and_2 (and_2_out, a, b);
  and and_3 (and_3_out, b, c_in);
  or or_1 (c_out, and_1_out, and_2_out, and_3_out);
  xor xor_2 (c, xor_1_out, c_in);
endmodule

module somador_8bit (
  input  c_in,
  input  [7:0] a_8bit,
  input  [7:0] b_8bit,
  output [7:0] s_8bit,
  output c_out
);

  wire somador_1bit_1_c_out, somador_1bit_2_c_out, somador_1bit_3_c_out, somador_1bit_4_c_out,
       somador_1bit_5_c_out, somador_1bit_6_c_out, somador_1bit_7_c_out;

  somador_1bit somador_1bit_1 (.a(a_8bit[0]), .b(b_8bit[0]), .c_in(c_in), .c_out(somador_1bit_1_c_out), .c(s_8bit[0]));
  somador_1bit somador_1bit_2 (
    .a(a_8bit[1]), .b(b_8bit[1]), .c_in(somador_1bit_1_c_out), .c_out(somador_1bit_2_c_out), .c(s_8bit[1]));
  somador_1bit somador_1bit_3 (
    .a(a_8bit[2]), .b(b_8bit[2]), .c_in(somador_1bit_2_c_out), .c_out(somador_1bit_3_c_out), .c(s_8bit[2]));
  somador_1bit somador_1bit_4 (
    .a(a_8bit[3]), .b(b_8bit[3]), .c_in(somador_1bit_3_c_out), .c_out(somador_1bit_4_c_out), .c(s_8bit[3]));
  somador_1bit somador_1bit_5 (
    .a(a_8bit[4]), .b(b_8bit[4]), .c_in(somador_1bit_4_c_out), .c_out(somador_1bit_5_c_out), .c(s_8bit[4]));
  somador_1bit somador_1bit_6 (
    .a(a_8bit[5]), .b(b_8bit[5]), .c_in(somador_1bit_5_c_out), .c_out(somador_1bit_6_c_out), .c(s_8bit[5]));
  somador_1bit somador_1bit_7 (
    .a(a_8bit[6]), .b(b_8bit[6]), .c_in(somador_1bit_6_c_out), .c_out(somador_1bit_7_c_out), .c(s_8bit[6]));
  somador_1bit somador_1bit_8 (.a(a_8bit[7]), .b(b_8bit[7]), .c_in(somador_1bit_7_c_out), .c_out(c_out), .c(s_8bit[7]));
endmodule

module memoria_1bit (
  input  i,
  input  s,
  output o
);

  wire nand_1_out, nand_2_out, nand_4_out;

  nand nand_1 (nand_1_out, i, s);
  nand nand_2 (nand_2_out, nand_1_out, s);
  nand nand_3 (o, nand_1_out, nand_4_out);
  nand nand_4 (nand_4_out, o, nand_2_out);
endmodule

module memoria_8bit (
  input  [7:0] i_8bit,
  input  s,
  output [7:0] o_8bit
);

  memoria_1bit memoria_1bit_1 (.i(i_8bit[0]), .s(s), .o(o_8bit[0]));
  memoria_1bit memoria_1bit_2 (.i(i_8bit[1]), .s(s), .o(o_8bit[1]));
  memoria_1bit memoria_1bit_3 (.i(i_8bit[2]), .s(s), .o(o_8bit[2]));
  memoria_1bit memoria_1bit_4 (.i(i_8bit[3]), .s(s), .o(o_8bit[3]));
  memoria_1bit memoria_1bit_5 (.i(i_8bit[4]), .s(s), .o(o_8bit[4]));
  memoria_1bit memoria_1bit_6 (.i(i_8bit[5]), .s(s), .o(o_8bit[5]));
  memoria_1bit memoria_1bit_7 (.i(i_8bit[6]), .s(s), .o(o_8bit[6]));
  memoria_1bit memoria_1bit_8 (.i(i_8bit[7]), .s(s), .o(o_8bit[7]));
endmodule

module enable (
  input  [7:0] in_1,
  input  e,
  output [7:0] out_3
);

  and and_1 (out_3[0], in_1[0], e);
  and and_2 (out_3[1], in_1[1], e);
  and and_3 (out_3[2], in_1[2], e);
  and and_4 (out_3[3], in_1[3], e);
  and and_5 (out_3[4], in_1[4], e);
  and and_6 (out_3[5], in_1[5], e);
  and and_7 (out_3[6], in_1[6], e);
  and and_8 (out_3[7], in_1[7], e);
endmodule

module registrador_set_enable (
  input  [7:0] in_1,
  input  s,
  input  e,
  output [7:0] out_4
);

  wire [7:0] memoria_8bit_1_o_8bit;

  memoria_8bit memoria_8bit_1 (.i_8bit(in_1), .s(s), .o_8bit(memoria_8bit_1_o_8bit));
  enable enable_1 (.in_1(memoria_8bit_1_o_8bit), .e(e), .out_3(out_4));
endmodule
