// Logisim project Logsim_projeto_OC.circ as structural Verilog: 6 circuits, main circuit main
module main (
  input  in_1,
  input  in_2,
  input  in_3,
  input  in_4,
  input  in_5,
  input  in_6,
  input  [7:0] in_7,
  input  in_8,
  input  in_9,
  input  in_10,
  input  in_11,
  input  in_12,
  input  in_13,
  input  in_14,
  input  in_15,
  input  in_16,
  input  in_17,
  output out_18,
  output out_19,
  output out_20,
  output [7:0] out_21,
  output out_22,
  output out_23
);

  wire and_1_out, and_2_out, and_3_out, xor_1_out;
  wire [7:0] memoria_8bit_enable_1_out_4;

  and and_1 (and_1_out, in_1, in_3);
  xor xor_1 (xor_1_out, in_3, in_1);
  Memoria_8bit_enable memoria_8bit_enable_1 (
    .in_1(memoria_8bit_enable_1_out_4), .in_2(in_10), .in_3(in_11), .out_4(memoria_8bit_enable_1_out_4));
  and and_2 (and_2_out, in_4, in_2);
  Somador_completo somador_completo_1 (.in_2(in_6), .in_3(in_8), .in_1(in_5), .out_4(out_22), .out_5(out_23));
  Memoria_8bit_enable memoria_8bit_enable_2 (
    .in_1(memoria_8bit_enable_1_out_4), .in_2(in_13), .in_3(in_14), .out_4(memoria_8bit_enable_1_out_4));
  xor xor_2 (out_20, in_2, in_4);
  Memoria_8bit_enable memoria_8bit_enable_3 (
    .in_1(memoria_8bit_enable_1_out_4), .in_2(in_12), .in_3(in_15), .out_4(memoria_8bit_enable_1_out_4));
  xor xor_3 (out_19, xor_1_out, and_2_out);
  and and_3 (and_3_out, xor_1_out, and_2_out);
  Memoria_8bit_enable memoria_8bit_enable_4 (
    .in_1(memoria_8bit_enable_1_out_4), .in_2(in_16), .in_3(in_17), .out_4(memoria_8bit_enable_1_out_4));
  xor xor_4 (out_18, and_1_out, and_3_out);
  Registrador_8bit registrador_8bit_1 (.in_1(in_7), .in_2(in_9), .out_3(out_21));

  // Notes on the sheet:
  //   Lucas Saraiva de Moura
endmodule

module Somador_completo (
  input  in_1,
  input  in_2,
  input  in_3,
  output out_4,
  output out_5
);

  wire and_1_out, and_2_out, xor_1_out;

  xor xor_1 (xor_1_out, in_2, in_3);
  xor xor_2 (out_4, xor_1_out, in_1);
  and and_1 (and_1_out, xor_1_out, in_1);
  and and_2 (and_2_out, in_2, in_3);
  or or_1 (out_5, and_2_out, and_1_out);
endmodule

module Somador_8_bits (
  input  in_1,
  input  [7:0] in_2,
  input  [7:0] in_3,
  output [7:0] out_4,
  output out_5
);

  wire somador_completo_1_out_5, somador_completo_2_out_5, somador_completo_3_out_5,
       somador_completo_4_out_5, somador_completo_5_out_5, somador_completo_6_out_5, somador_completo_7_out_5;

  Somador_completo somador_completo_1 (
    .in_2(in_2[0]), .in_3(in_3[0]), .in_1(in_1), .out_4(out_4[0]), .out_5(somador_completo_1_out_5));
  Somador_completo somador_completo_2 (
    .in_2(in_2[1]), .in_3(in_3[1]), .in_1(somador_completo_1_out_5), .out_4(out_4[1]),
    .out_5(somador_completo_2_out_5));
  Somador_completo somador_completo_3 (
    .in_2(in_2[2]), .in_3(in_3[2]), .in_1(somador_completo_2_out_5), .out_4(out_4[2]),
    .out_5(somador_completo_3_out_5));
  Somador_completo somador_completo_4 (
    .in_2(in_2[3]), .in_3(in_3[3]), .in_1(somador_completo_3_out_5), .out_4(out_4[3]),
    .out_5(somador_completo_4_out_5));
  Somador_completo somador_completo_5 (
    .in_2(in_2[4]), .in_3(in_3[4]), .in_1(somador_completo_4_out_5), .out_4(out_4[4]),
    .out_5(somador_completo_5_out_5));
  Somador_completo somador_completo_6 (
    .in_2(in_2[5]), .in_3(in_3[5]), .in_1(somador_completo_5_out_5), .out_4(out_4[5]),
    .out_5(somador_completo_6_out_5));
  Somador_completo somador_completo_7 (
    .in_2(in_3[6]), .in_3(in_2[6]), .in_1(somador_completo_6_out_5), .out_4(out_4[6]),
    .out_5(somador_completo_7_out_5));
  Somador_completo somador_completo_8 (
    .in_2(in_2[7]), .in_3(in_3[7]), .in_1(somador_completo_7_out_5), .out_4(out_4[7]), .out_5(out_5));
endmodule

module Flip_flop (
  input  in_1,
  input  in_2,
  output out_3
);

  wire nand_1_out, nand_2_out, nand_4_out;

  nand nand_1 (nand_1_out, in_1, in_2);
  nand nand_2 (nand_2_out, nand_1_out, in_2);
  nand nand_3 (out_3, nand_1_out, nand_4_out);
  nand nand_4 (nand_4_out, out_3, nand_2_out);
endmodule

module Registrador_8bit (
  input  [7:0] in_1,
  input  in_2,
  output [7:0] out_3
);

  Flip_flop flip_flop_1 (.in_1(in_1[0]), .in_2(in_2), .out_3(out_3[0]));
  Flip_flop flip_flop_2 (.in_1(in_1[1]), .in_2(in_2), .out_3(out_3[1]));
  Flip_flop flip_flop_3 (.in_1(in_1[2]), .in_2(in_2), .out_3(out_3[2]));
  Flip_flop flip_flop_4 (.in_1(in_1[3]), .in_2(in_2), .out_3(out_3[3]));
  Flip_flop flip_flop_5 (.in_1(in_1[4]), .in_2(in_2), .out_3(out_3[4]));
  Flip_flop flip_flop_6 (.in_1(in_1[5]), .in_2(in_2), .out_3(out_3[5]));
  Flip_flop flip_flop_7 (.in_1(in_1[6]), .in_2(in_2), .out_3(out_3[6]));
  Flip_flop flip_flop_8 (.in_1(in_1[7]), .in_2(in_2), .out_3(out_3[7]));
endmodule

module Memoria_8bit_enable (
  input  [7:0] in_1,
  input  in_2,
  input  in_3,
  output [7:0] out_4
);

  wire flip_flop_1_out_3, flip_flop_2_out_3, flip_flop_3_out_3, flip_flop_4_out_3, flip_flop_5_out_3,
       flip_flop_6_out_3, flip_flop_7_out_3, flip_flop_8_out_3;

  Flip_flop flip_flop_1 (.in_1(in_1[0]), .in_2(in_2), .out_3(flip_flop_1_out_3));
  Flip_flop flip_flop_2 (.in_1(in_1[1]), .in_2(in_2), .out_3(flip_flop_2_out_3));
  Flip_flop flip_flop_3 (.in_1(in_1[2]), .in_2(in_2), .out_3(flip_flop_3_out_3));
  Flip_flop flip_flop_4 (.in_1(in_1[3]), .in_2(in_2), .out_3(flip_flop_4_out_3));
  Flip_flop flip_flop_5 (.in_1(in_1[4]), .in_2(in_2), .out_3(flip_flop_5_out_3));
  Flip_flop flip_flop_6 (.in_1(in_1[5]), .in_2(in_2), .out_3(flip_flop_6_out_3));
  Flip_flop flip_flop_7 (.in_1(in_1[6]), .in_2(in_2), .out_3(flip_flop_7_out_3));
  Flip_flop flip_flop_8 (.in_1(in_1[7]), .in_2(in_2), .out_3(flip_flop_8_out_3));
  and and_1 (out_4[0], flip_flop_1_out_3, in_3);
  and and_2 (out_4[1], flip_flop_2_out_3, in_3);
  and and_3 (out_4[2], flip_flop_3_out_3, in_3);
  and and_4 (out_4[7], flip_flop_8_out_3, in_3);
  and and_5 (out_4[3], flip_flop_4_out_3, in_3);
  and and_6 (out_4[4], flip_flop_5_out_3, in_3);
  and and_7 (out_4[5], flip_flop_6_out_3, in_3);
  and and_8 (out_4[6], flip_flop_7_out_3, in_3);
endmodule
