// Logisim project Lorena_Anjos.circ as structural Verilog: 10 circuits, main circuit main
module main (
  input  in_1,
  input  in_2,
  input  in_3,
  input  in_4,
  input  in_5,
  input  in_6,
  input  in_7,
  input  in_8
);

  wire [7:0] registrador_1_out_4;

  registrador registrador_1 (.in_1(registrador_1_out_4), .in_2(in_1), .in_3(in_2), .out_4(registrador_1_out_4));
  registrador registrador_2 (.in_1(registrador_1_out_4), .in_2(in_3), .in_3(in_4), .out_4(registrador_1_out_4));
  registrador registrador_3 (.in_1(registrador_1_out_4), .in_2(in_5), .in_3(in_6), .out_4(registrador_1_out_4));
  registrador registrador_4 (.in_1(registrador_1_out_4), .in_2(in_7), .in_3(in_8), .out_4(registrador_1_out_4));

  // Notes on the sheet:
  //                                      Lorena Pantoja dos Anjos
  //   Matrícula: 22252592
endmodule

module somador_semcarry (
  input  in_1,
  input  in_2,
  input  in_3,
  output out_4
);

  wire xor_1_out;

  xor xor_1 (xor_1_out, in_2, in_3);
  xor xor_2 (out_4, xor_1_out, in_1);
endmodule

module meio_somador (
  input  in_1,
  input  b,
  output out,
  output c_out
);

  xor xor_1 (out, in_1, b);
  and and_1 (c_out, in_1, b);

  // Notes on the sheet:
  //      a
endmodule

module somador_1bit (
  input  in_1,
  input  in_2,
  input  in_3,
  output out,
  output out_5
);

  wire and_1_out, and_2_out, and_3_out, xor_1_out;

  xor xor_1 (xor_1_out, in_2, in_3);
  and and_1 (and_1_out, in_2, in_1);
  and and_2 (and_2_out, in_2, in_3);
  and and_3 (and_3_out, in_3, in_1);
  or or_1 (out_5, and_1_out, and_2_out, and_3_out);
  xor xor_2 (out, xor_1_out, in_1);
endmodule

module somador_8bit (
  input  in_1,
  input  [7:0] in_2,
  input  [7:0] in_3,
  output [7:0] out_4,
  output out_5
);

  wire somador_1bit_1_out_5, somador_1bit_2_out_5, somador_1bit_3_out_5, somador_1bit_4_out_5,
       somador_1bit_5_out_5, somador_1bit_6_out_5, somador_1bit_7_out_5;

  somador_1bit somador_1bit_1 (
    .in_2(in_2[0]), .in_3(in_3[0]), .in_1(in_1), .out_5(somador_1bit_1_out_5), .out(out_4[0]));
  somador_1bit somador_1bit_2 (
    .in_2(in_2[1]), .in_3(in_3[1]), .in_1(somador_1bit_1_out_5), .out_5(somador_1bit_2_out_5), .out(out_4[1]));
  somador_1bit somador_1bit_3 (
    .in_2(in_2[2]), .in_3(in_3[2]), .in_1(somador_1bit_2_out_5), .out_5(somador_1bit_3_out_5), .out(out_4[2]));
  somador_1bit somador_1bit_4 (
    .in_2(in_2[3]), .in_3(in_3[3]), .in_1(somador_1bit_3_out_5), .out_5(somador_1bit_4_out_5), .out(out_4[3]));
  somador_1bit somador_1bit_5 (
    .in_2(in_2[4]), .in_3(in_3[4]), .in_1(somador_1bit_4_out_5), .out_5(somador_1bit_5_out_5), .out(out_4[4]));
  somador_1bit somador_1bit_6 (
    .in_2(in_2[5]), .in_3(in_3[5]), .in_1(somador_1bit_5_out_5), .out_5(somador_1bit_6_out_5), .out(out_4[5]));
  somador_1bit somador_1bit_7 (
    .in_2(in_2[6]), .in_3(in_3[6]), .in_1(somador_1bit_6_out_5), .out_5(somador_1bit_7_out_5), .out(out_4[6]));
  somador_1bit somador_1bit_8 (
    .in_2(in_2[7]), .in_3(in_3[7]), .in_1(somador_1bit_7_out_5), .out_5(out_5), .out(out_4[7]));
endmodule

module memoria_1bit (
  input  in_1,
  input  in_2,
  output o
);

  wire nand_1_out, nand_2_out, nand_4_out;

  nand nand_1 (nand_1_out, in_1, in_2);
  nand nand_2 (nand_2_out, nand_1_out, in_2);
  nand nand_3 (o, nand_1_out, nand_4_out);
  nand nand_4 (nand_4_out, o, nand_2_out);
endmodule

module memoria_2bit (
  input  in_1,
  input  in_2,
  input  in_3,
  output o1,
  output o2
);

  memoria_1bit memoria_1bit_1 (.in_1(in_1), .in_2(in_3), .o(o1));
  memoria_1bit memoria_1bit_2 (.in_1(in_2), .in_2(in_3), .o(o2));
endmodule

module memoria_8bit (
  input  [7:0] in_1,
  input  in_2,
  output [7:0] out_3
);

  memoria_1bit memoria_1bit_1 (.in_1(in_1[0]), .in_2(in_2), .o(out_3[0]));
  memoria_1bit memoria_1bit_2 (.in_1(in_1[1]), .in_2(in_2), .o(out_3[1]));
  memoria_1bit memoria_1bit_3 (.in_1(in_1[2]), .in_2(in_2), .o(out_3[2]));
  memoria_1bit memoria_1bit_4 (.in_1(in_1[3]), .in_2(in_2), .o(out_3[3]));
  memoria_1bit memoria_1bit_5 (.in_1(in_1[4]), .in_2(in_2), .o(out_3[4]));
  memoria_1bit memoria_1bit_6 (.in_1(in_1[5]), .in_2(in_2), .o(out_3[5]));
  memoria_1bit memoria_1bit_7 (.in_1(in_1[6]), .in_2(in_2), .o(out_3[6]));
  memoria_1bit memoria_1bit_8 (.in_1(in_1[7]), .in_2(in_2), .o(out_3[7]));
endmodule

module enable (
  input  [7:0] in_1,
  input  in_2,
  output [7:0] out_3
);

  and and_1 (out_3[0], in_1[0], in_2);
  and and_2 (out_3[1], in_1[1], in_2);
  and and_3 (out_3[2], in_1[2], in_2);
  and and_4 (out_3[3], in_1[3], in_2);
  and and_5 (out_3[4], in_1[4], in_2);
  and and_6 (out_3[5], in_1[5], in_2);
  and and_7 (out_3[6], in_1[6], in_2);
  and and_8 (out_3[7], in_1[7], in_2);
endmodule

module registrador (
  input  [7:0] in_1,
  input  in_2,
  input  in_3,
  output [7:0] out_4
);

  wire [7:0] enable_1_out_3;

  enable enable_1 (.in_1(in_1), .in_2(in_2), .out_3(enable_1_out_3));
  enable enable_2 (.in_1(enable_1_out_3), .in_2(in_3), .out_3(out_4));
endmodule
