// Logisim project Lorena_Flávia_Marinho_de_Souza.circ as structural Verilog: 7 circuits, main circuit somador_1bit
module main (
  input  set,
  input  enable_1,
  input  set_2,
  input  enable_2,
  input  set_3,
  input  enable_3,
  input  set_4,
  input  enable_4,
  input  c_in,
  input  [7:0] a,
  input  [7:0] b,
  output [7:0] c,
  output c_out
);

  wire [7:0] registrador_enable_1_out_4;

  registrador_enable registrador_enable_1 (
    .in_1(registrador_enable_1_out_4), .set(set), .enable_1(enable_1), .out_4(registrador_enable_1_out_4));
  registrador_enable registrador_enable_2 (
    .in_1(registrador_enable_1_out_4), .set(set_2), .enable_1(enable_2), .out_4(registrador_enable_1_out_4));
  registrador_enable registrador_enable_3 (
    .in_1(registrador_enable_1_out_4), .set(set_3), .enable_1(enable_3), .out_4(registrador_enable_1_out_4));
  somador_8bits somador_8bits_1 (.a(a), .b(b), .c_in(c_in), .c(c), .c_out(c_out));
  registrador_enable registrador_enable_4 (
    .in_1(registrador_enable_1_out_4), .set(set_4), .enable_1(enable_4), .out_4(registrador_enable_1_out_4));

  // Notes on the sheet:
  //   Lorena Flavia Marinho de Souza
  //   22450321
  //   Registradores 8 bits
  //   somador 8 bits
endmodule

module somador_1bit (
  input  c_in,
  input  a,
  input  b,
  output c,
  output c_out
);

  wire and_1_out, and_2_out, and_3_out, xor_1_out;

  xor xor_1 (xor_1_out, a, b);
  and and_1 (and_1_out, a, c_in);
  and and_2 (and_2_out, a, b);
  and and_3 (and_3_out, b, c_in);
  xor xor_2 (c, xor_1_out, c_in);
  or or_1 (c_out, and_1_out, and_2_out, and_3_out);

  // Notes on the sheet:
  //   Lorena Flavia Marinho de Souza
endmodule

module somador_8bits (
  input  c_in,
  input  [7:0] a,
  input  [7:0] b,
  output [7:0] c,
  output c_out
);

  wire somador_1bit_1_c_out, somador_1bit_2_c_out, somador_1bit_3_c_out, somador_1bit_4_c_out,
       somador_1bit_5_c_out, somador_1bit_6_c_out, somador_1bit_7_c_out;

  somador_1bit somador_1bit_1 (.a(a[0]), .b(b[0]), .c_in(c_in), .c(c[0]), .c_out(somador_1bit_1_c_out));
  somador_1bit somador_1bit_2 (.a(a[1]), .b(b[1]), .c_in(somador_1bit_1_c_out), .c(c[1]), .c_out(somador_1bit_2_c_out));
  somador_1bit somador_1bit_3 (.a(a[2]), .b(b[2]), .c_in(somador_1bit_2_c_out), .c(c[2]), .c_out(somador_1bit_3_c_out));
  somador_1bit somador_1bit_4 (.a(a[3]), .b(b[3]), .c_in(somador_1bit_3_c_out), .c(c[3]), .c_out(somador_1bit_4_c_out));
  somador_1bit somador_1bit_5 (.a(a[4]), .b(b[4]), .c_in(somador_1bit_4_c_out), .c(c[4]), .c_out(somador_1bit_5_c_out));
  somador_1bit somador_1bit_6 (.a(a[5]), .b(b[5]), .c_in(somador_1bit_5_c_out), .c(c[5]), .c_out(somador_1bit_6_c_out));
  somador_1bit somador_1bit_7 (.a(a[6]), .b(b[6]), .c_in(somador_1bit_6_c_out), .c(c[6]), .c_out(somador_1bit_7_c_out));
  somador_1bit somador_1bit_8 (.a(a[7]), .b(b[7]), .c_in(somador_1bit_7_c_out), .c(c[7]), .c_out(c_out));

  // Notes on the sheet:
  //   Lorena Flavia Marinho de Souza
endmodule

module memoria_1bit (
  input  a,
  input  set,
  output s
);

  wire nand_1_out, nand_2_out, nand_4_out;

  nand nand_1 (nand_1_out, a, set);
  nand nand_2 (nand_2_out, nand_1_out, set);
  nand nand_3 (s, nand_1_out, nand_4_out);
  nand nand_4 (nand_4_out, s, nand_2_out);

  // Notes on the sheet:
  //   Lorena Flavia Marinho de Souza
endmodule

module registrador (
  input  [7:0] in_1,
  input  set,
  output out_3,
  output out_4,
  output out_5,
  output out_6,
  output out_7,
  output out_8,
  output out_9,
  output out_10
);

  memoria_1bit memoria_1bit_1 (.a(in_1[0]), .set(set), .s(out_3));
  memoria_1bit memoria_1bit_2 (.a(in_1[1]), .set(set), .s(out_4));
  memoria_1bit memoria_1bit_3 (.a(in_1[2]), .set(set), .s(out_5));
  memoria_1bit memoria_1bit_4 (.a(in_1[3]), .set(set), .s(out_6));
  memoria_1bit memoria_1bit_5 (.a(in_1[4]), .set(set), .s(out_7));
  memoria_1bit memoria_1bit_6 (.a(in_1[5]), .set(set), .s(out_8));
  memoria_1bit memoria_1bit_7 (.a(in_1[6]), .set(set), .s(out_9));
  memoria_1bit memoria_1bit_8 (.a(in_1[7]), .set(set), .s(out_10));

  // Notes on the sheet:
  //   Lorena Flavia Marinho de Souza
endmodule

module ativador (
  input  in_1,
  input  in_2,
  input  in_3,
  input  in_4,
  input  in_5,
  input  in_6,
  input  in_7,
  input  in_8,
  input  enabled,
  output [7:0] out_10
);

  and and_1 (out_10[0], in_1, enabled);
  and and_2 (out_10[1], in_2, enabled);
  and and_3 (out_10[2], in_3, enabled);
  and and_4 (out_10[3], in_4, enabled);
  and and_5 (out_10[4], in_5, enabled);
  and and_6 (out_10[5], in_6, enabled);
  and and_7 (out_10[6], in_7, enabled);
  and and_8 (out_10[7], in_8, enabled);

  // Notes on the sheet:
  //   Lorena Flavia Marinho de Souza
endmodule

module registrador_enable (
  input  [7:0] in_1,
  input  set,
  input  enable_1,
  output [7:0] out_4
);

  wire registrador_1_out_3, registrador_1_out_4, registrador_1_out_5, registrador_1_out_6,
       registrador_1_out_7, registrador_1_out_8, registrador_1_out_9, registrador_1_out_10;

  registrador registrador_1 (
    .in_1(in_1), .set(set), .out_3(registrador_1_out_3), .out_4(registrador_1_out_4),
    .out_5(registrador_1_out_5), .out_6(registrador_1_out_6), .out_7(registrador_1_out_7),
    .out_8(registrador_1_out_8), .out_9(registrador_1_out_9), .out_10(registrador_1_out_10));
  ativador ativador_1 (
    .in_1(registrador_1_out_3), .in_2(registrador_1_out_4), .in_3(registrador_1_out_5),
    .in_4(registrador_1_out_6), .in_5(registrador_1_out_7), .in_6(registrador_1_out_8),
    .in_7(registrador_1_out_9), .in_8(registrador_1_out_10), .enabled(enable_1), .out_10(out_4));

  // Notes on the sheet:
  //   Registrador
  //   Lorena Flavia Marinho de Souza
  //   Enable
endmodule
