// Logisim project Lucas_Nascimento.circ as structural Verilog: 8 circuits, main circuit main
module main (
  input  [7:0] in_1,
  input  set,
  input  set_2,
  input  set_3,
  input  set_4,
  input  e,
  input  e_2,
  input  e_3,
  input  e_4,
  output [7:0] out_10
);

  wire not_1_out, or_1_out;
  wire [7:0] memoria_1byte_1_out_4, memoria_1byte_2_out_4, memoria_1byte_3_out_4, memoria_1byte_4_out_4,
       or_2_out;

  memoria_1byte memoria_1byte_1 (.in_1(in_1), .Set(set), .E(e), .out_4(memoria_1byte_1_out_4));
  memoria_1byte memoria_1byte_2 (.in_1(in_1), .Set(set_2), .E(e_2), .out_4(memoria_1byte_2_out_4));
  memoria_1byte memoria_1byte_3 (.in_1(in_1), .Set(set_3), .E(e_3), .out_4(memoria_1byte_3_out_4));
  memoria_1byte memoria_1byte_4 (.in_1(in_1), .Set(set_4), .E(e_4), .out_4(memoria_1byte_4_out_4));
  assign out_10 = not_1_out ? in_1 : 8'bz;  // Controlled_Buffer controlled_buffer_1
  not not_1 (not_1_out, or_1_out);
  or or_1 (or_1_out, e_4, e_3, e_2, e);
  assign or_2_out = memoria_1byte_4_out_4 | memoria_1byte_3_out_4 | memoria_1byte_2_out_4 | memoria_1byte_1_out_4;  // OR_Gate or_2, 8 bits wide
  // Probe on out_10
  assign out_10 = or_1_out ? or_2_out : 8'bz;  // Controlled_Buffer controlled_buffer_2

  // Notes on the sheet:
  //   Lucas do Nascimento Silva - 22250552
endmodule

module somador_1bit (
  input  in_1,
  input  in_2,
  input  in_3,
  output out_4
);

  wire xor_1_out;

  xor xor_1 (xor_1_out, in_2, in_3);
  xor xor_2 (out_4, xor_1_out, in_1);
endmodule

module somador (
  input  in_1,
  input  A,
  input  B,
  output out,
  output c_out
);

  wire and_1_out, and_2_out, and_3_out, xor_1_out;

  xor xor_1 (xor_1_out, A, B);
  and and_1 (and_1_out, A, in_1);
  and and_2 (and_2_out, A, B);
  and and_3 (and_3_out, B, in_1);
  xor xor_2 (out, xor_1_out, in_1);
  or or_1 (c_out, and_1_out, and_2_out, and_3_out);

  // Notes on the sheet:
  //   c_in
endmodule

module somador_8bits (
  input  in_1,
  input  [7:0] in_2,
  input  [7:0] in_3,
  output [7:0] out_4,
  output out_5
);

  wire somador_1_c_out, somador_2_c_out, somador_3_c_out, somador_4_c_out, somador_5_c_out, somador_6_c_out,
       somador_7_c_out;

  somador somador_1 (.A(in_2[0]), .B(in_3[0]), .in_1(in_1), .out(out_4[0]), .c_out(somador_1_c_out));
  somador somador_2 (.A(in_2[1]), .B(in_3[1]), .in_1(somador_1_c_out), .out(out_4[1]), .c_out(somador_2_c_out));
  somador somador_3 (.A(in_2[2]), .B(in_3[2]), .in_1(somador_2_c_out), .out(out_4[2]), .c_out(somador_3_c_out));
  somador somador_4 (.A(in_2[3]), .B(in_3[3]), .in_1(somador_3_c_out), .out(out_4[3]), .c_out(somador_4_c_out));
  somador somador_5 (.A(in_2[4]), .B(in_3[4]), .in_1(somador_4_c_out), .out(out_4[4]), .c_out(somador_5_c_out));
  somador somador_6 (.A(in_2[5]), .B(in_3[5]), .in_1(somador_5_c_out), .out(out_4[5]), .c_out(somador_6_c_out));
  somador somador_7 (.A(in_2[6]), .B(in_3[6]), .in_1(somador_6_c_out), .out(out_4[6]), .c_out(somador_7_c_out));
  somador somador_8 (.A(in_2[7]), .B(in_3[7]), .in_1(somador_7_c_out), .out(out_4[7]), .c_out(out_5));
endmodule

module memoria_1bit (
  input  in_1,
  input  in_2,
  output out_3
);

  wire nand_1_out, nand_2_out, nand_4_out;

  nand nand_1 (nand_1_out, in_1, in_2);
  nand nand_2 (nand_2_out, nand_1_out, in_2);
  nand nand_3 (out_3, nand_1_out, nand_4_out);
  nand nand_4 (nand_4_out, out_3, nand_2_out);
endmodule

module memoria_8bit (
  input  [7:0] in_1,
  input  in_2,
  output [7:0] out_3
);

  memoria_1bit memoria_1bit_1 (.in_1(in_1[0]), .in_2(in_2), .out_3(out_3[0]));
  memoria_1bit memoria_1bit_2 (.in_1(in_1[1]), .in_2(in_2), .out_3(out_3[1]));
  memoria_1bit memoria_1bit_3 (.in_1(in_1[2]), .in_2(in_2), .out_3(out_3[2]));
  memoria_1bit memoria_1bit_4 (.in_1(in_1[3]), .in_2(in_2), .out_3(out_3[3]));
  memoria_1bit memoria_1bit_5 (.in_1(in_1[4]), .in_2(in_2), .out_3(out_3[4]));
  memoria_1bit memoria_1bit_6 (.in_1(in_1[5]), .in_2(in_2), .out_3(out_3[5]));
  memoria_1bit memoria_1bit_7 (.in_1(in_1[6]), .in_2(in_2), .out_3(out_3[6]));
  memoria_1bit memoria_1bit_8 (.in_1(in_1[7]), .in_2(in_2), .out_3(out_3[7]));
endmodule

module memoria_1byte (
  input  [7:0] in_1,
  input  Set,
  input  E,
  output [7:0] out_4
);

  wire [7:0] memoria_8bit_1_out_3;

  memoria_8bit memoria_8bit_1 (.in_1(in_1), .in_2(Set), .out_3(memoria_8bit_1_out_3));
  enable enable_1 (.in_1(memoria_8bit_1_out_3), .in_2(E), .out_3(out_4));
endmodule

module enable (
  input  [7:0] in_1,
  input  in_2,
  output [7:0] out_3
);

  and and_1 (out_3[0], in_1[0], in_2);
  and and_2 (out_3[1], in_1[1], in_2);
  and and_3 (out_3[2], in_1[2], in_2);
  and and_4 (out_3[3], in_1[3], in_2);
  and and_5 (out_3[4], in_1[4], in_2);
  and and_6 (out_3[5], in_1[5], in_2);
  and and_7 (out_3[6], in_1[6], in_2);
  and and_8 (out_3[7], in_1[7], in_2);
endmodule
