// Logisim project Luis_Felipe.circ as structural Verilog: 7 circuits, main circuit main
module main (
  input  [7:0] in_1,
  input  in_2,
  input  in_3,
  input  in_4,
  input  in_5,
  input  in_6,
  input  in_7,
  input  in_8,
  input  in_9,
  output [7:0] out_10
);

  wire not_1_out, or_1_out;
  wire [7:0] or_2_out, registrador_1_out_4, registrador_2_out_4, registrador_3_out_4, registrador_4_out_4;

  Registrador registrador_1 (.in_1(in_1), .in_2(in_2), .in_3(in_6), .out_4(registrador_1_out_4));
  Registrador registrador_2 (.in_1(in_1), .in_2(in_3), .in_3(in_7), .out_4(registrador_2_out_4));
  Registrador registrador_3 (.in_1(in_1), .in_2(in_4), .in_3(in_8), .out_4(registrador_3_out_4));
  Registrador registrador_4 (.in_1(in_1), .in_2(in_5), .in_3(in_9), .out_4(registrador_4_out_4));
  or or_1 (or_1_out, in_9, in_8, in_7, in_6);
  assign out_10 = not_1_out ? in_1 : 8'bz;  // Controlled_Buffer controlled_buffer_1
  not not_1 (not_1_out, or_1_out);
  assign or_2_out = registrador_4_out_4 | registrador_3_out_4 | registrador_2_out_4 | registrador_1_out_4;  // OR_Gate or_2, 8 bits wide
  assign out_10 = or_1_out ? or_2_out : 8'bz;  // Controlled_Buffer controlled_buffer_2

  // Notes on the sheet:
  //   Luis Felipe dos Santos Lima 
  //   R1
  //   22250554
  //   R2
  //   R3
  //   R4
endmodule

module somador_1bit (
  input  in_1,
  input  a,
  input  b,
  output c,
  output out_5
);

  wire and_1_out, and_2_out, and_3_out, xor_1_out;

  xor xor_1 (xor_1_out, a, b);
  and and_1 (and_1_out, a, in_1);
  and and_2 (and_2_out, a, b);
  and and_3 (and_3_out, b, in_1);
  xor xor_2 (c, xor_1_out, in_1);
  or or_1 (out_5, and_1_out, and_2_out, and_3_out);

  // Notes on the sheet:
  //   Luis Felipe dos Santos Lima
  //   c_in
  //   c_out
endmodule

module somador_8bit (
  input  in_1,
  input  [7:0] in_2,
  input  [7:0] in_3,
  output [7:0] out_4,
  output out_5
);

  wire somador_1bit_1_out_5, somador_1bit_2_out_5, somador_1bit_3_out_5, somador_1bit_4_out_5,
       somador_1bit_5_out_5, somador_1bit_6_out_5, somador_1bit_7_out_5;

  somador_1bit somador_1bit_1 (.a(in_2[0]), .b(in_3[0]), .in_1(in_1), .out_5(somador_1bit_1_out_5), .c(out_4[0]));
  somador_1bit somador_1bit_2 (
    .a(in_2[1]), .b(in_3[1]), .in_1(somador_1bit_1_out_5), .out_5(somador_1bit_2_out_5), .c(out_4[1]));
  somador_1bit somador_1bit_3 (
    .a(in_2[2]), .b(in_3[2]), .in_1(somador_1bit_2_out_5), .out_5(somador_1bit_3_out_5), .c(out_4[2]));
  somador_1bit somador_1bit_4 (
    .a(in_2[3]), .b(in_3[3]), .in_1(somador_1bit_3_out_5), .out_5(somador_1bit_4_out_5), .c(out_4[3]));
  somador_1bit somador_1bit_5 (
    .a(in_2[4]), .b(in_3[4]), .in_1(somador_1bit_4_out_5), .out_5(somador_1bit_5_out_5), .c(out_4[4]));
  somador_1bit somador_1bit_6 (
    .a(in_2[5]), .b(in_3[5]), .in_1(somador_1bit_5_out_5), .out_5(somador_1bit_6_out_5), .c(out_4[5]));
  somador_1bit somador_1bit_7 (
    .a(in_2[6]), .b(in_3[6]), .in_1(somador_1bit_6_out_5), .out_5(somador_1bit_7_out_5), .c(out_4[6]));
  somador_1bit somador_1bit_8 (.a(in_2[7]), .b(in_3[7]), .in_1(somador_1bit_7_out_5), .out_5(out_5), .c(out_4[7]));
endmodule

module menoria_1bit (
  input  in_1,
  input  in_2,
  output out_3
);

  wire nand_1_out, nand_2_out, nand_4_out;

  nand nand_1 (nand_1_out, in_1, in_2);
  nand nand_2 (nand_2_out, nand_1_out, in_2);
  nand nand_3 (out_3, nand_1_out, nand_4_out);
  nand nand_4 (nand_4_out, out_3, nand_2_out);
endmodule

module menoria_8bit (
  input  [7:0] in_1,
  input  in_2,
  output [7:0] out_3
);

  menoria_1bit menoria_1bit_1 (.in_1(in_1[0]), .in_2(in_2), .out_3(out_3[0]));
  menoria_1bit menoria_1bit_2 (.in_1(in_1[1]), .in_2(in_2), .out_3(out_3[1]));
  menoria_1bit menoria_1bit_3 (.in_1(in_1[2]), .in_2(in_2), .out_3(out_3[2]));
  menoria_1bit menoria_1bit_4 (.in_1(in_1[3]), .in_2(in_2), .out_3(out_3[3]));
  menoria_1bit menoria_1bit_5 (.in_1(in_1[4]), .in_2(in_2), .out_3(out_3[4]));
  menoria_1bit menoria_1bit_6 (.in_1(in_1[5]), .in_2(in_2), .out_3(out_3[5]));
  menoria_1bit menoria_1bit_7 (.in_1(in_1[6]), .in_2(in_2), .out_3(out_3[6]));
  menoria_1bit menoria_1bit_8 (.in_1(in_1[7]), .in_2(in_2), .out_3(out_3[7]));
endmodule

module enable (
  input  [7:0] in_1,
  input  in_2,
  output [7:0] out_3
);

  and and_1 (out_3[0], in_1[0], in_2);
  and and_2 (out_3[1], in_1[1], in_2);
  and and_3 (out_3[2], in_1[2], in_2);
  and and_4 (out_3[3], in_1[3], in_2);
  and and_5 (out_3[4], in_1[4], in_2);
  and and_6 (out_3[5], in_1[5], in_2);
  and and_7 (out_3[6], in_1[6], in_2);
  and and_8 (out_3[7], in_1[7], in_2);
endmodule

module Registrador (
  input  [7:0] in_1,
  input  in_2,
  input  in_3,
  output [7:0] out_4
);

  wire [7:0] menoria_8bit_1_out_3;

  menoria_8bit menoria_8bit_1 (.in_1(in_1), .in_2(in_2), .out_3(menoria_8bit_1_out_3));
  enable enable_1 (.in_1(menoria_8bit_1_out_3), .in_2(in_3), .out_3(out_4));
endmodule
