// Logisim project Maria_Rita_Souza_Farias.circ as structural Verilog: 7 circuits, main circuit main
module main (
  input  [7:0] in_1,
  input  in_2,
  input  in_3,
  input  in_4,
  input  in_5,
  input  in_6,
  input  in_7,
  input  in_8,
  input  in_9,
  input  in_10,
  output [7:0] out_11
);

  assign out_11 = in_2 ? in_1 : 8'bz;  // Controlled_Buffer controlled_buffer_1
  registrador_set_enable registrador_set_enable_1 (.in_1(out_11), .in_2(in_3), .in_3(in_7), .out_4(out_11));
  registrador_set_enable registrador_set_enable_2 (.in_1(out_11), .in_2(in_4), .in_3(in_8), .out_4(out_11));
  registrador_set_enable registrador_set_enable_3 (.in_1(out_11), .in_2(in_5), .in_3(in_9), .out_4(out_11));
  registrador_set_enable registrador_set_enable_4 (.in_1(out_11), .in_2(in_6), .in_3(in_10), .out_4(out_11));

  // Notes on the sheet:
  //   Maria Rita Souza Farias - 22401908
endmodule

module somador_1bt (
  input  in_1,
  input  in_2,
  input  in_3,
  output out_4,
  output out_5
);

  wire and_1_out, and_2_out, and_3_out, xor_1_out;

  xor xor_1 (xor_1_out, in_2, in_3);
  and and_1 (and_1_out, in_2, in_1);
  and and_2 (and_2_out, in_2, in_3);
  and and_3 (and_3_out, in_3, in_1);
  xor xor_2 (out_4, xor_1_out, in_1);
  or or_1 (out_5, and_1_out, and_3_out);
endmodule

module somador_8bts (
  input  in_1,
  input  [7:0] in_2,
  input  [7:0] in_3,
  output [7:0] out_4,
  output out_5
);

  wire somador_1bt_1_out_5, somador_1bt_2_out_5, somador_1bt_3_out_5, somador_1bt_4_out_5,
       somador_1bt_5_out_5, somador_1bt_6_out_5, somador_1bt_7_out_5;

  somador_1bt somador_1bt_1 (
    .in_2(in_2[0]), .in_3(in_3[0]), .in_1(in_1), .out_5(somador_1bt_1_out_5), .out_4(out_4[0]));
  somador_1bt somador_1bt_2 (
    .in_2(in_2[1]), .in_3(in_3[1]), .in_1(somador_1bt_1_out_5), .out_5(somador_1bt_2_out_5), .out_4(out_4[1]));
  somador_1bt somador_1bt_3 (
    .in_2(in_2[2]), .in_3(in_3[2]), .in_1(somador_1bt_2_out_5), .out_5(somador_1bt_3_out_5), .out_4(out_4[2]));
  somador_1bt somador_1bt_4 (
    .in_2(in_2[3]), .in_3(in_3[3]), .in_1(somador_1bt_3_out_5), .out_5(somador_1bt_4_out_5), .out_4(out_4[3]));
  somador_1bt somador_1bt_5 (
    .in_2(in_2[4]), .in_3(in_3[4]), .in_1(somador_1bt_4_out_5), .out_5(somador_1bt_5_out_5), .out_4(out_4[4]));
  somador_1bt somador_1bt_6 (
    .in_2(in_2[5]), .in_3(in_3[5]), .in_1(somador_1bt_5_out_5), .out_5(somador_1bt_6_out_5), .out_4(out_4[5]));
  somador_1bt somador_1bt_7 (
    .in_2(in_2[6]), .in_3(in_3[6]), .in_1(somador_1bt_6_out_5), .out_5(somador_1bt_7_out_5), .out_4(out_4[6]));
  somador_1bt somador_1bt_8 (
    .in_2(in_2[7]), .in_3(in_3[7]), .in_1(somador_1bt_7_out_5), .out_5(out_5), .out_4(out_4[7]));
endmodule

module memory_1bit (
  input  in_1,
  input  in_2,
  output out_3
);

  wire nand_1_out, nand_2_out, nand_4_out;

  nand nand_1 (nand_1_out, in_1, in_2);
  nand nand_2 (nand_2_out, in_2, nand_1_out);
  nand nand_3 (out_3, nand_1_out, nand_4_out);
  nand nand_4 (nand_4_out, out_3, nand_2_out);
endmodule

module registrador (
  input  [7:0] in_1,
  input  in_2,
  output [7:0] out_3
);

  memory_1bit memory_1bit_1 (.in_1(in_1[0]), .in_2(in_2), .out_3(out_3[0]));
  memory_1bit memory_1bit_2 (.in_1(in_1[1]), .in_2(in_2), .out_3(out_3[1]));
  memory_1bit memory_1bit_3 (.in_1(in_1[2]), .in_2(in_2), .out_3(out_3[2]));
  memory_1bit memory_1bit_4 (.in_1(in_1[3]), .in_2(in_2), .out_3(out_3[3]));
  memory_1bit memory_1bit_5 (.in_1(in_1[4]), .in_2(in_2), .out_3(out_3[4]));
  memory_1bit memory_1bit_6 (.in_1(in_1[5]), .in_2(in_2), .out_3(out_3[5]));
  memory_1bit memory_1bit_7 (.in_1(in_1[6]), .in_2(in_2), .out_3(out_3[6]));
  memory_1bit memory_1bit_8 (.in_1(in_1[7]), .in_2(in_2), .out_3(out_3[7]));
endmodule

module enable (
  input  [7:0] in_1,
  input  in_2,
  output [7:0] out_3
);

  assign out_3 = in_2 ? in_1 : 8'bz;  // Controlled_Buffer controlled_buffer_1
endmodule

module registrador_set_enable (
  input  [7:0] in_1,
  input  in_2,
  input  in_3,
  output [7:0] out_4
);

  wire [7:0] registrador_1_out_3;

  registrador registrador_1 (.in_1(in_1), .in_2(in_2), .out_3(registrador_1_out_3));
  enable enable_1 (.in_1(registrador_1_out_3), .in_2(in_3), .out_3(out_4));
endmodule
