// Logisim project Matheus_Ferreira_Unten.circ as structural Verilog: 7 circuits, main circuit main
module main (
  input  in_1,
  input  [7:0] in_2,
  input  [7:0] in_3,
  input  [7:0] barramento,
  input  sMAR,
  input  eMAR,
  input  s1,
  input  s2,
  input  s3,
  input  s4,
  input  e1,
  input  e2,
  input  e3,
  input  e4,
  output [7:0] out_15,
  output out_16,
  output [7:0] out_17
);

  wire [7:0] MAR_out_4, R1_out_4, R2_out_4, R3_out_4, R4_out_4;

  Somador_8bit somador_8bit_1 (.in_2(in_2), .in_3(in_3), .in_1(in_1), .out_5(out_16), .out_4(out_15));
  Regi_set_en MAR (.in_1(barramento), .in_2(sMAR), .in_3(eMAR), .out_4(MAR_out_4));
  assign out_17 = eMAR ? MAR_out_4 : 8'bz;  // Controlled_Buffer controlled_buffer_1
  assign out_17 = e1 ? R1_out_4 : 8'bz;  // Controlled_Buffer controlled_buffer_2
  Regi_set_en R1 (.in_1(out_17), .in_2(s1), .in_3(e1), .out_4(R1_out_4));
  Regi_set_en R2 (.in_1(out_17), .in_2(s2), .in_3(e2), .out_4(R2_out_4));
  assign out_17 = e2 ? R2_out_4 : 8'bz;  // Controlled_Buffer controlled_buffer_3
  assign out_17 = e3 ? R3_out_4 : 8'bz;  // Controlled_Buffer controlled_buffer_4
  Regi_set_en R3 (.in_1(out_17), .in_2(s3), .in_3(e3), .out_4(R3_out_4));
  Regi_set_en R4 (.in_1(out_17), .in_2(s4), .in_3(e4), .out_4(R4_out_4));
  assign out_17 = e4 ? R4_out_4 : 8'bz;  // Controlled_Buffer controlled_buffer_5

  // Notes on the sheet:
  //   Matheus Ferreira Unten
  //   22450082
endmodule

module Somador_1bit (
  input  C_in,
  input  a,
  input  b,
  output c,
  output c_out
);

  wire and_1_out, and_2_out, and_3_out, xor_1_out;

  xor xor_1 (xor_1_out, a, b);
  xor xor_2 (c, xor_1_out, C_in);
  and and_1 (and_1_out, C_in, a);
  and and_2 (and_2_out, C_in, b);
  and and_3 (and_3_out, b, a);
  or or_1 (c_out, and_1_out, and_2_out, and_3_out);
endmodule

module Somador_8bit (
  input  in_1,
  input  [7:0] in_2,
  input  [7:0] in_3,
  output [7:0] out_4,
  output out_5
);

  wire somador_1bit_1_c_out, somador_1bit_2_c_out, somador_1bit_3_c_out, somador_1bit_4_c_out,
       somador_1bit_5_c_out, somador_1bit_6_c_out, somador_1bit_7_c_out;

  Somador_1bit somador_1bit_1 (.a(in_2[0]), .b(in_3[0]), .C_in(in_1), .c_out(somador_1bit_1_c_out), .c(out_4[0]));
  Somador_1bit somador_1bit_2 (
    .a(in_2[1]), .b(in_3[1]), .C_in(somador_1bit_1_c_out), .c_out(somador_1bit_2_c_out), .c(out_4[1]));
  Somador_1bit somador_1bit_3 (
    .a(in_2[2]), .b(in_3[2]), .C_in(somador_1bit_2_c_out), .c_out(somador_1bit_3_c_out), .c(out_4[2]));
  Somador_1bit somador_1bit_4 (
    .a(in_2[3]), .b(in_3[3]), .C_in(somador_1bit_3_c_out), .c_out(somador_1bit_4_c_out), .c(out_4[3]));
  Somador_1bit somador_1bit_5 (
    .a(in_2[4]), .b(in_3[4]), .C_in(somador_1bit_4_c_out), .c_out(somador_1bit_5_c_out), .c(out_4[4]));
  Somador_1bit somador_1bit_6 (
    .a(in_2[5]), .b(in_3[5]), .C_in(somador_1bit_5_c_out), .c_out(somador_1bit_6_c_out), .c(out_4[5]));
  Somador_1bit somador_1bit_7 (
    .a(in_2[6]), .b(in_3[6]), .C_in(somador_1bit_6_c_out), .c_out(somador_1bit_7_c_out), .c(out_4[6]));
  Somador_1bit somador_1bit_8 (.a(in_2[7]), .b(in_3[7]), .C_in(somador_1bit_7_c_out), .c_out(out_5), .c(out_4[7]));
endmodule

module Memory_1bit (
  input  i,
  input  set,
  output o
);

  wire nand_1_out, nand_2_out, nand_4_out;

  nand nand_1 (nand_1_out, i, set);
  nand nand_2 (nand_2_out, nand_1_out, set);
  nand nand_3 (o, nand_1_out, nand_4_out);
  nand nand_4 (nand_4_out, o, nand_2_out);
endmodule

module Memory_8bit (
  input  [7:0] in_1,
  input  S,
  output [7:0] out_3
);

  Memory_1bit memory_1bit_1 (.i(in_1[0]), .set(S), .o(out_3[0]));
  Memory_1bit memory_1bit_2 (.i(in_1[1]), .set(S), .o(out_3[1]));
  Memory_1bit memory_1bit_3 (.i(in_1[2]), .set(S), .o(out_3[2]));
  Memory_1bit memory_1bit_4 (.i(in_1[3]), .set(S), .o(out_3[3]));
  Memory_1bit memory_1bit_5 (.i(in_1[4]), .set(S), .o(out_3[4]));
  Memory_1bit memory_1bit_6 (.i(in_1[5]), .set(S), .o(out_3[5]));
  Memory_1bit memory_1bit_7 (.i(in_1[6]), .set(S), .o(out_3[6]));
  Memory_1bit memory_1bit_8 (.i(in_1[7]), .set(S), .o(out_3[7]));
endmodule

module Enable (
  input  [7:0] in_1,
  input  in_2,
  output [7:0] out_3
);

  assign out_3[0] = in_2 ? in_1[0] : 1'bz;  // Controlled_Buffer controlled_buffer_1
  assign out_3[1] = in_2 ? in_1[1] : 1'bz;  // Controlled_Buffer controlled_buffer_2
  assign out_3[2] = in_2 ? in_1[2] : 1'bz;  // Controlled_Buffer controlled_buffer_3
  assign out_3[3] = in_2 ? in_1[3] : 1'bz;  // Controlled_Buffer controlled_buffer_4
  assign out_3[4] = in_2 ? in_1[4] : 1'bz;  // Controlled_Buffer controlled_buffer_5
  assign out_3[5] = in_2 ? in_1[5] : 1'bz;  // Controlled_Buffer controlled_buffer_6
  assign out_3[6] = in_2 ? in_1[6] : 1'bz;  // Controlled_Buffer controlled_buffer_7
  assign out_3[7] = in_2 ? in_1[7] : 1'bz;  // Controlled_Buffer controlled_buffer_8
endmodule

module Regi_set_en (
  input  [7:0] in_1,
  input  in_2,
  input  in_3,
  output [7:0] out_4
);

  wire [7:0] memory_8bit_1_out_3;

  Memory_8bit memory_8bit_1 (.in_1(in_1), .S(in_2), .out_3(memory_8bit_1_out_3));
  Enable enable_1 (.in_1(memory_8bit_1_out_3), .in_2(in_3), .out_3(out_4));
endmodule
