// Logisim project Matheus_Henrique_de_Oliveira_Garcia_aluno.circ as structural Verilog: 13 circuits, main circuit main
module main (
  input  in_1,
  input  [7:0] in_2,
  input  [7:0] in_3,
  input  [7:0] in_4,
  input  in_5,
  input  enable,
  input  [7:0] in_7,
  input  in_8,
  input  in_9,
  input  in_10,
  input  in_11,
  input  in_12,
  input  in_13,
  input  in_14,
  input  in_15,
  output [7:0] out_16,
  output out_17,
  output [7:0] out_18,
  output [7:0] out_19
);

  wire not_1_out, or_2_out;
  wire [7:0] or_1_out, registrador_8b_1_out_10, set_enable_1_out_4, set_enable_2_out_4, set_enable_3_out_4,
       set_enable_4_out_4;

  somador_8b somador_8b_1 (.in_2(in_2), .in_3(in_3), .in_1(in_1), .out_5(out_17), .out_4(out_16));
  set_enable set_enable_1 (.in_3(in_7), .in_1(in_8), .in_2(in_12), .out_4(set_enable_1_out_4));
  set_enable set_enable_2 (.in_3(in_7), .in_1(in_9), .in_2(in_13), .out_4(set_enable_2_out_4));
  assign or_1_out = set_enable_1_out_4 | set_enable_2_out_4 | set_enable_3_out_4 | set_enable_4_out_4;  // OR_Gate or_1, 8 bits wide
  set_enable set_enable_3 (.in_3(in_7), .in_1(in_10), .in_2(in_14), .out_4(set_enable_3_out_4));
  registrador_8b registrador_8b_1 (
    .in_1(in_4[0]), .in_2(in_4[1]), .in_3(in_4[2]), .in_4(in_4[3]), .in_5(in_4[4]), .in_6(in_4[5]),
    .in_7(in_4[6]), .in_8(in_4[7]), .in_9(in_5), .out_10(registrador_8b_1_out_10[0]),
    .out_11(registrador_8b_1_out_10[1]), .out_12(registrador_8b_1_out_10[2]),
    .out_13(registrador_8b_1_out_10[3]), .out_14(registrador_8b_1_out_10[4]),
    .out_15(registrador_8b_1_out_10[5]), .out_16(registrador_8b_1_out_10[6]),
    .out_17(registrador_8b_1_out_10[7]));
  set_enable set_enable_4 (.in_3(in_7), .in_1(in_11), .in_2(in_15), .out_4(set_enable_4_out_4));
  EnableV2 enablev2_1 (
    .in_1(registrador_8b_1_out_10[0]), .in_2(registrador_8b_1_out_10[1]), .in_3(registrador_8b_1_out_10[2]),
    .in_4(registrador_8b_1_out_10[3]), .in_5(registrador_8b_1_out_10[4]), .in_6(registrador_8b_1_out_10[5]),
    .in_7(registrador_8b_1_out_10[6]), .in_8(registrador_8b_1_out_10[7]), .in_9(enable), .out_10(out_18[0]),
    .out_11(out_18[1]), .out_12(out_18[2]), .out_13(out_18[3]), .out_14(out_18[4]), .out_15(out_18[5]),
    .out_16(out_18[6]), .out_17(out_18[7]));
  or or_2 (or_2_out, in_15, in_14, in_13, in_12);
  assign out_19 = not_1_out ? in_7 : 8'bz;  // Controlled_Buffer controlled_buffer_1
  not not_1 (not_1_out, or_2_out);
  assign out_19 = or_2_out ? or_1_out : 8'bz;  // Controlled_Buffer controlled_buffer_2

  // Notes on the sheet:
  //   Matheus Henrique
  //   SOMADOR_8B
  //   22450747
  //   4 REGISTRADORES NO BARRAMENTO
  //   REGISTRADOR DE 8 BITS
  //   set
endmodule

module Somador_1b (
  input  in_1,
  input  in_2,
  input  in_3,
  output out_4,
  output out_5
);

  wire and_1_out, and_2_out, and_3_out, xor_1_out;

  xor xor_1 (xor_1_out, in_2, in_3);
  and and_1 (and_1_out, in_2, in_1);
  and and_2 (and_2_out, in_2, in_3);
  and and_3 (and_3_out, in_3, in_2);
  xor xor_2 (out_4, xor_1_out, in_1);
  or or_1 (out_5, and_1_out, and_2_out, and_3_out);
endmodule

module somador_8b (
  input  in_1,
  input  [7:0] in_2,
  input  [7:0] in_3,
  output [7:0] out_4,
  output out_5
);

  wire somador_1b_1_out_5, somador_1b_2_out_5, somador_1b_3_out_5, somador_1b_4_out_5, somador_1b_5_out_5,
       somador_1b_6_out_5, somador_1b_7_out_5;

  Somador_1b somador_1b_1 (.in_2(in_2[0]), .in_3(in_3[0]), .in_1(in_1), .out_5(somador_1b_1_out_5), .out_4(out_4[0]));
  Somador_1b somador_1b_2 (
    .in_2(in_2[1]), .in_3(in_3[1]), .in_1(somador_1b_1_out_5), .out_5(somador_1b_2_out_5), .out_4(out_4[1]));
  Somador_1b somador_1b_3 (
    .in_2(in_2[2]), .in_3(in_3[2]), .in_1(somador_1b_2_out_5), .out_5(somador_1b_3_out_5), .out_4(out_4[2]));
  Somador_1b somador_1b_4 (
    .in_2(in_2[3]), .in_3(in_3[3]), .in_1(somador_1b_3_out_5), .out_5(somador_1b_4_out_5), .out_4(out_4[3]));
  Somador_1b somador_1b_5 (
    .in_2(in_2[4]), .in_3(in_3[4]), .in_1(somador_1b_4_out_5), .out_5(somador_1b_5_out_5), .out_4(out_4[4]));
  Somador_1b somador_1b_6 (
    .in_2(in_2[5]), .in_3(in_3[5]), .in_1(somador_1b_5_out_5), .out_5(somador_1b_6_out_5), .out_4(out_4[5]));
  Somador_1b somador_1b_7 (
    .in_2(in_2[6]), .in_3(in_3[6]), .in_1(somador_1b_6_out_5), .out_5(somador_1b_7_out_5), .out_4(out_4[6]));
  Somador_1b somador_1b_8 (.in_2(in_2[7]), .in_3(in_3[7]), .in_1(somador_1b_7_out_5), .out_5(out_5), .out_4(out_4[7]));
endmodule

module registrador_8b (
  input  in_1,
  input  in_2,
  input  in_3,
  input  in_4,
  input  in_5,
  input  in_6,
  input  in_7,
  input  in_8,
  input  in_9,
  output out_10,
  output out_11,
  output out_12,
  output out_13,
  output out_14,
  output out_15,
  output out_16,
  output out_17
);

  registrador1b registrador1b_1 (.in_1(in_1), .in_2(in_9), .out_3(out_10));
  registrador1b registrador1b_2 (.in_1(in_2), .in_2(in_9), .out_3(out_11));
  registrador1b registrador1b_3 (.in_1(in_3), .in_2(in_9), .out_3(out_12));
  registrador1b registrador1b_4 (.in_1(in_4), .in_2(in_9), .out_3(out_13));
  registrador1b registrador1b_5 (.in_1(in_5), .in_2(in_9), .out_3(out_14));
  registrador1b registrador1b_6 (.in_1(in_6), .in_2(in_9), .out_3(out_15));
  registrador1b registrador1b_7 (.in_1(in_7), .in_2(in_9), .out_3(out_16));
  registrador1b registrador1b_8 (.in_1(in_8), .in_2(in_9), .out_3(out_17));
endmodule

module registrador1b (
  input  in_1,
  input  in_2,
  output out_3
);

  wire nand_1_out, nand_2_out, nand_4_out;

  nand nand_1 (nand_1_out, in_1, in_2);
  nand nand_2 (nand_2_out, nand_1_out, in_2);
  nand nand_3 (out_3, nand_1_out, nand_4_out);
  nand nand_4 (nand_4_out, out_3, nand_2_out);
endmodule

module set_enable (
  input  in_1,
  input  in_2,
  input  [7:0] in_3,
  output [7:0] out_4
);

  wire nand_1_out, nand_2_out, nand_3_out, nand_4_out, nand_5_out, nand_6_out, nand_7_out, nand_8_out,
       nand_9_out, nand_10_out, nand_11_out, nand_12_out, nand_13_out, nand_14_out, nand_15_out, nand_16_out,
       nand_17_out, nand_18_out, nand_19_out, nand_20_out, nand_21_out, nand_22_out, nand_23_out,
       nand_24_out, nand_25_out, nand_26_out, nand_27_out, nand_28_out, nand_29_out, nand_30_out,
       nand_31_out, nand_32_out;

  nand nand_1 (nand_1_out, in_3[0], in_1);
  nand nand_2 (nand_2_out, in_3[1], in_1);
  nand nand_3 (nand_3_out, in_3[2], in_1);
  nand nand_4 (nand_4_out, in_3[3], in_1);
  nand nand_5 (nand_5_out, in_3[4], in_1);
  nand nand_6 (nand_6_out, in_3[5], in_1);
  nand nand_7 (nand_7_out, in_3[6], in_1);
  nand nand_8 (nand_8_out, in_3[7], in_1);
  nand nand_9 (nand_9_out, nand_1_out, in_1);
  nand nand_10 (nand_10_out, nand_2_out, in_1);
  nand nand_11 (nand_11_out, nand_3_out, in_1);
  nand nand_12 (nand_12_out, nand_4_out, in_1);
  nand nand_13 (nand_13_out, nand_5_out, in_1);
  nand nand_14 (nand_14_out, nand_6_out, in_1);
  nand nand_15 (nand_15_out, nand_7_out, in_1);
  nand nand_16 (nand_16_out, nand_8_out, in_1);
  nand nand_17 (nand_17_out, nand_1_out, nand_18_out);
  nand nand_18 (nand_18_out, nand_17_out, nand_9_out);
  nand nand_19 (nand_19_out, nand_2_out, nand_20_out);
  nand nand_20 (nand_20_out, nand_19_out, nand_10_out);
  nand nand_21 (nand_21_out, nand_3_out, nand_22_out);
  nand nand_22 (nand_22_out, nand_21_out, nand_11_out);
  nand nand_23 (nand_23_out, nand_4_out, nand_24_out);
  nand nand_24 (nand_24_out, nand_23_out, nand_12_out);
  nand nand_25 (nand_25_out, nand_5_out, nand_26_out);
  nand nand_26 (nand_26_out, nand_25_out, nand_13_out);
  nand nand_27 (nand_27_out, nand_6_out, nand_28_out);
  nand nand_28 (nand_28_out, nand_27_out, nand_14_out);
  nand nand_29 (nand_29_out, nand_7_out, nand_30_out);
  nand nand_30 (nand_30_out, nand_29_out, nand_15_out);
  nand nand_31 (nand_31_out, nand_8_out, nand_32_out);
  nand nand_32 (nand_32_out, nand_31_out, nand_16_out);
  and and_1 (out_4[0], nand_17_out, in_2);
  and and_2 (out_4[1], nand_19_out, in_2);
  and and_3 (out_4[2], nand_21_out, in_2);
  and and_4 (out_4[3], nand_23_out, in_2);
  and and_5 (out_4[4], nand_25_out, in_2);
  and and_6 (out_4[5], nand_27_out, in_2);
  and and_7 (out_4[6], nand_29_out, in_2);
  and and_8 (out_4[7], nand_31_out, in_2);
endmodule

module memoria_4registradores (
  input  [7:0] in_1,
  input  in_2,
  input  in_3,
  input  in_4,
  input  in_5,
  input  in_6,
  input  in_7,
  input  in_8,
  input  in_9,
  output [7:0] out_10
);

  wire [7:0] set_enable_1_out_4, set_enable_2_out_4, set_enable_3_out_4, set_enable_4_out_4;

  set_enable set_enable_1 (.in_3(in_1), .in_1(in_2), .in_2(in_6), .out_4(set_enable_1_out_4));
  set_enable set_enable_2 (.in_3(in_1), .in_1(in_3), .in_2(in_7), .out_4(set_enable_2_out_4));
  assign out_10 = set_enable_1_out_4 | set_enable_2_out_4 | set_enable_3_out_4 | set_enable_4_out_4;  // OR_Gate or_1, 8 bits wide
  set_enable set_enable_3 (.in_3(in_1), .in_1(in_4), .in_2(in_8), .out_4(set_enable_3_out_4));
  set_enable set_enable_4 (.in_3(in_1), .in_1(in_5), .in_2(in_9), .out_4(set_enable_4_out_4));
endmodule

module EnableV2 (
  input  in_1,
  input  in_2,
  input  in_3,
  input  in_4,
  input  in_5,
  input  in_6,
  input  in_7,
  input  in_8,
  input  in_9,
  output out_10,
  output out_11,
  output out_12,
  output out_13,
  output out_14,
  output out_15,
  output out_16,
  output out_17
);

  and and_1 (out_10, in_1, in_9);
  and and_2 (out_11, in_2, in_9);
  and and_3 (out_12, in_3, in_9);
  and and_4 (out_13, in_4, in_9);
  and and_5 (out_14, in_5, in_9);
  and and_6 (out_15, in_6, in_9);
  and and_7 (out_16, in_7, in_9);
  and and_8 (out_17, in_8, in_9);
endmodule

module decoder_2x4 (
  input  in_1,
  input  in_2
);

  wire not_1_out, not_2_out;

  not not_1 (not_1_out, in_2);
  not not_2 (not_2_out, in_1);
  // AND_Gate and_1 has open pins: in0=not_2_out, in1=not_1_out, out=open
  // AND_Gate and_2 has open pins: in0=not_2_out, in1=in_2, out=open
  // AND_Gate and_3 has open pins: in0=in_1, in1=not_1_out, out=open
  // AND_Gate and_4 has open pins: in0=in_1, in1=in_2, out=open
endmodule

module memoriaV1 (
  input  in_1,
  input  in_2,
  input  [7:0] in_3,
  input  [7:0] in_4,
  output [7:0] out_5
);

  wire and_1_out, and_2_out, decoder_1_out0, decoder_1_out1, decoder_1_out2, decoder_1_out3, decoder_1_out4,
       decoder_1_out5, decoder_1_out6, decoder_1_out7, decoder_1_out8, decoder_1_out9, decoder_1_out10,
       decoder_1_out11, decoder_1_out12, decoder_1_out13, decoder_1_out14, decoder_1_out15, decoder_2_out0,
       decoder_2_out1, decoder_2_out2, decoder_2_out3, decoder_2_out4, decoder_2_out5, decoder_2_out6,
       decoder_2_out7, decoder_2_out8, decoder_2_out9, decoder_2_out10, decoder_2_out11, decoder_2_out12,
       decoder_2_out13, decoder_2_out14, decoder_2_out15;

  Decoder #(.enable("false"), .select(4)) decoder_1 (
    .out0(decoder_1_out0), .out1(decoder_1_out1), .out2(decoder_1_out2), .out3(decoder_1_out3),
    .out4(decoder_1_out4), .out5(decoder_1_out5), .out6(decoder_1_out6), .out7(decoder_1_out7),
    .out8(decoder_1_out8), .out9(decoder_1_out9), .out10(decoder_1_out10), .out11(decoder_1_out11),
    .out12(decoder_1_out12), .out13(decoder_1_out13), .out14(decoder_1_out14), .out15(decoder_1_out15),
    .sel(in_3[7:4]));
  Decoder #(.enable("false"), .select(4)) decoder_2 (
    .out0(decoder_2_out0), .out1(decoder_2_out1), .out2(decoder_2_out2), .out3(decoder_2_out3),
    .out4(decoder_2_out4), .out5(decoder_2_out5), .out6(decoder_2_out6), .out7(decoder_2_out7),
    .out8(decoder_2_out8), .out9(decoder_2_out9), .out10(decoder_2_out10), .out11(decoder_2_out11),
    .out12(decoder_2_out12), .out13(decoder_2_out13), .out14(decoder_2_out14), .out15(decoder_2_out15),
    .sel(in_3[3:0]));
  and and_1 (and_1_out, decoder_1_out0, in_1);
  and and_2 (and_2_out, in_2, decoder_2_out0);
  set_enable set_enable_1 (.in_3(in_4), .in_1(and_1_out), .in_2(and_2_out), .out_4(out_5));

  // Other names for the same wires on the sheet: ao = in_2; aw = in_1
endmodule

module ShifterWRITE (
  input  in_1,
  input  [7:0] in_2,
  output [7:0] out_3,
  output out_4
);


  assign out_3 = {in_1, in_2[7:1]};
  assign out_4 = in_2[0];
endmodule

module ULA_minha (
  input  [7:0] in_1,
  input  [7:0] in_2,
  input  in_3,
  input  in_4,
  output [7:0] out_5,
  output out_6,
  output [7:0] out_7,
  output out_8
);

  ShifterWRITE shifterwrite_1 (.in_2(in_1), .in_1(in_3), .out_4(out_6), .out_3(out_5));
  Shift_left shift_left_1 (.in_2(in_1), .in_1(in_4), .out_4(out_8), .out_3(out_7));
endmodule

module Shift_left (
  input  in_1,
  input  [7:0] in_2,
  output [7:0] out_3,
  output out_4
);


  assign out_3 = {in_2[6:0], in_1};
  assign out_4 = in_2[7];
endmodule
