// Logisim project Miguel_Oliveira_Moraes_de_Souza.circ as structural Verilog: 10 circuits, main circuit main
module main (
  input  [7:0] in_1,
  input  in_2,
  input  in_3,
  input  s1,
  input  s2,
  input  s3,
  input  s4,
  input  e1,
  input  e2,
  input  e3,
  input  e4,
  input  c_in,
  input  [7:0] A_s,
  input  [7:0] B_s,
  input  cout,
  output [7:0] out_16,
  output [7:0] out_17
);

  wire [7:0] R1_out_4, R2_out_4, R3_out_4, R4_out_4, registrador_1_out_4;

  registrador registrador_1 (.in_1(in_1), .s(in_2), .e(in_3), .out_4(registrador_1_out_4));
  assign out_16 = registrador_1_out_4;  // Buffer buffer_1, 8 bits wide
  assign out_16 = R1_out_4;  // Buffer buffer_2, 8 bits wide
  registrador R1 (.in_1(out_16), .s(s1), .e(e1), .out_4(R1_out_4));
  somador8bits somador8bits_1 (.in_2(A_s), .in_3(B_s), .cin(c_in), .cout(cout), .out_4(out_17));
  assign out_16 = R2_out_4;  // Buffer buffer_3, 8 bits wide
  registrador R2 (.in_1(out_16), .s(s2), .e(e2), .out_4(R2_out_4));
  assign out_16 = R3_out_4;  // Buffer buffer_4, 8 bits wide
  registrador R3 (.in_1(out_16), .s(s3), .e(e3), .out_4(R3_out_4));
  assign out_16 = R4_out_4;  // Buffer buffer_5, 8 bits wide
  registrador R4 (.in_1(out_16), .s(s4), .e(e4), .out_4(R4_out_4));

  // Notes on the sheet:
  //                22450211
  //   Miguel Oliveira Moraes de Souza 
  //   Registradores
  //   Somador
endmodule

module somador1bti (
  input  cin,
  input  a,
  input  b,
  output c,
  output cout
);

  wire and_1_out, and_2_out, and_3_out, xor_1_out;

  xor xor_1 (xor_1_out, a, b);
  and and_1 (and_1_out, a, cin);
  and and_2 (and_2_out, a, b);
  and and_3 (and_3_out, b, cin);
  xor xor_2 (c, xor_1_out, cin);
  or or_1 (cout, and_1_out, and_2_out, and_3_out);
endmodule

module somador8bits (
  input  cin,
  input  [7:0] in_2,
  input  [7:0] in_3,
  output [7:0] out_4,
  output cout
);

  wire somador1bti_1_cout, somador1bti_2_cout, somador1bti_3_cout, somador1bti_4_cout, somador1bti_5_cout,
       somador1bti_6_cout, somador1bti_7_cout;

  somador1bti somador1bti_1 (.a(in_2[0]), .b(in_3[0]), .cin(cin), .c(out_4[0]), .cout(somador1bti_1_cout));
  somador1bti somador1bti_2 (
    .a(in_2[1]), .b(in_3[1]), .cin(somador1bti_1_cout), .c(out_4[1]), .cout(somador1bti_2_cout));
  somador1bti somador1bti_3 (
    .a(in_2[2]), .b(in_3[2]), .cin(somador1bti_2_cout), .c(out_4[2]), .cout(somador1bti_3_cout));
  somador1bti somador1bti_4 (
    .a(in_2[3]), .b(in_3[3]), .cin(somador1bti_3_cout), .c(out_4[3]), .cout(somador1bti_4_cout));
  somador1bti somador1bti_5 (
    .a(in_2[4]), .b(in_3[4]), .cin(somador1bti_4_cout), .c(out_4[4]), .cout(somador1bti_5_cout));
  somador1bti somador1bti_6 (
    .a(in_2[5]), .b(in_3[5]), .cin(somador1bti_5_cout), .c(out_4[5]), .cout(somador1bti_6_cout));
  somador1bti somador1bti_7 (
    .a(in_2[6]), .b(in_3[6]), .cin(somador1bti_6_cout), .c(out_4[6]), .cout(somador1bti_7_cout));
  somador1bti somador1bti_8 (.a(in_2[7]), .b(in_3[7]), .cin(somador1bti_7_cout), .c(out_4[7]), .cout(cout));
endmodule

module memory1bit (
  input  i,
  input  set,
  output out_3
);

  wire nand_1_out, nand_2_out, nand_4_out;

  nand nand_1 (nand_1_out, i, set);
  nand nand_2 (nand_2_out, set, nand_1_out);
  nand nand_3 (out_3, nand_1_out, nand_4_out);
  nand nand_4 (nand_4_out, out_3, nand_2_out);
endmodule

module memory8bits (
  input  i1,
  input  i2,
  input  i3,
  input  i4,
  input  i5,
  input  i6,
  input  i7,
  input  i8,
  input  set,
  output out_10,
  output out_11,
  output out_12,
  output out_13,
  output out_14,
  output out_15,
  output out_16,
  output out_17
);

  memory1bit memory1bit_1 (.i(i1), .set(set), .out_3(out_10));
  memory1bit memory1bit_2 (.i(i2), .set(set), .out_3(out_11));
  memory1bit memory1bit_3 (.i(i3), .set(set), .out_3(out_12));
  memory1bit memory1bit_4 (.i(i4), .set(set), .out_3(out_13));
  memory1bit memory1bit_5 (.i(i5), .set(set), .out_3(out_14));
  memory1bit memory1bit_6 (.i(i6), .set(set), .out_3(out_15));
  memory1bit memory1bit_7 (.i(i7), .set(set), .out_3(out_16));
  memory1bit memory1bit_8 (.i(i8), .set(set), .out_3(out_17));
endmodule

module memory1byte (
  input  in_1,
  input  in_2,
  input  in_3,
  input  in_4,
  input  in_5,
  input  in_6,
  input  in_7,
  input  in_8,
  input  set,
  output out_10,
  output out_11,
  output out_12,
  output out_13,
  output out_14,
  output out_15,
  output out_16,
  output out_17
);

  memory8bits memory8bits_1 (
    .i1(in_1), .i2(in_2), .i3(in_3), .i4(in_4), .i5(in_5), .i6(in_6), .i7(in_7), .i8(in_8), .set(set),
    .out_10(out_10), .out_11(out_11), .out_12(out_12), .out_13(out_13), .out_14(out_14), .out_15(out_15),
    .out_16(out_16), .out_17(out_17));
endmodule

module enable (
  input  i1,
  input  i2,
  input  i3,
  input  i4,
  input  i5,
  input  i6,
  input  i7,
  input  i8,
  input  e,
  output out_10,
  output out_11,
  output out_12,
  output out_13,
  output out_14,
  output out_15,
  output out_16,
  output out_17
);

  and and_1 (out_10, i1, e);
  and and_2 (out_11, i2, e);
  and and_3 (out_12, i3, e);
  and and_4 (out_13, i4, e);
  and and_5 (out_14, i5, e);
  and and_6 (out_15, i6, e);
  and and_7 (out_16, i7, e);
  and and_8 (out_17, i8, e);
endmodule

module mem1bytese (
  input  in_1,
  input  in_2,
  input  in_3,
  input  in_4,
  input  in_5,
  input  in_6,
  input  in_7,
  input  in_8,
  input  s,
  input  en,
  output out_11,
  output out_12,
  output out_13,
  output out_14,
  output out_15,
  output out_16,
  output out_17,
  output out_18
);

  wire B_out_10, B_out_11, B_out_12, B_out_13, B_out_14, B_out_15, B_out_16, B_out_17;

  memory1byte B (
    .in_1(in_1), .in_2(in_2), .in_3(in_3), .in_4(in_4), .in_5(in_5), .in_6(in_6), .in_7(in_7), .in_8(in_8),
    .set(s), .out_10(B_out_10), .out_11(B_out_11), .out_12(B_out_12), .out_13(B_out_13), .out_14(B_out_14),
    .out_15(B_out_15), .out_16(B_out_16), .out_17(B_out_17));
  enable E (
    .i1(B_out_10), .i2(B_out_11), .i3(B_out_12), .i4(B_out_13), .i5(B_out_14), .i6(B_out_15), .i7(B_out_16),
    .i8(B_out_17), .e(en), .out_10(out_11), .out_11(out_12), .out_12(out_13), .out_13(out_14),
    .out_14(out_15), .out_15(out_16), .out_16(out_17), .out_17(out_18));
endmodule

module registrador (
  input  [7:0] in_1,
  input  s,
  input  e,
  output [7:0] out_4
);

  mem1bytese r (
    .in_1(in_1[0]), .in_2(in_1[1]), .in_3(in_1[2]), .in_4(in_1[3]), .in_5(in_1[4]), .in_6(in_1[5]),
    .in_7(in_1[6]), .in_8(in_1[7]), .s(s), .en(e), .out_11(out_4[0]), .out_12(out_4[1]), .out_13(out_4[2]),
    .out_14(out_4[3]), .out_15(out_4[4]), .out_16(out_4[5]), .out_17(out_4[6]), .out_18(out_4[7]));
endmodule

module registrador8bits (
  input  [7:0] in_1
);

  // registrador registrador_1: pin names not known; wires that end beside it: in_1[0]
  // registrador registrador_2: pin names not known; wires that end beside it: in_1[1]
  // registrador registrador_3: pin names not known; wires that end beside it: in_1[2]
  // registrador registrador_4: pin names not known; wires that end beside it: in_1[3]
  // registrador registrador_5: pin names not known; wires that end beside it: in_1[4]
  // registrador registrador_6: pin names not known; wires that end beside it: in_1[5]
  // registrador registrador_7: pin names not known; wires that end beside it: in_1[6]
  // registrador registrador_8: pin names not known; wires that end beside it: in_1[7]
endmodule
