// Logisim project Mikaelle_Costa_de_Santana.circ as structural Verilog: 7 circuits, main circuit main
module main (
  input  [7:0] in_1,
  input  in_2,
  input  in_3,
  input  in_4,
  input  in_5,
  input  in_6,
  input  in_7,
  input  in_8,
  input  in_9,
  input  in_10,
  output [7:0] out_11
);

  assign out_11 = in_2 ? in_1 : 8'bz;  // Controlled_Buffer controlled_buffer_1
  registrador_set_enable registrador_set_enable_1 (.in_1(out_11), .in_2(in_3), .in_3(in_4), .out_4(out_11));
  registrador_set_enable registrador_set_enable_2 (.in_1(out_11), .in_2(in_5), .in_3(in_6), .out_4(out_11));
  registrador_set_enable registrador_set_enable_3 (.in_1(out_11), .in_2(in_7), .in_3(in_8), .out_4(out_11));
  registrador_set_enable registrador_set_enable_4 (.in_1(out_11), .in_2(in_9), .in_3(in_10), .out_4(out_11));

  // Notes on the sheet:
  //   Mikaelle Costa de Santana - 22401909
endmodule

module somador1bit (
  input  in_1,
  input  a,
  input  b,
  output out_4,
  output out_5
);

  wire and_1_out, and_2_out, and_3_out, xor_1_out;

  xor xor_1 (xor_1_out, a, b);
  and and_1 (and_1_out, a, in_1);
  and and_2 (and_2_out, a, b);
  and and_3 (and_3_out, b, in_1);
  xor xor_2 (out_4, xor_1_out, in_1);
  or or_1 (out_5, and_1_out, and_2_out, and_3_out);
endmodule

module somador8bit (
  input  in_1,
  input  [7:0] in_2,
  input  [7:0] in_3,
  output [7:0] out_4,
  output out_5
);

  wire somador1bit_1_out_5, somador1bit_2_out_5, somador1bit_3_out_5, somador1bit_4_out_5,
       somador1bit_5_out_5, somador1bit_6_out_5, somador1bit_7_out_5;

  somador1bit somador1bit_1 (.a(in_2[0]), .b(in_3[0]), .in_1(in_1), .out_4(out_4[0]), .out_5(somador1bit_1_out_5));
  somador1bit somador1bit_2 (
    .a(in_2[1]), .b(in_3[1]), .in_1(somador1bit_1_out_5), .out_4(out_4[1]), .out_5(somador1bit_2_out_5));
  somador1bit somador1bit_3 (
    .a(in_2[2]), .b(in_3[2]), .in_1(somador1bit_2_out_5), .out_4(out_4[2]), .out_5(somador1bit_3_out_5));
  somador1bit somador1bit_4 (
    .a(in_2[3]), .b(in_3[3]), .in_1(somador1bit_3_out_5), .out_4(out_4[3]), .out_5(somador1bit_4_out_5));
  somador1bit somador1bit_5 (
    .a(in_2[4]), .b(in_3[4]), .in_1(somador1bit_4_out_5), .out_4(out_4[4]), .out_5(somador1bit_5_out_5));
  somador1bit somador1bit_6 (
    .a(in_2[5]), .b(in_3[5]), .in_1(somador1bit_5_out_5), .out_4(out_4[5]), .out_5(somador1bit_6_out_5));
  somador1bit somador1bit_7 (
    .a(in_2[6]), .b(in_3[6]), .in_1(somador1bit_6_out_5), .out_4(out_4[6]), .out_5(somador1bit_7_out_5));
  somador1bit somador1bit_8 (.a(in_2[7]), .b(in_3[7]), .in_1(somador1bit_7_out_5), .out_4(out_4[7]), .out_5(out_5));
endmodule

module memory1bit (
  input  in_1,
  input  in_2,
  output out_3
);

  wire nand_1_out, nand_2_out, nand_3_out;

  nand nand_1 (nand_1_out, in_1, in_2);
  nand nand_2 (nand_2_out, nand_1_out, in_2);
  nand nand_3 (nand_3_out, out_3, nand_2_out);
  nand nand_4 (out_3, nand_1_out, nand_3_out);
endmodule

module memory8bit (
  input  [7:0] in_1,
  input  in_2,
  output [7:0] out_3
);

  memory1bit memory1bit_1 (.in_1(in_1[0]), .in_2(in_2), .out_3(out_3[0]));
  memory1bit memory1bit_2 (.in_1(in_1[1]), .in_2(in_2), .out_3(out_3[1]));
  memory1bit memory1bit_3 (.in_1(in_1[2]), .in_2(in_2), .out_3(out_3[2]));
  memory1bit memory1bit_4 (.in_1(in_1[3]), .in_2(in_2), .out_3(out_3[3]));
  memory1bit memory1bit_5 (.in_1(in_1[4]), .in_2(in_2), .out_3(out_3[4]));
  memory1bit memory1bit_6 (.in_1(in_1[5]), .in_2(in_2), .out_3(out_3[5]));
  memory1bit memory1bit_7 (.in_1(in_1[6]), .in_2(in_2), .out_3(out_3[6]));
  memory1bit memory1bit_8 (.in_1(in_1[7]), .in_2(in_2), .out_3(out_3[7]));
endmodule

module enable (
  input  [7:0] in_1,
  input  in_2,
  output [7:0] out_3
);

  assign out_3 = in_2 ? in_1 : 8'bz;  // Controlled_Buffer controlled_buffer_1
endmodule

module registrador_set_enable (
  input  [7:0] in_1,
  input  in_2,
  input  in_3,
  output [7:0] out_4
);

  wire [7:0] memory8bit_1_out_3;

  memory8bit memory8bit_1 (.in_1(in_1), .in_2(in_2), .out_3(memory8bit_1_out_3));
  enable enable_1 (.in_1(memory8bit_1_out_3), .in_2(in_3), .out_3(out_4));
endmodule
