// Logisim project Paulo_Victor_Fernandes_de_Melo.circ as structural Verilog: 8 circuits, main circuit main
module main (
  input  [7:0] i,
  input  ie,
  input  r1s,
  input  r1e,
  input  r2s,
  input  r2e,
  input  r3s,
  input  r3e,
  input  r4s,
  input  r4e,
  output [7:0] o
);

  assign o = ie ? i : 8'bz;  // Controlled_Buffer controlled_buffer_1
  reg_8b reg_8b_1 (.i(o), .s(r1s), .e(r1e), .o(o));
  reg_8b reg_8b_2 (.i(o), .s(r2s), .e(r2e), .o(o));
  reg_8b reg_8b_3 (.i(o), .s(r3s), .e(r3e), .o(o));
  reg_8b reg_8b_4 (.i(o), .s(r4s), .e(r4e), .o(o));

  // Notes on the sheet:
  //   Matricula: 22400653
  //   Paulo Victor Fernandes de Melo
endmodule

module half_adder_1b (
  input  a,
  input  b,
  output o,
  output cout
);

  and and_1 (cout, a, b);
  xor xor_1 (o, a, b);
endmodule

module full_adder_1b (
  input  cin,
  input  a,
  input  b,
  output o,
  output co
);

  wire half_adder_1b_1_cout, half_adder_1b_2_cout, half_adder_1b_2_o;

  half_adder_1b half_adder_1b_1 (.a(cin), .b(half_adder_1b_2_o), .cout(half_adder_1b_1_cout), .o(o));
  half_adder_1b half_adder_1b_2 (.a(a), .b(b), .cout(half_adder_1b_2_cout), .o(half_adder_1b_2_o));
  or or_1 (co, half_adder_1b_1_cout, half_adder_1b_2_cout);
endmodule

module full_adder_8b (
  input  cin,
  input  [7:0] a,
  input  [7:0] b,
  output [7:0] o,
  output cout
);

  wire full_adder_1b_1_co, full_adder_1b_2_co, full_adder_1b_3_co, full_adder_1b_4_co, full_adder_1b_5_co,
       full_adder_1b_6_co, full_adder_1b_7_co;

  full_adder_1b full_adder_1b_1 (.a(a[0]), .b(b[0]), .cin(cin), .co(full_adder_1b_1_co), .o(o[0]));
  full_adder_1b full_adder_1b_2 (.a(a[1]), .b(b[1]), .cin(full_adder_1b_1_co), .co(full_adder_1b_2_co), .o(o[1]));
  full_adder_1b full_adder_1b_3 (.a(a[2]), .b(b[2]), .cin(full_adder_1b_2_co), .co(full_adder_1b_3_co), .o(o[2]));
  full_adder_1b full_adder_1b_4 (.a(a[3]), .b(b[3]), .cin(full_adder_1b_3_co), .co(full_adder_1b_4_co), .o(o[3]));
  full_adder_1b full_adder_1b_5 (.a(a[4]), .b(b[4]), .cin(full_adder_1b_4_co), .co(full_adder_1b_5_co), .o(o[4]));
  full_adder_1b full_adder_1b_6 (.a(a[5]), .b(b[5]), .cin(full_adder_1b_5_co), .co(full_adder_1b_6_co), .o(o[5]));
  full_adder_1b full_adder_1b_7 (.a(a[6]), .b(b[6]), .cin(full_adder_1b_6_co), .co(full_adder_1b_7_co), .o(o[6]));
  full_adder_1b full_adder_1b_8 (.a(a[7]), .b(b[7]), .cin(full_adder_1b_7_co), .co(cout), .o(o[7]));
endmodule

module mem_1b (
  input  i,
  input  s,
  output o
);

  wire nand_1_out, nand_2_out, nand_4_out;

  nand nand_1 (nand_1_out, i, s);
  nand nand_2 (nand_2_out, nand_1_out, s);
  nand nand_3 (o, nand_1_out, nand_4_out);
  nand nand_4 (nand_4_out, o, nand_2_out);
endmodule

module mem_8b (
  input  [7:0] i,
  input  s,
  output [7:0] o
);

  mem_1b mem_1b_1 (.i(i[0]), .s(s), .o(o[0]));
  mem_1b mem_1b_2 (.i(i[1]), .s(s), .o(o[1]));
  mem_1b mem_1b_3 (.i(i[2]), .s(s), .o(o[2]));
  mem_1b mem_1b_4 (.i(i[3]), .s(s), .o(o[3]));
  mem_1b mem_1b_5 (.i(i[4]), .s(s), .o(o[4]));
  mem_1b mem_1b_6 (.i(i[5]), .s(s), .o(o[5]));
  mem_1b mem_1b_7 (.i(i[6]), .s(s), .o(o[6]));
  mem_1b mem_1b_8 (.i(i[7]), .s(s), .o(o[7]));
endmodule

module reg_1b (
  input  i,
  input  s,
  input  e,
  output o
);

  wire mem_1b_1_o;

  mem_1b mem_1b_1 (.i(i), .s(s), .o(mem_1b_1_o));
  assign o = e ? mem_1b_1_o : 1'bz;  // Controlled_Buffer controlled_buffer_1
endmodule

module reg_8b (
  input  [7:0] i,
  input  s,
  input  e,
  output [7:0] o
);

  reg_1b reg_1b_1 (.i(i[0]), .s(s), .e(e), .o(o[0]));
  reg_1b reg_1b_2 (.i(i[1]), .s(s), .e(e), .o(o[1]));
  reg_1b reg_1b_3 (.i(i[2]), .s(s), .e(e), .o(o[2]));
  reg_1b reg_1b_4 (.i(i[3]), .s(s), .e(e), .o(o[3]));
  reg_1b reg_1b_5 (.i(i[4]), .s(s), .e(e), .o(o[4]));
  reg_1b reg_1b_6 (.i(i[5]), .s(s), .e(e), .o(o[5]));
  reg_1b reg_1b_7 (.i(i[6]), .s(s), .e(e), .o(o[6]));
  reg_1b reg_1b_8 (.i(i[7]), .s(s), .e(e), .o(o[7]));
endmodule
