// Logisim project Pedro Gabriel Motta Vieira.circ as structural Verilog: 8 circuits, main circuit main
module main (
  input  [7:0] in_1,
  input  sMAR,
  input  s1,
  input  s2,
  input  eMAR,
  input  e2,
  input  e1,
  input  s4,
  input  s3,
  input  e4,
  input  e3,
  output [7:0] out_12
);

  wire [7:0] MAR_out_4, R1_out_4, R2_out_4, R3_out_4, R4_out_4;

  registrador_set_enable MAR (.in_1(in_1), .in_2(sMAR), .in_3(eMAR), .out_4(MAR_out_4));
  assign out_12 = MAR_out_4;  // Buffer buffer_1, 8 bits wide
  registrador_set_enable R1 (.in_1(out_12), .in_2(s1), .in_3(e1), .out_4(R1_out_4));
  assign out_12 = R1_out_4;  // Buffer buffer_2, 8 bits wide
  assign out_12 = R2_out_4;  // Buffer buffer_3, 8 bits wide
  registrador_set_enable R2 (.in_1(out_12), .in_2(s2), .in_3(e2), .out_4(R2_out_4));
  assign out_12 = R3_out_4;  // Buffer buffer_4, 8 bits wide
  assign out_12 = R4_out_4;  // Buffer buffer_5, 8 bits wide
  registrador_set_enable R3 (.in_1(out_12), .in_2(s3), .in_3(e3), .out_4(R3_out_4));
  registrador_set_enable R4 (.in_1(out_12), .in_2(s4), .in_3(e4), .out_4(R4_out_4));

  // Notes on the sheet:
  //   Pedro Gabriel Motta Vieira
  //   Matrícula: 22450085
endmodule

module somador_completo (
  input  C_In,
  input  A,
  input  B,
  output R,
  output C_Out
);

  wire and_1_out, and_2_out, and_3_out, xor_1_out;

  xor xor_1 (xor_1_out, A, B);
  and and_1 (and_1_out, A, B);
  and and_2 (and_2_out, A, C_In);
  and and_3 (and_3_out, B, C_In);
  xor xor_2 (R, C_In, xor_1_out);
  or or_1 (C_Out, and_1_out, and_2_out, and_3_out);
endmodule

module somador_de_8bits (
  input  C_In,
  input  [7:0] A,
  input  [7:0] B,
  output [7:0] R,
  output C_Out
);

  wire somador_completo_1_c_out, somador_completo_2_c_out, somador_completo_3_c_out,
       somador_completo_4_c_out, somador_completo_5_c_out, somador_completo_6_c_out, somador_completo_7_c_out;

  somador_completo somador_completo_1 (.A(A[0]), .B(B[0]), .C_In(C_In), .C_Out(somador_completo_1_c_out), .R(R[0]));
  somador_completo somador_completo_2 (
    .A(A[1]), .B(B[1]), .C_In(somador_completo_1_c_out), .C_Out(somador_completo_2_c_out), .R(R[1]));
  somador_completo somador_completo_3 (
    .A(A[2]), .B(B[2]), .C_In(somador_completo_2_c_out), .C_Out(somador_completo_3_c_out), .R(R[2]));
  somador_completo somador_completo_4 (
    .A(A[3]), .B(B[3]), .C_In(somador_completo_3_c_out), .C_Out(somador_completo_4_c_out), .R(R[3]));
  somador_completo somador_completo_5 (
    .A(A[4]), .B(B[4]), .C_In(somador_completo_4_c_out), .C_Out(somador_completo_5_c_out), .R(R[4]));
  somador_completo somador_completo_6 (
    .A(A[5]), .B(B[5]), .C_In(somador_completo_5_c_out), .C_Out(somador_completo_6_c_out), .R(R[5]));
  somador_completo somador_completo_7 (
    .A(A[6]), .B(B[6]), .C_In(somador_completo_6_c_out), .C_Out(somador_completo_7_c_out), .R(R[6]));
  somador_completo somador_completo_8 (.A(A[7]), .B(B[7]), .C_In(somador_completo_7_c_out), .C_Out(C_Out), .R(R[7]));
endmodule

module registrador_1bit (
  input  in_1,
  input  in_2,
  output out_3
);

  wire nand_1_out, nand_2_out, nand_4_out;

  nand nand_1 (nand_1_out, in_1, in_2);
  nand nand_2 (nand_2_out, nand_1_out, in_2);
  nand nand_3 (out_3, nand_1_out, nand_4_out);
  nand nand_4 (nand_4_out, out_3, nand_2_out);
endmodule

module registrador_2bits (
  input  in_1,
  input  in_2,
  input  in_3,
  output [1:0] out_4
);

  registrador_1bit registrador_1bit_1 (.in_1(in_1), .in_2(in_3), .out_3(out_4[0]));
  registrador_1bit registrador_1bit_2 (.in_1(in_2), .in_2(in_3), .out_3(out_4[1]));
endmodule

module registrador_8bits (
  input  [7:0] in_1,
  input  in_2,
  output [7:0] out_3
);

  registrador_1bit registrador_1bit_1 (.in_1(in_1[0]), .in_2(in_2), .out_3(out_3[0]));
  registrador_1bit registrador_1bit_2 (.in_1(in_1[1]), .in_2(in_2), .out_3(out_3[1]));
  registrador_1bit registrador_1bit_3 (.in_1(in_1[2]), .in_2(in_2), .out_3(out_3[2]));
  registrador_1bit registrador_1bit_4 (.in_1(in_1[3]), .in_2(in_2), .out_3(out_3[3]));
  registrador_1bit registrador_1bit_5 (.in_1(in_1[4]), .in_2(in_2), .out_3(out_3[4]));
  registrador_1bit registrador_1bit_6 (.in_1(in_1[5]), .in_2(in_2), .out_3(out_3[5]));
  registrador_1bit registrador_1bit_7 (.in_1(in_1[6]), .in_2(in_2), .out_3(out_3[6]));
  registrador_1bit registrador_1bit_8 (.in_1(in_1[7]), .in_2(in_2), .out_3(out_3[7]));
endmodule

module enable (
  input  in_1,
  input  in_2,
  input  in_3,
  input  in_4,
  input  in_5,
  input  in_6,
  input  in_7,
  input  in_8,
  input  in_9,
  output out_10,
  output out_11,
  output out_12,
  output out_13,
  output out_14,
  output out_15,
  output out_16,
  output out_17
);

  assign out_10 = in_9 ? in_1 : 1'bz;  // Controlled_Buffer controlled_buffer_1
  assign out_11 = in_9 ? in_2 : 1'bz;  // Controlled_Buffer controlled_buffer_2
  assign out_14 = in_9 ? in_5 : 1'bz;  // Controlled_Buffer controlled_buffer_3
  assign out_15 = in_9 ? in_6 : 1'bz;  // Controlled_Buffer controlled_buffer_4
  assign out_16 = in_9 ? in_7 : 1'bz;  // Controlled_Buffer controlled_buffer_5
  assign out_17 = in_9 ? in_8 : 1'bz;  // Controlled_Buffer controlled_buffer_6
  assign out_12 = in_9 ? in_3 : 1'bz;  // Controlled_Buffer controlled_buffer_7
  assign out_13 = in_9 ? in_4 : 1'bz;  // Controlled_Buffer controlled_buffer_8
endmodule

module registrador_set_enable (
  input  [7:0] in_1,
  input  in_2,
  input  in_3,
  output [7:0] out_4
);

  wire [7:0] registrador_8bits_1_out_3;

  registrador_8bits registrador_8bits_1 (.in_1(in_1), .in_2(in_2), .out_3(registrador_8bits_1_out_3));
  enable enable_1 (
    .in_1(registrador_8bits_1_out_3[0]), .in_2(registrador_8bits_1_out_3[1]),
    .in_3(registrador_8bits_1_out_3[2]), .in_4(registrador_8bits_1_out_3[3]),
    .in_5(registrador_8bits_1_out_3[4]), .in_6(registrador_8bits_1_out_3[5]),
    .in_7(registrador_8bits_1_out_3[6]), .in_8(registrador_8bits_1_out_3[7]), .in_9(in_3), .out_10(out_4[0]),
    .out_11(out_4[1]), .out_12(out_4[2]), .out_13(out_4[3]), .out_14(out_4[4]), .out_15(out_4[5]),
    .out_16(out_4[6]), .out_17(out_4[7]));
endmodule
