// Logisim project Rebecca_Aimée_Lima_de_Lima.circ as structural Verilog: 9 circuits, main circuit main
module main (
  input  [7:0] in_1,
  input  s,
  input  in_3,
  input  in_4,
  input  in_5,
  input  e,
  input  in_7,
  input  in_8,
  input  in_9
);

  registrador registrador_1 (
    .in_1(in_1[0]), .in_2(in_1[1]), .in_3(in_1[2]), .in_4(in_1[3]), .in_5(in_1[4]), .in_6(in_1[5]),
    .in_7(in_1[6]), .in_8(in_1[7]), .s(s), .e(e), .out_11(in_1[0]), .out_12(in_1[1]), .out_13(in_1[2]),
    .out_14(in_1[3]), .out_15(in_1[4]), .out_16(in_1[5]), .out_17(in_1[6]), .out_18(in_1[7]));
  registrador registrador_2 (
    .in_1(in_1[0]), .in_2(in_1[1]), .in_3(in_1[2]), .in_4(in_1[3]), .in_5(in_1[4]), .in_6(in_1[5]),
    .in_7(in_1[6]), .in_8(in_1[7]), .s(in_3), .e(in_7), .out_11(in_1[0]), .out_12(in_1[1]), .out_13(in_1[2]),
    .out_14(in_1[3]), .out_15(in_1[4]), .out_16(in_1[5]), .out_17(in_1[6]), .out_18(in_1[7]));
  registrador registrador_3 (
    .in_1(in_1[0]), .in_2(in_1[1]), .in_3(in_1[2]), .in_4(in_1[3]), .in_5(in_1[4]), .in_6(in_1[5]),
    .in_7(in_1[6]), .in_8(in_1[7]), .s(in_4), .e(in_8), .out_11(in_1[0]), .out_12(in_1[1]), .out_13(in_1[2]),
    .out_14(in_1[3]), .out_15(in_1[4]), .out_16(in_1[5]), .out_17(in_1[6]), .out_18(in_1[7]));
  registrador registrador_4 (
    .in_1(in_1[0]), .in_2(in_1[1]), .in_3(in_1[2]), .in_4(in_1[3]), .in_5(in_1[4]), .in_6(in_1[5]),
    .in_7(in_1[6]), .in_8(in_1[7]), .s(in_5), .e(in_9), .out_11(in_1[0]), .out_12(in_1[1]), .out_13(in_1[2]),
    .out_14(in_1[3]), .out_15(in_1[4]), .out_16(in_1[5]), .out_17(in_1[6]), .out_18(in_1[7]));

  // Notes on the sheet:
  //   Nome: Rebecca Aimee Lima de Lima
  //   Matricula: 22450596
endmodule

module memoria (
  input  in_1,
  input  in_2,
  output out_3
);

  wire and_1_out, and_2_out, and_4_out;

  and and_1 (and_1_out, in_1, in_2);
  and and_2 (and_2_out, and_1_out, in_2);
  and and_3 (out_3, and_1_out, and_4_out);
  and and_4 (and_4_out, out_3, and_2_out);
endmodule

module memoria_8bits (
  input  in_1,
  input  in_2,
  input  in_3,
  input  in_4,
  input  in_5,
  input  in_6,
  input  in_7,
  input  in_8,
  input  in_9,
  output out_10,
  output out_11,
  output out_12,
  output out_13,
  output out_14,
  output out_15,
  output out_16,
  output out_17
);

  memoria memoria_1 (.in_1(in_1), .in_2(in_9), .out_3(out_10));
  memoria memoria_2 (.in_1(in_2), .in_2(in_9), .out_3(out_11));
  memoria memoria_3 (.in_1(in_3), .in_2(in_9), .out_3(out_12));
  memoria memoria_4 (.in_1(in_4), .in_2(in_9), .out_3(out_13));
  memoria memoria_5 (.in_1(in_5), .in_2(in_9), .out_3(out_14));
  memoria memoria_6 (.in_1(in_6), .in_2(in_9), .out_3(out_15));
  memoria memoria_7 (.in_1(in_7), .in_2(in_9), .out_3(out_16));
  memoria memoria_8 (.in_1(in_8), .in_2(in_9), .out_3(out_17));
endmodule

module set (
  input  in_1,
  input  in_2,
  input  in_3,
  input  in_4,
  input  in_5,
  input  in_6,
  input  in_7,
  input  in_8,
  input  s,
  output out_10,
  output out_11,
  output out_12,
  output out_13,
  output out_14,
  output out_15,
  output out_16,
  output out_17
);

  memoria_8bits memoria_8bits_1 (
    .in_1(in_1), .in_2(in_2), .in_3(in_3), .in_4(in_4), .in_5(in_5), .in_6(in_6), .in_7(in_7), .in_8(in_8),
    .in_9(s), .out_10(out_10), .out_11(out_11), .out_12(out_12), .out_13(out_13), .out_14(out_14),
    .out_15(out_15), .out_16(out_16), .out_17(out_17));
endmodule

module enable (
  input  in_1,
  input  in_2,
  input  in_3,
  input  in_4,
  input  in_5,
  input  in_6,
  input  in_7,
  input  in_8,
  input  e,
  output out_10,
  output out_11,
  output out_12,
  output out_13,
  output out_14,
  output out_15,
  output out_16,
  output out_17
);

  assign out_10 = e ? in_1 : 1'bz;  // Controlled_Buffer controlled_buffer_1
  assign out_11 = e ? in_2 : 1'bz;  // Controlled_Buffer controlled_buffer_2
  assign out_12 = e ? in_3 : 1'bz;  // Controlled_Buffer controlled_buffer_3
  assign out_13 = e ? in_4 : 1'bz;  // Controlled_Buffer controlled_buffer_4
  assign out_14 = e ? in_5 : 1'bz;  // Controlled_Buffer controlled_buffer_5
  assign out_15 = e ? in_6 : 1'bz;  // Controlled_Buffer controlled_buffer_6
  assign out_16 = e ? in_7 : 1'bz;  // Controlled_Buffer controlled_buffer_7
  assign out_17 = e ? in_8 : 1'bz;  // Controlled_Buffer controlled_buffer_8
endmodule

module registrador (
  input  in_1,
  input  in_2,
  input  in_3,
  input  in_4,
  input  in_5,
  input  in_6,
  input  in_7,
  input  in_8,
  input  s,
  input  e,
  output out_11,
  output out_12,
  output out_13,
  output out_14,
  output out_15,
  output out_16,
  output out_17,
  output out_18
);

  wire set_1_out_10, set_1_out_11, set_1_out_12, set_1_out_13, set_1_out_14, set_1_out_15, set_1_out_16,
       set_1_out_17;

  set set_1 (
    .in_1(in_1), .in_2(in_2), .in_3(in_3), .in_4(in_4), .in_5(in_5), .in_6(in_6), .in_7(in_7), .in_8(in_8),
    .s(s), .out_10(set_1_out_10), .out_11(set_1_out_11), .out_12(set_1_out_12), .out_13(set_1_out_13),
    .out_14(set_1_out_14), .out_15(set_1_out_15), .out_16(set_1_out_16), .out_17(set_1_out_17));
  enable enable_1 (
    .in_1(set_1_out_10), .in_2(set_1_out_11), .in_3(set_1_out_12), .in_4(set_1_out_13), .in_5(set_1_out_14),
    .in_6(set_1_out_15), .in_7(set_1_out_16), .in_8(set_1_out_17), .e(e), .out_10(out_11), .out_11(out_12),
    .out_12(out_13), .out_13(out_14), .out_14(out_15), .out_15(out_16), .out_16(out_17), .out_17(out_18));
endmodule

module somador_1bit (
  input  in_1,
  input  in_2,
  output o,
  output carry
);

  xor xor_1 (o, in_1, in_2);
  and and_1 (carry, in_1, in_2);
endmodule

module somadorcompleto_3bits (
  input  in_1,
  input  in_2,
  input  in_3,
  output o,
  output carry
);

  wire and_1_out, and_2_out, and_3_out, xor_1_out;

  xor xor_1 (xor_1_out, in_1, in_2);
  and and_1 (and_1_out, in_1, in_2);
  and and_2 (and_2_out, in_3, in_2);
  and and_3 (and_3_out, in_1, in_3);
  xor xor_2 (o, xor_1_out, in_3);
  or or_1 (carry, and_1_out, and_2_out, and_3_out);
endmodule

module somadorcompleto_1byte (
  input  in,
  input  in_2,
  input  in_3,
  input  in_4,
  input  in_5,
  input  in_6,
  input  in_7,
  input  in_8,
  input  in_9,
  input  in_10,
  input  in_11,
  input  in_12,
  input  in_13,
  input  in_14,
  input  in_15,
  input  in_16,
  input  in_17,
  output out_18,
  output out_19,
  output out_20,
  output out_21,
  output out_22,
  output out_23,
  output out_24,
  output out_25,
  output out_26
);

  wire somadorcompleto_3bits_1_carry, somadorcompleto_3bits_2_carry, somadorcompleto_3bits_3_carry,
       somadorcompleto_3bits_4_carry, somadorcompleto_3bits_5_carry, somadorcompleto_3bits_6_carry,
       somadorcompleto_3bits_7_carry;

  somadorcompleto_3bits somadorcompleto_3bits_1 (
    .in_1(in_2), .in_2(in_10), .in_3(in), .carry(somadorcompleto_3bits_1_carry), .o(out_18));
  somadorcompleto_3bits somadorcompleto_3bits_2 (
    .in_1(in_3), .in_2(in_11), .in_3(somadorcompleto_3bits_1_carry), .carry(somadorcompleto_3bits_2_carry),
    .o(out_19));
  somadorcompleto_3bits somadorcompleto_3bits_3 (
    .in_1(in_4), .in_2(in_12), .in_3(somadorcompleto_3bits_2_carry), .carry(somadorcompleto_3bits_3_carry),
    .o(out_20));
  somadorcompleto_3bits somadorcompleto_3bits_4 (
    .in_1(in_5), .in_2(in_13), .in_3(somadorcompleto_3bits_3_carry), .carry(somadorcompleto_3bits_4_carry),
    .o(out_21));
  somadorcompleto_3bits somadorcompleto_3bits_5 (
    .in_1(in_6), .in_2(in_14), .in_3(somadorcompleto_3bits_4_carry), .carry(somadorcompleto_3bits_5_carry),
    .o(out_22));
  somadorcompleto_3bits somadorcompleto_3bits_6 (
    .in_1(in_7), .in_2(in_15), .in_3(somadorcompleto_3bits_5_carry), .carry(somadorcompleto_3bits_6_carry),
    .o(out_23));
  somadorcompleto_3bits somadorcompleto_3bits_7 (
    .in_1(in_8), .in_2(in_16), .in_3(somadorcompleto_3bits_6_carry), .carry(somadorcompleto_3bits_7_carry),
    .o(out_24));
  somadorcompleto_3bits somadorcompleto_3bits_8 (
    .in_1(in_9), .in_2(in_17), .in_3(somadorcompleto_3bits_7_carry), .carry(out_26), .o(out_25));

  // Notes on the sheet:
  //   carry
  //   out
endmodule
