// Logisim project Ricardo_Oliveira_Pinho_Lima_somador_e_registrador.circ as structural Verilog: 9 circuits, main circuit main
module main (
  input  c_in,
  input  [7:0] A,
  input  [7:0] B,
  output [7:0] C,
  output c_out
);

  wire [7:0] undriven;

  Registrador_8bits registrador_8bits_1 (.in_2(undriven), .in_1(undriven));  // open: S, E
  Registrador_8bits registrador_8bits_2 (.in_2(undriven), .in_1(undriven));  // open: S, E
  Registrador_8bits registrador_8bits_3 (.in_2(undriven), .in_1(undriven));  // open: S, E
  somador_8bits somador_8bits_1 (.A(A), .B(B), .I(c_in), .c_out(c_out), .c(C));
  Registrador_8bits registrador_8bits_4 (.in_2(undriven), .in_1(undriven));  // open: S, E

  // Notes on the sheet:
  //   22251127
  //   Ricardo Oliveira Pinho de Lima
endmodule

module meio_somador (
  input  in_1,
  input  in_2,
  output out_3,
  output out_4
);

  xor xor_1 (out_3, in_1, in_2);
  and and_1 (out_4, in_1, in_2);

  // Notes on the sheet:
  //   R
endmodule

module somador_sem_c_out (
  input  entrada,
  input  A,
  input  B,
  output out_4
);

  wire xor_1_out;

  xor xor_1 (xor_1_out, A, B);
  xor xor_2 (out_4, xor_1_out, entrada);
endmodule

module somador_1bit (
  input  c_in,
  input  a,
  input  b,
  output c,
  output c_out
);

  wire and_1_out, and_2_out, and_3_out;

  somador_sem_c_out somador_sem_c_out_1 (.entrada(c_in), .A(a), .B(b), .out_4(c));
  and and_1 (and_1_out, c_in, b);
  and and_2 (and_2_out, a, b);
  and and_3 (and_3_out, a, c_in);
  or or_1 (c_out, and_1_out, and_2_out, and_3_out);
endmodule

module somador_8bits (
  input  I,
  input  [7:0] A,
  input  [7:0] B,
  output [7:0] c,
  output c_out
);

  wire somador_1bit_1_c_out, somador_1bit_2_c_out, somador_1bit_3_c_out, somador_1bit_4_c_out,
       somador_1bit_5_c_out, somador_1bit_6_c_out, somador_1bit_8_c_out;

  somador_1bit somador_1bit_1 (.a(A[0]), .b(B[0]), .c_in(I), .c_out(somador_1bit_1_c_out), .c(c[0]));
  somador_1bit somador_1bit_2 (.a(A[1]), .b(B[1]), .c_in(somador_1bit_1_c_out), .c_out(somador_1bit_2_c_out), .c(c[1]));
  somador_1bit somador_1bit_3 (.a(A[2]), .b(B[2]), .c_in(somador_1bit_2_c_out), .c_out(somador_1bit_3_c_out), .c(c[2]));
  somador_1bit somador_1bit_4 (.a(A[3]), .b(B[3]), .c_in(somador_1bit_3_c_out), .c_out(somador_1bit_4_c_out), .c(c[3]));
  somador_1bit somador_1bit_5 (.a(A[5]), .b(B[5]), .c_in(somador_1bit_8_c_out), .c_out(somador_1bit_5_c_out), .c(c[5]));
  somador_1bit somador_1bit_6 (.a(A[6]), .b(B[6]), .c_in(somador_1bit_5_c_out), .c_out(somador_1bit_6_c_out), .c(c[6]));
  somador_1bit somador_1bit_7 (.a(A[7]), .b(B[7]), .c_in(somador_1bit_6_c_out), .c_out(c_out), .c(c[7]));
  somador_1bit somador_1bit_8 (.a(A[4]), .b(B[4]), .c_in(somador_1bit_4_c_out), .c_out(somador_1bit_8_c_out), .c(c[4]));
endmodule

module memoria_1bit (
  input  in_1,
  input  in_2,
  output out_3
);

  wire nand_1_out, nand_2_out, nand_4_out;

  nand nand_1 (nand_1_out, in_1, in_2);
  nand nand_2 (nand_2_out, nand_1_out, in_2);
  nand nand_3 (out_3, nand_1_out, nand_4_out);
  nand nand_4 (nand_4_out, out_3, nand_2_out);
endmodule

module enebla_8bits (
  input  in_1,
  input  in_2,
  input  in_3,
  input  in_4,
  input  in_5,
  input  in_6,
  input  in_7,
  input  in_8,
  input  in_9,
  output out_10,
  output out_11,
  output out_12,
  output out_13,
  output out_14,
  output out_15,
  output out_16,
  output out_17
);

  and and_1 (out_10, in_1, in_9);
  and and_2 (out_11, in_2, in_9);
  and and_3 (out_12, in_3, in_9);
  and and_4 (out_13, in_4, in_9);
  and and_5 (out_14, in_5, in_9);
  and and_6 (out_15, in_6, in_9);
  and and_7 (out_16, in_7, in_9);
  and and_8 (out_17, in_8, in_9);
endmodule

module memoria_8bits (
  input  in_1,
  input  in_2,
  input  in_3,
  input  in_4,
  input  in_5,
  input  in_6,
  input  in_7,
  input  in_8,
  input  in_9,
  output out_10,
  output out_11,
  output out_12,
  output out_13,
  output out_14,
  output out_15,
  output out_16,
  output out_17
);

  memoria_1bit memoria_1bit_1 (.in_1(in_1), .in_2(in_9), .out_3(out_10));
  memoria_1bit memoria_1bit_2 (.in_1(in_2), .in_2(in_9), .out_3(out_11));
  memoria_1bit memoria_1bit_3 (.in_1(in_3), .in_2(in_9), .out_3(out_12));
  memoria_1bit memoria_1bit_4 (.in_1(in_4), .in_2(in_9), .out_3(out_13));
  memoria_1bit memoria_1bit_5 (.in_1(in_5), .in_2(in_9), .out_3(out_14));
  memoria_1bit memoria_1bit_6 (.in_1(in_6), .in_2(in_9), .out_3(out_15));
  memoria_1bit memoria_1bit_7 (.in_1(in_7), .in_2(in_9), .out_3(out_16));
  memoria_1bit memoria_1bit_8 (.in_1(in_8), .in_2(in_9), .out_3(out_17));
endmodule

module Registrador_8bits (
  input  [7:0] in_1,
  input  [7:0] in_2,
  input  S,
  input  E
);

  wire memoria_8bits_1_out_10, memoria_8bits_1_out_11, memoria_8bits_1_out_12, memoria_8bits_1_out_13,
       memoria_8bits_1_out_14, memoria_8bits_1_out_15, memoria_8bits_1_out_16, memoria_8bits_1_out_17;

  memoria_8bits memoria_8bits_1 (
    .in_1(in_2[0]), .in_2(in_2[1]), .in_3(in_2[2]), .in_4(in_2[3]), .in_5(in_2[4]), .in_6(in_2[5]),
    .in_7(in_2[6]), .in_8(in_2[7]), .in_9(S), .out_10(memoria_8bits_1_out_10),
    .out_11(memoria_8bits_1_out_11), .out_12(memoria_8bits_1_out_12), .out_13(memoria_8bits_1_out_13),
    .out_14(memoria_8bits_1_out_14), .out_15(memoria_8bits_1_out_15), .out_16(memoria_8bits_1_out_16),
    .out_17(memoria_8bits_1_out_17));
  enebla_8bits enebla_8bits_1 (
    .in_1(memoria_8bits_1_out_10), .in_2(memoria_8bits_1_out_11), .in_3(memoria_8bits_1_out_12),
    .in_4(memoria_8bits_1_out_13), .in_5(memoria_8bits_1_out_14), .in_6(memoria_8bits_1_out_15),
    .in_7(memoria_8bits_1_out_16), .in_8(memoria_8bits_1_out_17), .in_9(E), .out_10(in_1[0]),
    .out_11(in_1[1]), .out_12(in_1[2]), .out_13(in_1[3]), .out_14(in_1[4]), .out_15(in_1[5]),
    .out_16(in_1[6]), .out_17(in_1[7]));
endmodule
