// Logisim project Roberta_Brasil.circ as structural Verilog: 8 circuits, main circuit main
module main (
  input  in_1,
  input  in_2,
  input  in_3,
  input  in_4,
  input  [7:0] in_5,
  input  in_6,
  input  in_7,
  input  [7:0] in_8,
  input  in_9,
  input  in_10,
  input  in_11,
  input  in_12,
  input  in_13,
  input  in_14,
  input  in_15,
  input  in_16,
  input  in_17,
  input  in_18,
  input  in_19,
  input  in_20,
  input  in_21,
  input  in_22,
  input  in_23,
  input  [7:0] in_24,
  input  [7:0] in_25,
  output out_26,
  output out_27,
  output [7:0] out_28,
  output [7:0] out_29,
  output out_30,
  output out_31,
  output out_32
);

  wire xor_1_out;
  wire [7:0] registrador_2_out_4, registrador_3_out_4, registrador_4_out_4, registrador_5_out_4;

  // OR_Gate or_1 is placed but not wired
  // NOT_Gate not_1 has open pins: in=open, out=out_26
  registrador registrador_1 (.in_1(in_5), .in_2(in_6), .in_3(in_7), .out_4(out_28));
  xor xor_1 (xor_1_out, in_15, in_21);
  // somador_8bits somador_8bits_1: pin names not known; wires that end beside it: in_24, in_25
  xor xor_2 (out_31, xor_1_out, in_10);
  somador_completo somador_completo_1 (.in_2(in_22), .in_3(in_23), .in_1(in_20), .out_5(out_32), .out_4(out_30));
  assign out_29 = in_9 ? in_8 : 8'bz;  // Controlled_Buffer controlled_buffer_1
  assign out_29 = in_16 ? registrador_2_out_4 : 8'bz;  // Controlled_Buffer controlled_buffer_2
  registrador registrador_2 (.in_1(out_29), .in_2(in_13), .in_3(in_16), .out_4(registrador_2_out_4));
  assign out_29 = in_17 ? registrador_3_out_4 : 8'bz;  // Controlled_Buffer controlled_buffer_3
  registrador registrador_3 (.in_1(out_29), .in_2(in_14), .in_3(in_17), .out_4(registrador_3_out_4));
  assign out_29 = in_18 ? registrador_4_out_4 : 8'bz;  // Controlled_Buffer controlled_buffer_4
  registrador registrador_4 (.in_1(out_29), .in_2(in_11), .in_3(in_18), .out_4(registrador_4_out_4));
  assign out_29 = in_19 ? registrador_5_out_4 : 8'bz;  // Controlled_Buffer controlled_buffer_5
  registrador registrador_5 (.in_1(out_29), .in_2(in_12), .in_3(in_19), .out_4(registrador_5_out_4));

  // Notes on the sheet:
  //   Roberta Brasil
  //   Roberta Graziela de Oliveira Brasil 22400905
endmodule

module somador_completo (
  input  in_1,
  input  in_2,
  input  in_3,
  output out_4,
  output out_5
);

  wire and_1_out, and_2_out, and_3_out, xor_1_out;

  xor xor_1 (xor_1_out, in_2, in_3);
  and and_1 (and_1_out, in_2, in_1);
  and and_2 (and_2_out, in_2, in_3);
  and and_3 (and_3_out, in_3, in_1);
  xor xor_2 (out_4, xor_1_out, in_1);
  or or_1 (out_5, and_1_out, and_2_out, and_3_out);
endmodule

module somador_8bits (
  input  in_1,
  input  [7:0] in_2,
  input  [7:0] in_3,
  output [7:0] out_4,
  output out_5
);

  wire somador_completo_1_out_5, somador_completo_2_out_5, somador_completo_3_out_5,
       somador_completo_4_out_5, somador_completo_5_out_5, somador_completo_6_out_5,
       somador_completo_7_out_5, somador_completo_8_out_5;

  somador_completo somador_completo_1 (
    .in_2(in_2[1]), .in_3(in_3[0]), .in_1(in_1), .out_5(somador_completo_1_out_5), .out_4(out_4[0]));
  somador_completo somador_completo_2 (
    .in_2(in_2[1]), .in_3(in_3[1]), .in_1(somador_completo_1_out_5), .out_5(somador_completo_2_out_5),
    .out_4(out_4[1]));
  somador_completo somador_completo_3 (
    .in_2(in_2[2]), .in_3(in_3[2]), .in_1(somador_completo_2_out_5), .out_5(somador_completo_3_out_5),
    .out_4(out_4[2]));
  somador_completo somador_completo_4 (
    .in_2(in_2[3]), .in_3(in_2[5]), .in_1(somador_completo_3_out_5), .out_5(somador_completo_4_out_5),
    .out_4(out_4[3]));
  somador_completo somador_completo_5 (
    .in_2(in_2[4]), .in_3(in_2[6]), .in_1(somador_completo_4_out_5), .out_5(somador_completo_5_out_5),
    .out_4(out_4[4]));
  somador_completo somador_completo_6 (
    .in_2(in_2[5]), .in_3(in_2[7]), .in_1(somador_completo_5_out_5), .out_5(somador_completo_6_out_5),
    .out_4(out_4[5]));
  somador_completo somador_completo_7 (
    .in_2(in_2[6]), .in_3(in_3[6]), .in_1(somador_completo_6_out_5), .out_5(somador_completo_7_out_5),
    .out_4(out_4[6]));
  somador_completo somador_completo_8 (
    .in_2(in_2[7]), .in_3(in_3[7]), .in_1(somador_completo_7_out_5), .out_5(somador_completo_8_out_5),
    .out_4(out_4[7]));

  assign in_2[0] = in_2[1];
  assign in_3[5:3] = in_2[7:5];
endmodule

module meio_somador (
  input  in_1,
  input  in_2,
  output out_3,
  output out_4
);

  xor xor_1 (out_3, in_1, in_2);
  and and_1 (out_4, in_1, in_2);
endmodule

module memoria1bit (
  input  in_1,
  input  in_2,
  output out_3
);

  wire nand_1_out, nand_2_out, nand_4_out;

  nand nand_1 (nand_1_out, in_1, in_2);
  nand nand_2 (nand_2_out, nand_1_out, in_2);
  nand nand_3 (out_3, nand_1_out, nand_4_out);
  nand nand_4 (nand_4_out, out_3, nand_2_out);
endmodule

module memoria8bits (
  input  in_1,
  input  in_2,
  input  in_3,
  input  in_4,
  input  in_5,
  input  in_6,
  input  in_7,
  input  in_8,
  input  in_9,
  output out_10,
  output out_11,
  output out_12,
  output out_13,
  output out_14,
  output out_15,
  output out_16,
  output out_17
);

  memoria1bit memoria1bit_1 (.in_1(in_1), .in_2(in_9), .out_3(out_10));
  memoria1bit memoria1bit_2 (.in_1(in_2), .in_2(in_9), .out_3(out_11));
  memoria1bit memoria1bit_3 (.in_1(in_3), .in_2(in_9), .out_3(out_12));
  memoria1bit memoria1bit_4 (.in_1(in_4), .in_2(in_9), .out_3(out_13));
  memoria1bit memoria1bit_5 (.in_1(in_5), .in_2(in_9), .out_3(out_14));
  memoria1bit memoria1bit_6 (.in_1(in_6), .in_2(in_9), .out_3(out_15));
  memoria1bit memoria1bit_7 (.in_1(in_7), .in_2(in_9), .out_3(out_16));
  memoria1bit memoria1bit_8 (.in_1(in_8), .in_2(in_9), .out_3(out_17));
endmodule

module enablebits (
  input  in_1,
  input  in_2,
  input  in_3,
  input  in_4,
  input  in_5,
  input  in_6,
  input  in_7,
  input  in_8,
  input  in_9,
  output out_10,
  output out_11,
  output out_12,
  output out_13,
  output out_14,
  output out_15,
  output out_16,
  output out_17
);

  and and_1 (out_10, in_1, in_9);
  and and_2 (out_11, in_2, in_9);
  and and_3 (out_12, in_3, in_9);
  and and_4 (out_13, in_4, in_9);
  and and_5 (out_14, in_5, in_9);
  and and_6 (out_15, in_6, in_9);
  and and_7 (out_16, in_7, in_9);
  and and_8 (out_17, in_8, in_9);
endmodule

module registrador (
  input  [7:0] in_1,
  input  in_2,
  input  in_3,
  output [7:0] out_4
);

  wire memoria8bits_1_out_10, memoria8bits_1_out_11, memoria8bits_1_out_12, memoria8bits_1_out_13,
       memoria8bits_1_out_14, memoria8bits_1_out_15, memoria8bits_1_out_16, memoria8bits_1_out_17;

  memoria8bits memoria8bits_1 (
    .in_1(in_1[0]), .in_2(in_1[1]), .in_3(in_1[2]), .in_4(in_1[3]), .in_5(in_1[4]), .in_6(in_1[5]),
    .in_7(in_1[6]), .in_8(in_1[7]), .in_9(in_2), .out_10(memoria8bits_1_out_10),
    .out_11(memoria8bits_1_out_11), .out_12(memoria8bits_1_out_12), .out_13(memoria8bits_1_out_13),
    .out_14(memoria8bits_1_out_14), .out_15(memoria8bits_1_out_15), .out_16(memoria8bits_1_out_16),
    .out_17(memoria8bits_1_out_17));
  enablebits enablebits_1 (
    .in_1(memoria8bits_1_out_10), .in_2(memoria8bits_1_out_11), .in_3(memoria8bits_1_out_12),
    .in_4(memoria8bits_1_out_13), .in_5(memoria8bits_1_out_14), .in_6(memoria8bits_1_out_15),
    .in_7(memoria8bits_1_out_16), .in_8(memoria8bits_1_out_17), .in_9(in_3), .out_10(out_4[0]),
    .out_11(out_4[1]), .out_12(out_4[2]), .out_13(out_4[3]), .out_14(out_4[4]), .out_15(out_4[5]),
    .out_16(out_4[6]), .out_17(out_4[7]));
endmodule
