// Logisim project Sven_Maximilian_Kalisch.circ as structural Verilog: 5 circuits, main circuit main
module main (
  input  [7:0] in_1,
  input  in_2,
  input  [7:0] in_3,
  input  in_4,
  input  in_5,
  input  in_6,
  input  in_7,
  input  in_8,
  input  in_9,
  input  in_10,
  input  in_11,
  output [7:0] out_12,
  output out_13,
  output [7:0] out_14
);

  memory_8bit memory_8bit_1 (.in_3(in_4), .in_1(out_14), .out_4(out_14), .in_2(in_5));
  somador_8bit somador_8bit_1 (.in_2(in_1), .in_3(in_3), .in_1(in_2), .out_5(out_13), .out_4(out_12));
  memory_8bit memory_8bit_2 (.in_3(in_6), .in_1(out_14), .out_4(out_14), .in_2(in_7));
  memory_8bit memory_8bit_3 (.in_3(in_8), .in_1(out_14), .out_4(out_14), .in_2(in_9));
  memory_8bit memory_8bit_4 (.in_3(in_10), .in_1(out_14), .out_4(out_14), .in_2(in_11));

  // Notes on the sheet:
  //   Sven Maximilian Kalisch
  //   22401143
endmodule

module somador_1bit (
  input  c_in,
  input  a,
  input  b,
  output c,
  output c_out
);

  wire and_1_out, and_2_out, and_3_out, or_1_out, xor_1_out;

  xor xor_1 (xor_1_out, a, b);
  and and_1 (and_1_out, c_in, b);
  and and_2 (and_2_out, c_in, a);
  and and_3 (and_3_out, a, b);
  xor xor_2 (c, xor_1_out, c_in);
  or or_1 (or_1_out, and_1_out, and_2_out);
  or or_2 (c_out, or_1_out, and_3_out);
endmodule

module somador_8bit (
  input  in_1,
  input  [7:0] in_2,
  input  [7:0] in_3,
  output [7:0] out_4,
  output out_5
);

  wire somador_1bit_1_c_out, somador_1bit_2_c_out, somador_1bit_3_c_out, somador_1bit_4_c_out,
       somador_1bit_5_c_out, somador_1bit_6_c_out, somador_1bit_7_c_out;

  somador_1bit somador_1bit_1 (.a(in_2[0]), .b(in_3[0]), .c_in(in_1), .c_out(somador_1bit_1_c_out), .c(out_4[0]));
  somador_1bit somador_1bit_2 (
    .a(in_2[1]), .b(in_3[1]), .c_in(somador_1bit_1_c_out), .c_out(somador_1bit_2_c_out), .c(out_4[1]));
  somador_1bit somador_1bit_3 (
    .a(in_2[2]), .b(in_3[2]), .c_in(somador_1bit_2_c_out), .c_out(somador_1bit_3_c_out), .c(out_4[2]));
  somador_1bit somador_1bit_4 (
    .a(in_2[3]), .b(in_3[3]), .c_in(somador_1bit_3_c_out), .c_out(somador_1bit_4_c_out), .c(out_4[3]));
  somador_1bit somador_1bit_5 (
    .a(in_2[4]), .b(in_3[4]), .c_in(somador_1bit_4_c_out), .c_out(somador_1bit_5_c_out), .c(out_4[4]));
  somador_1bit somador_1bit_6 (
    .a(in_2[5]), .b(in_3[5]), .c_in(somador_1bit_5_c_out), .c_out(somador_1bit_6_c_out), .c(out_4[5]));
  somador_1bit somador_1bit_7 (
    .a(in_2[6]), .b(in_3[6]), .c_in(somador_1bit_6_c_out), .c_out(somador_1bit_7_c_out), .c(out_4[6]));
  somador_1bit somador_1bit_8 (.a(in_2[7]), .b(in_3[7]), .c_in(somador_1bit_7_c_out), .c_out(out_5), .c(out_4[7]));
endmodule

module memory_1bit (
  input  in_1,
  input  in_2,
  output out_3
);

  wire nand_1_out, nand_2_out, nand_4_out;

  nand nand_1 (nand_1_out, in_1, in_2);
  nand nand_2 (nand_2_out, nand_1_out, in_2);
  nand nand_3 (out_3, nand_1_out, nand_4_out);
  nand nand_4 (nand_4_out, out_3, nand_2_out);
endmodule

module memory_8bit (
  input  [7:0] in_1,
  input  in_2,
  input  in_3,
  output [7:0] out_4
);

  wire [7:0] memory_1bit_1_out_3;

  memory_1bit memory_1bit_1 (.in_1(in_1[0]), .in_2(in_3), .out_3(memory_1bit_1_out_3[0]));
  memory_1bit memory_1bit_2 (.in_1(in_1[1]), .in_2(in_3), .out_3(memory_1bit_1_out_3[1]));
  memory_1bit memory_1bit_3 (.in_1(in_1[2]), .in_2(in_3), .out_3(memory_1bit_1_out_3[2]));
  memory_1bit memory_1bit_4 (.in_1(in_1[3]), .in_2(in_3), .out_3(memory_1bit_1_out_3[3]));
  memory_1bit memory_1bit_5 (.in_1(in_1[4]), .in_2(in_3), .out_3(memory_1bit_1_out_3[4]));
  memory_1bit memory_1bit_6 (.in_1(in_1[5]), .in_2(in_3), .out_3(memory_1bit_1_out_3[5]));
  memory_1bit memory_1bit_7 (.in_1(in_1[6]), .in_2(in_3), .out_3(memory_1bit_1_out_3[6]));
  memory_1bit memory_1bit_8 (.in_1(in_1[7]), .in_2(in_3), .out_3(memory_1bit_1_out_3[7]));
  and and_1 (out_4[0], memory_1bit_1_out_3[0], in_2);
  and and_2 (out_4[1], memory_1bit_1_out_3[1], in_2);
  and and_3 (out_4[2], memory_1bit_1_out_3[2], in_2);
  and and_4 (out_4[3], memory_1bit_1_out_3[3], in_2);
  and and_5 (out_4[4], memory_1bit_1_out_3[4], in_2);
  and and_6 (out_4[5], memory_1bit_1_out_3[5], in_2);
  and and_7 (out_4[6], memory_1bit_1_out_3[6], in_2);
  and and_8 (out_4[7], memory_1bit_1_out_3[7], in_2);
endmodule
