// Logisim project VitorOliveira.circ as structural Verilog: 10 circuits, main circuit somador1bit
module somador1bit (
  input  cin,
  input  a,
  input  b,
  output s,
  output cout
);

  wire and_1_out, and_2_out, and_3_out, xor_1_out;

  and and_1 (and_1_out, a, cin);
  and and_2 (and_2_out, a, b);
  and and_3 (and_3_out, b, cin);
  xor xor_1 (xor_1_out, a, b);
  xor xor_2 (s, xor_1_out, cin);
  or or_1 (cout, and_1_out, and_2_out, and_3_out);
endmodule

module somador4bits (
  input  cin,
  input  a0,
  input  b0,
  input  a1,
  input  b1,
  input  a2,
  input  b2,
  input  a3,
  input  b3,
  output c0,
  output c1,
  output c2,
  output c3,
  output cout
);

  wire somador1bit_1_cout, somador1bit_2_cout, somador1bit_3_cout;

  somador1bit somador1bit_1 (.cin(cin), .a(a0), .b(b0), .s(c0), .cout(somador1bit_1_cout));
  somador1bit somador1bit_2 (.cin(somador1bit_1_cout), .a(a1), .b(b1), .s(c1), .cout(somador1bit_2_cout));
  somador1bit somador1bit_3 (.cin(somador1bit_2_cout), .a(a2), .b(b2), .s(c2), .cout(somador1bit_3_cout));
  somador1bit somador1bit_4 (.cin(somador1bit_3_cout), .a(a3), .b(b3), .s(c3), .cout(cout));
endmodule

module somador8bits (
  input  in_1,
  input  in_2,
  input  in_3,
  input  in_4,
  input  in_5,
  input  in_6,
  input  in_7,
  input  in_8,
  input  in_9,
  input  in_10,
  input  in_11,
  input  in_12,
  input  in_13,
  input  in_14,
  input  in_15,
  input  in_16,
  output out_17,
  output out_18,
  output out_19,
  output out_20,
  output out_21,
  output out_22,
  output out_23,
  output out_24,
  output out_25
);

  wire somador4bits_2_cout;

  somador4bits somador4bits_1 (
    .cin(somador4bits_2_cout), .a0(in_1), .b0(in_3), .a1(in_5), .b1(in_7), .a2(in_9), .b2(in_11), .a3(in_13),
    .b3(in_15), .c0(out_17), .c1(out_19), .c2(out_21), .c3(out_23), .cout(out_25));
  somador4bits somador4bits_2 (
    .a0(in_2), .b0(in_4), .a1(in_6), .b1(in_8), .a2(in_10), .b2(in_12), .a3(in_14), .b3(in_16), .c0(out_18),
    .c1(out_20), .c2(out_22), .c3(out_24), .cout(somador4bits_2_cout));  // open: cin
endmodule

module circuito (
  input  in_1,
  input  in_2,
  output out_3
);

  wire nand_1_out, nand_2_out, nand_4_out;

  nand nand_1 (nand_1_out, in_1, in_2);
  nand nand_2 (nand_2_out, nand_1_out, in_2);
  nand nand_3 (out_3, nand_1_out, nand_4_out);
  nand nand_4 (nand_4_out, out_3, nand_2_out);
endmodule

module registrador1bit (
  input  in_1,
  input  in_2,
  input  in_3,
  input  in_4,
  input  in_5,
  input  in_6,
  input  in_7,
  input  in_8,
  input  in_9,
  output out_10,
  output out_11,
  output out_12,
  output out_13,
  output out_14,
  output out_15,
  output out_16,
  output out_17
);

  circuito circuito_1 (.in_1(in_1), .in_2(in_9), .out_3(out_10));
  circuito circuito_2 (.in_1(in_2), .in_2(in_9), .out_3(out_11));
  circuito circuito_3 (.in_1(in_3), .in_2(in_9), .out_3(out_12));
  circuito circuito_4 (.in_1(in_4), .in_2(in_9), .out_3(out_13));
  circuito circuito_5 (.in_1(in_5), .in_2(in_9), .out_3(out_14));
  circuito circuito_6 (.in_1(in_6), .in_2(in_9), .out_3(out_15));
  circuito circuito_7 (.in_1(in_7), .in_2(in_9), .out_3(out_16));
  circuito circuito_8 (.in_1(in_8), .in_2(in_9), .out_3(out_17));
endmodule

module umbytecomset (
  input  in_1,
  input  in_2,
  input  in_3,
  input  in_4,
  input  in_5,
  input  in_6,
  input  in_7,
  input  in_8,
  input  set,
  output out_10,
  output out_11,
  output out_12,
  output out_13,
  output out_14,
  output out_15,
  output out_16,
  output out_17
);

  registrador1bit registrador1bit_1 (
    .in_1(in_1), .in_2(in_2), .in_3(in_3), .in_4(in_4), .in_5(in_5), .in_6(in_6), .in_7(in_7), .in_8(in_8),
    .in_9(set), .out_10(out_10), .out_11(out_11), .out_12(out_12), .out_13(out_13), .out_14(out_14),
    .out_15(out_15), .out_16(out_16), .out_17(out_17));
endmodule

module umbytecomEnable (
  input  in_1,
  input  in_2,
  input  in_3,
  input  in_4,
  input  in_5,
  input  in_6,
  input  in_7,
  input  in_8,
  input  enable,
  output out_10,
  output out_11,
  output out_12,
  output out_13,
  output out_14,
  output out_15,
  output out_16,
  output out_17
);

  and and_1 (out_10, in_1, enable);
  and and_2 (out_11, in_2, enable);
  and and_3 (out_12, in_3, enable);
  and and_4 (out_13, in_4, enable);
  and and_5 (out_14, in_5, enable);
  and and_6 (out_15, in_6, enable);
  and and_7 (out_16, in_7, enable);
  and and_8 (out_17, in_8, enable);
endmodule

module registrador1bytecomSETeENABLE (
  input  in_1,
  input  in_2,
  input  in_3,
  input  in_4,
  input  in_5,
  input  in_6,
  input  in_7,
  input  in_8,
  input  set,
  input  enable,
  output out_11,
  output out_12,
  output out_13,
  output out_14,
  output out_15,
  output out_16,
  output out_17,
  output out_18
);

  wire umbytecomset_1_out_10, umbytecomset_1_out_11, umbytecomset_1_out_12, umbytecomset_1_out_13,
       umbytecomset_1_out_14, umbytecomset_1_out_15, umbytecomset_1_out_16, umbytecomset_1_out_17;

  umbytecomset umbytecomset_1 (
    .in_1(in_1), .in_2(in_2), .in_3(in_3), .in_4(in_4), .in_5(in_5), .in_6(in_6), .in_7(in_7), .in_8(in_8),
    .set(set), .out_10(umbytecomset_1_out_10), .out_11(umbytecomset_1_out_11),
    .out_12(umbytecomset_1_out_12), .out_13(umbytecomset_1_out_13), .out_14(umbytecomset_1_out_14),
    .out_15(umbytecomset_1_out_15), .out_16(umbytecomset_1_out_16), .out_17(umbytecomset_1_out_17));
  umbytecomEnable umbytecomenable_1 (
    .in_1(umbytecomset_1_out_10), .in_2(umbytecomset_1_out_11), .in_3(umbytecomset_1_out_12),
    .in_4(umbytecomset_1_out_13), .in_5(umbytecomset_1_out_14), .in_6(umbytecomset_1_out_15),
    .in_7(umbytecomset_1_out_16), .in_8(umbytecomset_1_out_17), .enable(enable), .out_10(out_11),
    .out_11(out_12), .out_12(out_13), .out_13(out_14), .out_14(out_15), .out_15(out_16), .out_16(out_17),
    .out_17(out_18));
endmodule

module registrador8bits (
  input  [7:0] in_1,
  input  set,
  input  enable,
  output [7:0] out_4
);

  registrador1bytecomSETeENABLE registrador1bytecomseteenable_1 (
    .in_1(in_1[0]), .in_2(in_1[1]), .in_3(in_1[2]), .in_4(in_1[3]), .in_5(in_1[4]), .in_6(in_1[5]),
    .in_7(in_1[6]), .in_8(in_1[7]), .set(set), .enable(enable), .out_11(out_4[0]), .out_12(out_4[1]),
    .out_13(out_4[2]), .out_14(out_4[3]), .out_15(out_4[4]), .out_16(out_4[5]), .out_17(out_4[6]),
    .out_18(out_4[7]));
endmodule

module main (
);


  // Notes on the sheet:
  //   Nome: Vitor de Souza Oliveira
  //   Matrícula: 22450322
endmodule
