// Logisim project Wellington_de_Souza_Bezerra.circ as structural Verilog: 12 circuits, main circuit main
module main (
  input  in_1,
  input  [7:0] in_2,
  input  [7:0] in_3,
  input  in_4,
  input  in_5,
  input  in_6,
  input  in_7,
  input  in_8,
  input  in_9,
  input  in_10,
  input  in_11,
  output [7:0] out_12,
  output out_13
);

  wire [7:0] R1_out_4;

  Somador_8bits somador_8bits_1 (.in_2(in_2), .in_3(in_3), .in_1(in_1), .out_5(out_13), .out_4(out_12));
  registrador_1byte R1 (.in_1(R1_out_4), .s(in_4), .e(in_8), .out_4(R1_out_4));
  registrador_1byte R2 (.in_1(R1_out_4), .s(in_5), .e(in_9), .out_4(R1_out_4));
  registrador_1byte R3 (.in_1(R1_out_4), .s(in_6), .e(in_10), .out_4(R1_out_4));
  registrador_1byte R4 (.in_1(R1_out_4), .s(in_7), .e(in_11), .out_4(R1_out_4));

  // Notes on the sheet:
  //   Mátricula: 22250543
  //   Somador_8 bits
  //   Aluno: Wellington de Souza Bezerra
  //   Registradores
endmodule

module Somador_1bit (
  input  c_in,
  input  in_2,
  input  in_3,
  output c,
  output c_out
);

  wire and_1_out, and_2_out, and_3_out, xor_1_out;

  xor xor_1 (xor_1_out, in_2, in_3);
  and and_1 (and_1_out, in_2, c_in);
  and and_2 (and_2_out, in_2, in_3);
  and and_3 (and_3_out, in_3, c_in);
  xor xor_2 (c, xor_1_out, c_in);
  or or_1 (c_out, and_1_out, and_2_out, and_3_out);

  // Notes on the sheet:
  //   Somador Completo
endmodule

module somador_1bit_encapsulado (
  input  in_1,
  input  in_2,
  input  in_3,
  output out_4,
  output out_5
);

  // Somador_1bit somador_1bit_1: pin names not known; wires that end beside it: in_2, in_3, in_1, out_4, out_5
endmodule

module Somador_8bits (
  input  in_1,
  input  [7:0] in_2,
  input  [7:0] in_3,
  output [7:0] out_4,
  output out_5
);

  wire somador_1bit_1_c_out, somador_1bit_2_c_out, somador_1bit_3_c_out, somador_1bit_4_c_out,
       somador_1bit_5_c_out, somador_1bit_6_c_out, somador_1bit_7_c_out;

  Somador_1bit somador_1bit_1 (.in_2(in_2[0]), .in_3(in_3[0]), .c_in(in_1), .c_out(somador_1bit_1_c_out), .c(out_4[0]));
  Somador_1bit somador_1bit_2 (
    .in_2(in_2[1]), .in_3(in_3[1]), .c_in(somador_1bit_1_c_out), .c_out(somador_1bit_2_c_out), .c(out_4[1]));
  Somador_1bit somador_1bit_3 (
    .in_2(in_2[2]), .in_3(in_3[2]), .c_in(somador_1bit_2_c_out), .c_out(somador_1bit_3_c_out), .c(out_4[2]));
  Somador_1bit somador_1bit_4 (
    .in_2(in_2[3]), .in_3(in_3[3]), .c_in(somador_1bit_3_c_out), .c_out(somador_1bit_4_c_out), .c(out_4[3]));
  Somador_1bit somador_1bit_5 (
    .in_2(in_2[4]), .in_3(in_3[4]), .c_in(somador_1bit_4_c_out), .c_out(somador_1bit_5_c_out), .c(out_4[4]));
  Somador_1bit somador_1bit_6 (
    .in_2(in_2[5]), .in_3(in_3[5]), .c_in(somador_1bit_5_c_out), .c_out(somador_1bit_6_c_out), .c(out_4[5]));
  Somador_1bit somador_1bit_7 (
    .in_2(in_2[6]), .in_3(in_3[6]), .c_in(somador_1bit_6_c_out), .c_out(somador_1bit_7_c_out), .c(out_4[6]));
  Somador_1bit somador_1bit_8 (
    .in_2(in_2[7]), .in_3(in_3[7]), .c_in(somador_1bit_7_c_out), .c_out(out_5), .c(out_4[7]));
endmodule

module Somador_8bits_encapsulado (
  input  in_1,
  input  [7:0] in_2,
  input  [7:0] in_3,
  output [7:0] out_4,
  output out_5
);

  Somador_8bits somador_8bits_1 (.in_2(in_2), .in_3(in_3), .in_1(in_1), .out_5(out_5), .out_4(out_4));
endmodule

// M
module memoria_1bit (
  input  in_1,
  input  in_2,
  output out_3
);

  wire nand_1_out, nand_2_out, nand_4_out;

  nand nand_1 (nand_1_out, in_1, in_2);
  nand nand_2 (nand_2_out, nand_1_out, in_2);
  nand nand_3 (out_3, nand_1_out, nand_4_out);
  nand nand_4 (nand_4_out, out_3, nand_2_out);
endmodule

module memoria_1bit_encapsulada (
  input  in_1,
  input  in_2,
  output out_3
);

  memoria_1bit memoria_1bit_1 (.in_1(in_1), .in_2(in_2), .out_3(out_3));
endmodule

// B
module memoria_8bits (
  input  i0,
  input  i1,
  input  i2,
  input  i3,
  input  i4,
  input  i5,
  input  i6,
  input  i7,
  input  s,
  output o0,
  output o1,
  output o2,
  output o3,
  output o4,
  output o5,
  output o6,
  output o7
);

  memoria_1bit memoria_1bit_1 (.in_1(i0), .in_2(s), .out_3(o0));
  memoria_1bit memoria_1bit_2 (.in_1(i1), .in_2(s), .out_3(o1));
  memoria_1bit memoria_1bit_3 (.in_1(i2), .in_2(s), .out_3(o2));
  memoria_1bit memoria_1bit_4 (.in_1(i3), .in_2(s), .out_3(o3));
  memoria_1bit memoria_1bit_5 (.in_1(i4), .in_2(s), .out_3(o4));
  memoria_1bit memoria_1bit_6 (.in_1(i5), .in_2(s), .out_3(o5));
  memoria_1bit memoria_1bit_7 (.in_1(i6), .in_2(s), .out_3(o6));
  memoria_1bit memoria_1bit_8 (.in_1(i7), .in_2(s), .out_3(o7));
endmodule

// B
module memoria_1byte_set_bit (
  input  in_1,
  input  in_2,
  input  in_3,
  input  in_4,
  input  in_5,
  input  in_6,
  input  in_7,
  input  in_8,
  input  in_9,
  output out_10,
  output out_11,
  output out_12,
  output out_13,
  output out_14,
  output out_15,
  output out_16,
  output out_17
);

  memoria_8bits memoria_8bits_1 (
    .i0(in_1), .i1(in_2), .i2(in_3), .i3(in_4), .i4(in_5), .i5(in_6), .i6(in_7), .i7(in_8), .s(in_9),
    .o0(out_10), .o1(out_11), .o2(out_12), .o3(out_13), .o4(out_14), .o5(out_15), .o6(out_16), .o7(out_17));
endmodule

// E
module enable (
  input  in_1,
  input  in_2,
  input  in_3,
  input  in_4,
  input  in_5,
  input  in_6,
  input  in_7,
  input  in_8,
  input  in_9,
  output out_10,
  output out_11,
  output out_12,
  output out_13,
  output out_14,
  output out_15,
  output out_16,
  output out_17
);

  and and_1 (out_10, in_1, in_9);
  and and_2 (out_11, in_2, in_9);
  and and_3 (out_12, in_3, in_9);
  and and_4 (out_13, in_4, in_9);
  and and_5 (out_14, in_5, in_9);
  and and_6 (out_15, in_6, in_9);
  and and_7 (out_16, in_7, in_9);
  and and_8 (out_17, in_8, in_9);
endmodule

// R
module memoria_1byte_set_enable_bits (
  input  in_1,
  input  in_2,
  input  in_3,
  input  in_4,
  input  in_5,
  input  in_6,
  input  in_7,
  input  in_8,
  input  in_9,
  input  in_10,
  output out_11,
  output out_12,
  output out_13,
  output out_14,
  output out_15,
  output out_16,
  output out_17,
  output out_18
);

  wire memoria_1byte_set_bit_1_out_10, memoria_1byte_set_bit_1_out_11, memoria_1byte_set_bit_1_out_12,
       memoria_1byte_set_bit_1_out_13, memoria_1byte_set_bit_1_out_14, memoria_1byte_set_bit_1_out_15,
       memoria_1byte_set_bit_1_out_16, memoria_1byte_set_bit_1_out_17;

  memoria_1byte_set_bit memoria_1byte_set_bit_1 (
    .in_1(in_1), .in_2(in_2), .in_3(in_3), .in_4(in_4), .in_5(in_5), .in_6(in_6), .in_7(in_7), .in_8(in_8),
    .in_9(in_9), .out_10(memoria_1byte_set_bit_1_out_10), .out_11(memoria_1byte_set_bit_1_out_11),
    .out_12(memoria_1byte_set_bit_1_out_12), .out_13(memoria_1byte_set_bit_1_out_13),
    .out_14(memoria_1byte_set_bit_1_out_14), .out_15(memoria_1byte_set_bit_1_out_15),
    .out_16(memoria_1byte_set_bit_1_out_16), .out_17(memoria_1byte_set_bit_1_out_17));
  enable enable_1 (
    .in_1(memoria_1byte_set_bit_1_out_10), .in_2(memoria_1byte_set_bit_1_out_11),
    .in_3(memoria_1byte_set_bit_1_out_12), .in_4(memoria_1byte_set_bit_1_out_13),
    .in_5(memoria_1byte_set_bit_1_out_14), .in_6(memoria_1byte_set_bit_1_out_15),
    .in_7(memoria_1byte_set_bit_1_out_16), .in_8(memoria_1byte_set_bit_1_out_17), .in_9(in_10),
    .out_10(out_11), .out_11(out_12), .out_12(out_13), .out_13(out_14), .out_14(out_15), .out_15(out_16),
    .out_16(out_17), .out_17(out_18));
endmodule

module registrador_1byte (
  input  [7:0] in_1,
  input  s,
  input  e,
  output [7:0] out_4
);

  memoria_1byte_set_enable_bits memoria_1byte_set_enable_bits_1 (
    .in_1(in_1[0]), .in_2(in_1[1]), .in_3(in_1[2]), .in_4(in_1[3]), .in_5(in_1[4]), .in_6(in_1[5]),
    .in_7(in_1[6]), .in_8(in_1[7]), .in_9(s), .in_10(e), .out_11(out_4[0]), .out_12(out_4[1]),
    .out_13(out_4[2]), .out_14(out_4[3]), .out_15(out_4[4]), .out_16(out_4[5]), .out_17(out_4[6]),
    .out_18(out_4[7]));
endmodule
