// Logisim project atv1_RebecaMadiOliveira.circ as structural Verilog: 7 circuits, main circuit main
module main (
  input  carry_in,
  input  [7:0] a,
  input  [7:0] b,
  input  [7:0] i,
  input  s,
  input  e,
  input  [7:0] in_7,
  input  sMAR,
  input  eMAR,
  input  [7:0] in_10,
  input  in_11,
  input  in_12,
  input  [7:0] in_13,
  input  in_14,
  input  in_15,
  input  [7:0] in_16,
  input  in_17,
  input  in_18,
  input  [7:0] in_19,
  input  in_20,
  input  in_21,
  output [7:0] o_soma,
  output carry_out,
  output [7:0] o,
  output [7:0] out_25
);

  wire [7:0] R1_o, R2_o, R3_o, R4_o, R5_o;

  registrador_8_bits registrador_8_bits_1 (.i(i), .s(s), .e(e), .o(o));
  registrador_8_bits R1 (.i(in_7), .s(sMAR), .e(eMAR), .o(R1_o));
  somador_8_bits somador_8_bits_1 (.a(a), .b(b), .carry_in(carry_in), .carry_out(carry_out), .o(o_soma));
  assign out_25 = eMAR ? R1_o : 8'bz;  // Controlled_Buffer controlled_buffer_1
  assign out_25 = in_12 ? R2_o : 8'bz;  // Controlled_Buffer controlled_buffer_2
  registrador_8_bits R2 (.i(in_10), .s(in_11), .e(in_12), .o(R2_o));
  assign out_25 = in_15 ? R3_o : 8'bz;  // Controlled_Buffer controlled_buffer_3
  registrador_8_bits R3 (.i(in_13), .s(in_14), .e(in_15), .o(R3_o));
  registrador_8_bits R4 (.i(in_16), .s(in_17), .e(in_18), .o(R4_o));
  assign out_25 = in_18 ? R4_o : 8'bz;  // Controlled_Buffer controlled_buffer_4
  assign out_25 = in_21 ? R5_o : 8'bz;  // Controlled_Buffer controlled_buffer_5
  registrador_8_bits R5 (.i(in_19), .s(in_20), .e(in_21), .o(R5_o));

  // Notes on the sheet:
  //   Nome: Rebeca Madi Oliveira
  //   Matricula: 22400981
  //   Somador de 8 bits completo:
  //   Registrador de 1byte com set e enable
  //   Cinco registradores no barramento
endmodule

module somador1bCompleto (
  input  c_in,
  input  a,
  input  b,
  output out1,
  output c_out
);

  wire and_1_out, and_2_out, and_3_out, xor_1_out;

  xor xor_1 (xor_1_out, a, b);
  and and_1 (and_1_out, a, c_in);
  and and_2 (and_2_out, a, b);
  and and_3 (and_3_out, b, c_in);
  xor xor_2 (out1, xor_1_out, c_in);
  or or_1 (c_out, and_1_out, and_2_out, and_3_out);
endmodule

module somador_8_bits (
  input  carry_in,
  input  [7:0] a,
  input  [7:0] b,
  output [7:0] o,
  output carry_out
);

  wire somador1bcompleto_1_c_out, somador1bcompleto_2_c_out, somador1bcompleto_3_c_out,
       somador1bcompleto_4_c_out, somador1bcompleto_5_c_out, somador1bcompleto_6_c_out,
       somador1bcompleto_7_c_out;

  somador1bCompleto somador1bcompleto_1 (
    .a(a[0]), .b(b[0]), .c_in(carry_in), .c_out(somador1bcompleto_1_c_out), .out1(o[0]));
  somador1bCompleto somador1bcompleto_2 (
    .a(a[1]), .b(b[1]), .c_in(somador1bcompleto_1_c_out), .c_out(somador1bcompleto_2_c_out), .out1(o[1]));
  somador1bCompleto somador1bcompleto_3 (
    .a(a[2]), .b(b[2]), .c_in(somador1bcompleto_2_c_out), .c_out(somador1bcompleto_3_c_out), .out1(o[2]));
  somador1bCompleto somador1bcompleto_4 (
    .a(a[3]), .b(b[3]), .c_in(somador1bcompleto_3_c_out), .c_out(somador1bcompleto_4_c_out), .out1(o[3]));
  somador1bCompleto somador1bcompleto_5 (
    .a(a[4]), .b(b[4]), .c_in(somador1bcompleto_4_c_out), .c_out(somador1bcompleto_5_c_out), .out1(o[4]));
  somador1bCompleto somador1bcompleto_6 (
    .a(a[5]), .b(b[5]), .c_in(somador1bcompleto_5_c_out), .c_out(somador1bcompleto_6_c_out), .out1(o[5]));
  somador1bCompleto somador1bcompleto_7 (
    .a(a[6]), .b(b[6]), .c_in(somador1bcompleto_6_c_out), .c_out(somador1bcompleto_7_c_out), .out1(o[6]));
  somador1bCompleto somador1bcompleto_8 (
    .a(a[7]), .b(b[7]), .c_in(somador1bcompleto_7_c_out), .c_out(carry_out), .out1(o[7]));
endmodule

module memoria_8_bits (
  input  i0,
  input  i1,
  input  i2,
  input  i3,
  input  i4,
  input  i5,
  input  i6,
  input  i7,
  input  s,
  output o0,
  output o1,
  output o2,
  output o3,
  output o4,
  output o5,
  output o6,
  output o7
);

  memoria_1_bit memoria_1_bit_1 (.i(i0), .s(s), .o(o0));
  memoria_1_bit memoria_1_bit_2 (.i(i1), .s(s), .o(o1));
  memoria_1_bit memoria_1_bit_3 (.i(i2), .s(s), .o(o2));
  memoria_1_bit memoria_1_bit_4 (.i(i3), .s(s), .o(o3));
  memoria_1_bit memoria_1_bit_5 (.i(i4), .s(s), .o(o4));
  memoria_1_bit memoria_1_bit_6 (.i(i5), .s(s), .o(o5));
  memoria_1_bit memoria_1_bit_7 (.i(i6), .s(s), .o(o6));
  memoria_1_bit memoria_1_bit_8 (.i(i7), .s(s), .o(o7));
endmodule

module memoria_1_bit (
  input  i,
  input  s,
  output o
);

  wire nand_1_out, nand_2_out, nand_4_out;

  nand nand_1 (nand_1_out, i, s);
  nand nand_2 (nand_2_out, nand_1_out, s);
  nand nand_3 (o, nand_1_out, nand_4_out);
  nand nand_4 (nand_4_out, o, nand_2_out);
endmodule

module enable_bits (
  input  i0,
  input  i1,
  input  i2,
  input  i3,
  input  i4,
  input  i5,
  input  i6,
  input  i7,
  input  e,
  output o0,
  output o1,
  output o2,
  output o3,
  output o4,
  output o5,
  output o6,
  output o7
);

  and and_1 (o0, i0, e);
  and and_2 (o1, i1, e);
  and and_3 (o2, i2, e);
  and and_4 (o3, i3, e);
  and and_5 (o4, i4, e);
  and and_6 (o5, i5, e);
  and and_7 (o6, i6, e);
  and and_8 (o7, i7, e);
endmodule

module registrador_8_bits (
  input  [7:0] i,
  input  s,
  input  e,
  output [7:0] o
);

  wire memoria_8_bits_1_o0, memoria_8_bits_1_o1, memoria_8_bits_1_o2, memoria_8_bits_1_o3,
       memoria_8_bits_1_o4, memoria_8_bits_1_o5, memoria_8_bits_1_o6, memoria_8_bits_1_o7;

  memoria_8_bits memoria_8_bits_1 (
    .i0(i[0]), .i1(i[1]), .i2(i[2]), .i3(i[3]), .i4(i[4]), .i5(i[5]), .i6(i[6]), .i7(i[7]), .s(s),
    .o0(memoria_8_bits_1_o0), .o1(memoria_8_bits_1_o1), .o2(memoria_8_bits_1_o2), .o3(memoria_8_bits_1_o3),
    .o4(memoria_8_bits_1_o4), .o5(memoria_8_bits_1_o5), .o6(memoria_8_bits_1_o6), .o7(memoria_8_bits_1_o7));
  enable_bits enable_bits_1 (
    .i0(memoria_8_bits_1_o0), .i1(memoria_8_bits_1_o1), .i2(memoria_8_bits_1_o2), .i3(memoria_8_bits_1_o3),
    .i4(memoria_8_bits_1_o4), .i5(memoria_8_bits_1_o5), .i6(memoria_8_bits_1_o6), .i7(memoria_8_bits_1_o7),
    .e(e), .o0(o[0]), .o1(o[1]), .o2(o[2]), .o3(o[3]), .o4(o[4]), .o5(o[5]), .o6(o[6]), .o7(o[7]));
endmodule
