// Logisim project aula_3_Lucas_Melo.circ as structural Verilog: 8 circuits, main circuit Registrador
module Registrador (
  input  in_1,
  input  in_2,
  input  in_3,
  input  in_4,
  input  in_5,
  input  in_6,
  input  in_7,
  input  in_8,
  input  in_9,
  input  in_10,
  output out_11,
  output out_12,
  output out_13,
  output out_14,
  output out_15,
  output out_16,
  output out_17,
  output out_18
);

  wire flip_flop_1_out_3, flip_flop_2_out_3, flip_flop_3_out_3, flip_flop_4_out_3, flip_flop_5_out_3,
       flip_flop_6_out_3, flip_flop_7_out_3, flip_flop_8_out_3;

  Flip_Flop flip_flop_1 (.in_1(in_1), .in_2(in_9), .out_3(flip_flop_1_out_3));
  Flip_Flop flip_flop_2 (.in_1(in_2), .in_2(in_9), .out_3(flip_flop_2_out_3));
  Flip_Flop flip_flop_3 (.in_1(in_3), .in_2(in_9), .out_3(flip_flop_3_out_3));
  Flip_Flop flip_flop_4 (.in_1(in_4), .in_2(in_9), .out_3(flip_flop_4_out_3));
  Flip_Flop flip_flop_5 (.in_1(in_5), .in_2(in_9), .out_3(flip_flop_5_out_3));
  Flip_Flop flip_flop_6 (.in_1(in_6), .in_2(in_9), .out_3(flip_flop_6_out_3));
  Flip_Flop flip_flop_7 (.in_1(in_7), .in_2(in_9), .out_3(flip_flop_7_out_3));
  Flip_Flop flip_flop_8 (.in_1(in_8), .in_2(in_9), .out_3(flip_flop_8_out_3));
  and and_1 (out_11, flip_flop_1_out_3, in_10);
  and and_2 (out_12, flip_flop_2_out_3, in_10);
  and and_3 (out_13, flip_flop_3_out_3, in_10);
  and and_4 (out_14, flip_flop_4_out_3, in_10);
  and and_5 (out_15, flip_flop_5_out_3, in_10);
  and and_6 (out_16, flip_flop_6_out_3, in_10);
  and and_7 (out_17, flip_flop_7_out_3, in_10);
  and and_8 (out_18, flip_flop_8_out_3, in_10);

  // Notes on the sheet:
  //   Lucas Melo dos Santos - 22401903
endmodule

module Memoria_1_bit (
  input  in_1,
  input  in_2,
  output out_3
);

  Flip_Flop flip_flop_1 (.in_1(in_1), .in_2(in_2), .out_3(out_3));
endmodule

module Flip_Flop (
  input  in_1,
  input  in_2,
  output out_3
);

  wire nand_1_out, nand_2_out, nand_3_out;

  nand nand_1 (nand_1_out, in_1, in_2);
  nand nand_2 (nand_2_out, nand_1_out, in_2);
  nand nand_3 (nand_3_out, out_3, nand_2_out);
  nand nand_4 (out_3, nand_1_out, nand_3_out);

  // Notes on the sheet:
  //   Lucas Melo dos Santos - 22401903
endmodule

module Memoria_2_bits (
  input  in_1,
  input  in_2,
  input  in_3,
  output out_4,
  output out_5
);

  Flip_Flop flip_flop_1 (.in_1(in_1), .in_2(in_3), .out_3(out_4));
  Flip_Flop flip_flop_2 (.in_1(in_2), .in_2(in_3), .out_3(out_5));
endmodule

module main (
  input  in_1,
  input  in_2,
  input  in_3,
  input  in_4,
  input  in_5,
  input  in_6,
  input  in_7,
  input  in_8,
  input  [7:0] in_9,
  input  [7:0] in_10,
  input  in_11,
  input  in_12,
  input  in_13,
  input  in_14,
  input  in_15,
  input  in_16,
  input  in_17,
  input  in_18,
  input  in_19,
  input  in_20,
  output out_21,
  output out_22,
  output out_23,
  output out_24,
  output out_25,
  output [7:0] out_26,
  output [7:0] out_27
);

  wire and_1_out, and_2_out, and_3_out, xor_1_out;
  wire [7:0] convertor_1_out_4, convertor_2_out_4, convertor_3_out_4, convertor_4_out_4, convertor_5_out_4;

  and and_1 (and_1_out, in_1, in_3);
  xor xor_1 (xor_1_out, in_3, in_1);
  convertor convertor_1 (.in_1(in_10), .in_2(in_11), .in_3(in_13), .out_4(convertor_1_out_4));
  and and_2 (and_2_out, in_4, in_2);
  xor xor_2 (out_23, in_2, in_4);
  Somador somador_1 (.in_2(in_6), .in_3(in_7), .in_1(in_5), .out_4(out_24), .out_5(out_25));
  Somador_8_bits somador_8_bits_1 (.in_3(in_9), .in_2(in_8), .out_4(out_26));  // open: in_1, out_5
  assign out_27 = convertor_1_out_4;  // Buffer buffer_1, 8 bits wide
  and and_3 (and_3_out, xor_1_out, and_2_out);
  convertor convertor_2 (.in_1(out_27), .in_2(in_16), .in_3(in_20), .out_4(convertor_2_out_4));
  xor xor_3 (out_21, and_1_out, and_3_out);
  assign out_27 = convertor_2_out_4;  // Buffer buffer_2, 8 bits wide
  assign out_27 = convertor_3_out_4;  // Buffer buffer_3, 8 bits wide
  xor xor_4 (out_22, xor_1_out, and_2_out);
  assign out_27 = convertor_4_out_4;  // Buffer buffer_4, 8 bits wide
  convertor convertor_3 (.in_1(out_27), .in_2(in_15), .in_3(in_19), .out_4(convertor_3_out_4));
  convertor convertor_4 (.in_1(out_27), .in_2(in_14), .in_3(in_18), .out_4(convertor_4_out_4));
  convertor convertor_5 (.in_1(out_27), .in_2(in_12), .in_3(in_17), .out_4(convertor_5_out_4));
  assign out_27 = convertor_5_out_4;  // Buffer buffer_5, 8 bits wide

  // Notes on the sheet:
  //   Lucas Melo dos Santos - 22401903
endmodule

module Somador (
  input  in_1,
  input  in_2,
  input  in_3,
  output out_4,
  output out_5
);

  wire and_1_out, and_2_out, xor_1_out;

  xor xor_1 (xor_1_out, in_2, in_3);
  xor xor_2 (out_4, xor_1_out, in_1);
  and and_1 (and_1_out, in_2, in_3);
  and and_2 (and_2_out, xor_1_out, in_1);
  or or_1 (out_5, and_1_out, and_2_out);
endmodule

module Somador_8_bits (
  input  [7:0] in_1,
  input  in_2,
  input  [7:0] in_3,
  output [7:0] out_4,
  output out_5
);

  wire somador_1_out_5, somador_2_out_5, somador_3_out_5, somador_4_out_5, somador_5_out_5, somador_6_out_5,
       somador_7_out_5;

  Somador somador_1 (.in_2(in_1[0]), .in_3(in_3[0]), .in_1(in_2), .out_4(out_4[0]), .out_5(somador_1_out_5));
  Somador somador_2 (.in_2(in_1[1]), .in_3(in_3[1]), .in_1(somador_1_out_5), .out_4(out_4[1]), .out_5(somador_2_out_5));
  Somador somador_3 (.in_2(in_1[2]), .in_3(in_3[2]), .in_1(somador_2_out_5), .out_4(out_4[2]), .out_5(somador_3_out_5));
  Somador somador_4 (.in_2(in_1[3]), .in_3(in_3[3]), .in_1(somador_3_out_5), .out_4(out_4[3]), .out_5(somador_4_out_5));
  Somador somador_5 (.in_2(in_1[4]), .in_3(in_3[4]), .in_1(somador_4_out_5), .out_4(out_4[4]), .out_5(somador_5_out_5));
  Somador somador_6 (.in_2(in_1[5]), .in_3(in_3[5]), .in_1(somador_5_out_5), .out_4(out_4[5]), .out_5(somador_6_out_5));
  Somador somador_7 (.in_2(in_1[6]), .in_3(in_3[6]), .in_1(somador_6_out_5), .out_4(out_4[6]), .out_5(somador_7_out_5));
  Somador somador_8 (.in_2(in_1[7]), .in_3(in_3[7]), .in_1(somador_7_out_5), .out_4(out_4[7]), .out_5(out_5));
endmodule

module convertor (
  input  [7:0] in_1,
  input  in_2,
  input  in_3,
  output [7:0] out_4
);

  Registrador registrador_1 (
    .in_2(in_1[7]), .in_3(in_1[7]), .in_4(in_1[7]), .in_5(in_1[7]), .in_6(in_1[7]), .in_7(in_1[7]),
    .in_8(in_1[7]), .in_9(in_1[7]), .out_11(in_2), .out_12(in_2), .out_13(in_2), .out_14(in_2),
    .out_15(in_2), .out_16(in_2), .out_17(in_2), .out_18(in_2));  // open: in_1, in_10

  assign in_1[6:0] = {7{in_1[7]}};
  assign in_3 = in_1[7];
  assign out_4 = {8{in_2}};
endmodule
