// Logisim project aula_3_Vitoria_Kelren (1).circ as structural Verilog: 8 circuits, main circuit main
module main (
  input  in_1,
  input  in_2,
  input  in_3,
  input  in_4,
  input  in_5,
  input  in_6,
  input  in_7,
  input  [7:0] in_8,
  input  in_9,
  input  Soma_binaria,
  input  [7:0] in_11,
  input  in_12,
  input  in_13,
  input  [7:0] in_14,
  input  in_15,
  input  in_16,
  input  in_17,
  input  in_18,
  input  in_19,
  input  in_20,
  input  in_21,
  input  in_22,
  input  [1:0] in_23,
  output out_24,
  output out_25,
  output out_26,
  output out_27,
  output [7:0] out_28,
  output out_29,
  output out_30,
  output out_31,
  output [7:0] out_32,
  output out_33
);

  wire and_1_out, decoder_1_out0, decoder_1_out1, decoder_1_out2, decoder_1_out3, xor_2_out;

  and and_1 (and_1_out, in_1, in_3);
  and and_2 (out_27, in_6, in_7);
  xor xor_1 (out_29, Soma_binaria, in_12);
  not not_1 (out_24, and_1_out);
  and and_3 (out_31, Soma_binaria, in_12);
  xor xor_2 (xor_2_out, in_15, in_17);
  xor xor_3 (out_33, xor_2_out, in_13);
  assign out_32 = in_16 ? in_14 : 8'bz;  // Controlled_Buffer controlled_buffer_1
  Decoder #(.disabled("Z"), .select(2)) decoder_1 (
    .out0(decoder_1_out0), .out1(decoder_1_out1), .out2(decoder_1_out2), .out3(decoder_1_out3), .sel(in_23),
    .en(in_22));
  Memoria_1byte_set_enable memoria_1byte_set_enable_1 (
    .in_1(out_32), .in_2(in_18), .in_3(decoder_1_out0), .out_4(out_32));
  Somador_1bit somador_1bit_1 (.a(in_4), .b(in_5), .in_1(in_2), .c(out_25));  // open: c_out
  Memoria_1byte_set_enable memoria_1byte_set_enable_2 (
    .in_1(out_32), .in_2(in_19), .in_3(decoder_1_out1), .out_4(out_32));
  Somador_8bits somador_8bits_1 (.in_1(in_8), .in_2(in_11), .in_3(in_9), .out_4(out_28), .out_5(out_30));
  Memoria_1byte_set_enable memoria_1byte_set_enable_3 (
    .in_1(out_32), .in_2(in_20), .in_3(decoder_1_out2), .out_4(out_32));
  Memoria_1byte_set_enable memoria_1byte_set_enable_4 (
    .in_1(out_32), .in_2(in_21), .in_3(decoder_1_out3), .out_4(out_32));

  // Notes on the sheet:
  //   Vitória Kélren Félix Farias
  //   matrícula: 22400441
  //   Somador Completo
  //   barramento com 4 registradores
  //   Somador Completo de 8 bits
endmodule

module Somador_1bit (
  input  in_1,
  input  a,
  input  b,
  output c,
  output c_out
);

  wire and_1_out, and_2_out, and_3_out, xor_1_out;

  xor xor_1 (xor_1_out, a, b);
  and and_1 (and_1_out, a, in_1);
  and and_2 (and_2_out, a, b);
  and and_3 (and_3_out, b, in_1);
  xor xor_2 (c, xor_1_out, in_1);
  or or_1 (c_out, and_1_out, and_2_out, and_3_out);
endmodule

module memoria_8bits (
  input  in_1,
  input  in_2,
  input  in_3,
  input  in_4,
  input  in_5,
  input  in_6,
  input  in_7,
  input  in_8,
  input  in_9,
  output out_10,
  output out_11,
  output out_12,
  output out_13,
  output out_14,
  output out_15,
  output out_16,
  output out_17
);

  Somador_1bit somador_1bit_1 (.a(in_1), .b(in_9), .c(out_10));  // open: in_1, c_out
  Somador_1bit somador_1bit_2 (.a(in_2), .c(out_11));  // open: b, in_1, c_out
  Somador_1bit somador_1bit_3 (.a(in_3), .c(out_12));  // open: b, in_1, c_out
  Somador_1bit somador_1bit_4 (.a(in_4), .c(out_13));  // open: b, in_1, c_out
  Somador_1bit somador_1bit_5 (.a(in_5), .c(out_14));  // open: b, in_1, c_out
  Somador_1bit somador_1bit_6 (.a(in_6), .c(out_15));  // open: b, in_1, c_out
  Somador_1bit somador_1bit_7 (.a(in_7), .c(out_16));  // open: b, in_1, c_out
  Somador_1bit somador_1bit_8 (.a(in_8), .c(out_17));  // open: b, in_1, c_out
endmodule

module Memoria1byte_com_setbit (
  input  in_1,
  input  in_2,
  input  in_3,
  input  in_4,
  input  in_5,
  input  in_6,
  input  in_7,
  input  in_8,
  input  in_9,
  output out_10,
  output out_11,
  output out_12,
  output out_13,
  output out_14,
  output out_15,
  output out_16,
  output out_17
);

  memoria_8bits memoria_8bits_1 (
    .in_1(in_1), .in_2(in_2), .in_3(in_3), .in_4(in_4), .in_5(in_5), .in_6(in_6), .in_7(in_7), .in_8(in_8),
    .in_9(in_9), .out_10(out_10), .out_11(out_11), .out_12(out_12), .out_13(out_13), .out_14(out_14),
    .out_15(out_15), .out_16(out_16), .out_17(out_17));
endmodule

module memoria_1bit (
  input  i,
  input  set,
  output out_3
);

  wire nand_1_out, nand_2_out, nand_4_out;

  nand nand_1 (nand_1_out, i, set);
  nand nand_2 (nand_2_out, nand_1_out, set);
  nand nand_3 (out_3, nand_1_out, nand_4_out);
  nand nand_4 (nand_4_out, out_3, nand_2_out);
endmodule

module Enable (
  input  in_1,
  input  in_2,
  input  in_3,
  input  in_4,
  input  in_5,
  input  in_6,
  input  in_7,
  input  in_8,
  input  in_9,
  output out_10,
  output out_11,
  output out_12,
  output out_13,
  output out_14,
  output out_15,
  output out_16,
  output out_17
);

  and and_1 (out_10, in_1, in_9);
  and and_2 (out_11, in_2, in_9);
  and and_3 (out_12, in_3, in_9);
  and and_4 (out_13, in_4, in_9);
  and and_5 (out_14, in_5, in_9);
  and and_6 (out_15, in_6, in_9);
  and and_7 (out_16, in_7, in_9);
  and and_8 (out_17, in_8, in_9);
endmodule

module Memoria_1byte_set_enable (
  input  [7:0] in_1,
  input  in_2,
  input  in_3,
  output [7:0] out_4
);

  wire memoria_8bits_1_out_10, memoria_8bits_1_out_11, memoria_8bits_1_out_12, memoria_8bits_1_out_13,
       memoria_8bits_1_out_14, memoria_8bits_1_out_15, memoria_8bits_1_out_16, memoria_8bits_1_out_17;

  memoria_8bits memoria_8bits_1 (
    .in_1(in_1[0]), .in_2(in_1[1]), .in_3(in_1[2]), .in_4(in_1[3]), .in_5(in_1[4]), .in_6(in_1[5]),
    .in_7(in_1[6]), .in_8(in_1[7]), .in_9(in_2), .out_10(memoria_8bits_1_out_10),
    .out_11(memoria_8bits_1_out_11), .out_12(memoria_8bits_1_out_12), .out_13(memoria_8bits_1_out_13),
    .out_14(memoria_8bits_1_out_14), .out_15(memoria_8bits_1_out_15), .out_16(memoria_8bits_1_out_16),
    .out_17(memoria_8bits_1_out_17));
  Enable enable_1 (
    .in_1(memoria_8bits_1_out_10), .in_2(memoria_8bits_1_out_11), .in_3(memoria_8bits_1_out_12),
    .in_4(memoria_8bits_1_out_13), .in_5(memoria_8bits_1_out_14), .in_6(memoria_8bits_1_out_15),
    .in_7(memoria_8bits_1_out_16), .in_8(memoria_8bits_1_out_17), .in_9(in_3), .out_10(out_4[0]),
    .out_11(out_4[1]), .out_12(out_4[2]), .out_13(out_4[3]), .out_14(out_4[4]), .out_15(out_4[5]),
    .out_16(out_4[6]), .out_17(out_4[7]));
endmodule

module Somador_8bits (
  input  [7:0] in_1,
  input  [7:0] in_2,
  input  in_3,
  output [7:0] out_4,
  output out_5
);

  wire undriven, undriven_2, undriven_3, undriven_4, undriven_5, undriven_6, undriven_7;

  Somador_1bit somador_1bit_1 (.a(in_2[0]), .b(in_1[0]), .in_1(in_3), .c(out_4[0]));  // open: c_out
  Somador_1bit somador_1bit_2 (.a(in_2[1]), .b(in_1[1]), .in_1(undriven), .c(out_4[1]));  // open: c_out
  Somador_1bit somador_1bit_3 (.a(in_2[2]), .b(in_1[2]), .in_1(undriven_2), .c(out_4[2]));  // open: c_out
  Somador_1bit somador_1bit_4 (.a(in_2[3]), .b(in_1[3]), .in_1(undriven_3), .c(out_4[3]));  // open: c_out
  Somador_1bit somador_1bit_5 (.a(in_2[4]), .b(in_1[4]), .in_1(undriven_4), .c(out_4[4]));  // open: c_out
  Somador_1bit somador_1bit_6 (.a(in_2[5]), .b(in_1[5]), .in_1(undriven_5), .c_out(out_4[5]));  // open: c
  Somador_1bit somador_1bit_7 (.a(in_2[6]), .b(in_1[6]), .in_1(undriven_6), .c(out_4[6]));  // open: c_out
  Somador_1bit somador_1bit_8 (.a(in_2[7]), .b(in_1[7]), .in_1(undriven_7), .c(out_4[7]));  // open: c_out
endmodule
