// Logisim project aula_3leticianatividade.circ as structural Verilog: 8 circuits, main circuit hadder_1bit
module main (
  input  in_1,
  input  in_2,
  input  in_3,
  input  in_4,
  input  in_5,
  input  in_6,
  input  in_7,
  input  in_8,
  input  in_9,
  input  in_10,
  input  in_11,
  output [7:0] out_12,
  output [7:0] out_13
);

  registrador2 registrador2_1 (.in_1(out_12), .in_2(in_1), .in_3(in_2), .out_4(out_12));
  registrador2 registrador2_2 (.in_1(out_12), .in_2(in_3), .in_3(in_5), .out_4(out_12));
  registrador2 registrador2_3 (.in_1(out_12), .in_2(in_9), .in_3(in_6), .out_4(out_12));
  registrador2 registrador2_4 (.in_1(out_12), .in_2(in_11), .in_3(in_10), .out_4(out_12));
  registrador2 registrador2_5 (.in_1(out_12), .in_2(in_7), .in_3(in_4), .out_4(out_12));

  assign in_8 = in_7;
  assign out_13 = out_12;

  // Notes on the sheet:
  //   LETICIA NATIVIDADE
endmodule

module hadder_1bit (
  input  c_in,
  input  in_2,
  input  in_3,
  output out_4,
  output c_out
);

  wire and_1_out, and_2_out, and_3_out, xor_1_out;

  xor xor_1 (xor_1_out, in_2, in_3);
  and and_1 (and_1_out, in_2, c_in);
  and and_2 (and_2_out, in_2, in_3);
  and and_3 (and_3_out, in_3, c_in);
  xor xor_2 (out_4, xor_1_out, c_in);
  or or_1 (c_out, and_1_out, and_2_out, and_3_out);

  // Notes on the sheet:
  //   out
endmodule

module somador_8bits (
  input  [7:0] in_1,
  input  in_2,
  input  [7:0] in_3,
  output [7:0] out_4,
  output out_5
);

  wire hadder_1bit_1_c_out, hadder_1bit_2_c_out, hadder_1bit_3_c_out, hadder_1bit_4_c_out,
       hadder_1bit_5_c_out, hadder_1bit_6_c_out, hadder_1bit_7_c_out;

  hadder_1bit hadder_1bit_1 (
    .in_2(in_3[0]), .in_3(in_1[0]), .c_in(in_2), .c_out(hadder_1bit_1_c_out), .out_4(out_4[0]));
  hadder_1bit hadder_1bit_2 (
    .in_2(in_3[1]), .in_3(in_1[1]), .c_in(hadder_1bit_1_c_out), .c_out(hadder_1bit_2_c_out), .out_4(out_4[1]));
  hadder_1bit hadder_1bit_3 (
    .in_2(in_3[2]), .in_3(in_1[2]), .c_in(hadder_1bit_2_c_out), .c_out(hadder_1bit_3_c_out), .out_4(out_4[2]));
  hadder_1bit hadder_1bit_4 (
    .in_2(in_3[3]), .in_3(in_1[3]), .c_in(hadder_1bit_3_c_out), .c_out(hadder_1bit_4_c_out), .out_4(out_4[3]));
  hadder_1bit hadder_1bit_5 (
    .in_2(in_3[4]), .in_3(in_1[4]), .c_in(hadder_1bit_4_c_out), .c_out(hadder_1bit_5_c_out), .out_4(out_4[4]));
  hadder_1bit hadder_1bit_6 (
    .in_2(in_3[5]), .in_3(in_1[5]), .c_in(hadder_1bit_5_c_out), .c_out(hadder_1bit_6_c_out), .out_4(out_4[5]));
  hadder_1bit hadder_1bit_7 (
    .in_2(in_3[6]), .in_3(in_1[6]), .c_in(hadder_1bit_6_c_out), .c_out(hadder_1bit_7_c_out), .out_4(out_4[6]));
  hadder_1bit hadder_1bit_8 (
    .in_2(in_3[7]), .in_3(in_1[7]), .c_in(hadder_1bit_7_c_out), .c_out(out_5), .out_4(out_4[7]));
endmodule

module registrador (
  input  in_1,
  input  in_2,
  input  in_3,
  input  in_4,
  input  in_5,
  input  in_6,
  input  in_7,
  input  in_8,
  input  in_9,
  input  in_10,
  output out_11,
  output out_12,
  output out_13,
  output out_14,
  output out_15,
  output out_16,
  output out_17,
  output out_18
);

  wire enable_1_out_10, enable_1_out_11, enable_1_out_12, enable_1_out_13, enable_1_out_14, enable_1_out_15,
       enable_1_out_16, enable_1_out_17;

  enable enable_1 (
    .in_1(in_1), .in_2(in_2), .in_3(in_3), .in_4(in_4), .in_5(in_5), .in_6(in_6), .in_7(in_9), .in_8(in_10),
    .out_10(enable_1_out_10), .out_11(enable_1_out_11), .out_12(enable_1_out_12), .out_13(enable_1_out_13),
    .out_14(enable_1_out_14), .out_15(enable_1_out_15), .out_16(enable_1_out_16), .out_17(enable_1_out_17),
    .in_9(in_7));
  enable enable_2 (
    .in_1(enable_1_out_10), .in_2(enable_1_out_11), .in_3(enable_1_out_12), .in_4(enable_1_out_13),
    .in_5(enable_1_out_14), .in_6(enable_1_out_15), .in_7(enable_1_out_16), .in_8(enable_1_out_17),
    .out_10(out_11), .out_11(out_12), .out_12(out_13), .out_13(out_14), .out_14(out_15), .out_15(out_16),
    .out_16(out_17), .out_17(out_18), .in_9(in_8));
endmodule

module memory_1bit (
  input  in_1,
  input  in_2,
  output out_3
);

  wire nand_1_out, nand_2_out, nand_4_out;

  nand nand_1 (nand_1_out, in_1, in_2);
  nand nand_2 (nand_2_out, nand_1_out, in_2);
  nand nand_3 (out_3, nand_1_out, nand_4_out);
  nand nand_4 (nand_4_out, out_3, nand_2_out);
endmodule

module memory_8bits (
  input  in_1,
  input  in_2,
  input  in_3,
  input  in_4,
  input  in_5,
  input  in_6,
  input  in_7,
  input  in_8,
  input  e,
  output out_10,
  output out_11,
  output out_12,
  output out_13,
  output out_14,
  output out_15,
  output out_16,
  output out_17
);

  memory_1bit memory_1bit_1 (.in_1(in_1), .in_2(e), .out_3(out_10));
  memory_1bit memory_1bit_2 (.in_1(in_2), .in_2(e), .out_3(out_11));
  memory_1bit memory_1bit_3 (.in_1(in_3), .in_2(e), .out_3(out_12));
  memory_1bit memory_1bit_4 (.in_1(in_4), .in_2(e), .out_3(out_13));
  memory_1bit memory_1bit_5 (.in_1(in_5), .in_2(e), .out_3(out_14));
  memory_1bit memory_1bit_6 (.in_1(in_6), .in_2(e), .out_3(out_15));
  memory_1bit memory_1bit_7 (.in_1(in_7), .in_2(e), .out_3(out_16));
  memory_1bit memory_1bit_8 (.in_1(in_8), .in_2(e), .out_3(out_17));
endmodule

module enable (
  input  in_1,
  input  in_2,
  input  in_3,
  input  in_4,
  input  in_5,
  input  in_6,
  input  in_7,
  input  in_8,
  input  in_9,
  output out_10,
  output out_11,
  output out_12,
  output out_13,
  output out_14,
  output out_15,
  output out_16,
  output out_17
);

  and and_1 (out_10, in_1, in_9);
  and and_2 (out_11, in_2, in_9);
  and and_3 (out_12, in_3, in_9);
  and and_4 (out_13, in_4, in_9);
  and and_5 (out_14, in_5, in_9);
  and and_6 (out_15, in_6, in_9);
  and and_7 (out_16, in_7, in_9);
  and and_8 (out_17, in_8, in_9);
endmodule

module registrador2 (
  input  [7:0] in_1,
  input  in_2,
  input  in_3,
  output [7:0] out_4
);

  // registrador registrador_1: pin names not known; wires that end beside it: in_1[0], in_1[1], in_1[2], in_1[3], in_1[4], in_1[5], in_1[6], in_1[7], in_2, in_3, out_4[0], out_4[1], out_4[2], out_4[3], out_4[4], out_4[5], out_4[6], out_4[7]
endmodule
