// Logisim project beatriz_jacauna.circ as structural Verilog: 8 circuits, main circuit main
module main (
);


  // Notes on the sheet:
  //   Beatriz Jacauna Martins
  //   22351236
endmodule

module somador_1bit (
  input  c_in,
  input  in_2,
  input  in_3,
  output out,
  output c_out
);

  wire and_1_out, and_2_out, and_3_out, xor_1_out;

  and and_1 (and_1_out, in_2, c_in);
  and and_2 (and_2_out, in_2, in_3);
  and and_3 (and_3_out, in_3, c_in);
  xor xor_1 (xor_1_out, in_2, in_3);
  xor xor_2 (out, xor_1_out, c_in);
  or or_1 (c_out, and_1_out, and_2_out, and_3_out);
endmodule

module somador_8bitd (
  input  [7:0] a,
  input  cin,
  input  [7:0] b,
  output [7:0] outt,
  output cout
);

  wire somador_1bit_1_c_out, somador_1bit_2_c_out, somador_1bit_3_c_out, somador_1bit_4_c_out,
       somador_1bit_5_c_out, somador_1bit_6_c_out, somador_1bit_7_c_out;

  somador_1bit somador_1bit_1 (.in_2(a[0]), .in_3(b[0]), .c_in(cin), .c_out(somador_1bit_1_c_out), .out(outt[0]));
  somador_1bit somador_1bit_2 (
    .in_2(a[1]), .in_3(b[1]), .c_in(somador_1bit_1_c_out), .c_out(somador_1bit_2_c_out), .out(outt[1]));
  somador_1bit somador_1bit_3 (
    .in_2(a[2]), .in_3(b[2]), .c_in(somador_1bit_2_c_out), .c_out(somador_1bit_3_c_out), .out(outt[2]));
  somador_1bit somador_1bit_4 (
    .in_2(a[3]), .in_3(b[3]), .c_in(somador_1bit_3_c_out), .c_out(somador_1bit_4_c_out), .out(outt[3]));
  somador_1bit somador_1bit_5 (
    .in_2(a[4]), .in_3(b[4]), .c_in(somador_1bit_4_c_out), .c_out(somador_1bit_5_c_out), .out(outt[4]));
  somador_1bit somador_1bit_6 (
    .in_2(a[5]), .in_3(b[5]), .c_in(somador_1bit_5_c_out), .c_out(somador_1bit_6_c_out), .out(outt[5]));
  somador_1bit somador_1bit_7 (
    .in_2(a[6]), .in_3(b[6]), .c_in(somador_1bit_6_c_out), .c_out(somador_1bit_7_c_out), .out(outt[6]));
  somador_1bit somador_1bit_8 (.in_2(a[7]), .in_3(b[7]), .c_in(somador_1bit_7_c_out), .c_out(cout), .out(outt[7]));
endmodule

module memory_1bit (
  input  iniput,
  input  set,
  output outt
);

  wire nand_1_out, nand_2_out, nand_4_out;

  nand nand_1 (nand_1_out, iniput, set);
  nand nand_2 (nand_2_out, nand_1_out, set);
  nand nand_3 (outt, nand_1_out, nand_4_out);
  nand nand_4 (nand_4_out, outt, nand_2_out);
endmodule

module memory_8bits (
  input  [7:0] in_1,
  input  in_2,
  output [7:0] out_3
);

  memory_1bit memory_1bit_1 (.iniput(in_1[0]), .set(in_2), .outt(out_3[0]));
  memory_1bit memory_1bit_2 (.iniput(in_1[1]), .set(in_2), .outt(out_3[1]));
  memory_1bit memory_1bit_3 (.iniput(in_1[2]), .set(in_2), .outt(out_3[2]));
  memory_1bit memory_1bit_4 (.iniput(in_1[3]), .set(in_2), .outt(out_3[3]));
  memory_1bit memory_1bit_5 (.iniput(in_1[4]), .set(in_2), .outt(out_3[4]));
  memory_1bit memory_1bit_6 (.iniput(in_1[5]), .set(in_2), .outt(out_3[5]));
  memory_1bit memory_1bit_7 (.iniput(in_1[6]), .set(in_2), .outt(out_3[6]));
  memory_1bit memory_1bit_8 (.iniput(in_1[7]), .set(in_2), .outt(out_3[7]));
endmodule

module registrador (
  input  [7:0] in_1,
  input  in_2,
  input  in_3,
  input  in_4,
  input  in_5,
  input  in_6,
  input  in_7,
  input  in_8,
  input  in_9,
  output [7:0] out_10
);

  // Probe on in_1
  registrador_8bits registrador_8bits_1 (.in_1(in_1), .set(in_2), .enable(in_6), .out_4(in_1));
  registrador_8bits registrador_8bits_2 (.in_1(in_1), .set(in_3), .enable(in_7), .out_4(in_1));
  registrador_8bits registrador_8bits_3 (.in_1(in_1), .set(in_4), .enable(in_8), .out_4(in_1));
  registrador_8bits registrador_8bits_4 (.in_1(in_1), .set(in_5), .enable(in_9), .out_4(in_1));

  assign out_10 = in_1;
endmodule

module regis (
  input  in_1,
  input  in_2,
  input  in_3,
  output out_4
);

  wire memory_1bit_1_outt;

  memory_1bit memory_1bit_1 (.iniput(in_1), .set(in_2), .outt(memory_1bit_1_outt));
  assign out_4 = in_3 ? memory_1bit_1_outt : 1'bz;  // Controlled_Buffer controlled_buffer_1
endmodule

module registrador_8bits (
  input  [7:0] in_1,
  input  set,
  input  enable,
  output [7:0] out_4
);

  regis regis_1 (.in_1(in_1[0]), .in_2(set), .in_3(enable), .out_4(out_4[0]));
  regis regis_2 (.in_1(in_1[1]), .in_2(set), .in_3(enable), .out_4(out_4[1]));
  regis regis_3 (.in_1(in_1[2]), .in_2(set), .in_3(enable), .out_4(out_4[2]));
  regis regis_4 (.in_1(in_1[3]), .in_2(set), .in_3(enable), .out_4(out_4[3]));
  regis regis_5 (.in_1(in_1[4]), .in_2(set), .in_3(enable), .out_4(out_4[4]));
  regis regis_6 (.in_1(in_1[5]), .in_2(set), .in_3(enable), .out_4(out_4[5]));
  regis regis_7 (.in_1(in_1[6]), .in_2(set), .in_3(enable), .out_4(out_4[6]));
  regis regis_8 (.in_1(in_1[7]), .in_2(set), .in_3(enable), .out_4(out_4[7]));
endmodule
