// Logisim project gabriel_rafael_lima_ferreira.circ as structural Verilog: 5 circuits, main circuit main
module main (
  input  c_in,
  input  [7:0] a,
  input  [7:0] in_3,
  input  in_4,
  input  [7:0] in_5,
  input  set,
  input  in_7,
  input  in_8,
  input  in_9,
  input  enable,
  input  in_11,
  input  in_12,
  input  in_13,
  output [7:0] out_14
);

  wire [7:0] memory_8bits_enable_set_1_out_4, memory_8bits_enable_set_2_out_4,
       memory_8bits_enable_set_3_out_4, memory_8bits_enable_set_4_out_4;

  // Probe on in_5
  Somador_8bits somador_8bits_1 (.in_2(a), .in_3(in_3), .c_in(c_in), .c_out(in_4), .out_4(out_14));
  memory_8bits_enable_set memory_8bits_enable_set_1 (
    .in_1(in_5), .in_2(set), .in_3(enable), .out_4(memory_8bits_enable_set_1_out_4));
  // Probe on memory_8bits_enable_set_1_out_4
  memory_8bits_enable_set memory_8bits_enable_set_2 (
    .in_1(in_5), .in_2(in_7), .in_3(in_11), .out_4(memory_8bits_enable_set_2_out_4));
  // Probe on memory_8bits_enable_set_2_out_4
  memory_8bits_enable_set memory_8bits_enable_set_3 (
    .in_1(in_5), .in_2(in_8), .in_3(in_12), .out_4(memory_8bits_enable_set_3_out_4));
  // Probe on memory_8bits_enable_set_3_out_4
  memory_8bits_enable_set memory_8bits_enable_set_4 (
    .in_1(in_5), .in_2(in_9), .in_3(in_13), .out_4(memory_8bits_enable_set_4_out_4));
  // Probe on memory_8bits_enable_set_4_out_4

  // Notes on the sheet:
  //   b
  //   Gabriel Rafael Lima Ferreira
  //   Somador completo - 8 bits
  //   4 registradores em barramento
  //   c_out
  //   out
endmodule

module Somador_8bits (
  input  c_in,
  input  [7:0] in_2,
  input  [7:0] in_3,
  output [7:0] out_4,
  output c_out
);

  wire somador_1bit_1_c_out, somador_1bit_2_c_out, somador_1bit_3_c_out, somador_1bit_4_c_out,
       somador_1bit_5_c_out, somador_1bit_6_c_out, somador_1bit_7_c_out;

  Somador_1bit somador_1bit_1 (.a(in_2[0]), .b(in_3[0]), .c_in(c_in), .c_out(somador_1bit_1_c_out), .out(out_4[0]));
  Somador_1bit somador_1bit_2 (
    .a(in_2[1]), .b(in_3[1]), .c_in(somador_1bit_1_c_out), .c_out(somador_1bit_2_c_out), .out(out_4[1]));
  Somador_1bit somador_1bit_3 (
    .a(in_2[2]), .b(in_3[2]), .c_in(somador_1bit_2_c_out), .c_out(somador_1bit_3_c_out), .out(out_4[2]));
  Somador_1bit somador_1bit_4 (
    .a(in_2[3]), .b(in_3[3]), .c_in(somador_1bit_3_c_out), .c_out(somador_1bit_4_c_out), .out(out_4[3]));
  Somador_1bit somador_1bit_5 (
    .a(in_2[4]), .b(in_3[4]), .c_in(somador_1bit_4_c_out), .c_out(somador_1bit_5_c_out), .out(out_4[4]));
  Somador_1bit somador_1bit_6 (
    .a(in_2[5]), .b(in_3[5]), .c_in(somador_1bit_5_c_out), .c_out(somador_1bit_6_c_out), .out(out_4[5]));
  Somador_1bit somador_1bit_7 (
    .a(in_2[6]), .b(in_3[6]), .c_in(somador_1bit_6_c_out), .c_out(somador_1bit_7_c_out), .out(out_4[6]));
  Somador_1bit somador_1bit_8 (.a(in_2[7]), .b(in_3[7]), .c_in(somador_1bit_7_c_out), .c_out(c_out), .out(out_4[7]));

  // Notes on the sheet:
  //   a
  //   b
  //   Somador - 8 bits
  //   out
endmodule

module Somador_1bit (
  input  c_in,
  input  a,
  input  b,
  output out,
  output c_out
);

  wire and_1_out, and_2_out, and_3_out, xor_1_out;

  xor xor_1 (xor_1_out, a, b);
  and and_1 (and_1_out, a, c_in);
  and and_2 (and_2_out, a, b);
  and and_3 (and_3_out, b, c_in);
  xor xor_2 (out, xor_1_out, c_in);
  or or_1 (c_out, and_1_out, and_2_out, and_3_out);

  // Notes on the sheet:
  //   Somador Completo - 1 bit
endmodule

module memory_8bits_enable_set (
  input  [7:0] in_1,
  input  in_2,
  input  in_3,
  output [7:0] out_4
);

  wire memory_1bit_1_out_3, memory_1bit_2_out_3, memory_1bit_3_out_3, memory_1bit_4_out_3,
       memory_1bit_5_out_3, memory_1bit_6_out_3, memory_1bit_7_out_3, memory_1bit_8_out_3;

  memory_1bit memory_1bit_1 (.in_1(in_1[0]), .in_2(in_2), .out_3(memory_1bit_1_out_3));
  memory_1bit memory_1bit_2 (.in_1(in_1[1]), .in_2(in_2), .out_3(memory_1bit_2_out_3));
  memory_1bit memory_1bit_3 (.in_1(in_1[2]), .in_2(in_2), .out_3(memory_1bit_3_out_3));
  memory_1bit memory_1bit_4 (.in_1(in_1[3]), .in_2(in_2), .out_3(memory_1bit_4_out_3));
  memory_1bit memory_1bit_5 (.in_1(in_1[4]), .in_2(in_2), .out_3(memory_1bit_5_out_3));
  memory_1bit memory_1bit_6 (.in_1(in_1[5]), .in_2(in_2), .out_3(memory_1bit_6_out_3));
  memory_1bit memory_1bit_7 (.in_1(in_1[6]), .in_2(in_2), .out_3(memory_1bit_7_out_3));
  memory_1bit memory_1bit_8 (.in_1(in_1[7]), .in_2(in_2), .out_3(memory_1bit_8_out_3));
  assign out_4[0] = in_3 ? memory_1bit_1_out_3 : 1'bz;  // Controlled_Buffer controlled_buffer_1
  assign out_4[1] = in_3 ? memory_1bit_2_out_3 : 1'bz;  // Controlled_Buffer controlled_buffer_2
  assign out_4[2] = in_3 ? memory_1bit_3_out_3 : 1'bz;  // Controlled_Buffer controlled_buffer_3
  assign out_4[3] = in_3 ? memory_1bit_4_out_3 : 1'bz;  // Controlled_Buffer controlled_buffer_4
  assign out_4[4] = in_3 ? memory_1bit_5_out_3 : 1'bz;  // Controlled_Buffer controlled_buffer_5
  assign out_4[5] = in_3 ? memory_1bit_6_out_3 : 1'bz;  // Controlled_Buffer controlled_buffer_6
  assign out_4[6] = in_3 ? memory_1bit_7_out_3 : 1'bz;  // Controlled_Buffer controlled_buffer_7
  assign out_4[7] = in_3 ? memory_1bit_8_out_3 : 1'bz;  // Controlled_Buffer controlled_buffer_8

  // Notes on the sheet:
  //   Memory 8 bits enable-set
endmodule

module memory_1bit (
  input  in_1,
  input  in_2,
  output out_3
);

  wire nand_1_out, nand_2_out, nand_4_out;

  nand nand_1 (nand_1_out, in_1, in_2);
  nand nand_2 (nand_2_out, nand_1_out, in_2);
  nand nand_3 (out_3, nand_1_out, nand_4_out);
  nand nand_4 (nand_4_out, out_3, nand_2_out);

  // Notes on the sheet:
  //   Flip-Flop
endmodule
