// Logisim project gabriela_malveira.circ as structural Verilog: 11 circuits, main circuit main
module main (
  input  [7:0] in_1,
  input  in_2,
  input  set_a,
  input  enable_a,
  input  set_b,
  input  enable_b,
  input  set_c,
  input  enable_c,
  input  set_d,
  input  enable_d,
  output [7:0] out_11
);

  wire [7:0] registrador_1byte_1_out_a, registrador_1byte_2_out_a, registrador_1byte_3_out_a,
       registrador_1byte_4_out_a;

  // Probe on out_11
  assign out_11 = in_2 ? in_1 : 8'bz;  // Controlled_Buffer controlled_buffer_1
  registrador_1byte registrador_1byte_1 (
    .input_a(out_11), .set(set_a), .enable(enable_a), .out_a(registrador_1byte_1_out_a));
  assign out_11 = enable_a ? registrador_1byte_1_out_a : 8'bz;  // Controlled_Buffer controlled_buffer_2
  assign out_11 = enable_b ? registrador_1byte_2_out_a : 8'bz;  // Controlled_Buffer controlled_buffer_3
  registrador_1byte registrador_1byte_2 (
    .input_a(out_11), .set(set_b), .enable(enable_b), .out_a(registrador_1byte_2_out_a));
  registrador_1byte registrador_1byte_3 (
    .input_a(out_11), .set(set_c), .enable(enable_c), .out_a(registrador_1byte_3_out_a));
  assign out_11 = enable_c ? registrador_1byte_3_out_a : 8'bz;  // Controlled_Buffer controlled_buffer_4
  assign out_11 = enable_d ? registrador_1byte_4_out_a : 8'bz;  // Controlled_Buffer controlled_buffer_5
  registrador_1byte registrador_1byte_4 (
    .input_a(out_11), .set(set_d), .enable(enable_d), .out_a(registrador_1byte_4_out_a));

  // Notes on the sheet:
  //   Gabriela Malveira - 22250539
endmodule

module somador_1bit (
  input  c_in,
  input  a,
  input  b,
  output c,
  output c_out
);

  wire and_1_out, and_2_out, and_3_out, xor_1_out;

  and and_1 (and_1_out, a, b);
  and and_2 (and_2_out, a, b);
  and and_3 (and_3_out, b, c_in);
  xor xor_1 (xor_1_out, a, b);
  xor xor_2 (c, xor_1_out, c_in);
  or or_1 (c_out, and_1_out, and_2_out, and_3_out);
endmodule

module somador_8bit (
  input  in_1,
  input  [7:0] in_2,
  input  [7:0] in_3,
  output [7:0] out_4
);

  wire somador_1bit_1_c_out, somador_1bit_2_c_out, somador_1bit_3_c_out, somador_1bit_4_c_out,
       somador_1bit_5_c_out, somador_1bit_6_c_out, somador_1bit_7_c_out;

  somador_1bit somador_1bit_1 (.a(in_2[0]), .b(in_3[0]), .c_in(in_1), .c_out(somador_1bit_1_c_out), .c(out_4[0]));
  somador_1bit somador_1bit_2 (
    .a(in_2[1]), .b(in_3[1]), .c_in(somador_1bit_1_c_out), .c_out(somador_1bit_2_c_out), .c(out_4[1]));
  somador_1bit somador_1bit_3 (
    .a(in_2[2]), .b(in_3[2]), .c_in(somador_1bit_2_c_out), .c_out(somador_1bit_3_c_out), .c(out_4[2]));
  somador_1bit somador_1bit_4 (
    .a(in_2[3]), .b(in_3[3]), .c_in(somador_1bit_3_c_out), .c_out(somador_1bit_4_c_out), .c(out_4[3]));
  somador_1bit somador_1bit_5 (
    .a(in_2[4]), .b(in_3[4]), .c_in(somador_1bit_4_c_out), .c_out(somador_1bit_5_c_out), .c(out_4[4]));
  somador_1bit somador_1bit_6 (
    .a(in_2[5]), .b(in_3[5]), .c_in(somador_1bit_5_c_out), .c_out(somador_1bit_6_c_out), .c(out_4[5]));
  somador_1bit somador_1bit_7 (
    .a(in_2[6]), .b(in_3[6]), .c_in(somador_1bit_6_c_out), .c_out(somador_1bit_7_c_out), .c(out_4[6]));
  somador_1bit somador_1bit_8 (.a(in_2[7]), .b(in_3[7]), .c_in(somador_1bit_7_c_out), .c(out_4[7]));  // open: c_out
endmodule

module registrador_1bit (
  input  in_1,
  input  in_2,
  output out_3
);

  wire nand_1_out, nand_2_out, nand_4_out;

  nand nand_1 (nand_1_out, in_1, in_2);
  nand nand_2 (nand_2_out, in_2, nand_1_out);
  nand nand_3 (out_3, nand_1_out, nand_4_out);
  nand nand_4 (nand_4_out, out_3, nand_2_out);
endmodule

module set_8bit (
  input  i0,
  input  i1,
  input  i2,
  input  i3,
  input  i4,
  input  i5,
  input  i6,
  input  i7,
  input  Set,
  output out_10,
  output out_11,
  output out_12,
  output out_13,
  output out_14,
  output out_15,
  output out_16,
  output out_17
);

  registrador_1bit registrador_1bit_1 (.in_1(i0), .in_2(Set), .out_3(out_10));
  registrador_1bit registrador_1bit_2 (.in_1(i1), .in_2(Set), .out_3(out_11));
  registrador_1bit registrador_1bit_3 (.in_1(i2), .in_2(Set), .out_3(out_12));
  registrador_1bit registrador_1bit_4 (.in_1(i3), .in_2(Set), .out_3(out_13));
  registrador_1bit registrador_1bit_5 (.in_1(i4), .in_2(Set), .out_3(out_14));
  registrador_1bit registrador_1bit_6 (.in_1(i5), .in_2(Set), .out_3(out_15));
  registrador_1bit registrador_1bit_7 (.in_1(i6), .in_2(Set), .out_3(out_16));
  registrador_1bit registrador_1bit_8 (.in_1(i7), .in_2(Set), .out_3(out_17));
endmodule

module memoria_1byte (
  input  i0,
  input  i1,
  input  i2,
  input  i3,
  input  i4,
  input  i5,
  input  i6,
  input  i7,
  input  set,
  input  enable,
  output out_11,
  output out_12,
  output out_13,
  output out_14,
  output out_15,
  output out_16,
  output out_17,
  output out_18
);

  wire set_8bit_1_out_10, set_8bit_1_out_11, set_8bit_1_out_12, set_8bit_1_out_13, set_8bit_1_out_14,
       set_8bit_1_out_15, set_8bit_1_out_16, set_8bit_1_out_17;

  set_8bit set_8bit_1 (
    .i0(i0), .i1(i1), .i2(i2), .i3(i3), .i4(i4), .i5(i5), .i6(i6), .i7(i7), .Set(set),
    .out_10(set_8bit_1_out_10), .out_11(set_8bit_1_out_11), .out_12(set_8bit_1_out_12),
    .out_13(set_8bit_1_out_13), .out_14(set_8bit_1_out_14), .out_15(set_8bit_1_out_15),
    .out_16(set_8bit_1_out_16), .out_17(set_8bit_1_out_17));
  enable_8bit enable_8bit_1 (
    .in_1(set_8bit_1_out_10), .in_2(set_8bit_1_out_11), .in_3(set_8bit_1_out_12), .in_4(set_8bit_1_out_13),
    .in_5(set_8bit_1_out_14), .in_6(set_8bit_1_out_15), .in_7(set_8bit_1_out_16), .in_8(set_8bit_1_out_17),
    .in_9(enable), .out_10(out_11), .out_11(out_12), .out_12(out_13), .out_13(out_14), .out_14(out_15),
    .out_15(out_16), .out_16(out_17), .out_17(out_18));
endmodule

module memoria_1bit (
  input  in_1,
  input  in_2,
  output out_3
);

  registrador_1bit registrador_1bit_1 (.in_1(in_1), .in_2(in_2), .out_3(out_3));
endmodule

module memoria_2bit (
  input  i1,
  input  i2,
  input  set,
  output o1,
  output o2
);

  registrador_1bit registrador_1bit_1 (.in_1(i1), .in_2(set), .out_3(o1));
  registrador_1bit registrador_1bit_2 (.in_1(i2), .in_2(set), .out_3(o2));
endmodule

module memoria_8bit (
  input  in_1,
  input  in_2,
  input  in_3,
  input  in_4,
  input  in_5,
  input  in_6,
  input  in_7,
  input  in_8,
  input  in_9,
  output out_10,
  output out_11,
  output out_12,
  output out_13,
  output out_14,
  output out_15,
  output out_16,
  output out_17
);

  registrador_1bit registrador_1bit_1 (.in_1(in_1), .in_2(in_9), .out_3(out_10));
  registrador_1bit registrador_1bit_2 (.in_1(in_2), .in_2(in_9), .out_3(out_11));
  registrador_1bit registrador_1bit_3 (.in_1(in_3), .in_2(in_9), .out_3(out_12));
  registrador_1bit registrador_1bit_4 (.in_1(in_4), .in_2(in_9), .out_3(out_13));
  registrador_1bit registrador_1bit_5 (.in_1(in_5), .in_2(in_9), .out_3(out_14));
  registrador_1bit registrador_1bit_6 (.in_1(in_6), .in_2(in_9), .out_3(out_15));
  registrador_1bit registrador_1bit_7 (.in_1(in_7), .in_2(in_9), .out_3(out_16));
  registrador_1bit registrador_1bit_8 (.in_1(in_8), .in_2(in_9), .out_3(out_17));
endmodule

module registrador_1byte (
  input  [7:0] input_a,
  input  set,
  input  enable,
  output [7:0] out_a
);

  memoria_1byte memoria_1byte_1 (
    .i0(input_a[0]), .i1(input_a[1]), .i2(input_a[2]), .i3(input_a[3]), .i4(input_a[4]), .i5(input_a[5]),
    .i6(input_a[6]), .i7(input_a[7]), .set(set), .enable(enable), .out_11(out_a[0]), .out_12(out_a[1]),
    .out_13(out_a[2]), .out_14(out_a[3]), .out_15(out_a[4]), .out_16(out_a[5]), .out_17(out_a[6]),
    .out_18(out_a[7]));
endmodule

module enable_8bit (
  input  in_1,
  input  in_2,
  input  in_3,
  input  in_4,
  input  in_5,
  input  in_6,
  input  in_7,
  input  in_8,
  input  in_9,
  output out_10,
  output out_11,
  output out_12,
  output out_13,
  output out_14,
  output out_15,
  output out_16,
  output out_17
);

  and and_1 (out_10, in_1, in_9);
  and and_2 (out_11, in_2, in_9);
  and and_3 (out_12, in_3, in_9);
  and and_4 (out_13, in_4, in_9);
  and and_5 (out_14, in_5, in_9);
  and and_6 (out_15, in_6, in_9);
  and and_7 (out_16, in_7, in_9);
  and and_8 (out_17, in_8, in_9);
endmodule
