// Logisim project giovana.circ as structural Verilog: 7 circuits, main circuit main
module main (
  input  in_1,
  input  in_2,
  input  in_3,
  input  in_4,
  input  [7:0] in_5,
  input  [7:0] in_6,
  output out_7,
  output out_8,
  output [7:0] out_9,
  output out_10
);

  Somador_1bit somador_1bit_1 (.in_2(in_2), .in_3(in_3), .in_1(in_1), .out_4(out_7));  // open: out_5
  somador_8bits somador_8bits_1 (.in_2(in_5), .in_3(in_6), .out_5(out_10), .out_4(out_9));  // open: in_1

  assign out_8 = out_7;

  // Notes on the sheet:
  //   Giovana Lago Moraes Cavalcante
  //   matricula:
  //   22450968
endmodule

module Somador_1bit (
  input  in_1,
  input  in_2,
  input  in_3,
  output out_4,
  output out_5
);

  wire and_1_out, and_2_out, and_3_out, xor_1_out;

  xor xor_1 (xor_1_out, in_2, in_3);
  and and_1 (and_1_out, in_2, in_3);
  and and_2 (and_2_out, in_2, in_3);
  and and_3 (and_3_out, in_3, in_1);
  xor xor_2 (out_4, xor_1_out, in_1);
  or or_1 (out_5, and_1_out, and_3_out);
endmodule

module somador_8bits (
  input  in_1,
  input  [7:0] in_2,
  input  [7:0] in_3,
  output [7:0] out_4,
  output out_5
);

  wire somador_1bit_1_out_5, somador_1bit_2_out_5, somador_1bit_3_out_5, somador_1bit_4_out_5,
       somador_1bit_5_out_5, somador_1bit_6_out_5, somador_1bit_7_out_5;

  Somador_1bit somador_1bit_1 (
    .in_2(in_2[0]), .in_3(in_2[0]), .in_1(in_1), .out_5(somador_1bit_1_out_5), .out_4(out_4[0]));
  Somador_1bit somador_1bit_2 (
    .in_2(in_2[1]), .in_3(in_2[4]), .in_1(somador_1bit_1_out_5), .out_5(somador_1bit_2_out_5),
    .out_4(out_4[1]));
  Somador_1bit somador_1bit_3 (
    .in_2(in_2[2]), .in_3(in_3[2]), .in_1(somador_1bit_2_out_5), .out_5(somador_1bit_3_out_5),
    .out_4(out_4[2]));
  Somador_1bit somador_1bit_4 (
    .in_2(in_2[3]), .in_3(in_3[3]), .in_1(somador_1bit_3_out_5), .out_5(somador_1bit_4_out_5),
    .out_4(out_4[3]));
  Somador_1bit somador_1bit_5 (
    .in_2(in_2[4]), .in_3(in_3[4]), .in_1(somador_1bit_4_out_5), .out_5(somador_1bit_5_out_5),
    .out_4(out_4[4]));
  Somador_1bit somador_1bit_6 (
    .in_2(in_2[5]), .in_3(in_3[5]), .in_1(somador_1bit_5_out_5), .out_5(somador_1bit_6_out_5),
    .out_4(out_4[5]));
  Somador_1bit somador_1bit_7 (
    .in_2(in_2[6]), .in_3(in_3[6]), .in_1(somador_1bit_6_out_5), .out_5(somador_1bit_7_out_5),
    .out_4(out_4[6]));
  Somador_1bit somador_1bit_8 (
    .in_2(in_2[7]), .in_3(in_3[7]), .in_1(somador_1bit_7_out_5), .out_5(out_5), .out_4(out_4[7]));

  assign in_3[1:0] = {in_2[4], in_2[0]};
endmodule

module memory_1bit (
  input  \input ,
  input  set,
  output cot
);

  wire nand_1_out, nand_2_out, nand_4_out;

  nand nand_1 (nand_1_out, \input , set);
  nand nand_2 (nand_2_out, set, nand_1_out);
  nand nand_3 (cot, nand_1_out, nand_4_out);
  nand nand_4 (nand_4_out, cot, nand_2_out);
endmodule

module memory_8bits (
  input  in_1,
  input  in_2,
  input  in_3,
  input  in_4,
  input  in_5,
  input  in_6,
  input  in_7,
  input  in_8,
  input  in_9,
  output out_10,
  output out_11,
  output out_12,
  output out_13,
  output out_14,
  output out_15,
  output out_16,
  output out_17
);

  memory_1bit memory_1bit_1 (.\input (in_1), .set(in_9), .cot(out_10));
  memory_1bit memory_1bit_2 (.\input (in_2), .set(in_9), .cot(out_11));
  memory_1bit memory_1bit_3 (.\input (in_3), .set(in_9), .cot(out_12));
  memory_1bit memory_1bit_4 (.\input (in_4), .set(in_9), .cot(out_13));
  memory_1bit memory_1bit_5 (.\input (in_5), .set(in_9), .cot(out_14));
  memory_1bit memory_1bit_6 (.\input (in_6), .set(in_9), .cot(out_15));
  memory_1bit memory_1bit_7 (.\input (in_7), .set(in_9), .cot(out_16));
  memory_1bit memory_1bit_8 (.\input (in_8), .set(in_9), .cot(out_17));
endmodule

module memoria_1bitSET (
  input  in_1,
  input  in_2,
  input  in_3,
  input  in_4,
  input  in_5,
  input  in_6,
  input  in_7,
  input  in_8,
  input  in_9,
  input  in_10,
  output out_11,
  output out_12,
  output out_13,
  output out_14,
  output out_15,
  output out_16,
  output out_17,
  output out_18
);

  wire memory_8bits_1_out_10, memory_8bits_1_out_11, memory_8bits_1_out_12, memory_8bits_1_out_13,
       memory_8bits_1_out_14, memory_8bits_1_out_15, memory_8bits_1_out_16, memory_8bits_1_out_17;

  memory_8bits memory_8bits_1 (
    .in_1(in_1), .in_2(in_2), .in_3(in_3), .in_4(in_4), .in_5(in_5), .in_6(in_6), .in_7(in_7), .in_8(in_8),
    .in_9(in_9), .out_10(memory_8bits_1_out_10), .out_11(memory_8bits_1_out_11),
    .out_12(memory_8bits_1_out_12), .out_13(memory_8bits_1_out_13), .out_14(memory_8bits_1_out_14),
    .out_15(memory_8bits_1_out_15), .out_16(memory_8bits_1_out_16), .out_17(memory_8bits_1_out_17));
  enable enable_1 (
    .in_1(memory_8bits_1_out_10), .in_2(memory_8bits_1_out_11), .in_3(memory_8bits_1_out_12),
    .in_4(memory_8bits_1_out_13), .in_5(memory_8bits_1_out_14), .in_6(memory_8bits_1_out_15),
    .in_7(memory_8bits_1_out_16), .in_8(memory_8bits_1_out_17), .in_9(in_10), .out_10(out_11),
    .out_11(out_12), .out_12(out_13), .out_13(out_14), .out_14(out_15), .out_15(out_16), .out_16(out_17),
    .out_17(out_18));
endmodule

module enable (
  input  in_1,
  input  in_2,
  input  in_3,
  input  in_4,
  input  in_5,
  input  in_6,
  input  in_7,
  input  in_8,
  input  in_9,
  output out_10,
  output out_11,
  output out_12,
  output out_13,
  output out_14,
  output out_15,
  output out_16,
  output out_17
);

  and and_1 (out_10, in_1, in_9);
  and and_2 (out_11, in_2, in_9);
  and and_3 (out_12, in_3, in_9);
  and and_4 (out_13, in_4, in_9);
  and and_5 (out_14, in_5, in_9);
  and and_6 (out_15, in_6, in_9);
  and and_7 (out_16, in_7, in_9);
  and and_8 (out_17, in_8, in_9);
endmodule
