// Logisim project iris_camille_esteves_guimaraes.circ as structural Verilog: 1 circuit, main circuit main
module main (
  input  [7:0] in_1,
  input  in_2,
  input  [1:0] in_3,
  input  in_4,
  input  in_5,
  input  in_6,
  input  in_7,
  input  [1:0] in_8,
  input  in_9,
  input  in_10,
  input  in_11,
  input  in_12,
  output [7:0] out_13
);

  wire [7:0] demultiplexer_1_out0, demultiplexer_1_out1, demultiplexer_1_out2, demultiplexer_1_out3,
       multiplexer_1_out, register_1_q, register_2_q, register_3_q, register_4_q;

  Demultiplexer #(.select(2), .width(8)) demultiplexer_1 (
    .out0(demultiplexer_1_out0), .out1(demultiplexer_1_out1), .out2(demultiplexer_1_out2),
    .out3(demultiplexer_1_out3), .in(in_1), .sel(in_3));
  Register register_1 (.D(demultiplexer_1_out0), .en(in_4), .clk(in_9), .Q(register_1_q));  // open: clr
  Register register_2 (.D(demultiplexer_1_out1), .en(in_5), .clk(in_10), .Q(register_2_q));  // open: clr
  Register register_3 (.D(demultiplexer_1_out2), .en(in_6), .clk(in_11), .Q(register_3_q));  // open: clr
  Register register_4 (.D(demultiplexer_1_out3), .en(in_7), .clk(in_12), .Q(register_4_q));  // open: clr
  Multiplexer #(.select(2), .width(8)) multiplexer_1 (
    .in0(register_1_q), .in1(register_2_q), .in2(register_3_q), .in3(register_4_q), .out(multiplexer_1_out),
    .sel(in_8));
  Multiplexer #(.width(8)) multiplexer_2 (.in0(in_1), .in1(multiplexer_1_out), .out(out_13), .sel(in_2));

  // Notes on the sheet:
  //   Íris Camille Esteves Guimarães 
  //   Matrícula 22450969
endmodule
