// Logisim project josue_brito_moura.circ as structural Verilog: 7 circuits, main circuit main
module main (
  input  in_1,
  input  [7:0] in_2,
  input  [7:0] in_3,
  input  [7:0] in_4,
  input  in_5,
  input  in_6,
  output [7:0] out_7,
  output out_8,
  output [7:0] out_9
);

  Memoria_set_enable memoria_set_enable_1 (
    .in_1(in_4[0]), .in_2(in_4[1]), .in_3(in_4[2]), .in_4(in_4[3]), .in_5(in_4[4]), .in_8(in_4[5]),
    .in_9(in_4[6]), .in_10(in_4[7]), .in_6(in_5), .in_7(in_6), .out_11(out_9[0]), .out_12(out_9[1]),
    .out_13(out_9[2]), .out_14(out_9[3]), .out_15(out_9[4]), .out_16(out_9[5]), .out_17(out_9[6]),
    .out_18(out_9[7]));
  Somador8bits somador8bits_1 (.in_2(in_2), .in_3(in_3), .in_1(in_1), .out_5(out_8), .out_4(out_7));

  // Notes on the sheet:
  //   Josue Brito Moura
  //   Matricula: 22450967
  //   Registrador de 8 bits
  //   Somador de 8 bits
endmodule

module meio_somador (
  input  in_1,
  input  in_2,
  input  in_3,
  output out_4,
  output out_5
);

  wire and_1_out, and_2_out, and_3_out, xor_1_out;

  xor xor_1 (xor_1_out, in_2, in_3);
  and and_1 (and_1_out, in_2, in_1);
  and and_2 (and_2_out, in_2, in_3);
  and and_3 (and_3_out, in_3, in_1);
  xor xor_2 (out_4, xor_1_out, in_1);
  or or_1 (out_5, and_1_out, and_2_out, and_3_out);
endmodule

module Somador8bits (
  input  in_1,
  input  [7:0] in_2,
  input  [7:0] in_3,
  output [7:0] out_4,
  output out_5
);

  wire meio_somador_1_out_5, meio_somador_2_out_5, meio_somador_3_out_5, meio_somador_4_out_5,
       meio_somador_5_out_5, meio_somador_6_out_5, meio_somador_8_out_5;

  meio_somador meio_somador_1 (
    .in_2(in_2[4]), .in_3(in_3[4]), .in_1(meio_somador_2_out_5), .out_5(meio_somador_1_out_5),
    .out_4(out_4[4]));
  meio_somador meio_somador_2 (
    .in_2(in_2[3]), .in_3(in_3[3]), .in_1(meio_somador_3_out_5), .out_5(meio_somador_2_out_5),
    .out_4(out_4[3]));
  meio_somador meio_somador_3 (
    .in_2(in_2[2]), .in_3(in_3[2]), .in_1(meio_somador_4_out_5), .out_5(meio_somador_3_out_5),
    .out_4(out_4[2]));
  meio_somador meio_somador_4 (
    .in_2(in_2[1]), .in_3(in_3[1]), .in_1(meio_somador_8_out_5), .out_5(meio_somador_4_out_5),
    .out_4(out_4[1]));
  meio_somador meio_somador_5 (
    .in_2(in_2[5]), .in_3(in_3[5]), .in_1(meio_somador_1_out_5), .out_5(meio_somador_5_out_5),
    .out_4(out_4[5]));
  meio_somador meio_somador_6 (
    .in_2(in_2[6]), .in_3(in_3[6]), .in_1(meio_somador_5_out_5), .out_5(meio_somador_6_out_5),
    .out_4(out_4[6]));
  meio_somador meio_somador_7 (
    .in_2(in_2[7]), .in_3(in_3[7]), .in_1(meio_somador_6_out_5), .out_5(out_5), .out_4(out_4[7]));
  meio_somador meio_somador_8 (
    .in_2(in_2[0]), .in_3(in_3[0]), .in_1(in_1), .out_5(meio_somador_8_out_5), .out_4(out_4[0]));
endmodule

module Registrador (
  input  in_1,
  input  in_2,
  input  in_3,
  input  in_4,
  input  in_5,
  input  in_6,
  input  in_7,
  input  in_8,
  input  in_9,
  output out_10,
  output out_11,
  output out_12,
  output out_13,
  output out_14,
  output out_15,
  output out_16,
  output out_17
);

  Circuito circuito_1 (.in_1(in_1), .in_2(in_9), .out_3(out_10));
  Circuito circuito_2 (.in_1(in_2), .in_2(in_9), .out_3(out_11));
  Circuito circuito_3 (.in_1(in_3), .in_2(in_9), .out_3(out_12));
  Circuito circuito_4 (.in_1(in_4), .in_2(in_9), .out_3(out_13));
  Circuito circuito_5 (.in_1(in_5), .in_2(in_9), .out_3(out_14));
  Circuito circuito_6 (.in_1(in_6), .in_2(in_9), .out_3(out_15));
  Circuito circuito_7 (.in_1(in_7), .in_2(in_9), .out_3(out_16));
  Circuito circuito_8 (.in_1(in_8), .in_2(in_9), .out_3(out_17));

  // Notes on the sheet:
  //   Registrador
endmodule

module Memoria_set_enable (
  input  in_1,
  input  in_2,
  input  in_3,
  input  in_4,
  input  in_5,
  input  in_6,
  input  in_7,
  input  in_8,
  input  in_9,
  input  in_10,
  output out_11,
  output out_12,
  output out_13,
  output out_14,
  output out_15,
  output out_16,
  output out_17,
  output out_18
);

  wire registrador_1_out_10, registrador_1_out_11, registrador_1_out_12, registrador_1_out_13,
       registrador_1_out_14, registrador_1_out_15, registrador_1_out_16, registrador_1_out_17;

  Registrador registrador_1 (
    .in_1(in_1), .in_2(in_2), .in_3(in_3), .in_4(in_4), .in_5(in_5), .in_6(in_8), .in_7(in_9), .in_8(in_10),
    .in_9(in_6), .out_10(registrador_1_out_10), .out_11(registrador_1_out_11), .out_12(registrador_1_out_12),
    .out_13(registrador_1_out_13), .out_14(registrador_1_out_14), .out_15(registrador_1_out_15),
    .out_16(registrador_1_out_16), .out_17(registrador_1_out_17));
  enable enable_1 (
    .in_1(registrador_1_out_10), .in_2(registrador_1_out_11), .in_3(registrador_1_out_12),
    .in_4(registrador_1_out_13), .in_5(registrador_1_out_14), .in_6(registrador_1_out_15),
    .in_7(registrador_1_out_16), .in_8(registrador_1_out_17), .in_9(in_7), .out_10(out_11), .out_11(out_12),
    .out_12(out_13), .out_13(out_14), .out_14(out_15), .out_15(out_16), .out_16(out_17), .out_17(out_18));
endmodule

module enable (
  input  in_1,
  input  in_2,
  input  in_3,
  input  in_4,
  input  in_5,
  input  in_6,
  input  in_7,
  input  in_8,
  input  in_9,
  output out_10,
  output out_11,
  output out_12,
  output out_13,
  output out_14,
  output out_15,
  output out_16,
  output out_17
);

  and and_1 (out_10, in_1, in_9);
  and and_2 (out_11, in_2, in_9);
  and and_3 (out_12, in_3, in_9);
  and and_4 (out_13, in_4, in_9);
  and and_5 (out_14, in_5, in_9);
  and and_6 (out_15, in_6, in_9);
  and and_7 (out_16, in_7, in_9);
  and and_8 (out_17, in_8, in_9);
endmodule

module Circuito (
  input  in_1,
  input  in_2,
  output out_3
);

  wire nand_1_out, nand_2_out, nand_4_out;

  nand nand_1 (nand_1_out, in_1, in_2);
  nand nand_2 (nand_2_out, nand_1_out, in_2);
  nand nand_3 (out_3, nand_1_out, nand_4_out);
  nand nand_4 (nand_4_out, out_3, nand_2_out);
endmodule
