// Logisim project kaikeMaciel_8bits.circ as structural Verilog: 9 circuits, main circuit main
module main (
  input  [7:0] in_1,
  input  in_2,
  input  set_b,
  input  set_c,
  input  set_d,
  input  set_a,
  input  enable_b,
  input  enable_c,
  input  enable_d,
  input  enable_a,
  output [7:0] out_11
);

  wire [7:0] registrador_1byte_1_out_a, registrador_1byte_2_out_a, registrador_1byte_3_out_a,
       registrador_1byte_4_out_a;

  // Probe on out_11
  assign out_11 = in_2 ? in_1 : 8'bz;  // Controlled_Buffer controlled_buffer_1
  registrador_1byte registrador_1byte_1 (
    .input_a(out_11), .set_main(set_a), .enable_main(enable_a), .out_a(registrador_1byte_1_out_a));
  assign out_11 = enable_a ? registrador_1byte_1_out_a : 8'bz;  // Controlled_Buffer controlled_buffer_2
  assign out_11 = enable_b ? registrador_1byte_2_out_a : 8'bz;  // Controlled_Buffer controlled_buffer_3
  registrador_1byte registrador_1byte_2 (
    .input_a(out_11), .set_main(set_b), .enable_main(enable_b), .out_a(registrador_1byte_2_out_a));
  registrador_1byte registrador_1byte_3 (
    .input_a(out_11), .set_main(set_c), .enable_main(enable_c), .out_a(registrador_1byte_3_out_a));
  assign out_11 = enable_c ? registrador_1byte_3_out_a : 8'bz;  // Controlled_Buffer controlled_buffer_4
  registrador_1byte registrador_1byte_4 (
    .input_a(out_11), .set_main(set_d), .enable_main(enable_d), .out_a(registrador_1byte_4_out_a));
  assign out_11 = enable_d ? registrador_1byte_4_out_a : 8'bz;  // Controlled_Buffer controlled_buffer_5

  // Notes on the sheet:
  //   Kaike Maciel - 22250538
endmodule

module somador_1bit (
  input  c_in,
  input  a,
  input  b,
  output c,
  output c_out
);

  wire and_1_out, and_2_out, and_3_out, xor_1_out;

  xor xor_1 (xor_1_out, a, b);
  and and_1 (and_1_out, a, c_in);
  and and_2 (and_2_out, a, b);
  and and_3 (and_3_out, b, c_in);
  xor xor_2 (c, xor_1_out, c_in);
  or or_1 (c_out, and_1_out, and_2_out, and_3_out);
endmodule

module somador_8bit (
  input  in_1,
  input  [7:0] in_2,
  input  [7:0] in_3,
  output [7:0] out_4,
  output out_5
);

  wire somador_1bit_1_c_out, somador_1bit_2_c_out, somador_1bit_3_c_out, somador_1bit_4_c_out,
       somador_1bit_5_c_out, somador_1bit_6_c_out, somador_1bit_7_c_out;

  somador_1bit somador_1bit_1 (.a(in_2[0]), .b(in_3[0]), .c_in(in_1), .c_out(somador_1bit_1_c_out), .c(out_4[0]));
  somador_1bit somador_1bit_2 (
    .a(in_2[1]), .b(in_3[1]), .c_in(somador_1bit_1_c_out), .c_out(somador_1bit_2_c_out), .c(out_4[1]));
  somador_1bit somador_1bit_3 (
    .a(in_2[2]), .b(in_3[2]), .c_in(somador_1bit_2_c_out), .c_out(somador_1bit_3_c_out), .c(out_4[2]));
  somador_1bit somador_1bit_4 (
    .a(in_2[3]), .b(in_3[3]), .c_in(somador_1bit_3_c_out), .c_out(somador_1bit_4_c_out), .c(out_4[3]));
  somador_1bit somador_1bit_5 (
    .a(in_2[4]), .b(in_3[4]), .c_in(somador_1bit_4_c_out), .c_out(somador_1bit_5_c_out), .c(out_4[4]));
  somador_1bit somador_1bit_6 (
    .a(in_2[5]), .b(in_3[5]), .c_in(somador_1bit_5_c_out), .c_out(somador_1bit_6_c_out), .c(out_4[5]));
  somador_1bit somador_1bit_7 (
    .a(in_2[6]), .b(in_3[6]), .c_in(somador_1bit_6_c_out), .c_out(somador_1bit_7_c_out), .c(out_4[6]));
  somador_1bit somador_1bit_8 (.a(in_2[7]), .b(in_3[7]), .c_in(somador_1bit_7_c_out), .c_out(out_5), .c(out_4[7]));
endmodule

module registrador_1bit (
  input  in_1,
  input  in_2,
  output out_3
);

  wire nand_1_out, nand_2_out, nand_4_out;

  nand nand_1 (nand_1_out, in_1, in_2);
  nand nand_2 (nand_2_out, nand_1_out, in_2);
  nand nand_3 (out_3, nand_1_out, nand_4_out);
  nand nand_4 (nand_4_out, out_3, nand_2_out);
endmodule

module set_8bit (
  input  in_1,
  input  in_2,
  input  in_3,
  input  in_4,
  input  in_5,
  input  in_6,
  input  in_7,
  input  in_8,
  input  in_9,
  output out_10,
  output out_11,
  output out_12,
  output out_13,
  output out_14,
  output out_15,
  output out_16,
  output out_17
);

  registrador_1bit registrador_1bit_1 (.in_1(in_1), .in_2(in_9), .out_3(out_10));
  registrador_1bit registrador_1bit_2 (.in_1(in_2), .in_2(in_9), .out_3(out_11));
  registrador_1bit registrador_1bit_3 (.in_1(in_3), .in_2(in_9), .out_3(out_12));
  registrador_1bit registrador_1bit_4 (.in_1(in_4), .in_2(in_9), .out_3(out_13));
  registrador_1bit registrador_1bit_5 (.in_1(in_5), .in_2(in_9), .out_3(out_14));
  registrador_1bit registrador_1bit_6 (.in_1(in_6), .in_2(in_9), .out_3(out_15));
  registrador_1bit registrador_1bit_7 (.in_1(in_7), .in_2(in_9), .out_3(out_16));
  registrador_1bit registrador_1bit_8 (.in_1(in_8), .in_2(in_9), .out_3(out_17));
endmodule

module memoria_8bit (
  input  [7:0] in_1,
  input  in_2,
  output [7:0] out_3
);

  set_8bit set_8bit_1 (
    .in_1(in_1[0]), .in_2(in_1[1]), .in_3(in_1[2]), .in_4(in_1[3]), .in_5(in_1[4]), .in_6(in_1[5]),
    .in_7(in_1[6]), .in_8(in_1[7]), .in_9(in_2), .out_10(out_3[0]), .out_11(out_3[1]), .out_12(out_3[2]),
    .out_13(out_3[3]), .out_14(out_3[4]), .out_15(out_3[5]), .out_16(out_3[6]), .out_17(out_3[7]));
endmodule

module memoria_1byte (
  input  in_1,
  input  in_2,
  input  in_3,
  input  in_4,
  input  in_5,
  input  in_6,
  input  in_7,
  input  in_8,
  input  set_reg,
  input  enable_reg,
  output out_11,
  output out_12,
  output out_13,
  output out_14,
  output out_15,
  output out_16,
  output out_17,
  output out_18
);

  wire s_out_10, s_out_11, s_out_12, s_out_13, s_out_14, s_out_15, s_out_16, s_out_17;

  set_8bit s (
    .in_1(in_1), .in_2(in_2), .in_3(in_3), .in_4(in_4), .in_5(in_5), .in_6(in_6), .in_7(in_7), .in_8(in_8),
    .in_9(set_reg), .out_10(s_out_10), .out_11(s_out_11), .out_12(s_out_12), .out_13(s_out_13),
    .out_14(s_out_14), .out_15(s_out_15), .out_16(s_out_16), .out_17(s_out_17));
  enable_8bit e (
    .in_1(s_out_10), .in_2(s_out_11), .in_3(s_out_12), .in_4(s_out_13), .in_5(s_out_14), .in_6(s_out_15),
    .in_7(s_out_16), .in_8(s_out_17), .enable(enable_reg), .out_10(out_11), .out_11(out_12), .out_12(out_13),
    .out_13(out_14), .out_14(out_15), .out_15(out_16), .out_16(out_17), .out_17(out_18));
endmodule

module enable_8bit (
  input  in_1,
  input  in_2,
  input  in_3,
  input  in_4,
  input  in_5,
  input  in_6,
  input  in_7,
  input  in_8,
  input  enable,
  output out_10,
  output out_11,
  output out_12,
  output out_13,
  output out_14,
  output out_15,
  output out_16,
  output out_17
);

  and and_1 (out_10, in_1, enable);
  and and_2 (out_11, in_2, enable);
  and and_3 (out_12, in_3, enable);
  and and_4 (out_13, in_4, enable);
  and and_5 (out_14, in_5, enable);
  and and_6 (out_15, in_6, enable);
  and and_7 (out_16, in_7, enable);
  and and_8 (out_17, in_8, enable);
endmodule

module registrador_1byte (
  input  [7:0] input_a,
  input  set_main,
  input  enable_main,
  output [7:0] out_a
);

  memoria_1byte memoria_1byte_1 (
    .in_1(input_a[0]), .in_2(input_a[1]), .in_3(input_a[2]), .in_4(input_a[3]), .in_5(input_a[4]),
    .in_6(input_a[5]), .in_7(input_a[6]), .in_8(input_a[7]), .set_reg(set_main), .enable_reg(enable_main),
    .out_11(out_a[0]), .out_12(out_a[1]), .out_13(out_a[2]), .out_14(out_a[3]), .out_15(out_a[4]),
    .out_16(out_a[5]), .out_17(out_a[6]), .out_18(out_a[7]));
endmodule
