// Logisim project luiz_fernando_p_de_albuquerque.circ as structural Verilog: 10 circuits, main circuit main
module main (
  input  cin,
  input  [7:0] in_2,
  input  [7:0] in_3,
  input  cout,
  input  [7:0] in_5,
  input  sMAR,
  input  eMAR,
  input  s1,
  input  s2,
  input  s3,
  input  s4,
  input  e1,
  input  e2,
  input  e3,
  input  e4,
  output [7:0] out_16,
  output [7:0] out_17
);

  wire [7:0] MAR_out_4, R1_out_4, R2_out_4, R3_out_4, R4_out_4;

  registrador MAR (.in_1(in_5), .s(sMAR), .e(eMAR), .out_4(MAR_out_4));
  assign out_17 = eMAR ? MAR_out_4 : 8'bz;  // Controlled_Buffer controlled_buffer_1
  somador_8bits somador_8bits_1 (.a(in_2), .b(in_3), .c_in(cin), .c_out(cout), .out_4(out_16));
  assign out_17 = e1 ? R1_out_4 : 8'bz;  // Controlled_Buffer controlled_buffer_2
  registrador R1 (.in_1(out_17), .s(s1), .e(e1), .out_4(R1_out_4));
  registrador R2 (.in_1(out_17), .s(s2), .e(e2), .out_4(R2_out_4));
  assign out_17 = e2 ? R2_out_4 : 8'bz;  // Controlled_Buffer controlled_buffer_3
  registrador R3 (.in_1(out_17), .s(s3), .e(e3), .out_4(R3_out_4));
  assign out_17 = e3 ? R3_out_4 : 8'bz;  // Controlled_Buffer controlled_buffer_4
  assign out_17 = e4 ? R4_out_4 : 8'bz;  // Controlled_Buffer controlled_buffer_5
  registrador R4 (.in_1(out_17), .s(s4), .e(e4), .out_4(R4_out_4));

  // Notes on the sheet:
  //   LUIZ FERNANDO P. DE ALBUQUERQUE
  //   CM: 22250549
endmodule

module half_adder (
  input  in_1,
  input  in_2,
  output out_3,
  output c_in
);

  xor xor_1 (out_3, in_1, in_2);
  and and_1 (c_in, in_1, in_2);
endmodule

module somador_1bit (
  input  c_in,
  input  a,
  input  b,
  output c,
  output c_out
);

  wire and_1_out, and_2_out, and_3_out, xor_1_out;

  xor xor_1 (xor_1_out, a, b);
  xor xor_2 (c, xor_1_out, c_in);
  and and_1 (and_1_out, a, c_in);
  and and_2 (and_2_out, a, b);
  and and_3 (and_3_out, b, c_in);
  or or_1 (c_out, and_1_out, and_2_out, and_3_out);
endmodule

module somador_8bits (
  input  c_in,
  input  [7:0] a,
  input  [7:0] b,
  output [7:0] out_4,
  output c_out
);

  wire somador_1bit_1_c_out, somador_1bit_2_c_out, somador_1bit_3_c_out, somador_1bit_4_c_out,
       somador_1bit_5_c_out, somador_1bit_6_c_out, somador_1bit_7_c_out;

  somador_1bit somador_1bit_1 (.a(a[0]), .b(b[0]), .c_in(c_in), .c(out_4[0]), .c_out(somador_1bit_1_c_out));
  somador_1bit somador_1bit_2 (
    .a(a[1]), .b(b[1]), .c_in(somador_1bit_1_c_out), .c(out_4[1]), .c_out(somador_1bit_2_c_out));
  somador_1bit somador_1bit_3 (
    .a(a[2]), .b(b[2]), .c_in(somador_1bit_2_c_out), .c(out_4[2]), .c_out(somador_1bit_3_c_out));
  somador_1bit somador_1bit_4 (
    .a(a[3]), .b(b[3]), .c_in(somador_1bit_3_c_out), .c(out_4[3]), .c_out(somador_1bit_4_c_out));
  somador_1bit somador_1bit_5 (
    .a(a[4]), .b(b[4]), .c_in(somador_1bit_4_c_out), .c(out_4[4]), .c_out(somador_1bit_5_c_out));
  somador_1bit somador_1bit_6 (
    .a(a[5]), .b(b[5]), .c_in(somador_1bit_5_c_out), .c(out_4[5]), .c_out(somador_1bit_6_c_out));
  somador_1bit somador_1bit_7 (
    .a(a[6]), .b(b[6]), .c_in(somador_1bit_6_c_out), .c(out_4[6]), .c_out(somador_1bit_7_c_out));
  somador_1bit somador_1bit_8 (.a(a[7]), .b(b[7]), .c_in(somador_1bit_7_c_out), .c(out_4[7]), .c_out(c_out));
endmodule

module memoria1bit (
  input  i,
  input  set,
  output out_3
);

  wire nand_1_out, nand_2_out, nand_4_out;

  nand nand_1 (nand_1_out, i, set);
  nand nand_2 (nand_2_out, set, nand_1_out);
  nand nand_3 (out_3, nand_1_out, nand_4_out);
  nand nand_4 (nand_4_out, out_3, nand_2_out);
endmodule

module memoria8bits (
  input  i1,
  input  i2,
  input  i3,
  input  i4,
  input  i5,
  input  i6,
  input  i7,
  input  i8,
  input  set,
  output out_10,
  output out_11,
  output out_12,
  output out_13,
  output out_14,
  output out_15,
  output out_16,
  output out_17
);

  memoria1bit memoria1bit_1 (.i(i1), .set(set), .out_3(out_10));
  memoria1bit memoria1bit_2 (.i(i2), .set(set), .out_3(out_11));
  memoria1bit memoria1bit_3 (.i(i3), .set(set), .out_3(out_12));
  memoria1bit memoria1bit_4 (.i(i4), .set(set), .out_3(out_13));
  memoria1bit memoria1bit_5 (.i(i5), .set(set), .out_3(out_14));
  memoria1bit memoria1bit_6 (.i(i6), .set(set), .out_3(out_15));
  memoria1bit memoria1bit_7 (.i(i7), .set(set), .out_3(out_16));
  memoria1bit memoria1bit_8 (.i(i8), .set(set), .out_3(out_17));
endmodule

module memoria1byte (
  input  in_1,
  input  in_2,
  input  in_3,
  input  in_4,
  input  in_5,
  input  in_6,
  input  in_7,
  input  in_8,
  input  set,
  output out_10,
  output out_11,
  output out_12,
  output out_13,
  output out_14,
  output out_15,
  output out_16,
  output out_17
);

  memoria8bits memoria8bits_1 (
    .i1(in_1), .i2(in_2), .i3(in_3), .i4(in_4), .i5(in_5), .i6(in_6), .i7(in_7), .i8(in_8), .set(set),
    .out_10(out_10), .out_11(out_11), .out_12(out_12), .out_13(out_13), .out_14(out_14), .out_15(out_15),
    .out_16(out_16), .out_17(out_17));
endmodule

module enable (
  input  i1,
  input  i2,
  input  i3,
  input  i4,
  input  i5,
  input  i6,
  input  i7,
  input  i8,
  input  e,
  output out_10,
  output out_11,
  output out_12,
  output out_13,
  output out_14,
  output out_15,
  output out_16,
  output out_17
);

  and and_1 (out_10, i1, e);
  and and_2 (out_11, i2, e);
  and and_3 (out_12, i3, e);
  and and_4 (out_13, i4, e);
  and and_5 (out_14, i5, e);
  and and_6 (out_15, i6, e);
  and and_7 (out_16, i7, e);
  and and_8 (out_17, i8, e);
endmodule

module memoria1bytese (
  input  in_1,
  input  in_2,
  input  in_3,
  input  in_4,
  input  in_5,
  input  in_6,
  input  in_7,
  input  in_8,
  input  s,
  input  en,
  output out_11,
  output out_12,
  output out_13,
  output out_14,
  output out_15,
  output out_16,
  output out_17,
  output out_18
);

  wire B_out_10, B_out_11, B_out_12, B_out_13, B_out_14, B_out_15, B_out_16, B_out_17;

  memoria1byte B (
    .in_1(in_1), .in_2(in_2), .in_3(in_3), .in_4(in_4), .in_5(in_5), .in_6(in_6), .in_7(in_7), .in_8(in_8),
    .set(s), .out_10(B_out_10), .out_11(B_out_11), .out_12(B_out_12), .out_13(B_out_13), .out_14(B_out_14),
    .out_15(B_out_15), .out_16(B_out_16), .out_17(B_out_17));
  memoria1byte E (
    .in_1(B_out_10), .in_2(B_out_11), .in_3(B_out_12), .in_4(B_out_13), .in_5(B_out_14), .in_6(B_out_15),
    .in_7(B_out_16), .in_8(B_out_17), .set(en), .out_10(out_11), .out_11(out_12), .out_12(out_13),
    .out_13(out_14), .out_14(out_15), .out_15(out_16), .out_16(out_17), .out_17(out_18));
endmodule

module registrador (
  input  [7:0] in_1,
  input  s,
  input  e,
  output [7:0] out_4
);

  memoria1bytese r (
    .in_1(in_1[0]), .in_2(in_1[1]), .in_3(in_1[2]), .in_4(in_1[3]), .in_5(in_1[4]), .in_6(in_1[5]),
    .in_7(in_1[6]), .in_8(in_1[7]), .s(s), .en(e), .out_11(out_4[0]), .out_12(out_4[1]), .out_13(out_4[2]),
    .out_14(out_4[3]), .out_15(out_4[4]), .out_16(out_4[5]), .out_17(out_4[6]), .out_18(out_4[7]));
endmodule
