// Logisim project marcos_paulo_vieira_pedrosa.circ as structural Verilog: 9 circuits, main circuit main
module main (
  input  [7:0] in_1,
  input  in_2,
  input  s,
  input  in_4,
  input  in_5,
  input  in_6,
  input  e,
  input  in_8,
  input  in_9,
  input  in_10,
  input  c_in,
  input  [7:0] a_8bit,
  input  [7:0] b_8bit,
  output [7:0] o_8bit,
  output c_out
);

  wire [7:0] controlled_buffer_1_out;

  assign controlled_buffer_1_out = in_2 ? in_1 : 8'bz;  // Controlled_Buffer controlled_buffer_1
  registrador_8bits_buffer registrador_8bits_buffer_1 (
    .i_8bit(controlled_buffer_1_out), .s(s), .e(e), .o_8bit(controlled_buffer_1_out));
  registrador_8bits_buffer registrador_8bits_buffer_2 (
    .i_8bit(controlled_buffer_1_out), .s(in_4), .e(in_8), .o_8bit(controlled_buffer_1_out));
  somador_8bit somador_8bit_1 (.a_8bit(a_8bit), .b_8bit(b_8bit), .c_in(c_in), .c_out(c_out), .o_8bit(o_8bit));
  registrador_8bits_buffer registrador_8bits_buffer_3 (
    .i_8bit(controlled_buffer_1_out), .s(in_5), .e(in_9), .o_8bit(controlled_buffer_1_out));
  registrador_8bits_buffer registrador_8bits_buffer_4 (
    .i_8bit(controlled_buffer_1_out), .s(in_6), .e(in_10), .o_8bit(controlled_buffer_1_out));
  // Probe on controlled_buffer_1_out

  // Notes on the sheet:
  //   Marcos Paulo Vieira Pedrosa - 22401906
endmodule

module meio_somador (
  input  c_in,
  input  a,
  output c_out,
  output o
);

  and and_1 (c_out, c_in, a);
  xor xor_1 (o, c_in, a);
endmodule

module somador_completo_1bit (
  input  c_in,
  input  a,
  input  b,
  output o,
  output c_out
);

  wire and_1_out, and_2_out, xor_1_out;

  and and_1 (and_1_out, a, b);
  xor xor_1 (xor_1_out, a, b);
  and and_2 (and_2_out, c_in, xor_1_out);
  xor xor_2 (o, xor_1_out, c_in);
  or or_1 (c_out, and_1_out, and_2_out);
endmodule

module somador_8bit (
  input  c_in,
  input  [7:0] a_8bit,
  input  [7:0] b_8bit,
  output [7:0] o_8bit,
  output c_out
);

  wire somador_completo_1bit_1_c_out, somador_completo_1bit_2_c_out, somador_completo_1bit_3_c_out,
       somador_completo_1bit_4_c_out, somador_completo_1bit_5_c_out, somador_completo_1bit_6_c_out,
       somador_completo_1bit_7_c_out;

  somador_completo_1bit somador_completo_1bit_1 (
    .a(a_8bit[0]), .b(b_8bit[0]), .c_in(c_in), .c_out(somador_completo_1bit_1_c_out), .o(o_8bit[0]));
  somador_completo_1bit somador_completo_1bit_2 (
    .a(a_8bit[1]), .b(b_8bit[1]), .c_in(somador_completo_1bit_1_c_out),
    .c_out(somador_completo_1bit_2_c_out), .o(o_8bit[1]));
  somador_completo_1bit somador_completo_1bit_3 (
    .a(a_8bit[2]), .b(b_8bit[2]), .c_in(somador_completo_1bit_2_c_out),
    .c_out(somador_completo_1bit_3_c_out), .o(o_8bit[2]));
  somador_completo_1bit somador_completo_1bit_4 (
    .a(a_8bit[3]), .b(b_8bit[3]), .c_in(somador_completo_1bit_3_c_out),
    .c_out(somador_completo_1bit_4_c_out), .o(o_8bit[3]));
  somador_completo_1bit somador_completo_1bit_5 (
    .a(a_8bit[4]), .b(b_8bit[4]), .c_in(somador_completo_1bit_4_c_out),
    .c_out(somador_completo_1bit_5_c_out), .o(o_8bit[4]));
  somador_completo_1bit somador_completo_1bit_6 (
    .a(a_8bit[5]), .b(b_8bit[5]), .c_in(somador_completo_1bit_5_c_out),
    .c_out(somador_completo_1bit_6_c_out), .o(o_8bit[5]));
  somador_completo_1bit somador_completo_1bit_7 (
    .a(a_8bit[6]), .b(b_8bit[6]), .c_in(somador_completo_1bit_6_c_out),
    .c_out(somador_completo_1bit_7_c_out), .o(o_8bit[6]));
  somador_completo_1bit somador_completo_1bit_8 (
    .a(a_8bit[7]), .b(b_8bit[7]), .c_in(somador_completo_1bit_7_c_out), .c_out(c_out), .o(o_8bit[7]));
endmodule

module memoria_1bit (
  input  i,
  input  set,
  output o
);

  wire nand_1_out, nand_2_out, nand_4_out;

  nand nand_1 (nand_1_out, i, set);
  nand nand_2 (nand_2_out, nand_1_out, set);
  nand nand_3 (o, nand_1_out, nand_4_out);
  nand nand_4 (nand_4_out, o, nand_2_out);
endmodule

module memoria_8bits (
  input  [7:0] i_8bit,
  input  set,
  output [7:0] o_8bit
);

  memoria_1bit memoria_1bit_1 (.i(i_8bit[0]), .set(set), .o(o_8bit[0]));
  memoria_1bit memoria_1bit_2 (.i(i_8bit[1]), .set(set), .o(o_8bit[1]));
  memoria_1bit memoria_1bit_3 (.i(i_8bit[2]), .set(set), .o(o_8bit[2]));
  memoria_1bit memoria_1bit_4 (.i(i_8bit[3]), .set(set), .o(o_8bit[3]));
  memoria_1bit memoria_1bit_5 (.i(i_8bit[4]), .set(set), .o(o_8bit[4]));
  memoria_1bit memoria_1bit_6 (.i(i_8bit[5]), .set(set), .o(o_8bit[5]));
  memoria_1bit memoria_1bit_7 (.i(i_8bit[6]), .set(set), .o(o_8bit[6]));
  memoria_1bit memoria_1bit_8 (.i(i_8bit[7]), .set(set), .o(o_8bit[7]));
endmodule

module enabler (
  input  [7:0] i_8bit,
  input  e,
  output [7:0] o_8bit
);

  and and_1 (o_8bit[0], i_8bit[0], e);
  and and_2 (o_8bit[1], i_8bit[1], e);
  and and_3 (o_8bit[2], i_8bit[2], e);
  and and_4 (o_8bit[3], i_8bit[3], e);
  and and_5 (o_8bit[4], i_8bit[4], e);
  and and_6 (o_8bit[5], i_8bit[5], e);
  and and_7 (o_8bit[6], i_8bit[6], e);
  and and_8 (o_8bit[7], i_8bit[7], e);
endmodule

module registrador_8bits (
  input  [7:0] i_8bit,
  input  s,
  input  e,
  output [7:0] o_8bit
);

  wire [7:0] memoria_8bits_1_o_8bit;

  memoria_8bits memoria_8bits_1 (.i_8bit(i_8bit), .set(s), .o_8bit(memoria_8bits_1_o_8bit));
  enabler enabler_1 (.i_8bit(memoria_8bits_1_o_8bit), .e(e), .o_8bit(o_8bit));
endmodule

module registrador_8bits_buffer (
  input  [7:0] i_8bit,
  input  s,
  input  e,
  output [7:0] o_8bit
);

  wire [7:0] registrador_8bits_1_o_8bit;

  assign o_8bit = e ? registrador_8bits_1_o_8bit : 8'bz;  // Controlled_Buffer controlled_buffer_1
  registrador_8bits registrador_8bits_1 (.i_8bit(i_8bit), .s(s), .e(e), .o_8bit(registrador_8bits_1_o_8bit));
endmodule
