// Logisim project maria_giovanna_sales.circ as structural Verilog: 6 circuits, main circuit main
module main (
  input  [7:0] in_1,
  input  in_2,
  input  in_3,
  input  in_4,
  input  in_5,
  input  in_6,
  input  in_7,
  input  in_8,
  input  in_9,
  input  cin,
  input  [7:0] a,
  input  [7:0] b,
  output [7:0] out_13,
  output [7:0] result,
  output cout
);

  wire not_1_out, or_1_out;
  wire [7:0] memoria_1byte_1_out_4, memoria_1byte_2_out_4, memoria_1byte_3_out_4, memoria_1byte_4_out_4,
       or_2_out;

  memoria_1byte memoria_1byte_1 (.in_1(in_1), .set(in_2), .en(in_6), .out_4(memoria_1byte_1_out_4));
  memoria_1byte memoria_1byte_2 (.in_1(in_1), .set(in_3), .en(in_7), .out_4(memoria_1byte_2_out_4));
  somador_8bits somador_8bits_1 (.a(a), .b(b), .in_1(cin), .saida(result), .cout(cout));
  memoria_1byte memoria_1byte_3 (.in_1(in_1), .set(in_4), .en(in_8), .out_4(memoria_1byte_3_out_4));
  memoria_1byte memoria_1byte_4 (.in_1(in_1), .set(in_5), .en(in_9), .out_4(memoria_1byte_4_out_4));
  assign out_13 = not_1_out ? in_1 : 8'bz;  // Controlled_Buffer controlled_buffer_1
  not not_1 (not_1_out, or_1_out);
  or or_1 (or_1_out, in_9, in_8, in_7, in_6);
  assign or_2_out = memoria_1byte_4_out_4 | memoria_1byte_3_out_4 | memoria_1byte_2_out_4 | memoria_1byte_1_out_4;  // OR_Gate or_2, 8 bits wide
  assign out_13 = or_1_out ? or_2_out : 8'bz;  // Controlled_Buffer controlled_buffer_2

  // Notes on the sheet:
  //   Maria Giovanna Gonçalves Sales - 22251138
  //   Somador de 8 bits
endmodule

module somador_1bit (
  input  crr_in,
  input  a,
  input  b,
  output out_4,
  output c_out
);

  wire and_1_out, and_2_out, and_3_out, xor_1_out;

  xor xor_1 (xor_1_out, a, b);
  and and_1 (and_1_out, a, crr_in);
  and and_2 (and_2_out, a, b);
  and and_3 (and_3_out, b, crr_in);
  xor xor_2 (out_4, xor_1_out, crr_in);
  or or_1 (c_out, and_1_out, and_2_out, and_3_out);
endmodule

module somador_8bits (
  input  in_1,
  input  [7:0] a,
  input  [7:0] b,
  output [7:0] saida,
  output cout
);

  wire somador_1bit_1_c_out, somador_1bit_2_c_out, somador_1bit_3_c_out, somador_1bit_4_c_out,
       somador_1bit_5_c_out, somador_1bit_6_c_out, somador_1bit_7_c_out;

  somador_1bit somador_1bit_1 (.a(a[0]), .b(b[0]), .crr_in(in_1), .c_out(somador_1bit_1_c_out), .out_4(saida[0]));
  somador_1bit somador_1bit_2 (
    .a(a[1]), .b(b[1]), .crr_in(somador_1bit_1_c_out), .c_out(somador_1bit_2_c_out), .out_4(saida[1]));
  somador_1bit somador_1bit_3 (
    .a(a[2]), .b(b[2]), .crr_in(somador_1bit_2_c_out), .c_out(somador_1bit_3_c_out), .out_4(saida[2]));
  somador_1bit somador_1bit_4 (
    .a(a[3]), .b(b[3]), .crr_in(somador_1bit_3_c_out), .c_out(somador_1bit_4_c_out), .out_4(saida[3]));
  somador_1bit somador_1bit_5 (
    .a(a[4]), .b(b[4]), .crr_in(somador_1bit_4_c_out), .c_out(somador_1bit_5_c_out), .out_4(saida[4]));
  somador_1bit somador_1bit_6 (
    .a(a[5]), .b(b[5]), .crr_in(somador_1bit_5_c_out), .c_out(somador_1bit_6_c_out), .out_4(saida[5]));
  somador_1bit somador_1bit_7 (
    .a(a[6]), .b(b[6]), .crr_in(somador_1bit_6_c_out), .c_out(somador_1bit_7_c_out), .out_4(saida[6]));
  somador_1bit somador_1bit_8 (.a(a[7]), .b(b[7]), .crr_in(somador_1bit_7_c_out), .c_out(cout), .out_4(saida[7]));
endmodule

module memoria_1bit (
  input  in_1,
  input  in_2,
  output out_3
);

  wire nand_1_out, nand_2_out, nand_4_out;

  nand nand_1 (nand_1_out, in_1, in_2);
  nand nand_2 (nand_2_out, nand_1_out, in_2);
  nand nand_3 (out_3, nand_1_out, nand_4_out);
  nand nand_4 (nand_4_out, out_3, nand_2_out);
endmodule

module memoria_8bits (
  input  [7:0] in_1,
  input  in_2,
  output [7:0] out_3
);

  memoria_1bit memoria_1bit_1 (.in_1(in_1[0]), .in_2(in_2), .out_3(out_3[0]));
  memoria_1bit memoria_1bit_2 (.in_1(in_1[1]), .in_2(in_2), .out_3(out_3[1]));
  memoria_1bit memoria_1bit_3 (.in_1(in_1[2]), .in_2(in_2), .out_3(out_3[2]));
  memoria_1bit memoria_1bit_4 (.in_1(in_1[3]), .in_2(in_2), .out_3(out_3[3]));
  memoria_1bit memoria_1bit_5 (.in_1(in_1[4]), .in_2(in_2), .out_3(out_3[4]));
  memoria_1bit memoria_1bit_6 (.in_1(in_1[5]), .in_2(in_2), .out_3(out_3[5]));
  memoria_1bit memoria_1bit_7 (.in_1(in_1[6]), .in_2(in_2), .out_3(out_3[6]));
  memoria_1bit memoria_1bit_8 (.in_1(in_1[7]), .in_2(in_2), .out_3(out_3[7]));
endmodule

module memoria_1byte (
  input  [7:0] in_1,
  input  set,
  input  en,
  output [7:0] out_4
);

  wire [7:0] memoria_8bits_1_out_3;

  memoria_8bits memoria_8bits_1 (.in_1(in_1), .in_2(set), .out_3(memoria_8bits_1_out_3));
  memoria_8bits memoria_8bits_2 (.in_1(memoria_8bits_1_out_3), .in_2(en), .out_3(out_4));
endmodule
