// Logisim project natasha_araujo_caxias.circ as structural Verilog: 7 circuits, main circuit main
module main (
  input  in_1,
  input  [7:0] in_2,
  input  [7:0] in_3,
  input  [7:0] in_4,
  input  in_5,
  input  in_6,
  input  in_7,
  input  in_8,
  input  in_9,
  input  [7:0] in_10,
  input  in_11,
  input  in_12,
  input  in_13,
  input  [1:0] in_14,
  output [7:0] out_15,
  output [7:0] out_16,
  output out_17,
  output [7:0] out_18
);

  wire decoder_1_out0, decoder_1_out1, decoder_1_out2, decoder_1_out3;
  wire [7:0] memoria1bytesetenable_2_out_4, memoria1bytesetenable_3_out_4, memoria1bytesetenable_4_out_4,
       memoria1bytesetenable_5_out_4;

  somador8bits somador8bits_1 (.a(in_2), .b(in_4), .c_in(in_1), .c_out(out_17), .saida(out_15));
  memoria1byteSetEnable memoria1bytesetenable_1 (.in_1(in_10), .in_2(in_11), .in_3(in_13), .out_4(out_18));
  assign out_16 = in_5 ? in_3 : 8'bz;  // Controlled_Buffer controlled_buffer_1
  Decoder #(.disabled("Z"), .select(2)) decoder_1 (
    .out0(decoder_1_out0), .out1(decoder_1_out1), .out2(decoder_1_out2), .out3(decoder_1_out3), .sel(in_14),
    .en(in_12));
  assign out_16 = decoder_1_out0 ? memoria1bytesetenable_2_out_4 : 8'bz;  // Controlled_Buffer controlled_buffer_2
  memoria1byteSetEnable memoria1bytesetenable_2 (
    .in_1(out_16), .in_2(in_6), .in_3(decoder_1_out0), .out_4(memoria1bytesetenable_2_out_4));
  assign out_16 = decoder_1_out1 ? memoria1bytesetenable_3_out_4 : 8'bz;  // Controlled_Buffer controlled_buffer_3
  memoria1byteSetEnable memoria1bytesetenable_3 (
    .in_1(out_16), .in_2(in_7), .in_3(decoder_1_out1), .out_4(memoria1bytesetenable_3_out_4));
  assign out_16 = decoder_1_out2 ? memoria1bytesetenable_4_out_4 : 8'bz;  // Controlled_Buffer controlled_buffer_4
  memoria1byteSetEnable memoria1bytesetenable_4 (
    .in_1(out_16), .in_2(in_8), .in_3(decoder_1_out2), .out_4(memoria1bytesetenable_4_out_4));
  assign out_16 = decoder_1_out3 ? memoria1bytesetenable_5_out_4 : 8'bz;  // Controlled_Buffer controlled_buffer_5
  memoria1byteSetEnable memoria1bytesetenable_5 (
    .in_1(out_16), .in_2(in_9), .in_3(decoder_1_out3), .out_4(memoria1bytesetenable_5_out_4));

  // Notes on the sheet:
  //   Natasha Araujo Caxias N 22401912
  //   Somador de 8 bits
  //   Registrador de 8 bits 
  //   com sinais set e enable
  //   Barramento com 4 registradores
endmodule

module somador1bit (
  input  c_in,
  input  a,
  input  b,
  output saida,
  output c_out
);

  wire and_1_out, and_2_out, and_3_out, xor_1_out;

  xor xor_1 (xor_1_out, a, b);
  and and_1 (and_1_out, a, c_in);
  and and_2 (and_2_out, a, b);
  and and_3 (and_3_out, b, c_in);
  xor xor_2 (saida, xor_1_out, c_in);
  or or_1 (c_out, and_1_out, and_2_out, and_3_out);
endmodule

module somador8bits (
  input  c_in,
  input  [7:0] a,
  input  [7:0] b,
  output [7:0] saida,
  output c_out
);

  wire somador1bit_1_c_out, somador1bit_2_c_out, somador1bit_3_c_out, somador1bit_4_c_out,
       somador1bit_5_c_out, somador1bit_6_c_out, somador1bit_7_c_out;

  somador1bit somador1bit_1 (.a(a[0]), .b(b[0]), .c_in(c_in), .c_out(somador1bit_1_c_out), .saida(saida[0]));
  somador1bit somador1bit_2 (
    .a(a[1]), .b(b[1]), .c_in(somador1bit_1_c_out), .c_out(somador1bit_2_c_out), .saida(saida[1]));
  somador1bit somador1bit_3 (
    .a(a[2]), .b(b[2]), .c_in(somador1bit_2_c_out), .c_out(somador1bit_3_c_out), .saida(saida[2]));
  somador1bit somador1bit_4 (
    .a(a[3]), .b(b[3]), .c_in(somador1bit_3_c_out), .c_out(somador1bit_4_c_out), .saida(saida[3]));
  somador1bit somador1bit_5 (
    .a(a[4]), .b(b[4]), .c_in(somador1bit_4_c_out), .c_out(somador1bit_5_c_out), .saida(saida[4]));
  somador1bit somador1bit_6 (
    .a(a[5]), .b(b[5]), .c_in(somador1bit_5_c_out), .c_out(somador1bit_6_c_out), .saida(saida[5]));
  somador1bit somador1bit_7 (
    .a(a[6]), .b(b[6]), .c_in(somador1bit_6_c_out), .c_out(somador1bit_7_c_out), .saida(saida[6]));
  somador1bit somador1bit_8 (.a(a[7]), .b(b[7]), .c_in(somador1bit_7_c_out), .c_out(c_out), .saida(saida[7]));
endmodule

module memoria1bit (
  input  entrada,
  input  set,
  output saida
);

  wire nand_1_out, nand_2_out, nand_4_out;

  nand nand_1 (nand_1_out, entrada, set);
  nand nand_2 (nand_2_out, nand_1_out, set);
  nand nand_3 (saida, nand_1_out, nand_4_out);
  nand nand_4 (nand_4_out, saida, nand_2_out);
endmodule

module memoria1byteSet (
  input  in_1,
  input  in_2,
  input  in_3,
  input  in_4,
  input  in_5,
  input  in_6,
  input  in_7,
  input  in_8,
  input  in_9,
  output out_10,
  output out_11,
  output out_12,
  output out_13,
  output out_14,
  output out_15,
  output out_16,
  output out_17
);

  memoria1bit memoria1bit_1 (.entrada(in_1), .set(in_9), .saida(out_10));
  memoria1bit memoria1bit_2 (.entrada(in_2), .set(in_9), .saida(out_11));
  memoria1bit memoria1bit_3 (.entrada(in_3), .set(in_9), .saida(out_12));
  memoria1bit memoria1bit_4 (.entrada(in_4), .set(in_9), .saida(out_13));
  memoria1bit memoria1bit_5 (.entrada(in_5), .set(in_9), .saida(out_14));
  memoria1bit memoria1bit_6 (.entrada(in_6), .set(in_9), .saida(out_15));
  memoria1bit memoria1bit_7 (.entrada(in_7), .set(in_9), .saida(out_16));
  memoria1bit memoria1bit_8 (.entrada(in_8), .set(in_9), .saida(out_17));
endmodule

module memoria1byteSetEnable (
  input  [7:0] in_1,
  input  in_2,
  input  in_3,
  output [7:0] out_4
);

  wire memoria1byteset_1_out_10, memoria1byteset_1_out_11, memoria1byteset_1_out_12,
       memoria1byteset_1_out_13, memoria1byteset_1_out_14, memoria1byteset_1_out_15,
       memoria1byteset_1_out_16, memoria1byteset_1_out_17;

  memoria1byteSet memoria1byteset_1 (
    .in_1(in_1[0]), .in_2(in_1[1]), .in_3(in_1[2]), .in_4(in_1[3]), .in_5(in_1[4]), .in_6(in_1[5]),
    .in_7(in_1[6]), .in_8(in_1[7]), .in_9(in_2), .out_10(memoria1byteset_1_out_10),
    .out_11(memoria1byteset_1_out_11), .out_12(memoria1byteset_1_out_12), .out_13(memoria1byteset_1_out_13),
    .out_14(memoria1byteset_1_out_14), .out_15(memoria1byteset_1_out_15), .out_16(memoria1byteset_1_out_16),
    .out_17(memoria1byteset_1_out_17));
  enable enable_1 (
    .in_1(memoria1byteset_1_out_10), .in_2(memoria1byteset_1_out_11), .in_3(memoria1byteset_1_out_12),
    .in_4(memoria1byteset_1_out_13), .in_5(memoria1byteset_1_out_14), .in_6(memoria1byteset_1_out_15),
    .in_7(memoria1byteset_1_out_16), .in_8(memoria1byteset_1_out_17), .in_9(in_3), .out_10(out_4[0]),
    .out_11(out_4[1]), .out_12(out_4[2]), .out_13(out_4[3]), .out_14(out_4[4]), .out_15(out_4[5]),
    .out_16(out_4[6]), .out_17(out_4[7]));
endmodule

module enable (
  input  in_1,
  input  in_2,
  input  in_3,
  input  in_4,
  input  in_5,
  input  in_6,
  input  in_7,
  input  in_8,
  input  in_9,
  output out_10,
  output out_11,
  output out_12,
  output out_13,
  output out_14,
  output out_15,
  output out_16,
  output out_17
);

  and and_1 (out_10, in_1, in_9);
  and and_2 (out_11, in_2, in_9);
  and and_3 (out_12, in_3, in_9);
  and and_4 (out_13, in_4, in_9);
  and and_5 (out_14, in_5, in_9);
  and and_6 (out_15, in_6, in_9);
  and and_7 (out_16, in_7, in_9);
  and and_8 (out_17, in_8, in_9);
endmodule
