// Logisim project renata_rodrigues.circ as structural Verilog: 7 circuits, main circuit main
module main (
  input  [7:0] in_1,
  input  s,
  input  s_2,
  input  s_3,
  input  s_4,
  input  e,
  input  e_2,
  input  e_3,
  input  e_4,
  output [7:0] \output 
);

  wire not_1_out, or_1_out;
  wire [7:0] or_2_out, registrador_1_out_4, registrador_2_out_4, registrador_3_out_4, registrador_4_out_4;

  registrador registrador_1 (.in_1(in_1), .s(s), .e(e), .out_4(registrador_1_out_4));
  registrador registrador_2 (.in_1(in_1), .s(s_2), .e(e_2), .out_4(registrador_2_out_4));
  registrador registrador_3 (.in_1(in_1), .s(s_3), .e(e_3), .out_4(registrador_3_out_4));
  registrador registrador_4 (.in_1(in_1), .s(s_4), .e(e_4), .out_4(registrador_4_out_4));
  not not_1 (not_1_out, or_1_out);
  or or_1 (or_1_out, e_4, e_3, e_2, e);
  assign or_2_out = registrador_4_out_4 | registrador_3_out_4 | registrador_2_out_4 | registrador_1_out_4;  // OR_Gate or_2, 8 bits wide
  assign \output  = not_1_out ? in_1 : 8'bz;  // Controlled_Buffer controlled_buffer_1
  assign \output  = or_1_out ? or_2_out : 8'bz;  // Controlled_Buffer controlled_buffer_2

  // Notes on the sheet:
  //   input
  //   Renata Rodrigues Coelho - 22251140
  //   R1
  //   R2
  //   R3
  //   R4
endmodule

module somador_1bit (
  input  c_in,
  input  a,
  input  b,
  output out,
  output c_out
);

  wire and_1_out, and_2_out, and_3_out, xor_1_out;

  xor xor_1 (xor_1_out, a, b);
  and and_1 (and_1_out, a, c_in);
  and and_2 (and_2_out, a, b);
  and and_3 (and_3_out, b, c_in);
  xor xor_2 (out, xor_1_out, c_in);
  or or_1 (c_out, and_1_out, and_2_out, and_3_out);
endmodule

module somador_8bits (
  input  in_1,
  input  [7:0] in_2,
  input  [7:0] in_3,
  output [7:0] out_4,
  output out_5
);

  wire somador_1bit_1_c_out, somador_1bit_2_c_out, somador_1bit_3_c_out, somador_1bit_4_c_out,
       somador_1bit_5_c_out, somador_1bit_6_c_out, somador_1bit_7_c_out;

  somador_1bit somador_1bit_1 (.a(in_2[0]), .b(in_3[0]), .c_in(in_1), .c_out(somador_1bit_1_c_out), .out(out_4[0]));
  somador_1bit somador_1bit_2 (
    .a(in_2[1]), .b(in_3[1]), .c_in(somador_1bit_1_c_out), .c_out(somador_1bit_2_c_out), .out(out_4[1]));
  somador_1bit somador_1bit_3 (
    .a(in_2[2]), .b(in_3[2]), .c_in(somador_1bit_2_c_out), .c_out(somador_1bit_3_c_out), .out(out_4[2]));
  somador_1bit somador_1bit_4 (
    .a(in_2[3]), .b(in_3[3]), .c_in(somador_1bit_3_c_out), .c_out(somador_1bit_4_c_out), .out(out_4[3]));
  somador_1bit somador_1bit_5 (
    .a(in_2[4]), .b(in_3[4]), .c_in(somador_1bit_4_c_out), .c_out(somador_1bit_5_c_out), .out(out_4[4]));
  somador_1bit somador_1bit_6 (
    .a(in_2[5]), .b(in_3[5]), .c_in(somador_1bit_5_c_out), .c_out(somador_1bit_6_c_out), .out(out_4[5]));
  somador_1bit somador_1bit_7 (
    .a(in_2[6]), .b(in_3[6]), .c_in(somador_1bit_6_c_out), .c_out(somador_1bit_7_c_out), .out(out_4[6]));
  somador_1bit somador_1bit_8 (.a(in_2[7]), .b(in_3[7]), .c_in(somador_1bit_7_c_out), .c_out(out_5), .out(out_4[7]));
endmodule

module memory_1bit (
  input  i,
  input  s,
  output out_3
);

  wire nand_1_out, nand_2_out, nand_4_out;

  nand nand_1 (nand_1_out, i, s);
  nand nand_2 (nand_2_out, nand_1_out, s);
  nand nand_3 (out_3, nand_1_out, nand_4_out);
  nand nand_4 (nand_4_out, out_3, nand_2_out);
endmodule

module memoria_8bits (
  input  i,
  input  in_2,
  input  in_3,
  input  in_4,
  input  in_5,
  input  in_6,
  input  in_7,
  input  in_8,
  input  s,
  output o,
  output out_11,
  output out_12,
  output out_13,
  output out_14,
  output out_15,
  output out_16,
  output out_17
);

  memory_1bit memory_1bit_1 (.i(i), .s(s), .out_3(o));
  memory_1bit memory_1bit_2 (.i(in_2), .s(s), .out_3(out_11));
  memory_1bit memory_1bit_3 (.i(in_3), .s(s), .out_3(out_12));
  memory_1bit memory_1bit_4 (.i(in_4), .s(s), .out_3(out_13));
  memory_1bit memory_1bit_5 (.i(in_5), .s(s), .out_3(out_14));
  memory_1bit memory_1bit_6 (.i(in_6), .s(s), .out_3(out_15));
  memory_1bit memory_1bit_7 (.i(in_7), .s(s), .out_3(out_16));
  memory_1bit memory_1bit_8 (.i(in_8), .s(s), .out_3(out_17));

  // Notes on the sheet:
  //   memoria 1 byte (8 bits) e set
endmodule

module registrador (
  input  [7:0] in_1,
  input  s,
  input  e,
  output [7:0] out_4
);

  wire memoria_8bits_1_o, memoria_8bits_1_out_11, memoria_8bits_1_out_12, memoria_8bits_1_out_13,
       memoria_8bits_1_out_14, memoria_8bits_1_out_15, memoria_8bits_1_out_16, memoria_8bits_1_out_17;

  memoria_8bits memoria_8bits_1 (
    .i(in_1[0]), .in_2(in_1[1]), .in_3(in_1[2]), .in_4(in_1[3]), .in_5(in_1[4]), .in_6(in_1[5]),
    .in_7(in_1[6]), .in_8(in_1[7]), .s(s), .o(memoria_8bits_1_o), .out_11(memoria_8bits_1_out_11),
    .out_12(memoria_8bits_1_out_12), .out_13(memoria_8bits_1_out_13), .out_14(memoria_8bits_1_out_14),
    .out_15(memoria_8bits_1_out_15), .out_16(memoria_8bits_1_out_16), .out_17(memoria_8bits_1_out_17));
  enable enable_1 (
    .in_1(memoria_8bits_1_o), .in_2(memoria_8bits_1_out_11), .in_3(memoria_8bits_1_out_12),
    .in_4(memoria_8bits_1_out_13), .in_5(memoria_8bits_1_out_14), .in_6(memoria_8bits_1_out_15),
    .in_7(memoria_8bits_1_out_16), .in_8(memoria_8bits_1_out_17), .in_9(e), .out_10(out_4[0]),
    .out_11(out_4[1]), .out_12(out_4[2]), .out_13(out_4[3]), .out_14(out_4[4]), .out_15(out_4[5]),
    .out_16(out_4[6]), .out_17(out_4[7]));

  // Notes on the sheet:
  //   memória 1 byte
  //   b
  //   enable
  //   e
endmodule

module enable (
  input  in_1,
  input  in_2,
  input  in_3,
  input  in_4,
  input  in_5,
  input  in_6,
  input  in_7,
  input  in_8,
  input  in_9,
  output out_10,
  output out_11,
  output out_12,
  output out_13,
  output out_14,
  output out_15,
  output out_16,
  output out_17
);

  and and_1 (out_10, in_1, in_9);
  and and_2 (out_11, in_2, in_9);
  and and_3 (out_12, in_3, in_9);
  and and_4 (out_13, in_4, in_9);
  and and_5 (out_14, in_5, in_9);
  and and_6 (out_15, in_6, in_9);
  and and_7 (out_16, in_7, in_9);
  and and_8 (out_17, in_8, in_9);
endmodule
