// Logisim project sophia_helena_queiroz_correa.circ as structural Verilog
module somador_bit (
  input  in_1,
  input  in_2,
  input  in_3,
  output out_4,
  output out_5
);

  wire and_1_out, and_2_out, and_3_out, xor_1_out;

  xor xor_1 (xor_1_out, in_2, in_3);
  and and_1 (and_1_out, in_2, in_1);
  and and_2 (and_2_out, in_2, in_3);
  and and_3 (and_3_out, in_3, in_1);
  xor xor_2 (out_4, xor_1_out, in_1);
  or or_1 (out_5, and_1_out, and_2_out, and_3_out);
endmodule

module somador_8bits (
  input  in_1,
  input  [7:0] in_2,
  input  [7:0] in_3,
  output [7:0] out_4
);

  wire somador_bit_1_out_5, somador_bit_2_out_5, somador_bit_3_out_5, somador_bit_4_out_5,
       somador_bit_5_out_5, somador_bit_6_out_5, somador_bit_7_out_5;

  somador_bit somador_bit_1 (
    .in_2(in_2[0]), .in_3(in_3[0]), .in_1(in_1), .out_5(somador_bit_1_out_5), .out_4(out_4[0]));
  somador_bit somador_bit_2 (
    .in_2(in_2[1]), .in_3(in_3[1]), .in_1(somador_bit_1_out_5), .out_5(somador_bit_2_out_5), .out_4(out_4[1]));
  somador_bit somador_bit_3 (
    .in_2(in_2[2]), .in_3(in_3[2]), .in_1(somador_bit_2_out_5), .out_5(somador_bit_3_out_5), .out_4(out_4[2]));
  somador_bit somador_bit_4 (
    .in_2(in_2[3]), .in_3(in_3[3]), .in_1(somador_bit_3_out_5), .out_5(somador_bit_4_out_5), .out_4(out_4[3]));
  somador_bit somador_bit_5 (
    .in_2(in_2[4]), .in_3(in_3[4]), .in_1(somador_bit_4_out_5), .out_5(somador_bit_5_out_5), .out_4(out_4[4]));
  somador_bit somador_bit_6 (
    .in_2(in_2[5]), .in_3(in_3[5]), .in_1(somador_bit_5_out_5), .out_5(somador_bit_6_out_5), .out_4(out_4[5]));
  somador_bit somador_bit_7 (
    .in_2(in_2[6]), .in_3(in_3[6]), .in_1(somador_bit_6_out_5), .out_5(somador_bit_7_out_5), .out_4(out_4[6]));
  somador_bit somador_bit_8 (
    .in_2(in_2[7]), .in_3(in_3[7]), .in_1(somador_bit_7_out_5), .out_4(out_4[7]));  // open: out_5
endmodule

module memory_1bit (
  input  in_1,
  input  in_2,
  output out_3
);

  wire nand_1_out, nand_2_out, nand_3_out, nand_4_out;

  nand nand_1 (nand_1_out, in_1, in_2);
  nand nand_2 (nand_2_out, nand_1_out, in_2);
  nand nand_3 (nand_3_out, nand_1_out, nand_4_out);
  nand nand_4 (nand_4_out, nand_3_out, nand_2_out);
endmodule
